// Logisim project dynamic-branch-prediction.circ as structural Verilog: 11 circuits, main circuit ◇动态分支预测
module \动态分支预测  (
  output RegWrite,
  output MemWrite,
  output [31:0] IF_PC,
  output [31:0] ID_PC,
  output [31:0] EX_PC,
  output [31:0] M_PC,
  output [31:0] WB_PC,
  output [31:0] RDin,
  output [31:0] MDin,
  output [31:0] LedData
);

  wire BP_Control, BP_Correct, BP_IDEnable, BP_Live, BP_Mismatch, BP_Train, CLK, clock_1_out,
       comparator_6_eq, comparator_6_lt, Count_Branch, Count_Branch_BeforeStopFix, Count_BranchSuccess,
       Count_BranchSuccess_BeforeStopFix, Count_Data, Count_Data_0, Count_Data_1, Count_Data_BeforeStopFix,
       Count_Jump, Count_Jump_BeforeStopFix, Count_LoadUse, Count_LoadUse_0, Count_LoadUse_1,
       Count_LoadUse_BeforeStopFix, Count_PredictFailure, Count_PredictSuccess, Count_Redirect,
       Count_Redirect_BeforeStopFix, Count_System, Count_System_0, d_ff_1_q, EX_ActualTake, EX_ALUSRC,
       EX_BEQ, EX_BGE, EX_BNE, EX_Branch, EX_Branch_0, EX_EQ, EX_GE, EX_Hazard, EX_Hazard1, EX_Hazard1_0,
       EX_Hazard2, EX_Hazard2_0, EX_Jump, EX_Match1, EX_Match2, EX_MemToReg, EX_MemWrite, EX_NE, EX_NotTake,
       EX_Producer, EX_RDNonzero, EX_RDZero, EX_RegWrite, EX_Take, EX_Take0, EX_TakeBR, EX_TakeEQ, EX_TakeGE,
       EX_TakeNE, EX_Valid, FWD_MEM1, FWD_MEM2, FWD_MEMMatch1, FWD_MEMMatch2, FWD_WB1, FWD_WB2, FWD_WBMatch1,
       FWD_WBMatch2, Go, Go_NoRise, Go_NotPrevious, Go_Previous, Go_Rise, halt, ID_AllRAW, ID_ALUSRC, ID_BEQ,
       ID_BGE, ID_BImm_p2, ID_BImm_p3, ID_BNE, ID_BR, ID_DataStall, ID_DataStall_0, ID_FGE, ID_Flush,
       ID_Flush_0, ID_Flush_1, ID_Flush_BeforeStopFix, ID_IsBranch, ID_IsI, ID_IsJR, ID_IsLoad, ID_IsR,
       ID_IsStore, ID_MemToReg, ID_MemWrite, ID_MemWriteRaw, ID_Ready, ID_RegWrite, ID_ST, ID_URET, ID_Use1,
       ID_Use1Raw, ID_Use1Raw_0, ID_Use1Raw_1, ID_Use1Raw_2, ID_Use1Raw_3, ID_Use1Raw_4, ID_Use2, ID_Use2Raw,
       ID_Use2Raw_0, ID_Use2Raw_1, ID_Valid, ID_WriteRaw, IF_Advance, IF_Enable, IF_Enable_BeforeStopFix,
       IF_Flush, IF_Flush_BeforeStopFix, IF_Hold, IF_Hold_BeforeStopFix, IF_Kill, IF_NotKill, IF_Stall,
       IF_Stall_0, IF_Wait, IF_Want, IR1, IR2, IR3, LED_WE, MEM_Forwardable, MEM_HalfSel, MEM_Hazard,
       MEM_Hazard1, MEM_Hazard1_0, MEM_Hazard2, MEM_Hazard2_0, MEM_Match1, MEM_Match2, MEM_MemToReg,
       MEM_NotLoad, MEM_Producer, MEM_RDNonzero, MEM_RDZero, MEM_RegWrite, MEM_WriteLive,
       MemWrite_BeforeStopFix, nand_1_out, NotGo, PAUSE_HOLD, Pause_Keep, PAUSE_NEXT, PAUSE_NEXT_Old, RST,
       RUN, SYS_Busy, SYS_Busy_0, SYS_Busy_BeforeStopFix, SYS_Issue, SYS_Issue_0, SYS_Issue_1, SYS_Issue_2,
       SYS_Issue_BeforeStopFix, SYS_Ready, WB_HaltEvent, WB_Hazard, WB_Hazard1, WB_Hazard1_0, WB_Hazard2,
       WB_Hazard2_0, WB_Match1, WB_Match2, WB_MemToReg, WB_NoStop, WB_NotPrint, WB_Print, WB_PrintRaw,
       WB_Producer, WB_RDNonzero, WB_RDZero, WB_StopFlush, WB_Wait, WB_WriteLive;
  wire [2:0] ID_F3;
  wire [3:0] EX_ALUOP, ID_ALUOP, ID_BImm_p0;
  wire [4:0] EX_RA1, EX_RA2, EX_RD, ID_I12, ID_RA1, ID_RA2, MEM_RD, WB_RD;
  wire [5:0] ID_BImm_p1;
  wire [7:2] ID_CtrlRaw;
  wire [9:0] ID_Ctrl, MEM_Ctrl, WB_Ctrl;
  wire [9:2] EX_Ctrl;
  wire [12:0] CNT_num;
  wire [15:0] COUNT_NEXT, \LoadUse次数 , \LoadUse次数_Next , MEM_Half, MEM_High16, MEM_Low16, \分支气泡数 ,
       \分支气泡数_Next , \总周期数 , \插入气泡数 , \数据气泡数 , \数据气泡数_Next , \无条件分支数 , \无条件分支数_Next , \条件分支成功数 ,
       \条件分支成功数_Next , \条件分支次数 , \条件分支次数_Next , \系统等待周期 , \系统等待周期_Next , \预测失败次数 , \预测失败次数_Next , \预测成功次数 ,
       \预测成功次数_Next ;
  wire [19:0] ID_IR;
  wire [23:0] DADDR;
  wire [31:0] BP_EXInput, BP_IDInput, BP_Next, EX_ActualNext, EX_ALU, EX_B, EX_BImm, EX_BTarget, EX_Imm,
       EX_IR, EX_JImm, EX_JRTarget, EX_JTarget, EX_PC4, EX_PredPC, EX_R1, EX_R2, EX_Raw1, EX_Raw2, EX_Res0,
       EX_Result, EX_Target, EX_Target0, FWD_Older1, FWD_Older2, ID_BImm, ID_BImm_half, ID_Bypass1,
       ID_Bypass2, ID_IImm, ID_Imm, ID_ImmIS, ID_JImm, ID_JImm_half, ID_PredPC, ID_R1, ID_R2, ID_SImm,
       ID_UImm, IF_BufferedIR, IF_BufferedPC, IF_IR, IF_PC4, MEM_IR, MEM_Load, MEM_PC4, MEM_R1, MEM_Result,
       MEM_SignedHalf, NEXT_PC, NEXT_PC_BeforeStopFix, WB_IR, WB_Load, WB_PC4, WB_R1, WB_R2, WB_Result;

  Button \u_总复位  (.out(RST));
  Button _1 (.out(IR1));
  Button _2 (.out(IR2));
  Button _3 (.out(IR3));
  // Probe on \总周期数 
  // Probe on \总周期数 
  Button \u_继续运行  (.out(Go));
  LED led_1 (.in(1'b0));
  LED led_2 (.in(1'b0));
  LED led_3 (.in(1'b0));
  Hex_Digit_Display hex_digit_display_1 (.value(LedData[31:28]));  // open: dp
  // Probe on IF_PC[19:0]
  // riscv_probe riscv_probe_1: pin names not known; wires that end beside it: IF_IR
  Register #(.width(32)) PC (.D(NEXT_PC), .en(IF_Enable), .Q(IF_PC), .clk(CLK), .clr(RST), .cs(1'b0), .preset(1'b0));
  Hex_Digit_Display hex_digit_display_2 (.value(LedData[23:20]));  // open: dp
  Hex_Digit_Display hex_digit_display_3 (.value(LedData[27:24]));  // open: dp
  // Probe on ID_PC[19:0]
  // riscv_probe riscv_probe_2: pin names not known; wires that end beside it: {ID_BImm_p3, ID_BImm_p1, ID_I12, ID_IR[19:15], ID_F3, ID_BImm_p0, ID_BImm_p2, ID_IR[6:0]}
  Comparator #(.width(2), .mode("unsigned")) comparator_1 (.a(ID_IR[1:0]), .b(2'b11), .eq(ID_Valid));  // open: gt, lt
  and and_1 (ID_RegWrite, ID_WriteRaw, ID_Valid);
  Hex_Digit_Display hex_digit_display_4 (.value(LedData[19:16]));  // open: dp
  Hex_Digit_Display hex_digit_display_5 (.value(LedData[15:12]));  // open: dp
  Adder #(.width(32)) adder_1 (.a(IF_PC), .b(32'h4), .out(IF_PC4), .cin(1'b0));  // open: cout
  Multiplexer #(.width(32), .enable("false")) multiplexer_1 (
    .in0(BP_Next), .in1(EX_ActualNext), .out(NEXT_PC_BeforeStopFix), .sel(EX_Take));
  Multiplexer #(.width(32), .enable("false")) multiplexer_2 (
    .in0(IF_IR), .in1({32{1'b0}}), .out(IF_BufferedIR), .sel(IF_Flush));
  Multiplexer #(.width(32), .enable("false")) multiplexer_3 (
    .in0(IF_PC), .in1({32{1'b0}}), .out(IF_BufferedPC), .sel(IF_Flush));
  Hex_Digit_Display hex_digit_display_6 (.value(LedData[11:8]));  // open: dp
  Hex_Digit_Display hex_digit_display_7 (.value(LedData[7:4]));  // open: dp
  // Probe on EX_PC[19:0]
  // riscv_probe riscv_probe_3: pin names not known; wires that end beside it: EX_IR
  ROM #(.addrWidth(20), .dataWidth(32), .Select("high")) rom_1 (.addr(IF_PC[21:2]), .data(IF_IR), .sel(1'b1));
  Hex_Digit_Display hex_digit_display_8 (.value(LedData[3:0]));  // open: dp
  IF_ID if_id_1 (
    .PredictJump(1'b0), .IR(IF_BufferedIR), .\气泡 (1'b0),
    .IR_2({ID_BImm_p3, ID_BImm_p1, ID_I12, ID_IR[19:15], ID_F3, ID_BImm_p0, ID_BImm_p2, ID_IR[6:0]}),
    .\EN_低电平有效 (IF_Hold), .CLK(CLK), .PC_2(ID_PC), .PC(IF_BufferedPC),
    .IR_3({ID_BImm_p3, ID_BImm_p1, ID_I12, ID_IR[19:15], ID_F3, ID_BImm_p0, ID_BImm_p2, ID_IR[6:0]}));  // open: PredictJump_2
  // Probe on \总周期数 
  // Probe on M_PC[19:0]
  // riscv_probe riscv_probe_4: pin names not known; wires that end beside it: MEM_IR
  // Probe on \总周期数 
  // Probe on \无条件分支数 
  // Probe on \条件分支成功数 
  // Probe on \插入气泡数 
  // Probe on \LoadUse次数 
  \单周期硬布线控制器  \u_单周期硬布线控制器_1  (
    .Funct({ID_BImm_p1[5], ID_BImm_p1[0], ID_F3}), .OP(ID_IR[6:2]), .ALU_OP(ID_ALUOP),
    .MemToReg(ID_MemToReg), .MemWrite(ID_MemWriteRaw), .ALU_SRC(ID_ALUSRC), .RegWrite(ID_WriteRaw),
    .ecall(ID_CtrlRaw[4]), .S_type(ID_ST), .Jalr(ID_CtrlRaw[3]), .Beq(ID_BEQ), .JAL(ID_CtrlRaw[2]),
    .Bne(ID_BNE), .in_3(ID_I12[1]), .uret(ID_URET));
  // Probe on IF_PC[11:0]
  // Probe on WB_PC[19:0]
  // riscv_probe riscv_probe_5: pin names not known; wires that end beside it: WB_IR
  Regifile regifile_1 (
    .Din(RDin), .Clk(CLK), .R1(ID_R1), .R2(ID_R2), .WE(RegWrite), .W_num(WB_RD), .R1_num(ID_RA1),
    .R2_num(ID_RA2));
  assign ID_IImm = {{20{ID_BImm_p3}}, {ID_BImm_p3, ID_BImm_p1, ID_I12}};  // Bit_Extender bit_extender_1
  assign ID_SImm = {{20{ID_BImm_p3}}, {ID_BImm_p3, ID_BImm_p1, ID_BImm_p0, ID_BImm_p2}};  // Bit_Extender bit_extender_2
  Multiplexer #(.width(32), .enable("false")) multiplexer_4 (.in0(ID_IImm), .in1(ID_SImm), .out(ID_ImmIS), .sel(ID_ST));
  assign ID_UImm = {ID_BImm_p3, ID_BImm_p1, ID_I12, ID_IR[19:15], ID_F3, ID_BImm_p0, ID_BImm_p2, ID_IR[6:0]} & 32'hfffff000;  // AND_Gate and_2, 32 bits wide
  Multiplexer #(.width(32), .enable("false")) multiplexer_5 (
    .in0(ID_ImmIS), .in1(ID_UImm), .out(ID_Imm), .sel(ID_CtrlRaw[6]));
  Comparator #(.width(7), .mode("unsigned")) comparator_2 (
    .a(ID_IR[6:0]), .b(7'b0110111), .eq(ID_CtrlRaw[6]));  // open: gt, lt
  Comparator #(.width(3), .mode("unsigned")) comparator_3 (.a(ID_F3), .b(3'b001), .eq(ID_CtrlRaw[7]));  // open: gt, lt
  Comparator #(.width(7), .mode("unsigned")) comparator_4 (.a(ID_IR[6:0]), .b(7'b1100011), .eq(ID_BR));  // open: gt, lt
  Comparator #(.width(3), .mode("unsigned")) comparator_5 (.a(ID_F3), .b(3'b101), .eq(ID_FGE));  // open: gt, lt
  and and_3 (ID_BGE, ID_BR, ID_FGE);
  Multiplexer #(.width(5), .enable("false")) multiplexer_6 (
    .in0(ID_IR[19:15]), .in1(5'b10001), .out(ID_RA1), .sel(ID_CtrlRaw[4]));
  Multiplexer #(.width(5), .enable("false")) multiplexer_7 (
    .in0(ID_I12), .in1(5'b01010), .out(ID_RA2), .sel(ID_CtrlRaw[4]));
  Multiplexer #(.width(10), .enable("false")) multiplexer_8 (
    .in0({10{1'b0}}), .in1({2'b00, ID_CtrlRaw[7:6], ID_BGE, ID_CtrlRaw[4:2], ID_BNE, ID_BEQ}), .out(ID_Ctrl),
    .sel(ID_Valid));
  // Probe on EX_PC[11:0]
  // Probe on ID_PC[11:0]
  assign ID_BImm_half = {{20{ID_BImm_p3}}, {ID_BImm_p3, ID_BImm_p2, ID_BImm_p1, ID_BImm_p0}};  // Bit_Extender bit_extender_3
  Shifter #(.width(32)) shifter_1 (.in(ID_BImm_half), .\dist (5'b00001), .out(ID_BImm));
  assign ID_JImm_half = {{12{ID_BImm_p3}}, {ID_BImm_p3, ID_IR[19:15], ID_F3, ID_I12[0], ID_BImm_p1, ID_I12[4:1]}};  // Bit_Extender bit_extender_4
  Shifter #(.width(32)) shifter_2 (.in(ID_JImm_half), .\dist (5'b00001), .out(ID_JImm));
  // Probe on M_PC[11:0]
  D_Flip_Flop #(.Pre_Clr_Positions("LEGACY"), .NewFFLayout("false")) d_ff_1 (.Q(d_ff_1_q));  // open: clk, D, Qn, preset, reset
  // Probe on 13'hc
  // Probe on WB_PC[11:0]
  Comparator #(.width(13)) comparator_6 (
    .a(CNT_num), .b(13'hc), .eq(comparator_6_eq), .lt(comparator_6_lt));  // open: gt
  Clock clock_1 (.out(clock_1_out));
  ID_EX id_ex_1 (
    .PC(ID_PC), .RS1(ID_Bypass1), .RS2(ID_Bypass2),
    .IR({ID_BImm_p3, ID_BImm_p1, ID_I12, ID_IR[19:15], ID_F3, ID_BImm_p0, ID_BImm_p2, ID_IR[6:0]}),
    .WriteReg_num({ID_BImm_p0, ID_BImm_p2}), .ALUOP(ID_ALUOP), .\气泡 (ID_Flush), .PC_2(EX_PC),
    .RS1_2(EX_Raw1), .RS2_2(EX_Raw2), .IR_2(EX_IR), .RegWrite_2(EX_RegWrite), .MemToReg_2(EX_MemToReg),
    .MemWrite_2(EX_MemWrite), .ALuSrc_2(EX_ALUSRC), .WriteReg_num_2(EX_RD), .RegWrite(ID_RegWrite),
    .MemToReg(ID_MemToReg), .MemWrite(ID_MemWrite), .ALuSrc(ID_ALUSRC), .ALUOP_2(EX_ALUOP),
    .\EN_低电平有效 (halt), .CLK(CLK), .Reserved1_2(EX_BImm), .Reserved1(ID_BImm), .Imm32_2(EX_Imm),
    .Imm32(ID_Imm), .rs2Fwd(2'b00), .rs1Fwd(2'b00), .PredictJump(1'b0), .\指令译码信号 (ID_Ctrl),
    .\指令译码信号_2 ({EX_Ctrl[9:6], EX_BGE, EX_Ctrl[4:2], EX_BNE, EX_BEQ}), .Reserved2(ID_JImm),
    .Reserved2_2(EX_JImm));  // open: rs2Fwd_2, rs1Fwd_2, PredictJump_2
  nand nand_1 (nand_1_out, d_ff_1_q, comparator_6_eq);
  Counter #(.width(13), .max('h1fff), .ongoal("stay"), .behavior("old")) counter_1 (
    .count(comparator_6_lt), .Q(CNT_num), .clk(clock_1_out));  // open: load, D, carry, clr, preset
  assign CLK = nand_1_out ? clock_1_out : 1'bz;  // Controlled_Buffer controlled_buffer_1
  ALU alu_1 (
    .X(EX_R1), .Y(EX_B), .AluOP(EX_ALUOP), .Equal(EX_EQ), .Result(EX_ALU), .out_4(EX_GE));  // open: Result_2, out_6
  Pull_Resistor #(.pull(1)) pull_resistor_1 (.node(CLK));
  Multiplexer #(.width(32), .enable("false")) multiplexer_9 (.in0(EX_R2), .in1(EX_Imm), .out(EX_B), .sel(EX_ALUSRC));
  Multiplexer #(.width(32), .enable("false")) multiplexer_10 (
    .in0(EX_ALU), .in1(EX_Imm), .out(EX_Res0), .sel(EX_Ctrl[6]));
  Adder #(.width(32)) adder_2 (.a(EX_PC), .b(32'h4), .out(EX_PC4), .cin(1'b0));  // open: cout
  or or_1 (EX_Jump, EX_Ctrl[2], EX_Ctrl[3]);
  Multiplexer #(.width(32), .enable("false")) multiplexer_11 (
    .in0(EX_Res0), .in1(EX_PC4), .out(EX_Result), .sel(EX_Jump));
  Adder #(.width(32)) adder_3 (.a(EX_PC), .b(EX_BImm), .out(EX_BTarget), .cin(1'b0));  // open: cout
  Adder #(.width(32)) adder_4 (.a(EX_PC), .b(EX_JImm), .out(EX_JTarget), .cin(1'b0));  // open: cout
  assign EX_JRTarget = EX_ALU & 32'hfffffffe;  // AND_Gate and_4, 32 bits wide
  and and_5 (EX_TakeEQ, EX_BEQ, EX_EQ);
  not not_1 (EX_NE, EX_EQ);
  and and_6 (EX_TakeNE, EX_BNE, EX_NE);
  and and_7 (EX_TakeGE, EX_BGE, EX_GE);
  or or_2 (EX_Take0, EX_TakeEQ, EX_TakeNE);
  or or_3 (EX_TakeBR, EX_Take0, EX_TakeGE);
  or or_4 (EX_ActualTake, EX_TakeBR, EX_Jump);
  Multiplexer #(.width(32), .enable("false")) multiplexer_12 (
    .in0(EX_BTarget), .in1(EX_JTarget), .out(EX_Target0), .sel(EX_Ctrl[2]));
  Multiplexer #(.width(32), .enable("false")) multiplexer_13 (
    .in0(EX_Target0), .in1(EX_JRTarget), .out(EX_Target), .sel(EX_Ctrl[3]));
  EX_MEM ex_mem_1 (
    .PC(EX_PC), .IR(EX_IR), .WriteReg_num(EX_RD), .\气泡 (WB_StopFlush), .PC_2(M_PC), .IR_2(MEM_IR),
    .RegWrite_2(MEM_RegWrite), .MemToReg_2(MEM_MemToReg), .MemWrite_2(MEM_WriteLive),
    .WriteReg_num_2(MEM_RD), .RegWrite(EX_RegWrite), .MemToReg(EX_MemToReg), .MemWrite(EX_MemWrite),
    .\EN_低电平有效 (halt), .CLK(CLK), .Reserved1_2(MEM_R1), .Reserved1(EX_R1),
    .\指令译码信号 ({EX_Ctrl[9:6], EX_BGE, EX_Ctrl[4:2], EX_BNE, EX_BEQ}), .\指令译码信号_2 (MEM_Ctrl),
    .Reserved2(EX_PC4), .Reserved2_2(MEM_PC4), .WriteData(EX_R2), .WriteData_2(MDin), .AluResult(EX_Result),
    .AluResult_2({MEM_Result[31:26], DADDR, MEM_HalfSel, MEM_Result[0]}));
  // Probe on \预测成功次数 
  RAM #(.addrWidth(24), .dataWidth(32), .bus("separate"), .Select("high"), .simpleMode("false")) ram_1 (
    .addr(DADDR), .din(MDin), .data({MEM_High16, MEM_Low16}), .str(MemWrite), .sel(1'b1), .clk(CLK),
    .ld(1'b1), .clr(1'b0));
  Multiplexer #(.width(16), .enable("false")) multiplexer_14 (
    .in0(MEM_Low16), .in1(MEM_High16), .out(MEM_Half), .sel(MEM_HalfSel));
  assign MEM_SignedHalf = {{16{MEM_Half[15]}}, MEM_Half};  // Bit_Extender bit_extender_5
  Multiplexer #(.width(32), .enable("false")) multiplexer_15 (
    .in0({MEM_High16, MEM_Low16}), .in1(MEM_SignedHalf), .out(MEM_Load), .sel(MEM_Ctrl[7]));
  // Probe on \预测失败次数 
  MEM_WB mem_wb_1 (
    .PC(M_PC), .IR(MEM_IR), .WriteReg_num(MEM_RD), .\气泡 (WB_StopFlush), .PC_2(WB_PC), .IR_2(WB_IR),
    .RegWrite_2(WB_WriteLive), .MemToReg_2(WB_MemToReg), .WriteReg_num_2(WB_RD), .RegWrite(MEM_RegWrite),
    .MemToReg(MEM_MemToReg), .\EN_低电平有效 (halt), .CLK(CLK), .Reserved1_2(WB_R1), .Reserved1(MEM_R1),
    .\指令译码信号 (MEM_Ctrl), .\指令译码信号_2 (WB_Ctrl), .Reserved2(MDin), .Reserved2_2(WB_R2), .MemData(MEM_Load),
    .MemData_2(WB_Load), .AluResult({MEM_Result[31:26], DADDR, MEM_HalfSel, MEM_Result[0]}),
    .AluResult_2(WB_Result));
  Multiplexer #(.width(32), .enable("false")) multiplexer_16 (
    .in0(WB_Result), .in1(WB_Load), .out(RDin), .sel(WB_MemToReg));
  Comparator #(.width(32), .mode("unsigned")) comparator_7 (.a(WB_R1), .b(32'h22), .eq(WB_Print));  // open: gt, lt
  and and_8 (WB_PrintRaw, WB_Ctrl[4], WB_Print);
  not not_2 (WB_NotPrint, WB_Print);
  and and_9 (WB_Wait, WB_Ctrl[4], WB_NotPrint);
  Register #(.width(32)) \ECALL显示锁存  (
    .D(WB_R2), .en(LED_WE), .Q(LedData), .clk(CLK), .clr(RST), .cs(1'b0), .preset(1'b0));
  Register #(.width(16)) \u_流水周期  (
    .D(COUNT_NEXT), .en(RUN), .Q(\总周期数 ), .clk(CLK), .clr(RST), .cs(1'b0), .preset(1'b0));
  Adder #(.width(16)) adder_5 (.a(\总周期数 ), .b(16'h1), .out(COUNT_NEXT), .cin(1'b0));  // open: cout
  Register #(.width(1)) \ECALL暂停状态  (
    .D(PAUSE_NEXT), .en(1'b1), .Q(halt), .clk(CLK), .clr(RST), .cs(1'b0), .preset(1'b0));
  and and_10 (RegWrite, WB_WriteLive, RUN);
  and and_11 (MemWrite_BeforeStopFix, MEM_WriteLive, RUN);
  Comparator #(.width(7), .mode("unsigned")) comparator_8 (
    .a(ID_IR[6:0]), .b(7'b0110011), .eq(ID_IsR));  // open: gt, lt
  Comparator #(.width(7), .mode("unsigned")) comparator_9 (
    .a(ID_IR[6:0]), .b(7'b0010011), .eq(ID_IsI));  // open: gt, lt
  Comparator #(.width(7), .mode("unsigned")) comparator_10 (
    .a(ID_IR[6:0]), .b(7'b0000011), .eq(ID_IsLoad));  // open: gt, lt
  Comparator #(.width(7), .mode("unsigned")) comparator_11 (
    .a(ID_IR[6:0]), .b(7'b0100011), .eq(ID_IsStore));  // open: gt, lt
  Comparator #(.width(7), .mode("unsigned")) comparator_12 (
    .a(ID_IR[6:0]), .b(7'b1100011), .eq(ID_IsBranch));  // open: gt, lt
  Comparator #(.width(7), .mode("unsigned")) comparator_13 (
    .a(ID_IR[6:0]), .b(7'b1100111), .eq(ID_IsJR));  // open: gt, lt
  or or_5 (ID_Use1Raw_0, ID_IsR, ID_IsI);
  or or_6 (ID_Use1Raw_1, ID_Use1Raw_0, ID_IsLoad);
  or or_7 (ID_Use1Raw_2, ID_Use1Raw_1, ID_IsStore);
  or or_8 (ID_Use1Raw_3, ID_Use1Raw_2, ID_IsBranch);
  or or_9 (ID_Use1Raw_4, ID_Use1Raw_3, ID_IsJR);
  or or_10 (ID_Use1Raw, ID_Use1Raw_4, ID_CtrlRaw[4]);
  or or_11 (ID_Use2Raw_0, ID_IsR, ID_IsStore);
  or or_12 (ID_Use2Raw_1, ID_Use2Raw_0, ID_IsBranch);
  or or_13 (ID_Use2Raw, ID_Use2Raw_1, ID_CtrlRaw[4]);
  and and_12 (ID_Use1, ID_Valid, ID_Use1Raw);
  and and_13 (ID_Use2, ID_Valid, ID_Use2Raw);
  and and_14 (ID_MemWrite, ID_MemWriteRaw, ID_Valid);
  Comparator #(.width(5), .mode("unsigned")) comparator_14 (.a(EX_RD), .b({5{1'b0}}), .eq(EX_RDZero));  // open: gt, lt
  not not_3 (EX_RDNonzero, EX_RDZero);
  and and_15 (EX_Producer, EX_RegWrite, EX_RDNonzero);
  Comparator #(.width(5), .mode("unsigned")) comparator_15 (.a(ID_RA1), .b(EX_RD), .eq(EX_Match1));  // open: gt, lt
  Register #(.width(16)) \u_数据气泡数  (
    .D(\数据气泡数_Next ), .en(Count_Data), .Q(\数据气泡数 ), .clk(CLK), .clr(RST), .cs(1'b0), .preset(1'b0));
  Adder #(.width(16)) adder_6 (.a(\数据气泡数 ), .b(16'h1), .out(\数据气泡数_Next ), .cin(1'b0));  // open: cout
  Adder #(.width(16)) adder_7 (.a(\数据气泡数 ), .b(\分支气泡数 ), .out(\插入气泡数 ), .cin(1'b0));  // open: cout
  and and_16 (EX_Hazard1_0, EX_Match1, ID_Use1);
  and and_17 (EX_Hazard1, EX_Hazard1_0, EX_Producer);
  Comparator #(.width(5), .mode("unsigned")) comparator_16 (.a(ID_RA2), .b(EX_RD), .eq(EX_Match2));  // open: gt, lt
  and and_18 (EX_Hazard2_0, EX_Match2, ID_Use2);
  and and_19 (EX_Hazard2, EX_Hazard2_0, EX_Producer);
  or or_14 (EX_Hazard, EX_Hazard1, EX_Hazard2);
  Comparator #(.width(5), .mode("unsigned")) comparator_17 (
    .a(MEM_RD), .b({5{1'b0}}), .eq(MEM_RDZero));  // open: gt, lt
  not not_4 (MEM_RDNonzero, MEM_RDZero);
  and and_20 (MEM_Producer, MEM_RegWrite, MEM_RDNonzero);
  Comparator #(.width(5), .mode("unsigned")) comparator_18 (.a(ID_RA1), .b(MEM_RD), .eq(MEM_Match1));  // open: gt, lt
  and and_21 (MEM_Hazard1_0, MEM_Match1, ID_Use1);
  and and_22 (MEM_Hazard1, MEM_Hazard1_0, MEM_Producer);
  Comparator #(.width(5), .mode("unsigned")) comparator_19 (.a(ID_RA2), .b(MEM_RD), .eq(MEM_Match2));  // open: gt, lt
  and and_23 (MEM_Hazard2_0, MEM_Match2, ID_Use2);
  and and_24 (MEM_Hazard2, MEM_Hazard2_0, MEM_Producer);
  or or_15 (MEM_Hazard, MEM_Hazard1, MEM_Hazard2);
  Comparator #(.width(5), .mode("unsigned")) comparator_20 (.a(WB_RD), .b({5{1'b0}}), .eq(WB_RDZero));  // open: gt, lt
  not not_5 (WB_RDNonzero, WB_RDZero);
  and and_25 (WB_Producer, WB_WriteLive, WB_RDNonzero);
  Comparator #(.width(5), .mode("unsigned")) comparator_21 (.a(ID_RA1), .b(WB_RD), .eq(WB_Match1));  // open: gt, lt
  and and_26 (WB_Hazard1_0, WB_Match1, ID_Use1);
  and and_27 (WB_Hazard1, WB_Hazard1_0, WB_Producer);
  Comparator #(.width(5), .mode("unsigned")) comparator_22 (.a(ID_RA2), .b(WB_RD), .eq(WB_Match2));  // open: gt, lt
  and and_28 (WB_Hazard2_0, WB_Match2, ID_Use2);
  Register #(.width(16)) \u_分支气泡数  (
    .D(\分支气泡数_Next ), .en(Count_Redirect), .Q(\分支气泡数 ), .clk(CLK), .clr(RST), .cs(1'b0), .preset(1'b0));
  Adder #(.width(16)) adder_8 (.a(\分支气泡数 ), .b(16'h2), .out(\分支气泡数_Next ), .cin(1'b0));  // open: cout
  and and_29 (WB_Hazard2, WB_Hazard2_0, WB_Producer);
  or or_16 (WB_Hazard, WB_Hazard1, WB_Hazard2);
  or or_17 (ID_DataStall_0, EX_Hazard, MEM_Hazard);
  or or_18 (ID_AllRAW, ID_DataStall_0, WB_Hazard);
  and and_30 (ID_DataStall, EX_Hazard, EX_MemToReg);
  or or_19 (SYS_Busy_0, EX_Ctrl[4], MEM_Ctrl[4]);
  or or_20 (SYS_Busy_BeforeStopFix, SYS_Busy_0, WB_Ctrl[4]);
  not not_6 (ID_Ready, ID_DataStall);
  not not_7 (SYS_Ready, SYS_Busy);
  not not_8 (EX_NotTake, EX_Take);
  and and_31 (SYS_Issue_0, ID_CtrlRaw[4], ID_Valid);
  and and_32 (SYS_Issue_1, SYS_Issue_0, ID_Ready);
  and and_33 (SYS_Issue_2, SYS_Issue_1, SYS_Ready);
  and and_34 (SYS_Issue_BeforeStopFix, SYS_Issue_2, EX_NotTake);
  or or_21 (IF_Stall_0, ID_DataStall, SYS_Busy);
  or or_22 (IF_Stall, IF_Stall_0, SYS_Issue);
  not not_9 (IF_Advance, IF_Stall);
  or or_23 (IF_Want, IF_Advance, EX_Take);
  not not_10 (RUN, halt);
  and and_35 (IF_Enable_BeforeStopFix, IF_Want, RUN);
  or or_24 (IF_Kill, EX_Take, SYS_Issue);
  not not_11 (IF_NotKill, IF_Kill);
  and and_36 (IF_Wait, IF_Stall, IF_NotKill);
  or or_25 (IF_Hold_BeforeStopFix, IF_Wait, halt);
  Register #(.width(16)) \u_LoadUse次数  (
    .D(\LoadUse次数_Next ), .en(Count_LoadUse), .Q(\LoadUse次数 ), .clk(CLK), .clr(RST), .cs(1'b0), .preset(1'b0));
  Adder #(.width(16)) adder_9 (.a(\LoadUse次数 ), .b(16'h1), .out(\LoadUse次数_Next ), .cin(1'b0));  // open: cout
  or or_26 (IF_Flush_BeforeStopFix, RST, IF_Kill);
  or or_27 (ID_Flush_0, RST, EX_Take);
  or or_28 (ID_Flush_1, ID_Flush_0, ID_DataStall);
  or or_29 (ID_Flush_BeforeStopFix, ID_Flush_1, SYS_Busy);
  and and_37 (WB_HaltEvent, WB_Wait, RUN);
  or or_30 (PAUSE_HOLD, halt, WB_HaltEvent);
  not not_12 (NotGo, Go);
  and and_38 (PAUSE_NEXT_Old, PAUSE_HOLD, NotGo);
  and and_39 (LED_WE, WB_PrintRaw, RUN);
  and and_40 (Count_Data_0, ID_DataStall, EX_NotTake);
  and and_41 (Count_Data_1, Count_Data_0, SYS_Ready);
  and and_42 (Count_Data_BeforeStopFix, Count_Data_1, RUN);
  and and_43 (Count_LoadUse_0, ID_DataStall, EX_NotTake);
  and and_44 (Count_LoadUse_1, Count_LoadUse_0, SYS_Ready);
  and and_45 (Count_LoadUse_BeforeStopFix, Count_LoadUse_1, RUN);
  and and_46 (Count_Redirect_BeforeStopFix, EX_Take, RUN);
  and and_47 (Count_BranchSuccess_BeforeStopFix, EX_TakeBR, RUN);
  or or_31 (EX_Branch_0, EX_BEQ, EX_BNE);
  or or_32 (EX_Branch, EX_Branch_0, EX_BGE);
  and and_48 (Count_Branch_BeforeStopFix, EX_Branch, RUN);
  and and_49 (Count_Jump_BeforeStopFix, EX_Jump, RUN);
  and and_50 (Count_System_0, SYS_Busy, EX_NotTake);
  and and_51 (Count_System, Count_System_0, RUN);
  Register #(.width(16)) \u_条件分支次数  (
    .D(\条件分支次数_Next ), .en(Count_Branch), .Q(\条件分支次数 ), .clk(CLK), .clr(RST), .cs(1'b0), .preset(1'b0));
  Adder #(.width(16)) adder_10 (.a(\条件分支次数 ), .b(16'h1), .out(\条件分支次数_Next ), .cin(1'b0));  // open: cout
  Register #(.width(16)) \u_条件分支成功数  (
    .D(\条件分支成功数_Next ), .en(Count_BranchSuccess), .Q(\条件分支成功数 ), .clk(CLK), .clr(RST), .cs(1'b0),
    .preset(1'b0));
  Adder #(.width(16)) adder_11 (.a(\条件分支成功数 ), .b(16'h1), .out(\条件分支成功数_Next ), .cin(1'b0));  // open: cout
  Multiplexer #(.width(32), .select(1), .enable("false")) multiplexer_17 (
    .in0(ID_R1), .in1(RDin), .out(ID_Bypass1), .sel(WB_Hazard1));
  Multiplexer #(.width(32), .select(1), .enable("false")) multiplexer_18 (
    .in0(ID_R2), .in1(RDin), .out(ID_Bypass2), .sel(WB_Hazard2));
  not not_13 (MEM_NotLoad, MEM_MemToReg);
  and and_52 (MEM_Forwardable, MEM_Producer, MEM_NotLoad);
  Comparator #(.width(5), .mode("unsigned")) comparator_23 (
    .a(EX_RA1), .b(MEM_RD), .eq(FWD_MEMMatch1));  // open: gt, lt
  and and_53 (FWD_MEM1, FWD_MEMMatch1, MEM_Forwardable);
  Comparator #(.width(5), .mode("unsigned")) comparator_24 (.a(EX_RA1), .b(WB_RD), .eq(FWD_WBMatch1));  // open: gt, lt
  and and_54 (FWD_WB1, FWD_WBMatch1, WB_Producer);
  Comparator #(.width(5), .mode("unsigned")) comparator_25 (
    .a(EX_RA2), .b(MEM_RD), .eq(FWD_MEMMatch2));  // open: gt, lt
  and and_55 (FWD_MEM2, FWD_MEMMatch2, MEM_Forwardable);
  Comparator #(.width(5), .mode("unsigned")) comparator_26 (.a(EX_RA2), .b(WB_RD), .eq(FWD_WBMatch2));  // open: gt, lt
  and and_56 (FWD_WB2, FWD_WBMatch2, WB_Producer);
  Register #(.width(16)) \u_无条件分支数  (
    .D(\无条件分支数_Next ), .en(Count_Jump), .Q(\无条件分支数 ), .clk(CLK), .clr(RST), .cs(1'b0), .preset(1'b0));
  Adder #(.width(16)) adder_12 (.a(\无条件分支数 ), .b(16'h1), .out(\无条件分支数_Next ), .cin(1'b0));  // open: cout
  Multiplexer #(.width(5), .select(1), .enable("false")) multiplexer_19 (
    .in0(EX_IR[19:15]), .in1(5'b10001), .out(EX_RA1), .sel(EX_Ctrl[4]));
  Multiplexer #(.width(5), .select(1), .enable("false")) multiplexer_20 (
    .in0(EX_IR[24:20]), .in1(5'b01010), .out(EX_RA2), .sel(EX_Ctrl[4]));
  Register #(.width(16)) \u_系统等待周期  (
    .D(\系统等待周期_Next ), .en(Count_System), .Q(\系统等待周期 ), .clk(CLK), .clr(RST), .cs(1'b0), .preset(1'b0));
  Adder #(.width(16)) adder_13 (.a(\系统等待周期 ), .b(16'h1), .out(\系统等待周期_Next ), .cin(1'b0));  // open: cout
  Multiplexer #(.width(32), .select(1), .enable("false")) multiplexer_21 (
    .in0(EX_Raw1), .in1(RDin), .out(FWD_Older1), .sel(FWD_WB1));
  Multiplexer #(.width(32), .select(1), .enable("false")) multiplexer_22 (
    .in0(EX_Raw2), .in1(RDin), .out(FWD_Older2), .sel(FWD_WB2));
  Multiplexer #(.width(32), .select(1), .enable("false")) multiplexer_23 (
    .in0(FWD_Older1), .in1({MEM_Result[31:26], DADDR, MEM_HalfSel, MEM_Result[0]}), .out(EX_R1),
    .sel(FWD_MEM1));
  Multiplexer #(.width(32), .select(1), .enable("false")) multiplexer_24 (
    .in0(FWD_Older2), .in1({MEM_Result[31:26], DADDR, MEM_HalfSel, MEM_Result[0]}), .out(EX_R2),
    .sel(FWD_MEM2));
  or or_33 (SYS_Issue, 1'b0, 1'b0);
  or or_34 (SYS_Busy, 1'b0, 1'b0);
  not not_14 (WB_NoStop, WB_HaltEvent);
  and and_57 (MemWrite, MemWrite_BeforeStopFix, WB_NoStop);
  Multiplexer #(.width(32), .select(1), .enable("false")) multiplexer_25 (
    .in0(NEXT_PC_BeforeStopFix), .in1(WB_PC4), .out(NEXT_PC), .sel(WB_HaltEvent));
  or or_35 (IF_Enable, IF_Enable_BeforeStopFix, WB_HaltEvent);
  or or_36 (IF_Flush, IF_Flush_BeforeStopFix, WB_HaltEvent);
  or or_37 (ID_Flush, ID_Flush_BeforeStopFix, WB_HaltEvent);
  and and_58 (IF_Hold, IF_Hold_BeforeStopFix, WB_NoStop);
  or or_38 (WB_StopFlush, RST, WB_HaltEvent);
  and and_59 (Count_Data, Count_Data_BeforeStopFix, WB_NoStop);
  and and_60 (Count_LoadUse, Count_LoadUse_BeforeStopFix, WB_NoStop);
  and and_61 (Count_Redirect, Count_Redirect_BeforeStopFix, WB_NoStop);
  and and_62 (Count_BranchSuccess, Count_BranchSuccess_BeforeStopFix, WB_NoStop);
  and and_63 (Count_Branch, Count_Branch_BeforeStopFix, WB_NoStop);
  and and_64 (Count_Jump, Count_Jump_BeforeStopFix, WB_NoStop);
  Adder #(.width(32)) adder_14 (.a(WB_PC), .b(32'h4), .out(WB_PC4), .cin(1'b0));  // open: cout
  Multiplexer #(.width(32), .select(1), .enable("false")) multiplexer_26 (
    .in0(EX_PC4), .in1(EX_Target), .out(EX_ActualNext), .sel(EX_ActualTake));
  Comparator #(.width(32), .mode("unsigned")) comparator_27 (
    .a(EX_PredPC), .b(EX_ActualNext), .eq(BP_Correct));  // open: gt, lt
  not not_15 (BP_Mismatch, BP_Correct);
  not not_16 (BP_IDEnable, IF_Hold);
  or or_39 (BP_Control, EX_Branch, EX_Jump);
  Register #(.width(1), .trigger("rising"), .Select("low")) u_Go_Previous (
    .D(Go), .en(1'b1), .Q(Go_Previous), .clk(CLK), .clr(RST), .cs(1'b0), .preset(1'b0));
  not not_17 (Go_NoRise, Go_Rise);
  and and_65 (Count_PredictSuccess, BP_Train, BP_Correct);
  Register #(.width(16), .trigger("rising"), .Select("low")) \u_预测成功次数_2  (
    .D(\预测成功次数_Next ), .en(Count_PredictSuccess), .Q(\预测成功次数 ), .clk(CLK), .clr(RST), .cs(1'b0), .preset(1'b0));
  Adder #(.width(16)) adder_15 (.a(\预测成功次数 ), .b(16'h1), .out(\预测成功次数_Next ), .cin(1'b0));  // open: cout
  and and_66 (EX_Take, EX_Valid, BP_Mismatch);
  Comparator #(.width(2), .mode("unsigned")) comparator_28 (.a(EX_IR[1:0]), .b(2'b11), .eq(EX_Valid));  // open: gt, lt
  Multiplexer #(.width(32), .select(1), .enable("false")) multiplexer_27 (
    .in0(BP_Next), .in1({32{1'b0}}), .out(BP_IDInput), .sel(IF_Flush));
  Multiplexer #(.width(32), .select(1), .enable("false")) multiplexer_28 (
    .in0(ID_PredPC), .in1({32{1'b0}}), .out(BP_EXInput), .sel(ID_Flush));
  and and_67 (BP_Live, BP_Control, RUN);
  not not_18 (Go_NotPrevious, Go_Previous);
  and and_68 (Pause_Keep, halt, Go_NoRise);
  and and_69 (Count_PredictFailure, BP_Train, BP_Mismatch);
  \动态分支预测器  \u_动态分支预测器_1  (
    .IF_PC(IF_PC), .IF_IR(IF_IR), .EX_PC(EX_PC), .EX_Target(EX_Target), .EX_ActualTake(EX_ActualTake),
    .BP_Train(BP_Train), .CLK(CLK), .RST(RST), .BP_Next(BP_Next));
  Register #(.width(16), .trigger("rising"), .Select("low")) \u_预测失败次数_2  (
    .D(\预测失败次数_Next ), .en(Count_PredictFailure), .Q(\预测失败次数 ), .clk(CLK), .clr(RST), .cs(1'b0), .preset(1'b0));
  Adder #(.width(16)) adder_16 (.a(\预测失败次数 ), .b(16'h1), .out(\预测失败次数_Next ), .cin(1'b0));  // open: cout
  Register #(.width(32), .trigger("rising"), .Select("low")) u_ID_PredPC (
    .D(BP_IDInput), .en(BP_IDEnable), .Q(ID_PredPC), .clk(CLK), .clr(RST), .cs(1'b0), .preset(1'b0));
  Register #(.width(32), .trigger("rising"), .Select("low")) u_EX_PredPC (
    .D(BP_EXInput), .en(RUN), .Q(EX_PredPC), .clk(CLK), .clr(RST), .cs(1'b0), .preset(1'b0));
  and and_70 (BP_Train, BP_Live, WB_NoStop);
  and and_71 (Go_Rise, Go, Go_NotPrevious);
  or or_40 (PAUSE_NEXT, Pause_Keep, WB_HaltEvent);

  // Other names for the same wires on the sheet: EX_Ctrl (some bits) = {EX_BGE, EX_BNE, EX_BEQ}; EX_JAL = EX_Ctrl[2];
  //   EX_JALR = EX_Ctrl[3]; EX_ECALL = EX_Ctrl[4]; EX_LUI = EX_Ctrl[6]; EX_LH = EX_Ctrl[7]; EX_Low2[1:0] = EX_IR[1:0];
  //   EX_RS1[4:0] = EX_IR[19:15]; EX_RS2[4:0] = EX_IR[24:20]; PAUSED = halt;
  //   ID_BImm_raw[11:0] = {ID_BImm_p3, ID_BImm_p2, ID_BImm_p1, ID_BImm_p0};
  //   ID_IR (some bits) = {ID_BImm_p3, ID_BImm_p1, ID_I12, ID_F3, ID_BImm_p0, ID_BImm_p2};
  //   ID_RD[4:0] = {ID_BImm_p0, ID_BImm_p2}; ID_S12[11:0] = {ID_BImm_p3, ID_BImm_p1, ID_BImm_p0, ID_BImm_p2};
  //   ID_CtrlRaw (some bits) = {ID_BGE, ID_BNE, ID_BEQ}; ID_JAL = ID_CtrlRaw[2]; ID_JALR = ID_CtrlRaw[3];
  //   ID_ECALL = ID_CtrlRaw[4]; ID_LUI = ID_CtrlRaw[6]; ID_LH = ID_CtrlRaw[7]; ID_Low2[1:0] = ID_IR[1:0];
  //   ID_OP7[6:0] = ID_IR[6:0]; ID_OP5[4:0] = ID_IR[6:2]; ID_IR21 = ID_I12[1];
  //   ID_JImm_p0[9:0] = {ID_BImm_p1, ID_I12[4:1]};
  //   ID_JImm_raw[19:0] = {ID_BImm_p3, ID_IR[19:15], ID_F3, ID_I12[0], ID_BImm_p1, ID_I12[4:1]}; ID_RS2[4:0] = ID_I12;
  //   ID_FUN5[4:0] = {ID_BImm_p1[5], ID_BImm_p1[0], ID_F3}; ID_I12[11:5] = {ID_BImm_p3, ID_BImm_p1};
  //   ID_JImm_p1 = ID_I12[0]; ID_JImm_p2[7:0] = {ID_IR[19:15], ID_F3}; ID_RS1[4:0] = ID_IR[19:15];
  //   ID_JImm_p3 = ID_BImm_p3; ID_LoadUse = ID_DataStall; IADDR[19:0] = IF_PC[21:2]; LoadUse气泡[15:0] = \LoadUse次数 ;
  //   MEM_ECALL = MEM_Ctrl[4]; MEM_LH = MEM_Ctrl[7]; MEM_PC[31:0] = M_PC; MEM_Result[25:1] = {DADDR, MEM_HalfSel};
  //   MEM_Word[31:0] = {MEM_High16, MEM_Low16}; RAW_CLK = CLK; WB_ECALL = WB_Ctrl[4]

  // Notes on the sheet:
  //   中断源
  //   时空图监测，可删除
  //   中断等待指示
  //   IF：顺序与 EX 分支反馈
  //   Load-Use：保持前端，清空 ID-EX 一周期
  //   EX 预测错误优先：清空两级并恢复实际下一 PC
  //   ECALL 正常流动；WB 暂停取消年轻指令，Go 从下一条重取
  //   IF-ID 原气泡零源断开：外置清零，封装不变
  //   数码管输出
  //   contents of rom_1 (hex, n*v repeats v):
  //   00100493 0100006f 00100493 00200913 00300993 0100006f 00100493 00200913 00300993 0100006f 00100493
  //   00200913 00300993 0100006f 00100493 00200913 00300993 3dc000ef 00100413 00100493 01f49493 00900533
  //   02200893 00000073 0024d493 00048463 fedff06f 00900533 02200893 00000073 00100493 00249493 00900533
  //   02200893 00000073 00048463 fedff06f 00100493 01f49493 00900533 02200893 00000073 4034d493 00900533
  //   02200893 00000073 4044d493 00900533 02200893 00000073 4044d493 00900533 02200893 00000073 4044d493
  //   00900533 02200893 00000073 4044d493 00900533 02200893 00000073 4044d493 00900533 02200893 00000073
  //   4044d493 00900533 02200893 00000073 4044d493 00900533 02200893 00000073 00100413 01f41993 41f9d993
  //   00000433 00c00913 00300b13 00140413 00f47413 00800293 00100313 00499993 0089e9b3 01300533 02200893
  //   00000073 406282b3 fe0294e3 00140413 00f00f93 01f47433 01c41413 00800293 00100313 0049d993 0089e9b3
  //   01300533 02200893 00000073 406282b3 fe0294e3 01c45413 406b0b33 000b0463 f95ff06f 000002b3 fff2c293
  //   00829293 0ff2e293 00500533 02200893 00000073 fff00413 00000493 0084a023 00140413 00448493 0084a023
  //   00140413 00448493 0084a023 00140413 00448493 0084a023 00140413 00448493 0084a023 00140413 00448493
  //   0084a023 00140413 00448493 0084a023 00140413 00448493 0084a023 00140413 00448493 0084a023 00140413
  //   00448493 0084a023 00140413 00448493 0084a023 00140413 00448493 0084a023 00140413 00448493 0084a023
  //   00140413 00448493 0084a023 00140413 00448493 0084a023 00140413 00448493 0084a023 00140413 00448493
  //   00140413 00000433 03c00493 00042983 0004aa03 0149a2b3 00028663 0134a023 01442023 ffc48493 fe9412e3
  //   00800533 02200893 00000073 00440413 03c00493 fc9416e3 00a00893 00000073 fff00293 07700493 00849493
  //   07748493 00900533 02200893 00000073 01000e13 0054c4b3 00900533 02200893 00000073 fffe0e13 fe0e16e3
  //   00a00893 00000073 00800e13 fedc04b7 fff00413 01045413 0084e4b3 00900533 02200893 00000073 0ba984b7
  //   00900533 00000073 076544b7 00900533 00000073 032104b7 00900533 00000073 fffe0e13 fa0e1ee3 00a00893
  //   00000073 00000313 01000e13 08400493 00849493 08348493 00400913 00891913 00490913 00849493 08248493
  //   00849493 08148493 00891913 00490913 00891913 00490913 00932023 012484b3 00430313 fffe0e13 fe0e18e3
  //   02000e13 00000313 00031483 00900533 02200893 00000073 00230313 fffe0e13 fe0e14e3 00a00893 00000073
  //   00f00493 00900533 02200893 00000073 fff48493 fe04d8e3 00a00893 00000073 00a00893 00000073 ff9ff06f
  //   00000413 00140413 00800533 02200893 00000073 00240413 00800533 02200893 00000073 00340413 00800533
  //   02200893 00000073 00440413 00800533 02200893 00000073 00540413 00800533 02200893 00000073 00640413
  //   00800533 02200893 00000073 00740413 00800533 02200893 00000073 00840413 00800533 02200893 02200893
  //   00000073 00008067
  //   ID：立即数、控制信号
  //   控制位
  //   流水调试日志用
  //   暂停节拍，不能为0
  //   戳工具置1进入计数暂停模式，ctrl+k时钟自动运行到对应节拍暂停
  //   ctrl+k关闭时钟连续运行，将控制位置零，进入单步调试模式调试
  //   用这个时钟源需要去掉电路中的其他时钟源
  //   可计数暂停的时钟源
  //   EX：执行与分支
  //   为方便自动评测，需要输出流水线各段保存的PC值，注意是PC不是PC+4，另外ID段寄存器写入信息，Mem段内存写入信息也要输出
  //   动态分支预测统计（十进制）
  //   预测下一PC与实际下一PC比较；暂停冻结，复位清零
  //   MEM：访存与 LH
  //   Ctrl+R 全复位 / Ctrl+K 自动运行
  //   WB：写回与 ECALL
  //   气泡冲突检测：真实源寄存器 / x0 排除 / EX → MEM → WB
  //   气泡总数 = 数据停顿 + 2 × 预测错误次数
  //   数据重定向：MEM 非 load 结果优先；WB 实际写回次之
  //   MEM load 地址禁止转发；Load-Use 在 ID 停顿 1 周期
  //   ALU / 分支 / JALR / Store / ECALL 共用修正后的 R1、R2
  //   WB 暂停边界：前端不提前排空；取消年轻副作用并保存续行 PC
  //   16项 BTB + 2位饱和 BHT（双击查看）
  //   WB暂停优先于预测恢复；Go上升沿继续；停机期间计数、访存和预测器冻结
endmodule

// 单周期硬布线控制器
module \单周期硬布线控制器  (
  input  [4:0] OP,
  input  [4:0] Funct,
  input  in_3,
  output [3:0] ALU_OP,
  output uret,
  output MemToReg,
  output ecall,
  output MemWrite,
  output ALU_SRC,
  output RegWrite,
  output S_type,
  output Beq,
  output Bne,
  output Jalr,
  output JAL
);

  wire \控制信号自动生成_1_ecall ;

  \运算控制器自动生成  \u_运算控制器自动生成_1  (
    .OP2(OP[0]), .OP3(OP[1]), .OP4(OP[2]), .OP5(OP[3]), .OP6(OP[4]), .F12(Funct[0]), .F13(Funct[1]),
    .F14(Funct[2]), .F25(Funct[3]), .F30(Funct[4]), .S0(ALU_OP[0]), .S1(ALU_OP[1]), .S2(ALU_OP[2]),
    .S3(ALU_OP[3]));
  \控制信号自动生成  \u_控制信号自动生成_1  (
    .OP2(OP[0]), .MemToReg(MemToReg), .OP3(OP[1]), .MemWrite(MemWrite), .OP4(OP[2]), .ALU_SRC(ALU_SRC),
    .OP5(OP[3]), .RegWrite(RegWrite), .OP6(OP[4]), .ecall(\控制信号自动生成_1_ecall ), .F12(Funct[0]),
    .S_Type(S_type), .F13(Funct[1]), .BEQ(Beq), .F14(Funct[2]), .BNE(Bne), .F25(Funct[3]), .JALR(Jalr),
    .F30(Funct[4]), .JAL(JAL));
  and and_1 (uret, in_3, \控制信号自动生成_1_ecall );
  and and_2 (ecall, ~in_3, \控制信号自动生成_1_ecall );  // AND_Gate

  // Other names for the same wires on the sheet: IR21 = in_3; OP_CODE[4:0] = OP

  // Notes on the sheet:
  //   运算器控制器，根据指令生成运算器功能选择信号
  //   控制信号生成，产生数据通路需要的其他控制信号
endmodule

// 运算器控制器
module \运算控制器自动生成  (
  input  OP2,
  input  OP3,
  input  OP4,
  input  OP5,
  input  OP6,
  input  F12,
  input  F13,
  input  F14,
  input  F25,
  input  F30,
  output S0,
  output S1,
  output S2,
  output S3
);

  wire _ADD_0, _ADD_ALL_0, _ADD_ALL_1, _ADD_ALL_2, _S0_0, _S0_1, _S0_2, _S0_3, _S1_0, _S1_1, _S1_2, _S2_0,
       _S2_1, _S3_0, _S3_1, _S3_2, _SRA_0, _SRL_0, _SUB_0, ADD, ADD_ALL, AND, BR, F0, F1, F2, F3, F4, F5, F6,
       F7, I, J, JR, LD, N30, NSUB, OR, R, RI, SLT, SLTU, SRA, SRL, ST, SUB, SUBBIT, SYS, U, XOR;

  Comparator #(.width(5), .mode("unsigned")) comparator_1 (
    .a({OP6, OP5, OP4, OP3, OP2}), .b(5'b01100), .eq(R));  // open: gt, lt
  Comparator #(.width(5), .mode("unsigned")) comparator_2 (
    .a({OP6, OP5, OP4, OP3, OP2}), .b(5'b00100), .eq(I));  // open: gt, lt
  Comparator #(.width(5), .mode("unsigned")) comparator_3 (
    .a({OP6, OP5, OP4, OP3, OP2}), .b({5{1'b0}}), .eq(LD));  // open: gt, lt
  Comparator #(.width(5), .mode("unsigned")) comparator_4 (
    .a({OP6, OP5, OP4, OP3, OP2}), .b(5'b01000), .eq(ST));  // open: gt, lt
  Comparator #(.width(5), .mode("unsigned")) comparator_5 (
    .a({OP6, OP5, OP4, OP3, OP2}), .b(5'b11000), .eq(BR));  // open: gt, lt
  Comparator #(.width(5), .mode("unsigned")) comparator_6 (
    .a({OP6, OP5, OP4, OP3, OP2}), .b(5'b11001), .eq(JR));  // open: gt, lt
  Comparator #(.width(5), .mode("unsigned")) comparator_7 (
    .a({OP6, OP5, OP4, OP3, OP2}), .b(5'b11011), .eq(J));  // open: gt, lt
  Comparator #(.width(5), .mode("unsigned")) comparator_8 (
    .a({OP6, OP5, OP4, OP3, OP2}), .b(5'b01101), .eq(U));  // open: gt, lt
  Comparator #(.width(5), .mode("unsigned")) comparator_9 (
    .a({OP6, OP5, OP4, OP3, OP2}), .b(5'b11100), .eq(SYS));  // open: gt, lt
  Comparator #(.width(3), .mode("unsigned")) comparator_10 (.a({F14, F13, F12}), .b(3'b000), .eq(F0));  // open: gt, lt
  Comparator #(.width(3), .mode("unsigned")) comparator_11 (.a({F14, F13, F12}), .b(3'b001), .eq(F1));  // open: gt, lt
  Comparator #(.width(3), .mode("unsigned")) comparator_12 (.a({F14, F13, F12}), .b(3'b010), .eq(F2));  // open: gt, lt
  Comparator #(.width(3), .mode("unsigned")) comparator_13 (.a({F14, F13, F12}), .b(3'b011), .eq(F3));  // open: gt, lt
  Comparator #(.width(3), .mode("unsigned")) comparator_14 (.a({F14, F13, F12}), .b(3'b100), .eq(F4));  // open: gt, lt
  Comparator #(.width(3), .mode("unsigned")) comparator_15 (.a({F14, F13, F12}), .b(3'b101), .eq(F5));  // open: gt, lt
  Comparator #(.width(3), .mode("unsigned")) comparator_16 (.a({F14, F13, F12}), .b(3'b110), .eq(F6));  // open: gt, lt
  Comparator #(.width(3), .mode("unsigned")) comparator_17 (.a({F14, F13, F12}), .b(3'b111), .eq(F7));  // open: gt, lt
  not not_1 (N30, F30);
  not not_2 (NSUB, SUBBIT);
  or or_1 (RI, R, I);
  and and_1 (SUBBIT, R, F30);
  and and_2 (_ADD_0, RI, F0);
  and and_3 (ADD, _ADD_0, NSUB);
  and and_4 (_SUB_0, R, F0);
  and and_5 (SUB, _SUB_0, F30);
  and and_6 (SLT, RI, F2);
  and and_7 (SLTU, RI, F3);
  and and_8 (XOR, RI, F4);
  and and_9 (OR, RI, F6);
  and and_10 (AND, RI, F7);
  and and_11 (_SRA_0, RI, F5);
  and and_12 (SRA, _SRA_0, F30);
  and and_13 (_SRL_0, RI, F5);
  and and_14 (SRL, _SRL_0, N30);
  or or_2 (_ADD_ALL_0, ADD, LD);
  or or_3 (_ADD_ALL_1, _ADD_ALL_0, ST);
  or or_4 (_ADD_ALL_2, _ADD_ALL_1, JR);
  or or_5 (ADD_ALL, _ADD_ALL_2, U);
  or or_6 (_S0_0, ADD_ALL, AND);
  or or_7 (_S0_1, _S0_0, XOR);
  or or_8 (_S0_2, _S0_1, SLT);
  or or_9 (_S0_3, _S0_2, SRA);
  or or_10 (S0, _S0_3, BR);
  or or_11 (_S1_0, SUB, AND);
  or or_12 (_S1_1, _S1_0, SLT);
  or or_13 (_S1_2, _S1_1, SRL);
  or or_14 (S1, _S1_2, BR);
  or or_15 (_S2_0, ADD_ALL, SUB);
  or or_16 (_S2_1, _S2_0, AND);
  or or_17 (S2, _S2_1, SLTU);
  or or_18 (_S3_0, OR, XOR);
  or or_19 (_S3_1, _S3_0, SLT);
  or or_20 (_S3_2, _S3_1, SLTU);
  or or_21 (S3, _S3_2, BR);

  // Other names for the same wires on the sheet: FUN3[2:0] = {F14, F13, F12}; OP[4:0] = {OP6, OP5, OP4, OP3, OP2}

  // Notes on the sheet:
  //   ALU 编码：0 SLL / 1 SRA / 2 SRL / 5 ADD / 6 SUB / 7 AND / 8 OR / 9 XOR / 11 SLT / 12 SLTU
endmodule

// 控制信号生成
module \控制信号自动生成  (
  input  OP2,
  input  OP3,
  input  OP4,
  input  OP5,
  input  OP6,
  input  F12,
  input  F13,
  input  F14,
  input  F25,
  input  F30,
  output MemToReg,
  output MemWrite,
  output ALU_SRC,
  output RegWrite,
  output ecall,
  output S_Type,
  output BEQ,
  output BNE,
  output JALR,
  output JAL
);

  wire _ALU_SRC_0, _ALU_SRC_1, _ALU_SRC_2, _RegWrite_0, _RegWrite_1, _RegWrite_2, _RegWrite_3, BR, F0, F1,
       F2, F3, F4, F5, F6, F7, I, J, JR, LD, R, ST, SYS, U;

  Comparator #(.width(5), .mode("unsigned")) comparator_1 (
    .a({OP6, OP5, OP4, OP3, OP2}), .b(5'b01100), .eq(R));  // open: gt, lt
  Comparator #(.width(5), .mode("unsigned")) comparator_2 (
    .a({OP6, OP5, OP4, OP3, OP2}), .b(5'b00100), .eq(I));  // open: gt, lt
  Comparator #(.width(5), .mode("unsigned")) comparator_3 (
    .a({OP6, OP5, OP4, OP3, OP2}), .b({5{1'b0}}), .eq(LD));  // open: gt, lt
  Comparator #(.width(5), .mode("unsigned")) comparator_4 (
    .a({OP6, OP5, OP4, OP3, OP2}), .b(5'b01000), .eq(ST));  // open: gt, lt
  Comparator #(.width(5), .mode("unsigned")) comparator_5 (
    .a({OP6, OP5, OP4, OP3, OP2}), .b(5'b11000), .eq(BR));  // open: gt, lt
  Comparator #(.width(5), .mode("unsigned")) comparator_6 (
    .a({OP6, OP5, OP4, OP3, OP2}), .b(5'b11001), .eq(JR));  // open: gt, lt
  Comparator #(.width(5), .mode("unsigned")) comparator_7 (
    .a({OP6, OP5, OP4, OP3, OP2}), .b(5'b11011), .eq(J));  // open: gt, lt
  Comparator #(.width(5), .mode("unsigned")) comparator_8 (
    .a({OP6, OP5, OP4, OP3, OP2}), .b(5'b01101), .eq(U));  // open: gt, lt
  Comparator #(.width(5), .mode("unsigned")) comparator_9 (
    .a({OP6, OP5, OP4, OP3, OP2}), .b(5'b11100), .eq(SYS));  // open: gt, lt
  Comparator #(.width(3), .mode("unsigned")) comparator_10 (.a({F14, F13, F12}), .b(3'b000), .eq(F0));  // open: gt, lt
  Comparator #(.width(3), .mode("unsigned")) comparator_11 (.a({F14, F13, F12}), .b(3'b001), .eq(F1));  // open: gt, lt
  Comparator #(.width(3), .mode("unsigned")) comparator_12 (.a({F14, F13, F12}), .b(3'b010), .eq(F2));  // open: gt, lt
  Comparator #(.width(3), .mode("unsigned")) comparator_13 (.a({F14, F13, F12}), .b(3'b011), .eq(F3));  // open: gt, lt
  Comparator #(.width(3), .mode("unsigned")) comparator_14 (.a({F14, F13, F12}), .b(3'b100), .eq(F4));  // open: gt, lt
  Comparator #(.width(3), .mode("unsigned")) comparator_15 (.a({F14, F13, F12}), .b(3'b101), .eq(F5));  // open: gt, lt
  Comparator #(.width(3), .mode("unsigned")) comparator_16 (.a({F14, F13, F12}), .b(3'b110), .eq(F6));  // open: gt, lt
  Comparator #(.width(3), .mode("unsigned")) comparator_17 (.a({F14, F13, F12}), .b(3'b111), .eq(F7));  // open: gt, lt
  or or_1 (MemToReg, LD, LD);
  or or_2 (MemWrite, ST, ST);
  or or_3 (S_Type, ST, ST);
  or or_4 (_ALU_SRC_0, I, LD);
  or or_5 (_ALU_SRC_1, _ALU_SRC_0, ST);
  or or_6 (_ALU_SRC_2, _ALU_SRC_1, U);
  or or_7 (ALU_SRC, _ALU_SRC_2, JR);
  or or_8 (_RegWrite_0, R, I);
  or or_9 (_RegWrite_1, _RegWrite_0, LD);
  or or_10 (_RegWrite_2, _RegWrite_1, U);
  or or_11 (_RegWrite_3, _RegWrite_2, J);
  or or_12 (RegWrite, _RegWrite_3, JR);
  or or_13 (ecall, SYS, SYS);
  or or_14 (JALR, JR, JR);
  or or_15 (JAL, J, J);
  and and_1 (BEQ, BR, F0);
  and and_2 (BNE, BR, F1);

  // Other names for the same wires on the sheet: FUN3[2:0] = {F14, F13, F12}; OP[4:0] = {OP6, OP5, OP4, OP3, OP2}

  // Notes on the sheet:
  //   基本控制信号；BGE 与 LH / LUI 扩展选择在主电路
endmodule

// ALU
module ALU (
  input  [31:0] X,
  input  [31:0] Y,
  input  [3:0] AluOP,
  output out_4,
  output Equal,
  output out_6,
  output [31:0] Result,
  output [31:0] Result_2
);

  wire [0:0] comparator_1_lt, comparator_2_lt;
  wire [31:0] adder_1_out, AND_out, divider_1_out, divider_1_rem, multiplier_1_cout, multiplier_1_out,
       NOR_out, OR_out, shifter_1_out, shifter_2_out, shifter_3_out, subtractor_1_out, XOR_out;

  assign AND_out = X & Y;  // AND_Gate AND, 32 bits wide
  assign OR_out = X | Y;  // OR_Gate OR, 32 bits wide
  Shifter #(.width(32)) shifter_1 (.in(X), .\dist (Y[4:0]), .out(shifter_1_out));
  Shifter #(.width(32), .shift("ar")) shifter_2 (.in(X), .\dist (Y[4:0]), .out(shifter_2_out));
  Shifter #(.width(32), .shift("lr")) shifter_3 (.in(X), .\dist (Y[4:0]), .out(shifter_3_out));
  Multiplier #(.width(32)) multiplier_1 (.a(X), .b(Y), .out(multiplier_1_out), .cout(multiplier_1_cout));  // open: cin
  Divider #(.width(32)) divider_1 (.a(X), .b(Y), .out(divider_1_out), .rem(divider_1_rem));  // open: upper
  Adder #(.width(32)) adder_1 (.a(X), .b(Y), .out(adder_1_out));  // open: cin, cout
  Subtractor #(.width(32)) subtractor_1 (.a(X), .b(Y), .out(subtractor_1_out));  // open: bin, bout
  assign XOR_out = X ^ Y;  // XOR_Gate XOR, 32 bits wide
  assign NOR_out = ~(X | Y);  // NOR_Gate NOR, 32 bits wide
  Comparator #(.width(32)) comparator_1 (.a(X), .b(Y), .eq(Equal), .lt(comparator_1_lt[0]));  // open: gt
  Comparator #(.width(32), .mode("unsigned")) comparator_2 (.a(X), .b(Y), .lt(comparator_2_lt[0]));  // open: gt, eq
  Multiplexer #(.select(4), .width(32), .enable("false")) multiplexer_1 (
    .in0(shifter_1_out), .in1(shifter_2_out), .in2(shifter_3_out), .in3(multiplier_1_out),
    .in4(divider_1_out), .in5(adder_1_out), .in6(subtractor_1_out), .in7(AND_out), .in8(OR_out),
    .in9(XOR_out), .in10(NOR_out), .in11({{31{1'b0}}, comparator_1_lt[0]}),
    .in12({{31{1'b0}}, comparator_2_lt[0]}), .in13({32{1'b0}}), .in14({32{1'b0}}), .in15({32{1'b0}}),
    .out(Result), .sel(AluOP));
  Multiplexer #(.select(4), .width(32), .enable("false")) multiplexer_2 (
    .in0({32{1'b0}}), .in1({32{1'b0}}), .in2({32{1'b0}}), .in3(multiplier_1_cout), .in4(divider_1_rem),
    .in5({32{1'b0}}), .in6({32{1'b0}}), .in7({32{1'b0}}), .in8({32{1'b0}}), .in9({32{1'b0}}),
    .in10({32{1'b0}}), .in11({32{1'b0}}), .in12({32{1'b0}}), .in13({32{1'b0}}), .in14({32{1'b0}}),
    .in15({32{1'b0}}), .out(Result_2), .sel(AluOP));
  Multiplexer #(.select(4), .enable("false")) multiplexer_3 (
    .in0(1'b0), .in1(1'b0), .in2(1'b0), .in3(1'b0), .in4(1'b0), .in5(1'b0), .in6(1'b0), .in7(1'b0),
    .in8(1'b0), .in9(1'b0), .in10(1'b0), .in11(comparator_1_lt[0]), .in12(comparator_2_lt[0]), .in13(1'b0),
    .in14(1'b0), .in15(1'b0), .out(out_6), .sel(AluOP));
  not not_1 (out_4, out_6);

  // Other names for the same wires on the sheet: Result2[31:0] = Result_2; S[3:0] = AluOP; tunnel = out_6;
  //   tunnel_t = out_4

  // Notes on the sheet:
  //   不要改变此引脚区域内容，也不要改变ALU封装形式
  //   输入引脚
  //   输出引脚
endmodule

module Regifile (
  input  [31:0] Din,
  input  Clk,
  input  WE,
  input  [4:0] R1_num,
  input  [4:0] W_num,
  input  [4:0] R2_num,
  output [31:0] R1,
  output [31:0] R2
);

  // register_file register_file_1: pin names not known; wires that end beside it: Din, Clk, WE, W_num, R1_num, R2_num, R1, R2
endmodule

// IF / ID
module IF_ID (
  input  PredictJump,
  input  [31:0] IR,
  input  [31:0] PC,
  input  \气泡 ,
  input  \EN_低电平有效 ,
  input  CLK,
  output PredictJump_2,
  output [31:0] IR_2,
  output [31:0] PC_2,
  output [31:0] IR_3
);

  wire multiplexer_1_out, not_1_out, pull_resistor_3_node;
  wire [31:0] multiplexer_2_out, multiplexer_3_out, undriven;

  Pull_Resistor pull_resistor_1 (.node(\气泡 ));
  Multiplexer #(.enable("false")) multiplexer_1 (.in0(PredictJump), .in1(1'b0), .out(multiplexer_1_out), .sel(\气泡 ));
  Multiplexer #(.width(32), .enable("false")) multiplexer_2 (
    .in0(IR), .in1(undriven), .out(multiplexer_2_out), .sel(\气泡 ));
  Multiplexer #(.width(32), .enable("false")) multiplexer_3 (
    .in0(PC), .in1(undriven), .out(multiplexer_3_out), .sel(\气泡 ));
  Pull_Resistor pull_resistor_2 (.node(\EN_低电平有效 ));
  Pull_Resistor pull_resistor_3 (.node(pull_resistor_3_node));
  not not_1 (not_1_out, \EN_低电平有效 );
  Register #(.width(1)) u_PredictJump (
    .D(multiplexer_1_out), .en(not_1_out), .Q(PredictJump_2), .clk(CLK));  // open: clr
  Register #(.width(32)) u_IR (.D(multiplexer_2_out), .en(not_1_out), .Q(IR_2), .clk(CLK));  // open: clr
  Register #(.width(32)) u_PC (.D(multiplexer_3_out), .en(not_1_out), .Q(PC_2), .clk(CLK));  // open: clr

  assign IR_3 = IR_2;

  // Notes on the sheet:
  //   气泡: pull=down
endmodule

// ID / EX
module ID_EX (
  input  [31:0] PC,
  input  [31:0] RS1,
  input  [31:0] RS2,
  input  RegWrite,
  input  MemToReg,
  input  MemWrite,
  input  ALuSrc,
  input  [31:0] Imm32,
  input  [1:0] rs2Fwd,
  input  [1:0] rs1Fwd,
  input  PredictJump,
  input  [31:0] IR,
  input  [31:0] Reserved1,
  input  [31:0] Reserved2,
  input  [4:0] WriteReg_num,
  input  [3:0] ALUOP,
  input  [9:0] \指令译码信号 ,
  input  \气泡 ,
  input  \EN_低电平有效 ,
  input  CLK,
  output [31:0] PC_2,
  output [31:0] RS1_2,
  output [31:0] RS2_2,
  output [31:0] Imm32_2,
  output [31:0] IR_2,
  output RegWrite_2,
  output MemToReg_2,
  output MemWrite_2,
  output ALuSrc_2,
  output [1:0] rs2Fwd_2,
  output [31:0] Reserved1_2,
  output [1:0] rs1Fwd_2,
  output PredictJump_2,
  output [31:0] Reserved2_2,
  output [4:0] WriteReg_num_2,
  output [3:0] ALUOP_2,
  output [9:0] \指令译码信号_2 
);

  wire not_1_out;
  wire [3:0] multiplexer_10_out;
  wire [4:0] multiplexer_9_out;
  wire [9:0] multiplexer_11_out;
  wire [15:0] multiplexer_8_out;
  wire [15:9] ControlBusIn, ControlBusOut;
  wire [31:0] multiplexer_1_out, multiplexer_2_out, multiplexer_3_out, multiplexer_4_out, multiplexer_5_out,
       multiplexer_6_out, multiplexer_7_out;

  Pull_Resistor pull_resistor_1 (.node({ControlBusIn, PredictJump, rs1Fwd, rs2Fwd, ALuSrc, MemWrite, MemToReg, RegWrite}));
  Pull_Resistor pull_resistor_2 (.node(\指令译码信号 ));
  Pull_Resistor pull_resistor_3 (.node(\气泡 ));
  Multiplexer #(.width(32), .enable("false")) multiplexer_1 (
    .in0(PC), .in1({32{1'b0}}), .out(multiplexer_1_out), .sel(\气泡 ));
  Multiplexer #(.width(32), .enable("false")) multiplexer_2 (
    .in0(RS1), .in1({32{1'b0}}), .out(multiplexer_2_out), .sel(\气泡 ));
  Multiplexer #(.width(32), .enable("false")) multiplexer_3 (
    .in0(RS2), .in1({32{1'b0}}), .out(multiplexer_3_out), .sel(\气泡 ));
  Multiplexer #(.width(32), .enable("false")) multiplexer_4 (
    .in0(Imm32), .in1({32{1'b0}}), .out(multiplexer_4_out), .sel(\气泡 ));
  Multiplexer #(.width(32), .enable("false")) multiplexer_5 (
    .in0(IR), .in1({32{1'b0}}), .out(multiplexer_5_out), .sel(\气泡 ));
  Multiplexer #(.width(32), .enable("false")) multiplexer_6 (
    .in0(Reserved1), .in1({32{1'b0}}), .out(multiplexer_6_out), .sel(\气泡 ));
  Multiplexer #(.width(32), .enable("false")) multiplexer_7 (
    .in0(Reserved2), .in1({32{1'b0}}), .out(multiplexer_7_out), .sel(\气泡 ));
  Multiplexer #(.width(16), .enable("false")) multiplexer_8 (
    .in0({ControlBusIn, PredictJump, rs1Fwd, rs2Fwd, ALuSrc, MemWrite, MemToReg, RegWrite}),
    .in1({16{1'b0}}), .out(multiplexer_8_out), .sel(\气泡 ));
  Multiplexer #(.width(5), .enable("false")) multiplexer_9 (
    .in0(WriteReg_num), .in1({5{1'b0}}), .out(multiplexer_9_out), .sel(\气泡 ));
  Multiplexer #(.width(4), .enable("false")) multiplexer_10 (
    .in0(ALUOP), .in1(4'b0000), .out(multiplexer_10_out), .sel(\气泡 ));
  Multiplexer #(.width(10), .enable("false")) multiplexer_11 (
    .in0(\指令译码信号 ), .in1({10{1'b0}}), .out(multiplexer_11_out), .sel(\气泡 ));
  not not_1 (not_1_out, \EN_低电平有效 );
  Pull_Resistor pull_resistor_4 (.node(\EN_低电平有效 ));
  Register #(.width(32)) u_PC (.D(multiplexer_1_out), .en(not_1_out), .Q(PC_2), .clk(CLK));  // open: clr
  Register #(.width(32)) register_1 (.D(multiplexer_2_out), .en(not_1_out), .Q(RS1_2), .clk(CLK));  // open: clr
  Register #(.width(32)) register_2 (.D(multiplexer_3_out), .en(not_1_out), .Q(RS2_2), .clk(CLK));  // open: clr
  Register #(.width(32)) register_3 (.D(multiplexer_4_out), .en(not_1_out), .Q(Imm32_2), .clk(CLK));  // open: clr
  Register #(.width(32)) register_4 (.D(multiplexer_5_out), .en(not_1_out), .Q(IR_2), .clk(CLK));  // open: clr
  Register #(.width(32)) register_5 (.D(multiplexer_6_out), .en(not_1_out), .Q(Reserved1_2), .clk(CLK));  // open: clr
  Register #(.width(32)) register_6 (.D(multiplexer_7_out), .en(not_1_out), .Q(Reserved2_2), .clk(CLK));  // open: clr
  Register #(.width(16)) register_7 (
    .D(multiplexer_8_out), .en(not_1_out),
    .Q({ControlBusOut, PredictJump_2, rs1Fwd_2, rs2Fwd_2, ALuSrc_2, MemWrite_2, MemToReg_2, RegWrite_2}),
    .clk(CLK));  // open: clr
  Register #(.width(5)) register_8 (.D(multiplexer_9_out), .en(not_1_out), .Q(WriteReg_num_2), .clk(CLK));  // open: clr
  Register #(.width(4)) register_9 (.D(multiplexer_10_out), .en(not_1_out), .Q(ALUOP_2), .clk(CLK));  // open: clr
  Register #(.width(10)) register_10 (.D(multiplexer_11_out), .en(not_1_out), .Q(\指令译码信号_2 ), .clk(CLK));  // open: clr

  // Other names for the same wires on the sheet: ControlBusIn[8:0] = {PredictJump, rs1Fwd, rs2Fwd, ALuSrc, MemWrite, MemToReg, RegWrite};
  //   ControlBusOut[8:0] = {PredictJump_2, rs1Fwd_2, rs2Fwd_2, ALuSrc_2, MemWrite_2, MemToReg_2, RegWrite_2}

  // Notes on the sheet:
  //   EN_低电平有效: pull=down
  //   PC、IR都应该一致传送，方便调试保留引脚，自己决定是否使用
  //   保留引脚，自己决定是否使用
  //   指令译码信号汇总在一起传输（bne，beq，jal，jalr，ecall，uret等）
  //   分线器已经设置好了，需要用的复制即可
  //   请将控制器输出的所有指令译码信号通过分线器汇总在一起后进行传输，后段需要使用的时候直接用分线器从多位宽线缆引出即可
  //   控制信号汇总在一起，预留了位宽，需要增加引脚可以利用剩余的线缆进行连接
endmodule

// EX/MEM
module EX_MEM (
  input  [31:0] PC,
  input  [31:0] AluResult,
  input  RegWrite,
  input  MemToReg,
  input  MemWrite,
  input  [31:0] WriteData,
  input  [31:0] IR,
  input  [31:0] Reserved1,
  input  [31:0] Reserved2,
  input  [4:0] WriteReg_num,
  input  [9:0] \指令译码信号 ,
  input  \气泡 ,
  input  \EN_低电平有效 ,
  input  CLK,
  output [31:0] PC_2,
  output [31:0] AluResult_2,
  output [31:0] WriteData_2,
  output [31:0] IR_2,
  output RegWrite_2,
  output MemToReg_2,
  output MemWrite_2,
  output [31:0] Reserved1_2,
  output [31:0] Reserved2_2,
  output [4:0] WriteReg_num_2,
  output [9:0] \指令译码信号_2 
);

  wire not_1_out;
  wire [4:0] multiplexer_8_out;
  wire [9:0] multiplexer_9_out;
  wire [15:0] multiplexer_7_out;
  wire [15:3] ControlBusIn, ControlBusOut;
  wire [31:0] multiplexer_1_out, multiplexer_2_out, multiplexer_3_out, multiplexer_4_out, multiplexer_5_out,
       multiplexer_6_out;

  Pull_Resistor pull_resistor_1 (.node({ControlBusIn, MemWrite, MemToReg, RegWrite}));
  Pull_Resistor pull_resistor_2 (.node(\指令译码信号 ));
  Pull_Resistor pull_resistor_3 (.node(\气泡 ));
  Multiplexer #(.width(32), .enable("false")) multiplexer_1 (
    .in0(PC), .in1({32{1'b0}}), .out(multiplexer_1_out), .sel(\气泡 ));
  Multiplexer #(.width(32), .enable("false")) multiplexer_2 (
    .in0(AluResult), .in1({32{1'b0}}), .out(multiplexer_2_out), .sel(\气泡 ));
  Multiplexer #(.width(32), .enable("false")) multiplexer_3 (
    .in0(WriteData), .in1({32{1'b0}}), .out(multiplexer_3_out), .sel(\气泡 ));
  Multiplexer #(.width(32), .enable("false")) multiplexer_4 (
    .in0(IR), .in1({32{1'b0}}), .out(multiplexer_4_out), .sel(\气泡 ));
  Multiplexer #(.width(32), .enable("false")) multiplexer_5 (
    .in0(Reserved1), .in1({32{1'b0}}), .out(multiplexer_5_out), .sel(\气泡 ));
  Multiplexer #(.width(32), .enable("false")) multiplexer_6 (
    .in0(Reserved2), .in1({32{1'b0}}), .out(multiplexer_6_out), .sel(\气泡 ));
  Multiplexer #(.width(16), .enable("false")) multiplexer_7 (
    .in0({ControlBusIn, MemWrite, MemToReg, RegWrite}), .in1({16{1'b0}}), .out(multiplexer_7_out), .sel(\气泡 ));
  Multiplexer #(.width(5), .enable("false")) multiplexer_8 (
    .in0(WriteReg_num), .in1({5{1'b0}}), .out(multiplexer_8_out), .sel(\气泡 ));
  Multiplexer #(.width(10), .enable("false")) multiplexer_9 (
    .in0(\指令译码信号 ), .in1({10{1'b0}}), .out(multiplexer_9_out), .sel(\气泡 ));
  not not_1 (not_1_out, \EN_低电平有效 );
  Pull_Resistor pull_resistor_4 (.node(\EN_低电平有效 ));
  Register #(.width(32)) u_PC (.D(multiplexer_1_out), .en(not_1_out), .Q(PC_2), .clk(CLK));  // open: clr
  Register #(.width(32)) register_1 (.D(multiplexer_2_out), .en(not_1_out), .Q(AluResult_2), .clk(CLK));  // open: clr
  Register #(.width(32)) register_2 (.D(multiplexer_3_out), .en(not_1_out), .Q(WriteData_2), .clk(CLK));  // open: clr
  Register #(.width(32)) register_3 (.D(multiplexer_4_out), .en(not_1_out), .Q(IR_2), .clk(CLK));  // open: clr
  Register #(.width(32)) register_4 (.D(multiplexer_5_out), .en(not_1_out), .Q(Reserved1_2), .clk(CLK));  // open: clr
  Register #(.width(32)) register_5 (.D(multiplexer_6_out), .en(not_1_out), .Q(Reserved2_2), .clk(CLK));  // open: clr
  Register #(.width(16)) register_6 (
    .D(multiplexer_7_out), .en(not_1_out), .Q({ControlBusOut, MemWrite_2, MemToReg_2, RegWrite_2}), .clk(CLK));  // open: clr
  Register #(.width(5)) register_7 (.D(multiplexer_8_out), .en(not_1_out), .Q(WriteReg_num_2), .clk(CLK));  // open: clr
  Register #(.width(10)) register_8 (.D(multiplexer_9_out), .en(not_1_out), .Q(\指令译码信号_2 ), .clk(CLK));  // open: clr

  // Other names for the same wires on the sheet: ControlBusIn[2:0] = {MemWrite, MemToReg, RegWrite};
  //   ControlBusOut[2:0] = {MemWrite_2, MemToReg_2, RegWrite_2}

  // Notes on the sheet:
  //   EN_低电平有效: pull=down
  //   保留引脚，自己决定是否使用
  //   PC、IR都应该一致传送，方便调试保留引脚，自己决定是否使用
  //   指令译码信号汇总在一起传输（bne，beq，jal，jalr，ecall，uret等）
  //   分线器已经设置好了，需要用的复制即可
  //   请将控制器输出的所有指令译码信号通过分线器汇总在一起后进行传输，后段需要使用的时候直接用分线器从多位宽线缆引出即可
endmodule

// MEM/WB
module MEM_WB (
  input  [31:0] PC,
  input  [31:0] AluResult,
  input  RegWrite,
  input  MemToReg,
  input  [31:0] MemData,
  input  [31:0] IR,
  input  [31:0] Reserved1,
  input  [31:0] Reserved2,
  input  [4:0] WriteReg_num,
  input  [9:0] \指令译码信号 ,
  input  \气泡 ,
  input  \EN_低电平有效 ,
  input  CLK,
  output [31:0] PC_2,
  output [31:0] AluResult_2,
  output [31:0] MemData_2,
  output [31:0] IR_2,
  output RegWrite_2,
  output MemToReg_2,
  output [31:0] Reserved1_2,
  output [31:0] Reserved2_2,
  output [4:0] WriteReg_num_2,
  output [9:0] \指令译码信号_2 
);

  wire not_1_out;
  wire [4:0] multiplexer_8_out;
  wire [9:0] multiplexer_9_out;
  wire [15:0] multiplexer_7_out;
  wire [15:2] ControlBusIn, ControlBusOut;
  wire [31:0] multiplexer_1_out, multiplexer_2_out, multiplexer_3_out, multiplexer_4_out, multiplexer_5_out,
       multiplexer_6_out;

  Pull_Resistor pull_resistor_1 (.node({ControlBusIn, MemToReg, RegWrite}));
  Pull_Resistor pull_resistor_2 (.node(\指令译码信号 ));
  Pull_Resistor pull_resistor_3 (.node(\气泡 ));
  Multiplexer #(.width(32), .enable("false")) multiplexer_1 (
    .in0(PC), .in1({32{1'b0}}), .out(multiplexer_1_out), .sel(\气泡 ));
  Multiplexer #(.width(32), .enable("false")) multiplexer_2 (
    .in0(AluResult), .in1({32{1'b0}}), .out(multiplexer_2_out), .sel(\气泡 ));
  Multiplexer #(.width(32), .enable("false")) multiplexer_3 (
    .in0(MemData), .in1({32{1'b0}}), .out(multiplexer_3_out), .sel(\气泡 ));
  Multiplexer #(.width(32), .enable("false")) multiplexer_4 (
    .in0(IR), .in1({32{1'b0}}), .out(multiplexer_4_out), .sel(\气泡 ));
  Multiplexer #(.width(32), .enable("false")) multiplexer_5 (
    .in0(Reserved1), .in1({32{1'b0}}), .out(multiplexer_5_out), .sel(\气泡 ));
  Multiplexer #(.width(32), .enable("false")) multiplexer_6 (
    .in0(Reserved2), .in1({32{1'b0}}), .out(multiplexer_6_out), .sel(\气泡 ));
  Multiplexer #(.width(16), .enable("false")) multiplexer_7 (
    .in0({ControlBusIn, MemToReg, RegWrite}), .in1({16{1'b0}}), .out(multiplexer_7_out), .sel(\气泡 ));
  Multiplexer #(.width(5), .enable("false")) multiplexer_8 (
    .in0(WriteReg_num), .in1({5{1'b0}}), .out(multiplexer_8_out), .sel(\气泡 ));
  Multiplexer #(.width(10), .enable("false")) multiplexer_9 (
    .in0(\指令译码信号 ), .in1({10{1'b0}}), .out(multiplexer_9_out), .sel(\气泡 ));
  not not_1 (not_1_out, \EN_低电平有效 );
  Pull_Resistor pull_resistor_4 (.node(\EN_低电平有效 ));
  Register #(.width(32)) u_PC (.D(multiplexer_1_out), .en(not_1_out), .Q(PC_2), .clk(CLK));  // open: clr
  Register #(.width(32)) register_1 (.D(multiplexer_2_out), .en(not_1_out), .Q(AluResult_2), .clk(CLK));  // open: clr
  Register #(.width(32)) register_2 (.D(multiplexer_3_out), .en(not_1_out), .Q(MemData_2), .clk(CLK));  // open: clr
  Register #(.width(32)) register_3 (.D(multiplexer_4_out), .en(not_1_out), .Q(IR_2), .clk(CLK));  // open: clr
  Register #(.width(32)) register_4 (.D(multiplexer_5_out), .en(not_1_out), .Q(Reserved1_2), .clk(CLK));  // open: clr
  Register #(.width(32)) register_5 (.D(multiplexer_6_out), .en(not_1_out), .Q(Reserved2_2), .clk(CLK));  // open: clr
  Register #(.width(16)) register_6 (
    .D(multiplexer_7_out), .en(not_1_out), .Q({ControlBusOut, MemToReg_2, RegWrite_2}), .clk(CLK));  // open: clr
  Register #(.width(5)) register_7 (.D(multiplexer_8_out), .en(not_1_out), .Q(WriteReg_num_2), .clk(CLK));  // open: clr
  Register #(.width(10)) register_8 (.D(multiplexer_9_out), .en(not_1_out), .Q(\指令译码信号_2 ), .clk(CLK));  // open: clr

  // Other names for the same wires on the sheet: ControlBusIn[1:0] = {MemToReg, RegWrite};
  //   ControlBusOut[1:0] = {MemToReg_2, RegWrite_2}

  // Notes on the sheet:
  //   EN_低电平有效: pull=down
  //   保留引脚，自己决定是否使用
  //   PC、IR都应该一致传送，方便调试保留引脚，自己决定是否使用
  //   指令译码信号汇总在一起传输（bne，beq，jal，jalr，ecall，uret等）
  //   分线器已经设置好了，需要用的复制即可
  //   请将控制器输出的所有指令译码信号通过分线器汇总在一起后进行传输，后段需要使用的时候直接用分线器从多位宽线缆引出即可
endmodule
module \动态分支预测器  (
  input  [31:0] IF_PC,
  input  [31:0] IF_IR,
  input  [31:0] EX_PC,
  input  [31:0] EX_Target,
  input  EX_ActualTake,
  input  BP_Train,
  input  CLK,
  input  RST,
  output [31:0] BP_Next
);

  wire BTB00_DownHi, BTB00_DownLo, BTB00_Hi, BTB00_Hit, BTB00_Lo, BTB00_NextHi, BTB00_NextLo, BTB00_NotLo,
       BTB00_ReadTag, BTB00_Same, BTB00_Select, BTB00_Taken, BTB00_UpHi, BTB00_UpLo, BTB00_Valid,
       BTB00_Write, BTB00_WriteTag, BTB01_DownHi, BTB01_DownLo, BTB01_Hi, BTB01_Hit, BTB01_Lo, BTB01_NextHi,
       BTB01_NextLo, BTB01_NotLo, BTB01_ReadTag, BTB01_Same, BTB01_Select, BTB01_Taken, BTB01_UpHi,
       BTB01_UpLo, BTB01_Valid, BTB01_Write, BTB01_WriteTag, BTB02_DownHi, BTB02_DownLo, BTB02_Hi, BTB02_Hit,
       BTB02_Lo, BTB02_NextHi, BTB02_NextLo, BTB02_NotLo, BTB02_ReadTag, BTB02_Same, BTB02_Select,
       BTB02_Taken, BTB02_UpHi, BTB02_UpLo, BTB02_Valid, BTB02_Write, BTB02_WriteTag, BTB03_DownHi,
       BTB03_DownLo, BTB03_Hi, BTB03_Hit, BTB03_Lo, BTB03_NextHi, BTB03_NextLo, BTB03_NotLo, BTB03_ReadTag,
       BTB03_Same, BTB03_Select, BTB03_Taken, BTB03_UpHi, BTB03_UpLo, BTB03_Valid, BTB03_Write,
       BTB03_WriteTag, BTB04_DownHi, BTB04_DownLo, BTB04_Hi, BTB04_Hit, BTB04_Lo, BTB04_NextHi, BTB04_NextLo,
       BTB04_NotLo, BTB04_ReadTag, BTB04_Same, BTB04_Select, BTB04_Taken, BTB04_UpHi, BTB04_UpLo,
       BTB04_Valid, BTB04_Write, BTB04_WriteTag, BTB05_DownHi, BTB05_DownLo, BTB05_Hi, BTB05_Hit, BTB05_Lo,
       BTB05_NextHi, BTB05_NextLo, BTB05_NotLo, BTB05_ReadTag, BTB05_Same, BTB05_Select, BTB05_Taken,
       BTB05_UpHi, BTB05_UpLo, BTB05_Valid, BTB05_Write, BTB05_WriteTag, BTB06_DownHi, BTB06_DownLo,
       BTB06_Hi, BTB06_Hit, BTB06_Lo, BTB06_NextHi, BTB06_NextLo, BTB06_NotLo, BTB06_ReadTag, BTB06_Same,
       BTB06_Select, BTB06_Taken, BTB06_UpHi, BTB06_UpLo, BTB06_Valid, BTB06_Write, BTB06_WriteTag,
       BTB07_DownHi, BTB07_DownLo, BTB07_Hi, BTB07_Hit, BTB07_Lo, BTB07_NextHi, BTB07_NextLo, BTB07_NotLo,
       BTB07_ReadTag, BTB07_Same, BTB07_Select, BTB07_Taken, BTB07_UpHi, BTB07_UpLo, BTB07_Valid,
       BTB07_Write, BTB07_WriteTag, BTB08_DownHi, BTB08_DownLo, BTB08_Hi, BTB08_Hit, BTB08_Lo, BTB08_NextHi,
       BTB08_NextLo, BTB08_NotLo, BTB08_ReadTag, BTB08_Same, BTB08_Select, BTB08_Taken, BTB08_UpHi,
       BTB08_UpLo, BTB08_Valid, BTB08_Write, BTB08_WriteTag, BTB09_DownHi, BTB09_DownLo, BTB09_Hi, BTB09_Hit,
       BTB09_Lo, BTB09_NextHi, BTB09_NextLo, BTB09_NotLo, BTB09_ReadTag, BTB09_Same, BTB09_Select,
       BTB09_Taken, BTB09_UpHi, BTB09_UpLo, BTB09_Valid, BTB09_Write, BTB09_WriteTag, BTB10_DownHi,
       BTB10_DownLo, BTB10_Hi, BTB10_Hit, BTB10_Lo, BTB10_NextHi, BTB10_NextLo, BTB10_NotLo, BTB10_ReadTag,
       BTB10_Same, BTB10_Select, BTB10_Taken, BTB10_UpHi, BTB10_UpLo, BTB10_Valid, BTB10_Write,
       BTB10_WriteTag, BTB11_DownHi, BTB11_DownLo, BTB11_Hi, BTB11_Hit, BTB11_Lo, BTB11_NextHi, BTB11_NextLo,
       BTB11_NotLo, BTB11_ReadTag, BTB11_Same, BTB11_Select, BTB11_Taken, BTB11_UpHi, BTB11_UpLo,
       BTB11_Valid, BTB11_Write, BTB11_WriteTag, BTB12_DownHi, BTB12_DownLo, BTB12_Hi, BTB12_Hit, BTB12_Lo,
       BTB12_NextHi, BTB12_NextLo, BTB12_NotLo, BTB12_ReadTag, BTB12_Same, BTB12_Select, BTB12_Taken,
       BTB12_UpHi, BTB12_UpLo, BTB12_Valid, BTB12_Write, BTB12_WriteTag, BTB13_DownHi, BTB13_DownLo,
       BTB13_Hi, BTB13_Hit, BTB13_Lo, BTB13_NextHi, BTB13_NextLo, BTB13_NotLo, BTB13_ReadTag, BTB13_Same,
       BTB13_Select, BTB13_Taken, BTB13_UpHi, BTB13_UpLo, BTB13_Valid, BTB13_Write, BTB13_WriteTag,
       BTB14_DownHi, BTB14_DownLo, BTB14_Hi, BTB14_Hit, BTB14_Lo, BTB14_NextHi, BTB14_NextLo, BTB14_NotLo,
       BTB14_ReadTag, BTB14_Same, BTB14_Select, BTB14_Taken, BTB14_UpHi, BTB14_UpLo, BTB14_Valid,
       BTB14_Write, BTB14_WriteTag, BTB15_DownHi, BTB15_DownLo, BTB15_Hi, BTB15_Hit, BTB15_Lo, BTB15_NextHi,
       BTB15_NextLo, BTB15_NotLo, BTB15_ReadTag, BTB15_Same, BTB15_Select, BTB15_Taken, BTB15_UpHi,
       BTB15_UpLo, BTB15_Valid, BTB15_Write, BTB15_WriteTag, IF_Branch, IF_Control, IF_JAL, IF_JALR, IF_Jump,
       IF_PredictTaken, ReadTaken1, ReadTaken2, ReadTaken3, ReadTaken4, ReadTaken5, ReadTaken6, ReadTaken7,
       ReadTaken8, ReadTaken9, ReadTaken10, ReadTaken11, ReadTaken12, ReadTaken13, ReadTaken14, ReadTaken15;
  wire [1:0] BTB00_NewState, BTB01_NewState, BTB02_NewState, BTB03_NewState, BTB04_NewState, BTB05_NewState,
       BTB06_NewState, BTB07_NewState, BTB08_NewState, BTB09_NewState, BTB10_NewState, BTB11_NewState,
       BTB12_NewState, BTB13_NewState, BTB14_NewState, BTB15_NewState, InitialState;
  wire [31:0] BTB00_ReadTarget, BTB00_Tag, BTB00_Target, BTB01_ReadTarget, BTB01_Tag, BTB01_Target,
       BTB02_ReadTarget, BTB02_Tag, BTB02_Target, BTB03_ReadTarget, BTB03_Tag, BTB03_Target,
       BTB04_ReadTarget, BTB04_Tag, BTB04_Target, BTB05_ReadTarget, BTB05_Tag, BTB05_Target,
       BTB06_ReadTarget, BTB06_Tag, BTB06_Target, BTB07_ReadTarget, BTB07_Tag, BTB07_Target,
       BTB08_ReadTarget, BTB08_Tag, BTB08_Target, BTB09_ReadTarget, BTB09_Tag, BTB09_Target,
       BTB10_ReadTarget, BTB10_Tag, BTB10_Target, BTB11_ReadTarget, BTB11_Tag, BTB11_Target,
       BTB12_ReadTarget, BTB12_Tag, BTB12_Target, BTB13_ReadTarget, BTB13_Tag, BTB13_Target,
       BTB14_ReadTarget, BTB14_Tag, BTB14_Target, BTB15_ReadTarget, BTB15_Tag, BTB15_Target, IF_PC4,
       ReadTarget1, ReadTarget2, ReadTarget3, ReadTarget4, ReadTarget5, ReadTarget6, ReadTarget7,
       ReadTarget8, ReadTarget9, ReadTarget10, ReadTarget11, ReadTarget12, ReadTarget13, ReadTarget14,
       ReadTarget15;

  Comparator #(.width(4), .mode("unsigned")) comparator_1 (
    .a(EX_PC[5:2]), .b(4'b0000), .eq(BTB00_Select));  // open: gt, lt
  Comparator #(.width(32), .mode("unsigned")) comparator_2 (
    .a(IF_PC), .b(BTB00_Tag), .eq(BTB00_ReadTag));  // open: gt, lt
  Comparator #(.width(32), .mode("unsigned")) comparator_3 (
    .a(EX_PC), .b(BTB00_Tag), .eq(BTB00_WriteTag));  // open: gt, lt
  not not_1 (BTB00_NotLo, BTB00_Lo);
  Comparator #(.width(4), .mode("unsigned")) comparator_4 (
    .a(EX_PC[5:2]), .b(4'b0100), .eq(BTB04_Select));  // open: gt, lt
  Comparator #(.width(32), .mode("unsigned")) comparator_5 (
    .a(IF_PC), .b(BTB04_Tag), .eq(BTB04_ReadTag));  // open: gt, lt
  Comparator #(.width(32), .mode("unsigned")) comparator_6 (
    .a(EX_PC), .b(BTB04_Tag), .eq(BTB04_WriteTag));  // open: gt, lt
  not not_2 (BTB04_NotLo, BTB04_Lo);
  Comparator #(.width(4), .mode("unsigned")) comparator_7 (
    .a(EX_PC[5:2]), .b(4'b1000), .eq(BTB08_Select));  // open: gt, lt
  Comparator #(.width(32), .mode("unsigned")) comparator_8 (
    .a(IF_PC), .b(BTB08_Tag), .eq(BTB08_ReadTag));  // open: gt, lt
  Comparator #(.width(32), .mode("unsigned")) comparator_9 (
    .a(EX_PC), .b(BTB08_Tag), .eq(BTB08_WriteTag));  // open: gt, lt
  not not_3 (BTB08_NotLo, BTB08_Lo);
  Comparator #(.width(4), .mode("unsigned")) comparator_10 (
    .a(EX_PC[5:2]), .b(4'b1100), .eq(BTB12_Select));  // open: gt, lt
  Comparator #(.width(32), .mode("unsigned")) comparator_11 (
    .a(IF_PC), .b(BTB12_Tag), .eq(BTB12_ReadTag));  // open: gt, lt
  Comparator #(.width(32), .mode("unsigned")) comparator_12 (
    .a(EX_PC), .b(BTB12_Tag), .eq(BTB12_WriteTag));  // open: gt, lt
  not not_4 (BTB12_NotLo, BTB12_Lo);
  assign ReadTarget1 = BTB00_ReadTarget | BTB01_ReadTarget;  // OR_Gate or_1, 32 bits wide
  assign ReadTarget5 = ReadTarget4 | BTB05_ReadTarget;  // OR_Gate or_2, 32 bits wide
  assign ReadTarget9 = ReadTarget8 | BTB09_ReadTarget;  // OR_Gate or_3, 32 bits wide
  assign ReadTarget13 = ReadTarget12 | BTB13_ReadTarget;  // OR_Gate or_4, 32 bits wide
  and and_1 (IF_PredictTaken, ReadTaken15, IF_Control);
  and and_2 (BTB00_Write, BTB00_Select, BP_Train);
  and and_3 (BTB00_Hit, BTB00_ReadTag, BTB00_Valid);
  and and_4 (BTB00_Same, BTB00_WriteTag, BTB00_Valid);
  or or_5 (BTB00_UpHi, BTB00_Hi, BTB00_Lo);
  and and_5 (BTB00_DownHi, BTB00_Hi, BTB00_Lo);
  Multiplexer #(.width(1), .select(1), .enable("false")) multiplexer_1 (
    .in0(BTB00_DownHi), .in1(BTB00_UpHi), .out(BTB00_NextHi), .sel(EX_ActualTake));
  and and_6 (BTB04_Write, BTB04_Select, BP_Train);
  and and_7 (BTB04_Hit, BTB04_ReadTag, BTB04_Valid);
  and and_8 (BTB04_Same, BTB04_WriteTag, BTB04_Valid);
  or or_6 (BTB04_UpHi, BTB04_Hi, BTB04_Lo);
  and and_9 (BTB04_DownHi, BTB04_Hi, BTB04_Lo);
  Multiplexer #(.width(1), .select(1), .enable("false")) multiplexer_2 (
    .in0(BTB04_DownHi), .in1(BTB04_UpHi), .out(BTB04_NextHi), .sel(EX_ActualTake));
  and and_10 (BTB08_Write, BTB08_Select, BP_Train);
  and and_11 (BTB08_Hit, BTB08_ReadTag, BTB08_Valid);
  and and_12 (BTB08_Same, BTB08_WriteTag, BTB08_Valid);
  or or_7 (BTB08_UpHi, BTB08_Hi, BTB08_Lo);
  and and_13 (BTB08_DownHi, BTB08_Hi, BTB08_Lo);
  Multiplexer #(.width(1), .select(1), .enable("false")) multiplexer_3 (
    .in0(BTB08_DownHi), .in1(BTB08_UpHi), .out(BTB08_NextHi), .sel(EX_ActualTake));
  and and_14 (BTB12_Write, BTB12_Select, BP_Train);
  and and_15 (BTB12_Hit, BTB12_ReadTag, BTB12_Valid);
  and and_16 (BTB12_Same, BTB12_WriteTag, BTB12_Valid);
  or or_8 (BTB12_UpHi, BTB12_Hi, BTB12_Lo);
  and and_17 (BTB12_DownHi, BTB12_Hi, BTB12_Lo);
  Multiplexer #(.width(1), .select(1), .enable("false")) multiplexer_4 (
    .in0(BTB12_DownHi), .in1(BTB12_UpHi), .out(BTB12_NextHi), .sel(EX_ActualTake));
  Comparator #(.width(7), .mode("unsigned")) comparator_13 (
    .a(IF_IR[6:0]), .b(7'b1100011), .eq(IF_Branch));  // open: gt, lt
  or or_9 (ReadTaken1, BTB00_Taken, BTB01_Taken);
  or or_10 (ReadTaken5, ReadTaken4, BTB05_Taken);
  or or_11 (ReadTaken9, ReadTaken8, BTB09_Taken);
  or or_12 (ReadTaken13, ReadTaken12, BTB13_Taken);
  Multiplexer #(.width(32), .select(1), .enable("false")) multiplexer_5 (
    .in0(IF_PC4), .in1(ReadTarget15), .out(BP_Next), .sel(IF_PredictTaken));
  Register #(.width(1), .trigger("rising"), .Select("low")) u_BTB00_Valid (
    .D(1'b1), .en(BTB00_Write), .Q(BTB00_Valid), .clk(CLK), .clr(RST), .cs(1'b0), .preset(1'b0));
  Register #(.width(32), .trigger("rising"), .Select("low")) u_BTB00_Target (
    .D(EX_Target), .en(BTB00_Write), .Q(BTB00_Target), .clk(CLK), .clr(RST), .cs(1'b0), .preset(1'b0));
  or or_13 (BTB00_UpLo, BTB00_Hi, BTB00_NotLo);
  and and_18 (BTB00_DownLo, BTB00_Hi, BTB00_NotLo);
  Multiplexer #(.width(1), .select(1), .enable("false")) multiplexer_6 (
    .in0(BTB00_DownLo), .in1(BTB00_UpLo), .out(BTB00_NextLo), .sel(EX_ActualTake));
  Register #(.width(1), .trigger("rising"), .Select("low")) u_BTB04_Valid (
    .D(1'b1), .en(BTB04_Write), .Q(BTB04_Valid), .clk(CLK), .clr(RST), .cs(1'b0), .preset(1'b0));
  Register #(.width(32), .trigger("rising"), .Select("low")) u_BTB04_Target (
    .D(EX_Target), .en(BTB04_Write), .Q(BTB04_Target), .clk(CLK), .clr(RST), .cs(1'b0), .preset(1'b0));
  or or_14 (BTB04_UpLo, BTB04_Hi, BTB04_NotLo);
  and and_19 (BTB04_DownLo, BTB04_Hi, BTB04_NotLo);
  Multiplexer #(.width(1), .select(1), .enable("false")) multiplexer_7 (
    .in0(BTB04_DownLo), .in1(BTB04_UpLo), .out(BTB04_NextLo), .sel(EX_ActualTake));
  Register #(.width(1), .trigger("rising"), .Select("low")) u_BTB08_Valid (
    .D(1'b1), .en(BTB08_Write), .Q(BTB08_Valid), .clk(CLK), .clr(RST), .cs(1'b0), .preset(1'b0));
  Register #(.width(32), .trigger("rising"), .Select("low")) u_BTB08_Target (
    .D(EX_Target), .en(BTB08_Write), .Q(BTB08_Target), .clk(CLK), .clr(RST), .cs(1'b0), .preset(1'b0));
  or or_15 (BTB08_UpLo, BTB08_Hi, BTB08_NotLo);
  and and_20 (BTB08_DownLo, BTB08_Hi, BTB08_NotLo);
  Multiplexer #(.width(1), .select(1), .enable("false")) multiplexer_8 (
    .in0(BTB08_DownLo), .in1(BTB08_UpLo), .out(BTB08_NextLo), .sel(EX_ActualTake));
  Register #(.width(1), .trigger("rising"), .Select("low")) u_BTB12_Valid (
    .D(1'b1), .en(BTB12_Write), .Q(BTB12_Valid), .clk(CLK), .clr(RST), .cs(1'b0), .preset(1'b0));
  Register #(.width(32), .trigger("rising"), .Select("low")) u_BTB12_Target (
    .D(EX_Target), .en(BTB12_Write), .Q(BTB12_Target), .clk(CLK), .clr(RST), .cs(1'b0), .preset(1'b0));
  or or_16 (BTB12_UpLo, BTB12_Hi, BTB12_NotLo);
  and and_21 (BTB12_DownLo, BTB12_Hi, BTB12_NotLo);
  Multiplexer #(.width(1), .select(1), .enable("false")) multiplexer_9 (
    .in0(BTB12_DownLo), .in1(BTB12_UpLo), .out(BTB12_NextLo), .sel(EX_ActualTake));
  Comparator #(.width(7), .mode("unsigned")) comparator_14 (
    .a(IF_IR[6:0]), .b(7'b1101111), .eq(IF_JAL));  // open: gt, lt
  Register #(.width(32), .trigger("rising"), .Select("low")) u_BTB00_Tag (
    .D(EX_PC), .en(BTB00_Write), .Q(BTB00_Tag), .clk(CLK), .clr(RST), .cs(1'b0), .preset(1'b0));
  Register #(.width(2), .trigger("rising"), .Select("low")) BTB00_State (
    .D(BTB00_NewState), .en(BTB00_Write), .Q({BTB00_Hi, BTB00_Lo}), .clk(CLK), .clr(RST), .cs(1'b0),
    .preset(1'b0));
  and and_22 (BTB00_Taken, BTB00_Hit, BTB00_Hi);
  Multiplexer #(.width(32), .select(1), .enable("false")) multiplexer_10 (
    .in0({32{1'b0}}), .in1(BTB00_Target), .out(BTB00_ReadTarget), .sel(BTB00_Taken));
  Multiplexer #(.width(2), .select(1), .enable("false")) multiplexer_11 (
    .in0(InitialState), .in1({BTB00_NextHi, BTB00_NextLo}), .out(BTB00_NewState), .sel(BTB00_Same));
  Register #(.width(32), .trigger("rising"), .Select("low")) u_BTB04_Tag (
    .D(EX_PC), .en(BTB04_Write), .Q(BTB04_Tag), .clk(CLK), .clr(RST), .cs(1'b0), .preset(1'b0));
  Register #(.width(2), .trigger("rising"), .Select("low")) BTB04_State (
    .D(BTB04_NewState), .en(BTB04_Write), .Q({BTB04_Hi, BTB04_Lo}), .clk(CLK), .clr(RST), .cs(1'b0),
    .preset(1'b0));
  and and_23 (BTB04_Taken, BTB04_Hit, BTB04_Hi);
  Multiplexer #(.width(32), .select(1), .enable("false")) multiplexer_12 (
    .in0({32{1'b0}}), .in1(BTB04_Target), .out(BTB04_ReadTarget), .sel(BTB04_Taken));
  Multiplexer #(.width(2), .select(1), .enable("false")) multiplexer_13 (
    .in0(InitialState), .in1({BTB04_NextHi, BTB04_NextLo}), .out(BTB04_NewState), .sel(BTB04_Same));
  Register #(.width(32), .trigger("rising"), .Select("low")) u_BTB08_Tag (
    .D(EX_PC), .en(BTB08_Write), .Q(BTB08_Tag), .clk(CLK), .clr(RST), .cs(1'b0), .preset(1'b0));
  Register #(.width(2), .trigger("rising"), .Select("low")) BTB08_State (
    .D(BTB08_NewState), .en(BTB08_Write), .Q({BTB08_Hi, BTB08_Lo}), .clk(CLK), .clr(RST), .cs(1'b0),
    .preset(1'b0));
  and and_24 (BTB08_Taken, BTB08_Hit, BTB08_Hi);
  Multiplexer #(.width(32), .select(1), .enable("false")) multiplexer_14 (
    .in0({32{1'b0}}), .in1(BTB08_Target), .out(BTB08_ReadTarget), .sel(BTB08_Taken));
  Multiplexer #(.width(2), .select(1), .enable("false")) multiplexer_15 (
    .in0(InitialState), .in1({BTB08_NextHi, BTB08_NextLo}), .out(BTB08_NewState), .sel(BTB08_Same));
  Register #(.width(32), .trigger("rising"), .Select("low")) u_BTB12_Tag (
    .D(EX_PC), .en(BTB12_Write), .Q(BTB12_Tag), .clk(CLK), .clr(RST), .cs(1'b0), .preset(1'b0));
  Register #(.width(2), .trigger("rising"), .Select("low")) BTB12_State (
    .D(BTB12_NewState), .en(BTB12_Write), .Q({BTB12_Hi, BTB12_Lo}), .clk(CLK), .clr(RST), .cs(1'b0),
    .preset(1'b0));
  and and_25 (BTB12_Taken, BTB12_Hit, BTB12_Hi);
  Multiplexer #(.width(32), .select(1), .enable("false")) multiplexer_16 (
    .in0({32{1'b0}}), .in1(BTB12_Target), .out(BTB12_ReadTarget), .sel(BTB12_Taken));
  Multiplexer #(.width(2), .select(1), .enable("false")) multiplexer_17 (
    .in0(InitialState), .in1({BTB12_NextHi, BTB12_NextLo}), .out(BTB12_NewState), .sel(BTB12_Same));
  Comparator #(.width(7), .mode("unsigned")) comparator_15 (
    .a(IF_IR[6:0]), .b(7'b1100111), .eq(IF_JALR));  // open: gt, lt
  or or_17 (IF_Jump, IF_JAL, IF_JALR);
  Comparator #(.width(4), .mode("unsigned")) comparator_16 (
    .a(EX_PC[5:2]), .b(4'b0001), .eq(BTB01_Select));  // open: gt, lt
  Comparator #(.width(32), .mode("unsigned")) comparator_17 (
    .a(IF_PC), .b(BTB01_Tag), .eq(BTB01_ReadTag));  // open: gt, lt
  Comparator #(.width(32), .mode("unsigned")) comparator_18 (
    .a(EX_PC), .b(BTB01_Tag), .eq(BTB01_WriteTag));  // open: gt, lt
  not not_5 (BTB01_NotLo, BTB01_Lo);
  Comparator #(.width(4), .mode("unsigned")) comparator_19 (
    .a(EX_PC[5:2]), .b(4'b0101), .eq(BTB05_Select));  // open: gt, lt
  Comparator #(.width(32), .mode("unsigned")) comparator_20 (
    .a(IF_PC), .b(BTB05_Tag), .eq(BTB05_ReadTag));  // open: gt, lt
  Comparator #(.width(32), .mode("unsigned")) comparator_21 (
    .a(EX_PC), .b(BTB05_Tag), .eq(BTB05_WriteTag));  // open: gt, lt
  not not_6 (BTB05_NotLo, BTB05_Lo);
  Comparator #(.width(4), .mode("unsigned")) comparator_22 (
    .a(EX_PC[5:2]), .b(4'b1001), .eq(BTB09_Select));  // open: gt, lt
  Comparator #(.width(32), .mode("unsigned")) comparator_23 (
    .a(IF_PC), .b(BTB09_Tag), .eq(BTB09_ReadTag));  // open: gt, lt
  Comparator #(.width(32), .mode("unsigned")) comparator_24 (
    .a(EX_PC), .b(BTB09_Tag), .eq(BTB09_WriteTag));  // open: gt, lt
  not not_7 (BTB09_NotLo, BTB09_Lo);
  Comparator #(.width(4), .mode("unsigned")) comparator_25 (
    .a(EX_PC[5:2]), .b(4'b1101), .eq(BTB13_Select));  // open: gt, lt
  Comparator #(.width(32), .mode("unsigned")) comparator_26 (
    .a(IF_PC), .b(BTB13_Tag), .eq(BTB13_ReadTag));  // open: gt, lt
  Comparator #(.width(32), .mode("unsigned")) comparator_27 (
    .a(EX_PC), .b(BTB13_Tag), .eq(BTB13_WriteTag));  // open: gt, lt
  not not_8 (BTB13_NotLo, BTB13_Lo);
  assign ReadTarget2 = ReadTarget1 | BTB02_ReadTarget;  // OR_Gate or_18, 32 bits wide
  assign ReadTarget6 = ReadTarget5 | BTB06_ReadTarget;  // OR_Gate or_19, 32 bits wide
  assign ReadTarget10 = ReadTarget9 | BTB10_ReadTarget;  // OR_Gate or_20, 32 bits wide
  assign ReadTarget14 = ReadTarget13 | BTB14_ReadTarget;  // OR_Gate or_21, 32 bits wide
  or or_22 (IF_Control, IF_Jump, IF_Branch);
  and and_26 (BTB01_Write, BTB01_Select, BP_Train);
  and and_27 (BTB01_Hit, BTB01_ReadTag, BTB01_Valid);
  and and_28 (BTB01_Same, BTB01_WriteTag, BTB01_Valid);
  or or_23 (BTB01_UpHi, BTB01_Hi, BTB01_Lo);
  and and_29 (BTB01_DownHi, BTB01_Hi, BTB01_Lo);
  Multiplexer #(.width(1), .select(1), .enable("false")) multiplexer_18 (
    .in0(BTB01_DownHi), .in1(BTB01_UpHi), .out(BTB01_NextHi), .sel(EX_ActualTake));
  and and_30 (BTB05_Write, BTB05_Select, BP_Train);
  and and_31 (BTB05_Hit, BTB05_ReadTag, BTB05_Valid);
  and and_32 (BTB05_Same, BTB05_WriteTag, BTB05_Valid);
  or or_24 (BTB05_UpHi, BTB05_Hi, BTB05_Lo);
  and and_33 (BTB05_DownHi, BTB05_Hi, BTB05_Lo);
  Multiplexer #(.width(1), .select(1), .enable("false")) multiplexer_19 (
    .in0(BTB05_DownHi), .in1(BTB05_UpHi), .out(BTB05_NextHi), .sel(EX_ActualTake));
  and and_34 (BTB09_Write, BTB09_Select, BP_Train);
  and and_35 (BTB09_Hit, BTB09_ReadTag, BTB09_Valid);
  and and_36 (BTB09_Same, BTB09_WriteTag, BTB09_Valid);
  or or_25 (BTB09_UpHi, BTB09_Hi, BTB09_Lo);
  and and_37 (BTB09_DownHi, BTB09_Hi, BTB09_Lo);
  Multiplexer #(.width(1), .select(1), .enable("false")) multiplexer_20 (
    .in0(BTB09_DownHi), .in1(BTB09_UpHi), .out(BTB09_NextHi), .sel(EX_ActualTake));
  and and_38 (BTB13_Write, BTB13_Select, BP_Train);
  and and_39 (BTB13_Hit, BTB13_ReadTag, BTB13_Valid);
  and and_40 (BTB13_Same, BTB13_WriteTag, BTB13_Valid);
  or or_26 (BTB13_UpHi, BTB13_Hi, BTB13_Lo);
  and and_41 (BTB13_DownHi, BTB13_Hi, BTB13_Lo);
  Multiplexer #(.width(1), .select(1), .enable("false")) multiplexer_21 (
    .in0(BTB13_DownHi), .in1(BTB13_UpHi), .out(BTB13_NextHi), .sel(EX_ActualTake));
  Adder #(.width(32)) adder_1 (.a(IF_PC), .b(32'h4), .out(IF_PC4), .cin(1'b0));  // open: cout
  or or_27 (ReadTaken2, ReadTaken1, BTB02_Taken);
  or or_28 (ReadTaken6, ReadTaken5, BTB06_Taken);
  or or_29 (ReadTaken10, ReadTaken9, BTB10_Taken);
  or or_30 (ReadTaken14, ReadTaken13, BTB14_Taken);
  Register #(.width(1), .trigger("rising"), .Select("low")) u_BTB01_Valid (
    .D(1'b1), .en(BTB01_Write), .Q(BTB01_Valid), .clk(CLK), .clr(RST), .cs(1'b0), .preset(1'b0));
  Register #(.width(32), .trigger("rising"), .Select("low")) u_BTB01_Target (
    .D(EX_Target), .en(BTB01_Write), .Q(BTB01_Target), .clk(CLK), .clr(RST), .cs(1'b0), .preset(1'b0));
  or or_31 (BTB01_UpLo, BTB01_Hi, BTB01_NotLo);
  and and_42 (BTB01_DownLo, BTB01_Hi, BTB01_NotLo);
  Multiplexer #(.width(1), .select(1), .enable("false")) multiplexer_22 (
    .in0(BTB01_DownLo), .in1(BTB01_UpLo), .out(BTB01_NextLo), .sel(EX_ActualTake));
  Register #(.width(1), .trigger("rising"), .Select("low")) u_BTB05_Valid (
    .D(1'b1), .en(BTB05_Write), .Q(BTB05_Valid), .clk(CLK), .clr(RST), .cs(1'b0), .preset(1'b0));
  Register #(.width(32), .trigger("rising"), .Select("low")) u_BTB05_Target (
    .D(EX_Target), .en(BTB05_Write), .Q(BTB05_Target), .clk(CLK), .clr(RST), .cs(1'b0), .preset(1'b0));
  or or_32 (BTB05_UpLo, BTB05_Hi, BTB05_NotLo);
  and and_43 (BTB05_DownLo, BTB05_Hi, BTB05_NotLo);
  Multiplexer #(.width(1), .select(1), .enable("false")) multiplexer_23 (
    .in0(BTB05_DownLo), .in1(BTB05_UpLo), .out(BTB05_NextLo), .sel(EX_ActualTake));
  Register #(.width(1), .trigger("rising"), .Select("low")) u_BTB09_Valid (
    .D(1'b1), .en(BTB09_Write), .Q(BTB09_Valid), .clk(CLK), .clr(RST), .cs(1'b0), .preset(1'b0));
  Register #(.width(32), .trigger("rising"), .Select("low")) u_BTB09_Target (
    .D(EX_Target), .en(BTB09_Write), .Q(BTB09_Target), .clk(CLK), .clr(RST), .cs(1'b0), .preset(1'b0));
  or or_33 (BTB09_UpLo, BTB09_Hi, BTB09_NotLo);
  and and_44 (BTB09_DownLo, BTB09_Hi, BTB09_NotLo);
  Multiplexer #(.width(1), .select(1), .enable("false")) multiplexer_24 (
    .in0(BTB09_DownLo), .in1(BTB09_UpLo), .out(BTB09_NextLo), .sel(EX_ActualTake));
  Register #(.width(1), .trigger("rising"), .Select("low")) u_BTB13_Valid (
    .D(1'b1), .en(BTB13_Write), .Q(BTB13_Valid), .clk(CLK), .clr(RST), .cs(1'b0), .preset(1'b0));
  Register #(.width(32), .trigger("rising"), .Select("low")) u_BTB13_Target (
    .D(EX_Target), .en(BTB13_Write), .Q(BTB13_Target), .clk(CLK), .clr(RST), .cs(1'b0), .preset(1'b0));
  or or_34 (BTB13_UpLo, BTB13_Hi, BTB13_NotLo);
  and and_45 (BTB13_DownLo, BTB13_Hi, BTB13_NotLo);
  Multiplexer #(.width(1), .select(1), .enable("false")) multiplexer_25 (
    .in0(BTB13_DownLo), .in1(BTB13_UpLo), .out(BTB13_NextLo), .sel(EX_ActualTake));
  Multiplexer #(.width(2), .select(1), .enable("false")) multiplexer_26 (
    .in0(2'b01), .in1(2'b10), .out(InitialState), .sel(EX_ActualTake));
  Register #(.width(32), .trigger("rising"), .Select("low")) u_BTB01_Tag (
    .D(EX_PC), .en(BTB01_Write), .Q(BTB01_Tag), .clk(CLK), .clr(RST), .cs(1'b0), .preset(1'b0));
  Register #(.width(2), .trigger("rising"), .Select("low")) BTB01_State (
    .D(BTB01_NewState), .en(BTB01_Write), .Q({BTB01_Hi, BTB01_Lo}), .clk(CLK), .clr(RST), .cs(1'b0),
    .preset(1'b0));
  and and_46 (BTB01_Taken, BTB01_Hit, BTB01_Hi);
  Multiplexer #(.width(32), .select(1), .enable("false")) multiplexer_27 (
    .in0({32{1'b0}}), .in1(BTB01_Target), .out(BTB01_ReadTarget), .sel(BTB01_Taken));
  Multiplexer #(.width(2), .select(1), .enable("false")) multiplexer_28 (
    .in0(InitialState), .in1({BTB01_NextHi, BTB01_NextLo}), .out(BTB01_NewState), .sel(BTB01_Same));
  Register #(.width(32), .trigger("rising"), .Select("low")) u_BTB05_Tag (
    .D(EX_PC), .en(BTB05_Write), .Q(BTB05_Tag), .clk(CLK), .clr(RST), .cs(1'b0), .preset(1'b0));
  Register #(.width(2), .trigger("rising"), .Select("low")) BTB05_State (
    .D(BTB05_NewState), .en(BTB05_Write), .Q({BTB05_Hi, BTB05_Lo}), .clk(CLK), .clr(RST), .cs(1'b0),
    .preset(1'b0));
  and and_47 (BTB05_Taken, BTB05_Hit, BTB05_Hi);
  Multiplexer #(.width(32), .select(1), .enable("false")) multiplexer_29 (
    .in0({32{1'b0}}), .in1(BTB05_Target), .out(BTB05_ReadTarget), .sel(BTB05_Taken));
  Multiplexer #(.width(2), .select(1), .enable("false")) multiplexer_30 (
    .in0(InitialState), .in1({BTB05_NextHi, BTB05_NextLo}), .out(BTB05_NewState), .sel(BTB05_Same));
  Register #(.width(32), .trigger("rising"), .Select("low")) u_BTB09_Tag (
    .D(EX_PC), .en(BTB09_Write), .Q(BTB09_Tag), .clk(CLK), .clr(RST), .cs(1'b0), .preset(1'b0));
  Register #(.width(2), .trigger("rising"), .Select("low")) BTB09_State (
    .D(BTB09_NewState), .en(BTB09_Write), .Q({BTB09_Hi, BTB09_Lo}), .clk(CLK), .clr(RST), .cs(1'b0),
    .preset(1'b0));
  and and_48 (BTB09_Taken, BTB09_Hit, BTB09_Hi);
  Multiplexer #(.width(32), .select(1), .enable("false")) multiplexer_31 (
    .in0({32{1'b0}}), .in1(BTB09_Target), .out(BTB09_ReadTarget), .sel(BTB09_Taken));
  Multiplexer #(.width(2), .select(1), .enable("false")) multiplexer_32 (
    .in0(InitialState), .in1({BTB09_NextHi, BTB09_NextLo}), .out(BTB09_NewState), .sel(BTB09_Same));
  Register #(.width(32), .trigger("rising"), .Select("low")) u_BTB13_Tag (
    .D(EX_PC), .en(BTB13_Write), .Q(BTB13_Tag), .clk(CLK), .clr(RST), .cs(1'b0), .preset(1'b0));
  Register #(.width(2), .trigger("rising"), .Select("low")) BTB13_State (
    .D(BTB13_NewState), .en(BTB13_Write), .Q({BTB13_Hi, BTB13_Lo}), .clk(CLK), .clr(RST), .cs(1'b0),
    .preset(1'b0));
  and and_49 (BTB13_Taken, BTB13_Hit, BTB13_Hi);
  Multiplexer #(.width(32), .select(1), .enable("false")) multiplexer_33 (
    .in0({32{1'b0}}), .in1(BTB13_Target), .out(BTB13_ReadTarget), .sel(BTB13_Taken));
  Multiplexer #(.width(2), .select(1), .enable("false")) multiplexer_34 (
    .in0(InitialState), .in1({BTB13_NextHi, BTB13_NextLo}), .out(BTB13_NewState), .sel(BTB13_Same));
  Comparator #(.width(4), .mode("unsigned")) comparator_28 (
    .a(EX_PC[5:2]), .b(4'b0010), .eq(BTB02_Select));  // open: gt, lt
  Comparator #(.width(32), .mode("unsigned")) comparator_29 (
    .a(IF_PC), .b(BTB02_Tag), .eq(BTB02_ReadTag));  // open: gt, lt
  Comparator #(.width(32), .mode("unsigned")) comparator_30 (
    .a(EX_PC), .b(BTB02_Tag), .eq(BTB02_WriteTag));  // open: gt, lt
  not not_9 (BTB02_NotLo, BTB02_Lo);
  Comparator #(.width(4), .mode("unsigned")) comparator_31 (
    .a(EX_PC[5:2]), .b(4'b0110), .eq(BTB06_Select));  // open: gt, lt
  Comparator #(.width(32), .mode("unsigned")) comparator_32 (
    .a(IF_PC), .b(BTB06_Tag), .eq(BTB06_ReadTag));  // open: gt, lt
  Comparator #(.width(32), .mode("unsigned")) comparator_33 (
    .a(EX_PC), .b(BTB06_Tag), .eq(BTB06_WriteTag));  // open: gt, lt
  not not_10 (BTB06_NotLo, BTB06_Lo);
  Comparator #(.width(4), .mode("unsigned")) comparator_34 (
    .a(EX_PC[5:2]), .b(4'b1010), .eq(BTB10_Select));  // open: gt, lt
  Comparator #(.width(32), .mode("unsigned")) comparator_35 (
    .a(IF_PC), .b(BTB10_Tag), .eq(BTB10_ReadTag));  // open: gt, lt
  Comparator #(.width(32), .mode("unsigned")) comparator_36 (
    .a(EX_PC), .b(BTB10_Tag), .eq(BTB10_WriteTag));  // open: gt, lt
  not not_11 (BTB10_NotLo, BTB10_Lo);
  Comparator #(.width(4), .mode("unsigned")) comparator_37 (
    .a(EX_PC[5:2]), .b(4'b1110), .eq(BTB14_Select));  // open: gt, lt
  Comparator #(.width(32), .mode("unsigned")) comparator_38 (
    .a(IF_PC), .b(BTB14_Tag), .eq(BTB14_ReadTag));  // open: gt, lt
  Comparator #(.width(32), .mode("unsigned")) comparator_39 (
    .a(EX_PC), .b(BTB14_Tag), .eq(BTB14_WriteTag));  // open: gt, lt
  not not_12 (BTB14_NotLo, BTB14_Lo);
  assign ReadTarget3 = ReadTarget2 | BTB03_ReadTarget;  // OR_Gate or_35, 32 bits wide
  assign ReadTarget7 = ReadTarget6 | BTB07_ReadTarget;  // OR_Gate or_36, 32 bits wide
  assign ReadTarget11 = ReadTarget10 | BTB11_ReadTarget;  // OR_Gate or_37, 32 bits wide
  assign ReadTarget15 = ReadTarget14 | BTB15_ReadTarget;  // OR_Gate or_38, 32 bits wide
  and and_50 (BTB02_Write, BTB02_Select, BP_Train);
  and and_51 (BTB02_Hit, BTB02_ReadTag, BTB02_Valid);
  and and_52 (BTB02_Same, BTB02_WriteTag, BTB02_Valid);
  or or_39 (BTB02_UpHi, BTB02_Hi, BTB02_Lo);
  and and_53 (BTB02_DownHi, BTB02_Hi, BTB02_Lo);
  Multiplexer #(.width(1), .select(1), .enable("false")) multiplexer_35 (
    .in0(BTB02_DownHi), .in1(BTB02_UpHi), .out(BTB02_NextHi), .sel(EX_ActualTake));
  and and_54 (BTB06_Write, BTB06_Select, BP_Train);
  and and_55 (BTB06_Hit, BTB06_ReadTag, BTB06_Valid);
  and and_56 (BTB06_Same, BTB06_WriteTag, BTB06_Valid);
  or or_40 (BTB06_UpHi, BTB06_Hi, BTB06_Lo);
  and and_57 (BTB06_DownHi, BTB06_Hi, BTB06_Lo);
  Multiplexer #(.width(1), .select(1), .enable("false")) multiplexer_36 (
    .in0(BTB06_DownHi), .in1(BTB06_UpHi), .out(BTB06_NextHi), .sel(EX_ActualTake));
  and and_58 (BTB10_Write, BTB10_Select, BP_Train);
  and and_59 (BTB10_Hit, BTB10_ReadTag, BTB10_Valid);
  and and_60 (BTB10_Same, BTB10_WriteTag, BTB10_Valid);
  or or_41 (BTB10_UpHi, BTB10_Hi, BTB10_Lo);
  and and_61 (BTB10_DownHi, BTB10_Hi, BTB10_Lo);
  Multiplexer #(.width(1), .select(1), .enable("false")) multiplexer_37 (
    .in0(BTB10_DownHi), .in1(BTB10_UpHi), .out(BTB10_NextHi), .sel(EX_ActualTake));
  and and_62 (BTB14_Write, BTB14_Select, BP_Train);
  and and_63 (BTB14_Hit, BTB14_ReadTag, BTB14_Valid);
  and and_64 (BTB14_Same, BTB14_WriteTag, BTB14_Valid);
  or or_42 (BTB14_UpHi, BTB14_Hi, BTB14_Lo);
  and and_65 (BTB14_DownHi, BTB14_Hi, BTB14_Lo);
  Multiplexer #(.width(1), .select(1), .enable("false")) multiplexer_38 (
    .in0(BTB14_DownHi), .in1(BTB14_UpHi), .out(BTB14_NextHi), .sel(EX_ActualTake));
  or or_43 (ReadTaken3, ReadTaken2, BTB03_Taken);
  or or_44 (ReadTaken7, ReadTaken6, BTB07_Taken);
  or or_45 (ReadTaken11, ReadTaken10, BTB11_Taken);
  or or_46 (ReadTaken15, ReadTaken14, BTB15_Taken);
  Register #(.width(1), .trigger("rising"), .Select("low")) u_BTB02_Valid (
    .D(1'b1), .en(BTB02_Write), .Q(BTB02_Valid), .clk(CLK), .clr(RST), .cs(1'b0), .preset(1'b0));
  Register #(.width(32), .trigger("rising"), .Select("low")) u_BTB02_Target (
    .D(EX_Target), .en(BTB02_Write), .Q(BTB02_Target), .clk(CLK), .clr(RST), .cs(1'b0), .preset(1'b0));
  or or_47 (BTB02_UpLo, BTB02_Hi, BTB02_NotLo);
  and and_66 (BTB02_DownLo, BTB02_Hi, BTB02_NotLo);
  Multiplexer #(.width(1), .select(1), .enable("false")) multiplexer_39 (
    .in0(BTB02_DownLo), .in1(BTB02_UpLo), .out(BTB02_NextLo), .sel(EX_ActualTake));
  Register #(.width(1), .trigger("rising"), .Select("low")) u_BTB06_Valid (
    .D(1'b1), .en(BTB06_Write), .Q(BTB06_Valid), .clk(CLK), .clr(RST), .cs(1'b0), .preset(1'b0));
  Register #(.width(32), .trigger("rising"), .Select("low")) u_BTB06_Target (
    .D(EX_Target), .en(BTB06_Write), .Q(BTB06_Target), .clk(CLK), .clr(RST), .cs(1'b0), .preset(1'b0));
  or or_48 (BTB06_UpLo, BTB06_Hi, BTB06_NotLo);
  and and_67 (BTB06_DownLo, BTB06_Hi, BTB06_NotLo);
  Multiplexer #(.width(1), .select(1), .enable("false")) multiplexer_40 (
    .in0(BTB06_DownLo), .in1(BTB06_UpLo), .out(BTB06_NextLo), .sel(EX_ActualTake));
  Register #(.width(1), .trigger("rising"), .Select("low")) u_BTB10_Valid (
    .D(1'b1), .en(BTB10_Write), .Q(BTB10_Valid), .clk(CLK), .clr(RST), .cs(1'b0), .preset(1'b0));
  Register #(.width(32), .trigger("rising"), .Select("low")) u_BTB10_Target (
    .D(EX_Target), .en(BTB10_Write), .Q(BTB10_Target), .clk(CLK), .clr(RST), .cs(1'b0), .preset(1'b0));
  or or_49 (BTB10_UpLo, BTB10_Hi, BTB10_NotLo);
  and and_68 (BTB10_DownLo, BTB10_Hi, BTB10_NotLo);
  Multiplexer #(.width(1), .select(1), .enable("false")) multiplexer_41 (
    .in0(BTB10_DownLo), .in1(BTB10_UpLo), .out(BTB10_NextLo), .sel(EX_ActualTake));
  Register #(.width(1), .trigger("rising"), .Select("low")) u_BTB14_Valid (
    .D(1'b1), .en(BTB14_Write), .Q(BTB14_Valid), .clk(CLK), .clr(RST), .cs(1'b0), .preset(1'b0));
  Register #(.width(32), .trigger("rising"), .Select("low")) u_BTB14_Target (
    .D(EX_Target), .en(BTB14_Write), .Q(BTB14_Target), .clk(CLK), .clr(RST), .cs(1'b0), .preset(1'b0));
  or or_50 (BTB14_UpLo, BTB14_Hi, BTB14_NotLo);
  and and_69 (BTB14_DownLo, BTB14_Hi, BTB14_NotLo);
  Multiplexer #(.width(1), .select(1), .enable("false")) multiplexer_42 (
    .in0(BTB14_DownLo), .in1(BTB14_UpLo), .out(BTB14_NextLo), .sel(EX_ActualTake));
  Multiplexer #(.width(2), .select(1), .enable("false")) multiplexer_43 (
    .in0(InitialState), .in1({BTB02_NextHi, BTB02_NextLo}), .out(BTB02_NewState), .sel(BTB02_Same));
  Multiplexer #(.width(2), .select(1), .enable("false")) multiplexer_44 (
    .in0(InitialState), .in1({BTB06_NextHi, BTB06_NextLo}), .out(BTB06_NewState), .sel(BTB06_Same));
  Multiplexer #(.width(2), .select(1), .enable("false")) multiplexer_45 (
    .in0(InitialState), .in1({BTB10_NextHi, BTB10_NextLo}), .out(BTB10_NewState), .sel(BTB10_Same));
  Multiplexer #(.width(2), .select(1), .enable("false")) multiplexer_46 (
    .in0(InitialState), .in1({BTB14_NextHi, BTB14_NextLo}), .out(BTB14_NewState), .sel(BTB14_Same));
  Register #(.width(32), .trigger("rising"), .Select("low")) u_BTB02_Tag (
    .D(EX_PC), .en(BTB02_Write), .Q(BTB02_Tag), .clk(CLK), .clr(RST), .cs(1'b0), .preset(1'b0));
  Register #(.width(2), .trigger("rising"), .Select("low")) BTB02_State (
    .D(BTB02_NewState), .en(BTB02_Write), .Q({BTB02_Hi, BTB02_Lo}), .clk(CLK), .clr(RST), .cs(1'b0),
    .preset(1'b0));
  and and_70 (BTB02_Taken, BTB02_Hit, BTB02_Hi);
  Multiplexer #(.width(32), .select(1), .enable("false")) multiplexer_47 (
    .in0({32{1'b0}}), .in1(BTB02_Target), .out(BTB02_ReadTarget), .sel(BTB02_Taken));
  Register #(.width(32), .trigger("rising"), .Select("low")) u_BTB06_Tag (
    .D(EX_PC), .en(BTB06_Write), .Q(BTB06_Tag), .clk(CLK), .clr(RST), .cs(1'b0), .preset(1'b0));
  Register #(.width(2), .trigger("rising"), .Select("low")) BTB06_State (
    .D(BTB06_NewState), .en(BTB06_Write), .Q({BTB06_Hi, BTB06_Lo}), .clk(CLK), .clr(RST), .cs(1'b0),
    .preset(1'b0));
  and and_71 (BTB06_Taken, BTB06_Hit, BTB06_Hi);
  Multiplexer #(.width(32), .select(1), .enable("false")) multiplexer_48 (
    .in0({32{1'b0}}), .in1(BTB06_Target), .out(BTB06_ReadTarget), .sel(BTB06_Taken));
  Register #(.width(32), .trigger("rising"), .Select("low")) u_BTB10_Tag (
    .D(EX_PC), .en(BTB10_Write), .Q(BTB10_Tag), .clk(CLK), .clr(RST), .cs(1'b0), .preset(1'b0));
  Register #(.width(2), .trigger("rising"), .Select("low")) BTB10_State (
    .D(BTB10_NewState), .en(BTB10_Write), .Q({BTB10_Hi, BTB10_Lo}), .clk(CLK), .clr(RST), .cs(1'b0),
    .preset(1'b0));
  and and_72 (BTB10_Taken, BTB10_Hit, BTB10_Hi);
  Multiplexer #(.width(32), .select(1), .enable("false")) multiplexer_49 (
    .in0({32{1'b0}}), .in1(BTB10_Target), .out(BTB10_ReadTarget), .sel(BTB10_Taken));
  Register #(.width(32), .trigger("rising"), .Select("low")) u_BTB14_Tag (
    .D(EX_PC), .en(BTB14_Write), .Q(BTB14_Tag), .clk(CLK), .clr(RST), .cs(1'b0), .preset(1'b0));
  Register #(.width(2), .trigger("rising"), .Select("low")) BTB14_State (
    .D(BTB14_NewState), .en(BTB14_Write), .Q({BTB14_Hi, BTB14_Lo}), .clk(CLK), .clr(RST), .cs(1'b0),
    .preset(1'b0));
  and and_73 (BTB14_Taken, BTB14_Hit, BTB14_Hi);
  Multiplexer #(.width(32), .select(1), .enable("false")) multiplexer_50 (
    .in0({32{1'b0}}), .in1(BTB14_Target), .out(BTB14_ReadTarget), .sel(BTB14_Taken));
  Comparator #(.width(4), .mode("unsigned")) comparator_40 (
    .a(EX_PC[5:2]), .b(4'b0011), .eq(BTB03_Select));  // open: gt, lt
  Comparator #(.width(32), .mode("unsigned")) comparator_41 (
    .a(IF_PC), .b(BTB03_Tag), .eq(BTB03_ReadTag));  // open: gt, lt
  Comparator #(.width(32), .mode("unsigned")) comparator_42 (
    .a(EX_PC), .b(BTB03_Tag), .eq(BTB03_WriteTag));  // open: gt, lt
  not not_13 (BTB03_NotLo, BTB03_Lo);
  Comparator #(.width(4), .mode("unsigned")) comparator_43 (
    .a(EX_PC[5:2]), .b(4'b0111), .eq(BTB07_Select));  // open: gt, lt
  Comparator #(.width(32), .mode("unsigned")) comparator_44 (
    .a(IF_PC), .b(BTB07_Tag), .eq(BTB07_ReadTag));  // open: gt, lt
  Comparator #(.width(32), .mode("unsigned")) comparator_45 (
    .a(EX_PC), .b(BTB07_Tag), .eq(BTB07_WriteTag));  // open: gt, lt
  not not_14 (BTB07_NotLo, BTB07_Lo);
  Comparator #(.width(4), .mode("unsigned")) comparator_46 (
    .a(EX_PC[5:2]), .b(4'b1011), .eq(BTB11_Select));  // open: gt, lt
  Comparator #(.width(32), .mode("unsigned")) comparator_47 (
    .a(IF_PC), .b(BTB11_Tag), .eq(BTB11_ReadTag));  // open: gt, lt
  Comparator #(.width(32), .mode("unsigned")) comparator_48 (
    .a(EX_PC), .b(BTB11_Tag), .eq(BTB11_WriteTag));  // open: gt, lt
  not not_15 (BTB11_NotLo, BTB11_Lo);
  Comparator #(.width(4), .mode("unsigned")) comparator_49 (
    .a(EX_PC[5:2]), .b(4'b1111), .eq(BTB15_Select));  // open: gt, lt
  Comparator #(.width(32), .mode("unsigned")) comparator_50 (
    .a(IF_PC), .b(BTB15_Tag), .eq(BTB15_ReadTag));  // open: gt, lt
  Comparator #(.width(32), .mode("unsigned")) comparator_51 (
    .a(EX_PC), .b(BTB15_Tag), .eq(BTB15_WriteTag));  // open: gt, lt
  not not_16 (BTB15_NotLo, BTB15_Lo);
  assign ReadTarget4 = ReadTarget3 | BTB04_ReadTarget;  // OR_Gate or_51, 32 bits wide
  assign ReadTarget8 = ReadTarget7 | BTB08_ReadTarget;  // OR_Gate or_52, 32 bits wide
  assign ReadTarget12 = ReadTarget11 | BTB12_ReadTarget;  // OR_Gate or_53, 32 bits wide
  and and_74 (BTB03_Write, BTB03_Select, BP_Train);
  and and_75 (BTB03_Hit, BTB03_ReadTag, BTB03_Valid);
  and and_76 (BTB03_Same, BTB03_WriteTag, BTB03_Valid);
  or or_54 (BTB03_UpHi, BTB03_Hi, BTB03_Lo);
  and and_77 (BTB03_DownHi, BTB03_Hi, BTB03_Lo);
  Multiplexer #(.width(1), .select(1), .enable("false")) multiplexer_51 (
    .in0(BTB03_DownHi), .in1(BTB03_UpHi), .out(BTB03_NextHi), .sel(EX_ActualTake));
  and and_78 (BTB07_Write, BTB07_Select, BP_Train);
  and and_79 (BTB07_Hit, BTB07_ReadTag, BTB07_Valid);
  and and_80 (BTB07_Same, BTB07_WriteTag, BTB07_Valid);
  or or_55 (BTB07_UpHi, BTB07_Hi, BTB07_Lo);
  and and_81 (BTB07_DownHi, BTB07_Hi, BTB07_Lo);
  Multiplexer #(.width(1), .select(1), .enable("false")) multiplexer_52 (
    .in0(BTB07_DownHi), .in1(BTB07_UpHi), .out(BTB07_NextHi), .sel(EX_ActualTake));
  and and_82 (BTB11_Write, BTB11_Select, BP_Train);
  and and_83 (BTB11_Hit, BTB11_ReadTag, BTB11_Valid);
  and and_84 (BTB11_Same, BTB11_WriteTag, BTB11_Valid);
  or or_56 (BTB11_UpHi, BTB11_Hi, BTB11_Lo);
  and and_85 (BTB11_DownHi, BTB11_Hi, BTB11_Lo);
  Multiplexer #(.width(1), .select(1), .enable("false")) multiplexer_53 (
    .in0(BTB11_DownHi), .in1(BTB11_UpHi), .out(BTB11_NextHi), .sel(EX_ActualTake));
  and and_86 (BTB15_Write, BTB15_Select, BP_Train);
  and and_87 (BTB15_Hit, BTB15_ReadTag, BTB15_Valid);
  and and_88 (BTB15_Same, BTB15_WriteTag, BTB15_Valid);
  or or_57 (BTB15_UpHi, BTB15_Hi, BTB15_Lo);
  and and_89 (BTB15_DownHi, BTB15_Hi, BTB15_Lo);
  Multiplexer #(.width(1), .select(1), .enable("false")) multiplexer_54 (
    .in0(BTB15_DownHi), .in1(BTB15_UpHi), .out(BTB15_NextHi), .sel(EX_ActualTake));
  or or_58 (ReadTaken4, ReadTaken3, BTB04_Taken);
  or or_59 (ReadTaken8, ReadTaken7, BTB08_Taken);
  or or_60 (ReadTaken12, ReadTaken11, BTB12_Taken);
  Register #(.width(1), .trigger("rising"), .Select("low")) u_BTB03_Valid (
    .D(1'b1), .en(BTB03_Write), .Q(BTB03_Valid), .clk(CLK), .clr(RST), .cs(1'b0), .preset(1'b0));
  Register #(.width(32), .trigger("rising"), .Select("low")) u_BTB03_Target (
    .D(EX_Target), .en(BTB03_Write), .Q(BTB03_Target), .clk(CLK), .clr(RST), .cs(1'b0), .preset(1'b0));
  or or_61 (BTB03_UpLo, BTB03_Hi, BTB03_NotLo);
  and and_90 (BTB03_DownLo, BTB03_Hi, BTB03_NotLo);
  Multiplexer #(.width(1), .select(1), .enable("false")) multiplexer_55 (
    .in0(BTB03_DownLo), .in1(BTB03_UpLo), .out(BTB03_NextLo), .sel(EX_ActualTake));
  Register #(.width(1), .trigger("rising"), .Select("low")) u_BTB07_Valid (
    .D(1'b1), .en(BTB07_Write), .Q(BTB07_Valid), .clk(CLK), .clr(RST), .cs(1'b0), .preset(1'b0));
  Register #(.width(32), .trigger("rising"), .Select("low")) u_BTB07_Target (
    .D(EX_Target), .en(BTB07_Write), .Q(BTB07_Target), .clk(CLK), .clr(RST), .cs(1'b0), .preset(1'b0));
  or or_62 (BTB07_UpLo, BTB07_Hi, BTB07_NotLo);
  and and_91 (BTB07_DownLo, BTB07_Hi, BTB07_NotLo);
  Multiplexer #(.width(1), .select(1), .enable("false")) multiplexer_56 (
    .in0(BTB07_DownLo), .in1(BTB07_UpLo), .out(BTB07_NextLo), .sel(EX_ActualTake));
  Register #(.width(1), .trigger("rising"), .Select("low")) u_BTB11_Valid (
    .D(1'b1), .en(BTB11_Write), .Q(BTB11_Valid), .clk(CLK), .clr(RST), .cs(1'b0), .preset(1'b0));
  Register #(.width(32), .trigger("rising"), .Select("low")) u_BTB11_Target (
    .D(EX_Target), .en(BTB11_Write), .Q(BTB11_Target), .clk(CLK), .clr(RST), .cs(1'b0), .preset(1'b0));
  or or_63 (BTB11_UpLo, BTB11_Hi, BTB11_NotLo);
  and and_92 (BTB11_DownLo, BTB11_Hi, BTB11_NotLo);
  Multiplexer #(.width(1), .select(1), .enable("false")) multiplexer_57 (
    .in0(BTB11_DownLo), .in1(BTB11_UpLo), .out(BTB11_NextLo), .sel(EX_ActualTake));
  Register #(.width(1), .trigger("rising"), .Select("low")) u_BTB15_Valid (
    .D(1'b1), .en(BTB15_Write), .Q(BTB15_Valid), .clk(CLK), .clr(RST), .cs(1'b0), .preset(1'b0));
  Register #(.width(32), .trigger("rising"), .Select("low")) u_BTB15_Target (
    .D(EX_Target), .en(BTB15_Write), .Q(BTB15_Target), .clk(CLK), .clr(RST), .cs(1'b0), .preset(1'b0));
  or or_64 (BTB15_UpLo, BTB15_Hi, BTB15_NotLo);
  and and_93 (BTB15_DownLo, BTB15_Hi, BTB15_NotLo);
  Multiplexer #(.width(1), .select(1), .enable("false")) multiplexer_58 (
    .in0(BTB15_DownLo), .in1(BTB15_UpLo), .out(BTB15_NextLo), .sel(EX_ActualTake));
  Multiplexer #(.width(2), .select(1), .enable("false")) multiplexer_59 (
    .in0(InitialState), .in1({BTB03_NextHi, BTB03_NextLo}), .out(BTB03_NewState), .sel(BTB03_Same));
  Multiplexer #(.width(2), .select(1), .enable("false")) multiplexer_60 (
    .in0(InitialState), .in1({BTB07_NextHi, BTB07_NextLo}), .out(BTB07_NewState), .sel(BTB07_Same));
  Multiplexer #(.width(2), .select(1), .enable("false")) multiplexer_61 (
    .in0(InitialState), .in1({BTB11_NextHi, BTB11_NextLo}), .out(BTB11_NewState), .sel(BTB11_Same));
  Multiplexer #(.width(2), .select(1), .enable("false")) multiplexer_62 (
    .in0(InitialState), .in1({BTB15_NextHi, BTB15_NextLo}), .out(BTB15_NewState), .sel(BTB15_Same));
  Register #(.width(32), .trigger("rising"), .Select("low")) u_BTB03_Tag (
    .D(EX_PC), .en(BTB03_Write), .Q(BTB03_Tag), .clk(CLK), .clr(RST), .cs(1'b0), .preset(1'b0));
  Register #(.width(2), .trigger("rising"), .Select("low")) BTB03_State (
    .D(BTB03_NewState), .en(BTB03_Write), .Q({BTB03_Hi, BTB03_Lo}), .clk(CLK), .clr(RST), .cs(1'b0),
    .preset(1'b0));
  and and_94 (BTB03_Taken, BTB03_Hit, BTB03_Hi);
  Multiplexer #(.width(32), .select(1), .enable("false")) multiplexer_63 (
    .in0({32{1'b0}}), .in1(BTB03_Target), .out(BTB03_ReadTarget), .sel(BTB03_Taken));
  Register #(.width(32), .trigger("rising"), .Select("low")) u_BTB07_Tag (
    .D(EX_PC), .en(BTB07_Write), .Q(BTB07_Tag), .clk(CLK), .clr(RST), .cs(1'b0), .preset(1'b0));
  Register #(.width(2), .trigger("rising"), .Select("low")) BTB07_State (
    .D(BTB07_NewState), .en(BTB07_Write), .Q({BTB07_Hi, BTB07_Lo}), .clk(CLK), .clr(RST), .cs(1'b0),
    .preset(1'b0));
  and and_95 (BTB07_Taken, BTB07_Hit, BTB07_Hi);
  Multiplexer #(.width(32), .select(1), .enable("false")) multiplexer_64 (
    .in0({32{1'b0}}), .in1(BTB07_Target), .out(BTB07_ReadTarget), .sel(BTB07_Taken));
  Register #(.width(32), .trigger("rising"), .Select("low")) u_BTB11_Tag (
    .D(EX_PC), .en(BTB11_Write), .Q(BTB11_Tag), .clk(CLK), .clr(RST), .cs(1'b0), .preset(1'b0));
  Register #(.width(2), .trigger("rising"), .Select("low")) BTB11_State (
    .D(BTB11_NewState), .en(BTB11_Write), .Q({BTB11_Hi, BTB11_Lo}), .clk(CLK), .clr(RST), .cs(1'b0),
    .preset(1'b0));
  and and_96 (BTB11_Taken, BTB11_Hit, BTB11_Hi);
  Multiplexer #(.width(32), .select(1), .enable("false")) multiplexer_65 (
    .in0({32{1'b0}}), .in1(BTB11_Target), .out(BTB11_ReadTarget), .sel(BTB11_Taken));
  Register #(.width(32), .trigger("rising"), .Select("low")) u_BTB15_Tag (
    .D(EX_PC), .en(BTB15_Write), .Q(BTB15_Tag), .clk(CLK), .clr(RST), .cs(1'b0), .preset(1'b0));
  Register #(.width(2), .trigger("rising"), .Select("low")) BTB15_State (
    .D(BTB15_NewState), .en(BTB15_Write), .Q({BTB15_Hi, BTB15_Lo}), .clk(CLK), .clr(RST), .cs(1'b0),
    .preset(1'b0));
  and and_97 (BTB15_Taken, BTB15_Hit, BTB15_Hi);
  Multiplexer #(.width(32), .select(1), .enable("false")) multiplexer_66 (
    .in0({32{1'b0}}), .in1(BTB15_Target), .out(BTB15_ReadTarget), .sel(BTB15_Taken));

  // Other names for the same wires on the sheet: BTB00_Saturated[1:0] = {BTB00_NextHi, BTB00_NextLo};
  //   BTB00_State[1:0] = {BTB00_Hi, BTB00_Lo}; BTB01_Saturated[1:0] = {BTB01_NextHi, BTB01_NextLo};
  //   BTB01_State[1:0] = {BTB01_Hi, BTB01_Lo}; BTB02_Saturated[1:0] = {BTB02_NextHi, BTB02_NextLo};
  //   BTB02_State[1:0] = {BTB02_Hi, BTB02_Lo}; BTB03_Saturated[1:0] = {BTB03_NextHi, BTB03_NextLo};
  //   BTB03_State[1:0] = {BTB03_Hi, BTB03_Lo}; BTB04_Saturated[1:0] = {BTB04_NextHi, BTB04_NextLo};
  //   BTB04_State[1:0] = {BTB04_Hi, BTB04_Lo}; BTB05_Saturated[1:0] = {BTB05_NextHi, BTB05_NextLo};
  //   BTB05_State[1:0] = {BTB05_Hi, BTB05_Lo}; BTB06_Saturated[1:0] = {BTB06_NextHi, BTB06_NextLo};
  //   BTB06_State[1:0] = {BTB06_Hi, BTB06_Lo}; BTB07_Saturated[1:0] = {BTB07_NextHi, BTB07_NextLo};
  //   BTB07_State[1:0] = {BTB07_Hi, BTB07_Lo}; BTB08_Saturated[1:0] = {BTB08_NextHi, BTB08_NextLo};
  //   BTB08_State[1:0] = {BTB08_Hi, BTB08_Lo}; BTB09_Saturated[1:0] = {BTB09_NextHi, BTB09_NextLo};
  //   BTB09_State[1:0] = {BTB09_Hi, BTB09_Lo}; BTB10_Saturated[1:0] = {BTB10_NextHi, BTB10_NextLo};
  //   BTB10_State[1:0] = {BTB10_Hi, BTB10_Lo}; BTB11_Saturated[1:0] = {BTB11_NextHi, BTB11_NextLo};
  //   BTB11_State[1:0] = {BTB11_Hi, BTB11_Lo}; BTB12_Saturated[1:0] = {BTB12_NextHi, BTB12_NextLo};
  //   BTB12_State[1:0] = {BTB12_Hi, BTB12_Lo}; BTB13_Saturated[1:0] = {BTB13_NextHi, BTB13_NextLo};
  //   BTB13_State[1:0] = {BTB13_Hi, BTB13_Lo}; BTB14_Saturated[1:0] = {BTB14_NextHi, BTB14_NextLo};
  //   BTB14_State[1:0] = {BTB14_Hi, BTB14_Lo}; BTB15_Saturated[1:0] = {BTB15_NextHi, BTB15_NextLo};
  //   BTB15_State[1:0] = {BTB15_Hi, BTB15_Lo}; EX_Index[3:0] = EX_PC[5:2]; IF_Opcode[6:0] = IF_IR[6:0]

  // Notes on the sheet:
  //   BTB00: PC[5:2]=0; valid / full PC tag / target / 2-bit state
  //   BTB04: PC[5:2]=4; valid / full PC tag / target / 2-bit state
  //   BTB08: PC[5:2]=8; valid / full PC tag / target / 2-bit state
  //   BTB12: PC[5:2]=12; valid / full PC tag / target / 2-bit state
  //   16-entry tagged BTB + 2-bit BHT; cold miss = PC+4; EX trains accepted control flow
  //   BTB01: PC[5:2]=1; valid / full PC tag / target / 2-bit state
  //   BTB05: PC[5:2]=5; valid / full PC tag / target / 2-bit state
  //   BTB09: PC[5:2]=9; valid / full PC tag / target / 2-bit state
  //   BTB13: PC[5:2]=13; valid / full PC tag / target / 2-bit state
  //   BTB02: PC[5:2]=2; valid / full PC tag / target / 2-bit state
  //   BTB06: PC[5:2]=6; valid / full PC tag / target / 2-bit state
  //   BTB10: PC[5:2]=10; valid / full PC tag / target / 2-bit state
  //   BTB14: PC[5:2]=14; valid / full PC tag / target / 2-bit state
  //   BTB03: PC[5:2]=3; valid / full PC tag / target / 2-bit state
  //   BTB07: PC[5:2]=7; valid / full PC tag / target / 2-bit state
  //   BTB11: PC[5:2]=11; valid / full PC tag / target / 2-bit state
  //   BTB15: PC[5:2]=15; valid / full PC tag / target / 2-bit state
endmodule
