// Logisim project ideal-pipeline.circ as structural Verilog: 10 circuits, main circuit ◇理想流水线
module \理想流水线  (
  output RegWrite,
  output MemWrite,
  output [31:0] IF_PC,
  output [31:0] ID_PC,
  output [31:0] EX_PC,
  output [31:0] M_PC,
  output [31:0] WB_PC,
  output [31:0] RDin,
  output [31:0] MDin,
  output [31:0] LedData
);

  wire CLK, clock_1_out, comparator_6_eq, comparator_6_lt, d_ff_1_q, EX_ALUSRC, EX_BEQ, EX_BGE, EX_BNE,
       EX_EQ, EX_GE, EX_Jump, EX_MemToReg, EX_MemWrite, EX_NE, EX_RegWrite, EX_Take, EX_Take0, EX_TakeBR,
       EX_TakeEQ, EX_TakeGE, EX_TakeNE, Go, halt, ID_ALUSRC, ID_BEQ, ID_BGE, ID_BImm_p2, ID_BImm_p3, ID_BNE,
       ID_BR, ID_FGE, ID_MemToReg, ID_MemWrite, ID_RegWrite, ID_ST, ID_URET, ID_Valid, ID_WriteRaw, IR1, IR2,
       IR3, LED_WE, MEM_HalfSel, MEM_MemToReg, MEM_RegWrite, nand_1_out, NotGo, PAUSE_HOLD, PAUSE_NEXT,
       RAW_CLK, RST, RUN, WAIT_REQUEST, WB_MemToReg, WB_NotPrint, WB_Print, WB_Wait;
  wire [2:0] ID_F3;
  wire [3:0] EX_ALUOP, ID_ALUOP, ID_BImm_p0;
  wire [4:0] EX_RD, ID_I12, ID_RA1, ID_RA2, MEM_RD, WB_RD;
  wire [5:0] ID_BImm_p1;
  wire [7:2] ID_Ctrl;
  wire [9:0] MEM_Ctrl, WB_Ctrl;
  wire [9:2] EX_Ctrl;
  wire [12:0] CNT_num;
  wire [15:0] COUNT_NEXT, \LoadUse次数 , MEM_Half, MEM_High16, MEM_Low16, \总周期数 , \无条件分支数 ;
  wire [19:0] ID_IR;
  wire [23:0] DADDR;
  wire [31:0] EX_ALU, EX_B, EX_BImm, EX_BTarget, EX_Imm, EX_IR, EX_JImm, EX_JRTarget, EX_JTarget, EX_PC4,
       EX_R1, EX_R2, EX_Res0, EX_Result, EX_Target, EX_Target0, ID_BImm, ID_BImm_half, ID_IImm, ID_Imm,
       ID_ImmIS, ID_JImm, ID_JImm_half, ID_R1, ID_R2, ID_SImm, ID_UImm, IF_IR, IF_PC4, MEM_IR, MEM_Load,
       MEM_PC4, MEM_R1, MEM_Result, MEM_SignedHalf, NEXT_PC, WB_IR, WB_Load, WB_R1, WB_R2, WB_Result;

  Button \u_总复位  (.out(RST));
  Button _1 (.out(IR1));
  Button _2 (.out(IR2));
  Button _3 (.out(IR3));
  // Probe on \总周期数 
  // Probe on \总周期数 
  Button \u_继续运行  (.out(Go));
  LED led_1 (.in(1'b0));
  LED led_2 (.in(1'b0));
  LED led_3 (.in(1'b0));
  Hex_Digit_Display hex_digit_display_1 (.value(LedData[31:28]));  // open: dp
  // Probe on IF_PC[19:0]
  // riscv_probe riscv_probe_1: pin names not known; wires that end beside it: IF_IR
  Register #(.width(32)) PC (.D(NEXT_PC), .en(1'b1), .Q(IF_PC), .clk(CLK), .clr(RST), .cs(1'b0), .preset(1'b0));
  Hex_Digit_Display hex_digit_display_2 (.value(LedData[27:24]));  // open: dp
  Hex_Digit_Display hex_digit_display_3 (.value(LedData[23:20]));  // open: dp
  // Probe on ID_PC[19:0]
  // riscv_probe riscv_probe_2: pin names not known; wires that end beside it: {ID_BImm_p3, ID_BImm_p1, ID_I12, ID_IR[19:15], ID_F3, ID_BImm_p0, ID_BImm_p2, ID_IR[6:0]}
  Comparator #(.width(2), .mode("unsigned")) comparator_1 (.a(ID_IR[1:0]), .b(2'b11), .eq(ID_Valid));  // open: gt, lt
  and and_1 (ID_RegWrite, ID_WriteRaw, ID_Valid);
  Hex_Digit_Display hex_digit_display_4 (.value(LedData[15:12]));  // open: dp
  Hex_Digit_Display hex_digit_display_5 (.value(LedData[19:16]));  // open: dp
  Adder #(.width(32)) adder_1 (.a(IF_PC), .b(32'h4), .out(IF_PC4), .cin(1'b0));  // open: cout
  Multiplexer #(.width(32), .enable("false")) multiplexer_1 (
    .in0(IF_PC4), .in1(EX_Target), .out(NEXT_PC), .sel(EX_Take));
  Hex_Digit_Display hex_digit_display_6 (.value(LedData[7:4]));  // open: dp
  Hex_Digit_Display hex_digit_display_7 (.value(LedData[11:8]));  // open: dp
  // Probe on EX_PC[19:0]
  // riscv_probe riscv_probe_3: pin names not known; wires that end beside it: EX_IR
  ROM #(.addrWidth(20), .dataWidth(32), .Select("high")) rom_1 (.addr(IF_PC[21:2]), .data(IF_IR), .sel(1'b1));
  Hex_Digit_Display hex_digit_display_8 (.value(LedData[3:0]));  // open: dp
  IF_ID if_id_1 (
    .PredictJump(1'b0), .IR(IF_IR), .\气泡 (RST),
    .IR_2({ID_BImm_p3, ID_BImm_p1, ID_I12, ID_IR[19:15], ID_F3, ID_BImm_p0, ID_BImm_p2, ID_IR[6:0]}),
    .\EN_低电平有效 (1'b0), .CLK(CLK), .PC_2(ID_PC), .PC(IF_PC),
    .IR_3({ID_BImm_p3, ID_BImm_p1, ID_I12, ID_IR[19:15], ID_F3, ID_BImm_p0, ID_BImm_p2, ID_IR[6:0]}));  // open: PredictJump_2
  // Probe on \总周期数 
  // Probe on M_PC[19:0]
  // riscv_probe riscv_probe_4: pin names not known; wires that end beside it: MEM_IR
  // Probe on \总周期数 
  // Probe on \无条件分支数 
  // Probe on {16{1'b0}}
  // Probe on {16{1'b0}}
  // Probe on \LoadUse次数 
  \单周期硬布线控制器  \u_单周期硬布线控制器_1  (
    .Funct({ID_BImm_p1[5], ID_BImm_p1[0], ID_F3}), .OP(ID_IR[6:2]), .ALU_OP(ID_ALUOP),
    .MemToReg(ID_MemToReg), .MemWrite(ID_MemWrite), .ALU_SRC(ID_ALUSRC), .RegWrite(ID_WriteRaw),
    .ecall(ID_Ctrl[4]), .S_type(ID_ST), .Jalr(ID_Ctrl[3]), .Beq(ID_BEQ), .JAL(ID_Ctrl[2]), .Bne(ID_BNE),
    .in_3(ID_I12[1]), .uret(ID_URET));
  // Probe on IF_PC[11:0]
  // Probe on WB_PC[19:0]
  // riscv_probe riscv_probe_5: pin names not known; wires that end beside it: WB_IR
  Regifile regifile_1 (
    .Din(RDin), .Clk(CLK), .R1(ID_R1), .R2(ID_R2), .WE(RegWrite), .W_num(WB_RD), .R1_num(ID_RA1),
    .R2_num(ID_RA2));
  assign ID_IImm = {{20{ID_BImm_p3}}, {ID_BImm_p3, ID_BImm_p1, ID_I12}};  // Bit_Extender bit_extender_1
  assign ID_SImm = {{20{ID_BImm_p3}}, {ID_BImm_p3, ID_BImm_p1, ID_BImm_p0, ID_BImm_p2}};  // Bit_Extender bit_extender_2
  Multiplexer #(.width(32), .enable("false")) multiplexer_2 (.in0(ID_IImm), .in1(ID_SImm), .out(ID_ImmIS), .sel(ID_ST));
  assign ID_UImm = {ID_BImm_p3, ID_BImm_p1, ID_I12, ID_IR[19:15], ID_F3, ID_BImm_p0, ID_BImm_p2, ID_IR[6:0]} & 32'hfffff000;  // AND_Gate and_2, 32 bits wide
  Multiplexer #(.width(32), .enable("false")) multiplexer_3 (
    .in0(ID_ImmIS), .in1(ID_UImm), .out(ID_Imm), .sel(ID_Ctrl[6]));
  Comparator #(.width(7), .mode("unsigned")) comparator_2 (
    .a(ID_IR[6:0]), .b(7'b0110111), .eq(ID_Ctrl[6]));  // open: gt, lt
  Comparator #(.width(3), .mode("unsigned")) comparator_3 (.a(ID_F3), .b(3'b001), .eq(ID_Ctrl[7]));  // open: gt, lt
  Comparator #(.width(7), .mode("unsigned")) comparator_4 (.a(ID_IR[6:0]), .b(7'b1100011), .eq(ID_BR));  // open: gt, lt
  Comparator #(.width(3), .mode("unsigned")) comparator_5 (.a(ID_F3), .b(3'b101), .eq(ID_FGE));  // open: gt, lt
  and and_3 (ID_BGE, ID_BR, ID_FGE);
  Multiplexer #(.width(5), .enable("false")) multiplexer_4 (
    .in0(ID_IR[19:15]), .in1(5'b10001), .out(ID_RA1), .sel(ID_Ctrl[4]));
  Multiplexer #(.width(5), .enable("false")) multiplexer_5 (
    .in0(ID_I12), .in1(5'b01010), .out(ID_RA2), .sel(ID_Ctrl[4]));
  // Probe on EX_PC[11:0]
  // Probe on ID_PC[11:0]
  assign ID_BImm_half = {{20{ID_BImm_p3}}, {ID_BImm_p3, ID_BImm_p2, ID_BImm_p1, ID_BImm_p0}};  // Bit_Extender bit_extender_3
  Shifter #(.width(32)) shifter_1 (.in(ID_BImm_half), .\dist (5'b00001), .out(ID_BImm));
  assign ID_JImm_half = {{12{ID_BImm_p3}}, {ID_BImm_p3, ID_IR[19:15], ID_F3, ID_I12[0], ID_BImm_p1, ID_I12[4:1]}};  // Bit_Extender bit_extender_4
  Shifter #(.width(32)) shifter_2 (.in(ID_JImm_half), .\dist (5'b00001), .out(ID_JImm));
  // Probe on M_PC[11:0]
  D_Flip_Flop #(.Pre_Clr_Positions("LEGACY"), .NewFFLayout("false")) d_ff_1 (.Q(d_ff_1_q));  // open: clk, D, Qn, preset, reset
  // Probe on 13'hc
  // Probe on WB_PC[11:0]
  Comparator #(.width(13)) comparator_6 (
    .a(CNT_num), .b(13'hc), .eq(comparator_6_eq), .lt(comparator_6_lt));  // open: gt
  Clock clock_1 (.out(clock_1_out));
  ID_EX id_ex_1 (
    .PC(ID_PC), .RS1(ID_R1), .RS2(ID_R2),
    .IR({ID_BImm_p3, ID_BImm_p1, ID_I12, ID_IR[19:15], ID_F3, ID_BImm_p0, ID_BImm_p2, ID_IR[6:0]}),
    .WriteReg_num({ID_BImm_p0, ID_BImm_p2}), .ALUOP(ID_ALUOP), .\气泡 (RST), .PC_2(EX_PC), .RS1_2(EX_R1),
    .RS2_2(EX_R2), .IR_2(EX_IR), .RegWrite_2(EX_RegWrite), .MemToReg_2(EX_MemToReg),
    .MemWrite_2(EX_MemWrite), .ALuSrc_2(EX_ALUSRC), .WriteReg_num_2(EX_RD), .RegWrite(ID_RegWrite),
    .MemToReg(ID_MemToReg), .MemWrite(ID_MemWrite), .ALuSrc(ID_ALUSRC), .ALUOP_2(EX_ALUOP),
    .\EN_低电平有效 (1'b0), .CLK(CLK), .Reserved1_2(EX_BImm), .Reserved1(ID_BImm), .Imm32_2(EX_Imm),
    .Imm32(ID_Imm), .rs2Fwd(2'b00), .rs1Fwd(2'b00), .PredictJump(1'b0),
    .\指令译码信号 ({2'b00, ID_Ctrl[7:6], ID_BGE, ID_Ctrl[4:2], ID_BNE, ID_BEQ}),
    .\指令译码信号_2 ({EX_Ctrl[9:6], EX_BGE, EX_Ctrl[4:2], EX_BNE, EX_BEQ}), .Reserved2(ID_JImm),
    .Reserved2_2(EX_JImm));  // open: rs2Fwd_2, rs1Fwd_2, PredictJump_2
  nand nand_1 (nand_1_out, d_ff_1_q, comparator_6_eq);
  Counter #(.width(13), .max('h1fff), .ongoal("stay"), .behavior("old")) counter_1 (
    .count(comparator_6_lt), .Q(CNT_num), .clk(clock_1_out));  // open: load, D, carry, clr, preset
  assign RAW_CLK = nand_1_out ? clock_1_out : 1'bz;  // Controlled_Buffer controlled_buffer_1
  ALU alu_1 (
    .X(EX_R1), .Y(EX_B), .AluOP(EX_ALUOP), .Equal(EX_EQ), .Result(EX_ALU), .out_4(EX_GE));  // open: Result_2, out_6
  Pull_Resistor #(.pull(1)) pull_resistor_1 (.node(RAW_CLK));
  Multiplexer #(.width(32), .enable("false")) multiplexer_6 (.in0(EX_R2), .in1(EX_Imm), .out(EX_B), .sel(EX_ALUSRC));
  Multiplexer #(.width(32), .enable("false")) multiplexer_7 (
    .in0(EX_ALU), .in1(EX_Imm), .out(EX_Res0), .sel(EX_Ctrl[6]));
  Adder #(.width(32)) adder_2 (.a(EX_PC), .b(32'h4), .out(EX_PC4), .cin(1'b0));  // open: cout
  or or_1 (EX_Jump, EX_Ctrl[2], EX_Ctrl[3]);
  Multiplexer #(.width(32), .enable("false")) multiplexer_8 (
    .in0(EX_Res0), .in1(EX_PC4), .out(EX_Result), .sel(EX_Jump));
  Adder #(.width(32)) adder_3 (.a(EX_PC), .b(EX_BImm), .out(EX_BTarget), .cin(1'b0));  // open: cout
  Adder #(.width(32)) adder_4 (.a(EX_PC), .b(EX_JImm), .out(EX_JTarget), .cin(1'b0));  // open: cout
  assign EX_JRTarget = EX_ALU & 32'hfffffffe;  // AND_Gate and_4, 32 bits wide
  and and_5 (EX_TakeEQ, EX_BEQ, EX_EQ);
  not not_1 (EX_NE, EX_EQ);
  and and_6 (EX_TakeNE, EX_BNE, EX_NE);
  and and_7 (EX_TakeGE, EX_BGE, EX_GE);
  or or_2 (EX_Take0, EX_TakeEQ, EX_TakeNE);
  or or_3 (EX_TakeBR, EX_Take0, EX_TakeGE);
  or or_4 (EX_Take, EX_TakeBR, EX_Jump);
  Multiplexer #(.width(32), .enable("false")) multiplexer_9 (
    .in0(EX_BTarget), .in1(EX_JTarget), .out(EX_Target0), .sel(EX_Ctrl[2]));
  Multiplexer #(.width(32), .enable("false")) multiplexer_10 (
    .in0(EX_Target0), .in1(EX_JRTarget), .out(EX_Target), .sel(EX_Ctrl[3]));
  EX_MEM ex_mem_1 (
    .PC(EX_PC), .IR(EX_IR), .WriteReg_num(EX_RD), .\气泡 (RST), .PC_2(M_PC), .IR_2(MEM_IR),
    .RegWrite_2(MEM_RegWrite), .MemToReg_2(MEM_MemToReg), .MemWrite_2(MemWrite), .WriteReg_num_2(MEM_RD),
    .RegWrite(EX_RegWrite), .MemToReg(EX_MemToReg), .MemWrite(EX_MemWrite), .\EN_低电平有效 (1'b0), .CLK(CLK),
    .Reserved1_2(MEM_R1), .Reserved1(EX_R1), .\指令译码信号 ({EX_Ctrl[9:6], EX_BGE, EX_Ctrl[4:2], EX_BNE, EX_BEQ}),
    .\指令译码信号_2 (MEM_Ctrl), .Reserved2(EX_PC4), .Reserved2_2(MEM_PC4), .WriteData(EX_R2), .WriteData_2(MDin),
    .AluResult(EX_Result), .AluResult_2({MEM_Result[31:26], DADDR, MEM_HalfSel, MEM_Result[0]}));
  RAM #(.addrWidth(24), .dataWidth(32), .bus("separate"), .Select("high"), .simpleMode("false")) ram_1 (
    .addr(DADDR), .din(MDin), .data({MEM_High16, MEM_Low16}), .str(MemWrite), .sel(1'b1), .clk(CLK),
    .ld(1'b1), .clr(1'b0));
  Multiplexer #(.width(16), .enable("false")) multiplexer_11 (
    .in0(MEM_Low16), .in1(MEM_High16), .out(MEM_Half), .sel(MEM_HalfSel));
  assign MEM_SignedHalf = {{16{MEM_Half[15]}}, MEM_Half};  // Bit_Extender bit_extender_5
  Multiplexer #(.width(32), .enable("false")) multiplexer_12 (
    .in0({MEM_High16, MEM_Low16}), .in1(MEM_SignedHalf), .out(MEM_Load), .sel(MEM_Ctrl[7]));
  MEM_WB mem_wb_1 (
    .PC(M_PC), .IR(MEM_IR), .WriteReg_num(MEM_RD), .\气泡 (RST), .PC_2(WB_PC), .IR_2(WB_IR),
    .RegWrite_2(RegWrite), .MemToReg_2(WB_MemToReg), .WriteReg_num_2(WB_RD), .RegWrite(MEM_RegWrite),
    .MemToReg(MEM_MemToReg), .\EN_低电平有效 (1'b0), .CLK(CLK), .Reserved1_2(WB_R1), .Reserved1(MEM_R1),
    .\指令译码信号 (MEM_Ctrl), .\指令译码信号_2 (WB_Ctrl), .Reserved2(MDin), .Reserved2_2(WB_R2), .MemData(MEM_Load),
    .MemData_2(WB_Load), .AluResult({MEM_Result[31:26], DADDR, MEM_HalfSel, MEM_Result[0]}),
    .AluResult_2(WB_Result));
  Multiplexer #(.width(32), .enable("false")) multiplexer_13 (
    .in0(WB_Result), .in1(WB_Load), .out(RDin), .sel(WB_MemToReg));
  Comparator #(.width(32), .mode("unsigned")) comparator_7 (.a(WB_R1), .b(32'h22), .eq(WB_Print));  // open: gt, lt
  and and_8 (LED_WE, WB_Ctrl[4], WB_Print);
  not not_2 (WB_NotPrint, WB_Print);
  and and_9 (WB_Wait, WB_Ctrl[4], WB_NotPrint);
  not not_3 (NotGo, Go);
  and and_10 (WAIT_REQUEST, WB_Wait, NotGo);
  Register #(.width(32)) \ECALL显示锁存  (
    .D(WB_R2), .en(LED_WE), .Q(LedData), .clk(CLK), .clr(RST), .cs(1'b0), .preset(1'b0));
  Register #(.width(16)) \u_流水周期  (
    .D(COUNT_NEXT), .en(1'b1), .Q(\总周期数 ), .clk(CLK), .clr(RST), .cs(1'b0), .preset(1'b0));
  Adder #(.width(16)) adder_5 (.a(\总周期数 ), .b(16'h1), .out(COUNT_NEXT), .cin(1'b0));  // open: cout
  or or_5 (PAUSE_HOLD, WAIT_REQUEST, halt);
  and and_11 (PAUSE_NEXT, PAUSE_HOLD, NotGo);
  Register #(.width(1)) \ECALL暂停状态  (
    .D(PAUSE_NEXT), .en(1'b1), .Q(halt), .clk(RAW_CLK), .clr(RST), .cs(1'b0), .preset(1'b0));
  not not_4 (RUN, halt);
  and and_12 (CLK, RAW_CLK, RUN);

  // Other names for the same wires on the sheet: EX_Ctrl (some bits) = {EX_BGE, EX_BNE, EX_BEQ}; EX_JAL = EX_Ctrl[2];
  //   EX_JALR = EX_Ctrl[3]; EX_ECALL = EX_Ctrl[4]; EX_LUI = EX_Ctrl[6]; EX_LH = EX_Ctrl[7]; PAUSED = halt;
  //   ID_BImm_raw[11:0] = {ID_BImm_p3, ID_BImm_p2, ID_BImm_p1, ID_BImm_p0};
  //   ID_IR (some bits) = {ID_BImm_p3, ID_BImm_p1, ID_I12, ID_F3, ID_BImm_p0, ID_BImm_p2};
  //   ID_RD[4:0] = {ID_BImm_p0, ID_BImm_p2}; ID_S12[11:0] = {ID_BImm_p3, ID_BImm_p1, ID_BImm_p0, ID_BImm_p2};
  //   ID_Ctrl (some bits) = {ID_BGE, ID_BNE, ID_BEQ}; ID_JAL = ID_Ctrl[2]; ID_JALR = ID_Ctrl[3];
  //   ID_ECALL = ID_Ctrl[4]; ID_LUI = ID_Ctrl[6]; ID_LH = ID_Ctrl[7]; ID_Low2[1:0] = ID_IR[1:0];
  //   ID_OP7[6:0] = ID_IR[6:0]; ID_OP5[4:0] = ID_IR[6:2]; ID_IR21 = ID_I12[1];
  //   ID_JImm_p0[9:0] = {ID_BImm_p1, ID_I12[4:1]};
  //   ID_JImm_raw[19:0] = {ID_BImm_p3, ID_IR[19:15], ID_F3, ID_I12[0], ID_BImm_p1, ID_I12[4:1]}; ID_RS2[4:0] = ID_I12;
  //   ID_FUN5[4:0] = {ID_BImm_p1[5], ID_BImm_p1[0], ID_F3}; ID_I12[11:5] = {ID_BImm_p3, ID_BImm_p1};
  //   ID_JImm_p1 = ID_I12[0]; ID_JImm_p2[7:0] = {ID_IR[19:15], ID_F3}; ID_RS1[4:0] = ID_IR[19:15];
  //   ID_JImm_p3 = ID_BImm_p3; IADDR[19:0] = IF_PC[21:2]; MEM_LH = MEM_Ctrl[7]; MEM_PC[31:0] = M_PC;
  //   MEM_Result[25:1] = {DADDR, MEM_HalfSel}; MEM_Word[31:0] = {MEM_High16, MEM_Low16}; WB_ECALL = WB_Ctrl[4]

  // Notes on the sheet:
  //   中断源
  //   时空图监测，可删除
  //   中断等待指示
  //   IF：顺序与 EX 分支反馈
  //   理想流水：程序用 NOP 消除冒险
  //   EX 决定转移；保留两条延迟槽
  //   数据生产者后留足 3 条 NOP
  //   数码管输出
  //   contents of rom_1 (hex, n*v repeats v):
  //   00000413 00000493 00000913 00000993 00046413 0014e493 00296913 0039e993 00842023 00942223 01242423
  //   01342623 00a00893 00000493 00000913 00000993 00000073
  //   ID：立即数、控制信号
  //   控制位
  //   流水调试日志用
  //   暂停节拍，不能为0
  //   戳工具置1进入计数暂停模式，ctrl+k时钟自动运行到对应节拍暂停
  //   ctrl+k关闭时钟连续运行，将控制位置零，进入单步调试模式调试
  //   用这个时钟源需要去掉电路中的其他时钟源
  //   可计数暂停的时钟源
  //   EX：执行与分支
  //   为方便自动评测，需要输出流水线各段保存的PC值，注意是PC不是PC+4，另外ID段寄存器写入信息，Mem段内存写入信息也要输出
  //   MEM：访存与 LH
  //   Ctrl+R 全复位 / Ctrl+K 自动运行
  //   WB：写回与 ECALL
endmodule

// 单周期硬布线控制器
module \单周期硬布线控制器  (
  input  [4:0] OP,
  input  [4:0] Funct,
  input  in_3,
  output [3:0] ALU_OP,
  output uret,
  output MemToReg,
  output ecall,
  output MemWrite,
  output ALU_SRC,
  output RegWrite,
  output S_type,
  output Beq,
  output Bne,
  output Jalr,
  output JAL
);

  wire \控制信号自动生成_1_ecall ;

  \运算控制器自动生成  \u_运算控制器自动生成_1  (
    .OP2(OP[0]), .OP3(OP[1]), .OP4(OP[2]), .OP5(OP[3]), .OP6(OP[4]), .F12(Funct[0]), .F13(Funct[1]),
    .F14(Funct[2]), .F25(Funct[3]), .F30(Funct[4]), .S0(ALU_OP[0]), .S1(ALU_OP[1]), .S2(ALU_OP[2]),
    .S3(ALU_OP[3]));
  \控制信号自动生成  \u_控制信号自动生成_1  (
    .OP2(OP[0]), .MemToReg(MemToReg), .OP3(OP[1]), .MemWrite(MemWrite), .OP4(OP[2]), .ALU_SRC(ALU_SRC),
    .OP5(OP[3]), .RegWrite(RegWrite), .OP6(OP[4]), .ecall(\控制信号自动生成_1_ecall ), .F12(Funct[0]),
    .S_Type(S_type), .F13(Funct[1]), .BEQ(Beq), .F14(Funct[2]), .BNE(Bne), .F25(Funct[3]), .JALR(Jalr),
    .F30(Funct[4]), .JAL(JAL));
  and and_1 (uret, in_3, \控制信号自动生成_1_ecall );
  and and_2 (ecall, ~in_3, \控制信号自动生成_1_ecall );  // AND_Gate

  // Other names for the same wires on the sheet: IR21 = in_3; OP_CODE[4:0] = OP

  // Notes on the sheet:
  //   运算器控制器，根据指令生成运算器功能选择信号
  //   控制信号生成，产生数据通路需要的其他控制信号
endmodule

// 运算器控制器
module \运算控制器自动生成  (
  input  OP2,
  input  OP3,
  input  OP4,
  input  OP5,
  input  OP6,
  input  F12,
  input  F13,
  input  F14,
  input  F25,
  input  F30,
  output S0,
  output S1,
  output S2,
  output S3
);

  wire _ADD_0, _ADD_ALL_0, _ADD_ALL_1, _ADD_ALL_2, _S0_0, _S0_1, _S0_2, _S0_3, _S1_0, _S1_1, _S1_2, _S2_0,
       _S2_1, _S3_0, _S3_1, _S3_2, _SRA_0, _SRL_0, _SUB_0, ADD, ADD_ALL, AND, BR, F0, F1, F2, F3, F4, F5, F6,
       F7, I, J, JR, LD, N30, NSUB, OR, R, RI, SLT, SLTU, SRA, SRL, ST, SUB, SUBBIT, SYS, U, XOR;

  Comparator #(.width(5), .mode("unsigned")) comparator_1 (
    .a({OP6, OP5, OP4, OP3, OP2}), .b(5'b01100), .eq(R));  // open: gt, lt
  Comparator #(.width(5), .mode("unsigned")) comparator_2 (
    .a({OP6, OP5, OP4, OP3, OP2}), .b(5'b00100), .eq(I));  // open: gt, lt
  Comparator #(.width(5), .mode("unsigned")) comparator_3 (
    .a({OP6, OP5, OP4, OP3, OP2}), .b({5{1'b0}}), .eq(LD));  // open: gt, lt
  Comparator #(.width(5), .mode("unsigned")) comparator_4 (
    .a({OP6, OP5, OP4, OP3, OP2}), .b(5'b01000), .eq(ST));  // open: gt, lt
  Comparator #(.width(5), .mode("unsigned")) comparator_5 (
    .a({OP6, OP5, OP4, OP3, OP2}), .b(5'b11000), .eq(BR));  // open: gt, lt
  Comparator #(.width(5), .mode("unsigned")) comparator_6 (
    .a({OP6, OP5, OP4, OP3, OP2}), .b(5'b11001), .eq(JR));  // open: gt, lt
  Comparator #(.width(5), .mode("unsigned")) comparator_7 (
    .a({OP6, OP5, OP4, OP3, OP2}), .b(5'b11011), .eq(J));  // open: gt, lt
  Comparator #(.width(5), .mode("unsigned")) comparator_8 (
    .a({OP6, OP5, OP4, OP3, OP2}), .b(5'b01101), .eq(U));  // open: gt, lt
  Comparator #(.width(5), .mode("unsigned")) comparator_9 (
    .a({OP6, OP5, OP4, OP3, OP2}), .b(5'b11100), .eq(SYS));  // open: gt, lt
  Comparator #(.width(3), .mode("unsigned")) comparator_10 (.a({F14, F13, F12}), .b(3'b000), .eq(F0));  // open: gt, lt
  Comparator #(.width(3), .mode("unsigned")) comparator_11 (.a({F14, F13, F12}), .b(3'b001), .eq(F1));  // open: gt, lt
  Comparator #(.width(3), .mode("unsigned")) comparator_12 (.a({F14, F13, F12}), .b(3'b010), .eq(F2));  // open: gt, lt
  Comparator #(.width(3), .mode("unsigned")) comparator_13 (.a({F14, F13, F12}), .b(3'b011), .eq(F3));  // open: gt, lt
  Comparator #(.width(3), .mode("unsigned")) comparator_14 (.a({F14, F13, F12}), .b(3'b100), .eq(F4));  // open: gt, lt
  Comparator #(.width(3), .mode("unsigned")) comparator_15 (.a({F14, F13, F12}), .b(3'b101), .eq(F5));  // open: gt, lt
  Comparator #(.width(3), .mode("unsigned")) comparator_16 (.a({F14, F13, F12}), .b(3'b110), .eq(F6));  // open: gt, lt
  Comparator #(.width(3), .mode("unsigned")) comparator_17 (.a({F14, F13, F12}), .b(3'b111), .eq(F7));  // open: gt, lt
  not not_1 (N30, F30);
  not not_2 (NSUB, SUBBIT);
  or or_1 (RI, R, I);
  and and_1 (SUBBIT, R, F30);
  and and_2 (_ADD_0, RI, F0);
  and and_3 (ADD, _ADD_0, NSUB);
  and and_4 (_SUB_0, R, F0);
  and and_5 (SUB, _SUB_0, F30);
  and and_6 (SLT, RI, F2);
  and and_7 (SLTU, RI, F3);
  and and_8 (XOR, RI, F4);
  and and_9 (OR, RI, F6);
  and and_10 (AND, RI, F7);
  and and_11 (_SRA_0, RI, F5);
  and and_12 (SRA, _SRA_0, F30);
  and and_13 (_SRL_0, RI, F5);
  and and_14 (SRL, _SRL_0, N30);
  or or_2 (_ADD_ALL_0, ADD, LD);
  or or_3 (_ADD_ALL_1, _ADD_ALL_0, ST);
  or or_4 (_ADD_ALL_2, _ADD_ALL_1, JR);
  or or_5 (ADD_ALL, _ADD_ALL_2, U);
  or or_6 (_S0_0, ADD_ALL, AND);
  or or_7 (_S0_1, _S0_0, XOR);
  or or_8 (_S0_2, _S0_1, SLT);
  or or_9 (_S0_3, _S0_2, SRA);
  or or_10 (S0, _S0_3, BR);
  or or_11 (_S1_0, SUB, AND);
  or or_12 (_S1_1, _S1_0, SLT);
  or or_13 (_S1_2, _S1_1, SRL);
  or or_14 (S1, _S1_2, BR);
  or or_15 (_S2_0, ADD_ALL, SUB);
  or or_16 (_S2_1, _S2_0, AND);
  or or_17 (S2, _S2_1, SLTU);
  or or_18 (_S3_0, OR, XOR);
  or or_19 (_S3_1, _S3_0, SLT);
  or or_20 (_S3_2, _S3_1, SLTU);
  or or_21 (S3, _S3_2, BR);

  // Other names for the same wires on the sheet: FUN3[2:0] = {F14, F13, F12}; OP[4:0] = {OP6, OP5, OP4, OP3, OP2}

  // Notes on the sheet:
  //   ALU 编码：0 SLL / 1 SRA / 2 SRL / 5 ADD / 6 SUB / 7 AND / 8 OR / 9 XOR / 11 SLT / 12 SLTU
endmodule

// 控制信号生成
module \控制信号自动生成  (
  input  OP2,
  input  OP3,
  input  OP4,
  input  OP5,
  input  OP6,
  input  F12,
  input  F13,
  input  F14,
  input  F25,
  input  F30,
  output MemToReg,
  output MemWrite,
  output ALU_SRC,
  output RegWrite,
  output ecall,
  output S_Type,
  output BEQ,
  output BNE,
  output JALR,
  output JAL
);

  wire _ALU_SRC_0, _ALU_SRC_1, _ALU_SRC_2, _RegWrite_0, _RegWrite_1, _RegWrite_2, _RegWrite_3, BR, F0, F1,
       F2, F3, F4, F5, F6, F7, I, J, JR, LD, R, ST, SYS, U;

  Comparator #(.width(5), .mode("unsigned")) comparator_1 (
    .a({OP6, OP5, OP4, OP3, OP2}), .b(5'b01100), .eq(R));  // open: gt, lt
  Comparator #(.width(5), .mode("unsigned")) comparator_2 (
    .a({OP6, OP5, OP4, OP3, OP2}), .b(5'b00100), .eq(I));  // open: gt, lt
  Comparator #(.width(5), .mode("unsigned")) comparator_3 (
    .a({OP6, OP5, OP4, OP3, OP2}), .b({5{1'b0}}), .eq(LD));  // open: gt, lt
  Comparator #(.width(5), .mode("unsigned")) comparator_4 (
    .a({OP6, OP5, OP4, OP3, OP2}), .b(5'b01000), .eq(ST));  // open: gt, lt
  Comparator #(.width(5), .mode("unsigned")) comparator_5 (
    .a({OP6, OP5, OP4, OP3, OP2}), .b(5'b11000), .eq(BR));  // open: gt, lt
  Comparator #(.width(5), .mode("unsigned")) comparator_6 (
    .a({OP6, OP5, OP4, OP3, OP2}), .b(5'b11001), .eq(JR));  // open: gt, lt
  Comparator #(.width(5), .mode("unsigned")) comparator_7 (
    .a({OP6, OP5, OP4, OP3, OP2}), .b(5'b11011), .eq(J));  // open: gt, lt
  Comparator #(.width(5), .mode("unsigned")) comparator_8 (
    .a({OP6, OP5, OP4, OP3, OP2}), .b(5'b01101), .eq(U));  // open: gt, lt
  Comparator #(.width(5), .mode("unsigned")) comparator_9 (
    .a({OP6, OP5, OP4, OP3, OP2}), .b(5'b11100), .eq(SYS));  // open: gt, lt
  Comparator #(.width(3), .mode("unsigned")) comparator_10 (.a({F14, F13, F12}), .b(3'b000), .eq(F0));  // open: gt, lt
  Comparator #(.width(3), .mode("unsigned")) comparator_11 (.a({F14, F13, F12}), .b(3'b001), .eq(F1));  // open: gt, lt
  Comparator #(.width(3), .mode("unsigned")) comparator_12 (.a({F14, F13, F12}), .b(3'b010), .eq(F2));  // open: gt, lt
  Comparator #(.width(3), .mode("unsigned")) comparator_13 (.a({F14, F13, F12}), .b(3'b011), .eq(F3));  // open: gt, lt
  Comparator #(.width(3), .mode("unsigned")) comparator_14 (.a({F14, F13, F12}), .b(3'b100), .eq(F4));  // open: gt, lt
  Comparator #(.width(3), .mode("unsigned")) comparator_15 (.a({F14, F13, F12}), .b(3'b101), .eq(F5));  // open: gt, lt
  Comparator #(.width(3), .mode("unsigned")) comparator_16 (.a({F14, F13, F12}), .b(3'b110), .eq(F6));  // open: gt, lt
  Comparator #(.width(3), .mode("unsigned")) comparator_17 (.a({F14, F13, F12}), .b(3'b111), .eq(F7));  // open: gt, lt
  or or_1 (MemToReg, LD, LD);
  or or_2 (MemWrite, ST, ST);
  or or_3 (S_Type, ST, ST);
  or or_4 (_ALU_SRC_0, I, LD);
  or or_5 (_ALU_SRC_1, _ALU_SRC_0, ST);
  or or_6 (_ALU_SRC_2, _ALU_SRC_1, U);
  or or_7 (ALU_SRC, _ALU_SRC_2, JR);
  or or_8 (_RegWrite_0, R, I);
  or or_9 (_RegWrite_1, _RegWrite_0, LD);
  or or_10 (_RegWrite_2, _RegWrite_1, U);
  or or_11 (_RegWrite_3, _RegWrite_2, J);
  or or_12 (RegWrite, _RegWrite_3, JR);
  or or_13 (ecall, SYS, SYS);
  or or_14 (JALR, JR, JR);
  or or_15 (JAL, J, J);
  and and_1 (BEQ, BR, F0);
  and and_2 (BNE, BR, F1);

  // Other names for the same wires on the sheet: FUN3[2:0] = {F14, F13, F12}; OP[4:0] = {OP6, OP5, OP4, OP3, OP2}

  // Notes on the sheet:
  //   基本控制信号；BGE 与 LH / LUI 扩展选择在主电路
endmodule

// ALU
module ALU (
  input  [31:0] X,
  input  [31:0] Y,
  input  [3:0] AluOP,
  output out_4,
  output Equal,
  output out_6,
  output [31:0] Result,
  output [31:0] Result_2
);

  wire [0:0] comparator_1_lt, comparator_2_lt;
  wire [31:0] adder_1_out, AND_out, divider_1_out, divider_1_rem, multiplier_1_cout, multiplier_1_out,
       NOR_out, OR_out, shifter_1_out, shifter_2_out, shifter_3_out, subtractor_1_out, XOR_out;

  assign AND_out = X & Y;  // AND_Gate AND, 32 bits wide
  assign OR_out = X | Y;  // OR_Gate OR, 32 bits wide
  Shifter #(.width(32)) shifter_1 (.in(X), .\dist (Y[4:0]), .out(shifter_1_out));
  Shifter #(.width(32), .shift("ar")) shifter_2 (.in(X), .\dist (Y[4:0]), .out(shifter_2_out));
  Shifter #(.width(32), .shift("lr")) shifter_3 (.in(X), .\dist (Y[4:0]), .out(shifter_3_out));
  Multiplier #(.width(32)) multiplier_1 (.a(X), .b(Y), .out(multiplier_1_out), .cout(multiplier_1_cout));  // open: cin
  Divider #(.width(32)) divider_1 (.a(X), .b(Y), .out(divider_1_out), .rem(divider_1_rem));  // open: upper
  Adder #(.width(32)) adder_1 (.a(X), .b(Y), .out(adder_1_out));  // open: cin, cout
  Subtractor #(.width(32)) subtractor_1 (.a(X), .b(Y), .out(subtractor_1_out));  // open: bin, bout
  assign XOR_out = X ^ Y;  // XOR_Gate XOR, 32 bits wide
  assign NOR_out = ~(X | Y);  // NOR_Gate NOR, 32 bits wide
  Comparator #(.width(32)) comparator_1 (.a(X), .b(Y), .eq(Equal), .lt(comparator_1_lt[0]));  // open: gt
  Comparator #(.width(32), .mode("unsigned")) comparator_2 (.a(X), .b(Y), .lt(comparator_2_lt[0]));  // open: gt, eq
  Multiplexer #(.select(4), .width(32), .enable("false")) multiplexer_1 (
    .in0(shifter_1_out), .in1(shifter_2_out), .in2(shifter_3_out), .in3(multiplier_1_out),
    .in4(divider_1_out), .in5(adder_1_out), .in6(subtractor_1_out), .in7(AND_out), .in8(OR_out),
    .in9(XOR_out), .in10(NOR_out), .in11({{31{1'b0}}, comparator_1_lt[0]}),
    .in12({{31{1'b0}}, comparator_2_lt[0]}), .in13({32{1'b0}}), .in14({32{1'b0}}), .in15({32{1'b0}}),
    .out(Result), .sel(AluOP));
  Multiplexer #(.select(4), .width(32), .enable("false")) multiplexer_2 (
    .in0({32{1'b0}}), .in1({32{1'b0}}), .in2({32{1'b0}}), .in3(multiplier_1_cout), .in4(divider_1_rem),
    .in5({32{1'b0}}), .in6({32{1'b0}}), .in7({32{1'b0}}), .in8({32{1'b0}}), .in9({32{1'b0}}),
    .in10({32{1'b0}}), .in11({32{1'b0}}), .in12({32{1'b0}}), .in13({32{1'b0}}), .in14({32{1'b0}}),
    .in15({32{1'b0}}), .out(Result_2), .sel(AluOP));
  Multiplexer #(.select(4), .enable("false")) multiplexer_3 (
    .in0(1'b0), .in1(1'b0), .in2(1'b0), .in3(1'b0), .in4(1'b0), .in5(1'b0), .in6(1'b0), .in7(1'b0),
    .in8(1'b0), .in9(1'b0), .in10(1'b0), .in11(comparator_1_lt[0]), .in12(comparator_2_lt[0]), .in13(1'b0),
    .in14(1'b0), .in15(1'b0), .out(out_6), .sel(AluOP));
  not not_1 (out_4, out_6);

  // Other names for the same wires on the sheet: Result2[31:0] = Result_2; S[3:0] = AluOP; tunnel = out_6;
  //   tunnel_t = out_4

  // Notes on the sheet:
  //   不要改变此引脚区域内容，也不要改变ALU封装形式
  //   输入引脚
  //   输出引脚
endmodule

module Regifile (
  input  [31:0] Din,
  input  Clk,
  input  WE,
  input  [4:0] R1_num,
  input  [4:0] W_num,
  input  [4:0] R2_num,
  output [31:0] R1,
  output [31:0] R2
);

  // register_file register_file_1: pin names not known; wires that end beside it: Din, Clk, WE, W_num, R1_num, R2_num, R1, R2
endmodule

// IF / ID
module IF_ID (
  input  PredictJump,
  input  [31:0] IR,
  input  [31:0] PC,
  input  \气泡 ,
  input  \EN_低电平有效 ,
  input  CLK,
  output PredictJump_2,
  output [31:0] IR_2,
  output [31:0] PC_2,
  output [31:0] IR_3
);

  wire multiplexer_1_out, not_1_out, pull_resistor_3_node;
  wire [31:0] multiplexer_2_out, multiplexer_3_out, undriven;

  Pull_Resistor pull_resistor_1 (.node(\气泡 ));
  Multiplexer #(.enable("false")) multiplexer_1 (.in0(PredictJump), .in1(1'b0), .out(multiplexer_1_out), .sel(\气泡 ));
  Multiplexer #(.width(32), .enable("false")) multiplexer_2 (
    .in0(IR), .in1(undriven), .out(multiplexer_2_out), .sel(\气泡 ));
  Multiplexer #(.width(32), .enable("false")) multiplexer_3 (
    .in0(PC), .in1(undriven), .out(multiplexer_3_out), .sel(\气泡 ));
  Pull_Resistor pull_resistor_2 (.node(\EN_低电平有效 ));
  Pull_Resistor pull_resistor_3 (.node(pull_resistor_3_node));
  not not_1 (not_1_out, \EN_低电平有效 );
  Register #(.width(1)) u_PredictJump (
    .D(multiplexer_1_out), .en(not_1_out), .Q(PredictJump_2), .clk(CLK));  // open: clr
  Register #(.width(32)) u_IR (.D(multiplexer_2_out), .en(not_1_out), .Q(IR_2), .clk(CLK));  // open: clr
  Register #(.width(32)) u_PC (.D(multiplexer_3_out), .en(not_1_out), .Q(PC_2), .clk(CLK));  // open: clr

  assign IR_3 = IR_2;

  // Notes on the sheet:
  //   气泡: pull=down
endmodule

// ID / EX
module ID_EX (
  input  [31:0] PC,
  input  [31:0] RS1,
  input  [31:0] RS2,
  input  RegWrite,
  input  MemToReg,
  input  MemWrite,
  input  ALuSrc,
  input  [31:0] Imm32,
  input  [1:0] rs2Fwd,
  input  [1:0] rs1Fwd,
  input  PredictJump,
  input  [31:0] IR,
  input  [31:0] Reserved1,
  input  [31:0] Reserved2,
  input  [4:0] WriteReg_num,
  input  [3:0] ALUOP,
  input  [9:0] \指令译码信号 ,
  input  \气泡 ,
  input  \EN_低电平有效 ,
  input  CLK,
  output [31:0] PC_2,
  output [31:0] RS1_2,
  output [31:0] RS2_2,
  output [31:0] Imm32_2,
  output [31:0] IR_2,
  output RegWrite_2,
  output MemToReg_2,
  output MemWrite_2,
  output ALuSrc_2,
  output [1:0] rs2Fwd_2,
  output [31:0] Reserved1_2,
  output [1:0] rs1Fwd_2,
  output PredictJump_2,
  output [31:0] Reserved2_2,
  output [4:0] WriteReg_num_2,
  output [3:0] ALUOP_2,
  output [9:0] \指令译码信号_2 
);

  wire not_1_out;
  wire [3:0] multiplexer_10_out;
  wire [4:0] multiplexer_9_out;
  wire [9:0] multiplexer_11_out;
  wire [15:0] multiplexer_8_out;
  wire [15:9] ControlBusIn, ControlBusOut;
  wire [31:0] multiplexer_1_out, multiplexer_2_out, multiplexer_3_out, multiplexer_4_out, multiplexer_5_out,
       multiplexer_6_out, multiplexer_7_out;

  Pull_Resistor pull_resistor_1 (.node({ControlBusIn, PredictJump, rs1Fwd, rs2Fwd, ALuSrc, MemWrite, MemToReg, RegWrite}));
  Pull_Resistor pull_resistor_2 (.node(\指令译码信号 ));
  Pull_Resistor pull_resistor_3 (.node(\气泡 ));
  Multiplexer #(.width(32), .enable("false")) multiplexer_1 (
    .in0(PC), .in1({32{1'b0}}), .out(multiplexer_1_out), .sel(\气泡 ));
  Multiplexer #(.width(32), .enable("false")) multiplexer_2 (
    .in0(RS1), .in1({32{1'b0}}), .out(multiplexer_2_out), .sel(\气泡 ));
  Multiplexer #(.width(32), .enable("false")) multiplexer_3 (
    .in0(RS2), .in1({32{1'b0}}), .out(multiplexer_3_out), .sel(\气泡 ));
  Multiplexer #(.width(32), .enable("false")) multiplexer_4 (
    .in0(Imm32), .in1({32{1'b0}}), .out(multiplexer_4_out), .sel(\气泡 ));
  Multiplexer #(.width(32), .enable("false")) multiplexer_5 (
    .in0(IR), .in1({32{1'b0}}), .out(multiplexer_5_out), .sel(\气泡 ));
  Multiplexer #(.width(32), .enable("false")) multiplexer_6 (
    .in0(Reserved1), .in1({32{1'b0}}), .out(multiplexer_6_out), .sel(\气泡 ));
  Multiplexer #(.width(32), .enable("false")) multiplexer_7 (
    .in0(Reserved2), .in1({32{1'b0}}), .out(multiplexer_7_out), .sel(\气泡 ));
  Multiplexer #(.width(16), .enable("false")) multiplexer_8 (
    .in0({ControlBusIn, PredictJump, rs1Fwd, rs2Fwd, ALuSrc, MemWrite, MemToReg, RegWrite}),
    .in1({16{1'b0}}), .out(multiplexer_8_out), .sel(\气泡 ));
  Multiplexer #(.width(5), .enable("false")) multiplexer_9 (
    .in0(WriteReg_num), .in1({5{1'b0}}), .out(multiplexer_9_out), .sel(\气泡 ));
  Multiplexer #(.width(4), .enable("false")) multiplexer_10 (
    .in0(ALUOP), .in1(4'b0000), .out(multiplexer_10_out), .sel(\气泡 ));
  Multiplexer #(.width(10), .enable("false")) multiplexer_11 (
    .in0(\指令译码信号 ), .in1({10{1'b0}}), .out(multiplexer_11_out), .sel(\气泡 ));
  not not_1 (not_1_out, \EN_低电平有效 );
  Pull_Resistor pull_resistor_4 (.node(\EN_低电平有效 ));
  Register #(.width(32)) u_PC (.D(multiplexer_1_out), .en(not_1_out), .Q(PC_2), .clk(CLK));  // open: clr
  Register #(.width(32)) register_1 (.D(multiplexer_2_out), .en(not_1_out), .Q(RS1_2), .clk(CLK));  // open: clr
  Register #(.width(32)) register_2 (.D(multiplexer_3_out), .en(not_1_out), .Q(RS2_2), .clk(CLK));  // open: clr
  Register #(.width(32)) register_3 (.D(multiplexer_4_out), .en(not_1_out), .Q(Imm32_2), .clk(CLK));  // open: clr
  Register #(.width(32)) register_4 (.D(multiplexer_5_out), .en(not_1_out), .Q(IR_2), .clk(CLK));  // open: clr
  Register #(.width(32)) register_5 (.D(multiplexer_6_out), .en(not_1_out), .Q(Reserved1_2), .clk(CLK));  // open: clr
  Register #(.width(32)) register_6 (.D(multiplexer_7_out), .en(not_1_out), .Q(Reserved2_2), .clk(CLK));  // open: clr
  Register #(.width(16)) register_7 (
    .D(multiplexer_8_out), .en(not_1_out),
    .Q({ControlBusOut, PredictJump_2, rs1Fwd_2, rs2Fwd_2, ALuSrc_2, MemWrite_2, MemToReg_2, RegWrite_2}),
    .clk(CLK));  // open: clr
  Register #(.width(5)) register_8 (.D(multiplexer_9_out), .en(not_1_out), .Q(WriteReg_num_2), .clk(CLK));  // open: clr
  Register #(.width(4)) register_9 (.D(multiplexer_10_out), .en(not_1_out), .Q(ALUOP_2), .clk(CLK));  // open: clr
  Register #(.width(10)) register_10 (.D(multiplexer_11_out), .en(not_1_out), .Q(\指令译码信号_2 ), .clk(CLK));  // open: clr

  // Other names for the same wires on the sheet: ControlBusIn[8:0] = {PredictJump, rs1Fwd, rs2Fwd, ALuSrc, MemWrite, MemToReg, RegWrite};
  //   ControlBusOut[8:0] = {PredictJump_2, rs1Fwd_2, rs2Fwd_2, ALuSrc_2, MemWrite_2, MemToReg_2, RegWrite_2}

  // Notes on the sheet:
  //   EN_低电平有效: pull=down
  //   PC、IR都应该一致传送，方便调试保留引脚，自己决定是否使用
  //   保留引脚，自己决定是否使用
  //   指令译码信号汇总在一起传输（bne，beq，jal，jalr，ecall，uret等）
  //   分线器已经设置好了，需要用的复制即可
  //   请将控制器输出的所有指令译码信号通过分线器汇总在一起后进行传输，后段需要使用的时候直接用分线器从多位宽线缆引出即可
  //   控制信号汇总在一起，预留了位宽，需要增加引脚可以利用剩余的线缆进行连接
endmodule

// EX/MEM
module EX_MEM (
  input  [31:0] PC,
  input  [31:0] AluResult,
  input  RegWrite,
  input  MemToReg,
  input  MemWrite,
  input  [31:0] WriteData,
  input  [31:0] IR,
  input  [31:0] Reserved1,
  input  [31:0] Reserved2,
  input  [4:0] WriteReg_num,
  input  [9:0] \指令译码信号 ,
  input  \气泡 ,
  input  \EN_低电平有效 ,
  input  CLK,
  output [31:0] PC_2,
  output [31:0] AluResult_2,
  output [31:0] WriteData_2,
  output [31:0] IR_2,
  output RegWrite_2,
  output MemToReg_2,
  output MemWrite_2,
  output [31:0] Reserved1_2,
  output [31:0] Reserved2_2,
  output [4:0] WriteReg_num_2,
  output [9:0] \指令译码信号_2 
);

  wire not_1_out;
  wire [4:0] multiplexer_8_out;
  wire [9:0] multiplexer_9_out;
  wire [15:0] multiplexer_7_out;
  wire [15:3] ControlBusIn, ControlBusOut;
  wire [31:0] multiplexer_1_out, multiplexer_2_out, multiplexer_3_out, multiplexer_4_out, multiplexer_5_out,
       multiplexer_6_out;

  Pull_Resistor pull_resistor_1 (.node({ControlBusIn, MemWrite, MemToReg, RegWrite}));
  Pull_Resistor pull_resistor_2 (.node(\指令译码信号 ));
  Pull_Resistor pull_resistor_3 (.node(\气泡 ));
  Multiplexer #(.width(32), .enable("false")) multiplexer_1 (
    .in0(PC), .in1({32{1'b0}}), .out(multiplexer_1_out), .sel(\气泡 ));
  Multiplexer #(.width(32), .enable("false")) multiplexer_2 (
    .in0(AluResult), .in1({32{1'b0}}), .out(multiplexer_2_out), .sel(\气泡 ));
  Multiplexer #(.width(32), .enable("false")) multiplexer_3 (
    .in0(WriteData), .in1({32{1'b0}}), .out(multiplexer_3_out), .sel(\气泡 ));
  Multiplexer #(.width(32), .enable("false")) multiplexer_4 (
    .in0(IR), .in1({32{1'b0}}), .out(multiplexer_4_out), .sel(\气泡 ));
  Multiplexer #(.width(32), .enable("false")) multiplexer_5 (
    .in0(Reserved1), .in1({32{1'b0}}), .out(multiplexer_5_out), .sel(\气泡 ));
  Multiplexer #(.width(32), .enable("false")) multiplexer_6 (
    .in0(Reserved2), .in1({32{1'b0}}), .out(multiplexer_6_out), .sel(\气泡 ));
  Multiplexer #(.width(16), .enable("false")) multiplexer_7 (
    .in0({ControlBusIn, MemWrite, MemToReg, RegWrite}), .in1({16{1'b0}}), .out(multiplexer_7_out), .sel(\气泡 ));
  Multiplexer #(.width(5), .enable("false")) multiplexer_8 (
    .in0(WriteReg_num), .in1({5{1'b0}}), .out(multiplexer_8_out), .sel(\气泡 ));
  Multiplexer #(.width(10), .enable("false")) multiplexer_9 (
    .in0(\指令译码信号 ), .in1({10{1'b0}}), .out(multiplexer_9_out), .sel(\气泡 ));
  not not_1 (not_1_out, \EN_低电平有效 );
  Pull_Resistor pull_resistor_4 (.node(\EN_低电平有效 ));
  Register #(.width(32)) u_PC (.D(multiplexer_1_out), .en(not_1_out), .Q(PC_2), .clk(CLK));  // open: clr
  Register #(.width(32)) register_1 (.D(multiplexer_2_out), .en(not_1_out), .Q(AluResult_2), .clk(CLK));  // open: clr
  Register #(.width(32)) register_2 (.D(multiplexer_3_out), .en(not_1_out), .Q(WriteData_2), .clk(CLK));  // open: clr
  Register #(.width(32)) register_3 (.D(multiplexer_4_out), .en(not_1_out), .Q(IR_2), .clk(CLK));  // open: clr
  Register #(.width(32)) register_4 (.D(multiplexer_5_out), .en(not_1_out), .Q(Reserved1_2), .clk(CLK));  // open: clr
  Register #(.width(32)) register_5 (.D(multiplexer_6_out), .en(not_1_out), .Q(Reserved2_2), .clk(CLK));  // open: clr
  Register #(.width(16)) register_6 (
    .D(multiplexer_7_out), .en(not_1_out), .Q({ControlBusOut, MemWrite_2, MemToReg_2, RegWrite_2}), .clk(CLK));  // open: clr
  Register #(.width(5)) register_7 (.D(multiplexer_8_out), .en(not_1_out), .Q(WriteReg_num_2), .clk(CLK));  // open: clr
  Register #(.width(10)) register_8 (.D(multiplexer_9_out), .en(not_1_out), .Q(\指令译码信号_2 ), .clk(CLK));  // open: clr

  // Other names for the same wires on the sheet: ControlBusIn[2:0] = {MemWrite, MemToReg, RegWrite};
  //   ControlBusOut[2:0] = {MemWrite_2, MemToReg_2, RegWrite_2}

  // Notes on the sheet:
  //   EN_低电平有效: pull=down
  //   保留引脚，自己决定是否使用
  //   PC、IR都应该一致传送，方便调试保留引脚，自己决定是否使用
  //   指令译码信号汇总在一起传输（bne，beq，jal，jalr，ecall，uret等）
  //   分线器已经设置好了，需要用的复制即可
  //   请将控制器输出的所有指令译码信号通过分线器汇总在一起后进行传输，后段需要使用的时候直接用分线器从多位宽线缆引出即可
endmodule

// MEM/WB
module MEM_WB (
  input  [31:0] PC,
  input  [31:0] AluResult,
  input  RegWrite,
  input  MemToReg,
  input  [31:0] MemData,
  input  [31:0] IR,
  input  [31:0] Reserved1,
  input  [31:0] Reserved2,
  input  [4:0] WriteReg_num,
  input  [9:0] \指令译码信号 ,
  input  \气泡 ,
  input  \EN_低电平有效 ,
  input  CLK,
  output [31:0] PC_2,
  output [31:0] AluResult_2,
  output [31:0] MemData_2,
  output [31:0] IR_2,
  output RegWrite_2,
  output MemToReg_2,
  output [31:0] Reserved1_2,
  output [31:0] Reserved2_2,
  output [4:0] WriteReg_num_2,
  output [9:0] \指令译码信号_2 
);

  wire not_1_out;
  wire [4:0] multiplexer_8_out;
  wire [9:0] multiplexer_9_out;
  wire [15:0] multiplexer_7_out;
  wire [15:2] ControlBusIn, ControlBusOut;
  wire [31:0] multiplexer_1_out, multiplexer_2_out, multiplexer_3_out, multiplexer_4_out, multiplexer_5_out,
       multiplexer_6_out;

  Pull_Resistor pull_resistor_1 (.node({ControlBusIn, MemToReg, RegWrite}));
  Pull_Resistor pull_resistor_2 (.node(\指令译码信号 ));
  Pull_Resistor pull_resistor_3 (.node(\气泡 ));
  Multiplexer #(.width(32), .enable("false")) multiplexer_1 (
    .in0(PC), .in1({32{1'b0}}), .out(multiplexer_1_out), .sel(\气泡 ));
  Multiplexer #(.width(32), .enable("false")) multiplexer_2 (
    .in0(AluResult), .in1({32{1'b0}}), .out(multiplexer_2_out), .sel(\气泡 ));
  Multiplexer #(.width(32), .enable("false")) multiplexer_3 (
    .in0(MemData), .in1({32{1'b0}}), .out(multiplexer_3_out), .sel(\气泡 ));
  Multiplexer #(.width(32), .enable("false")) multiplexer_4 (
    .in0(IR), .in1({32{1'b0}}), .out(multiplexer_4_out), .sel(\气泡 ));
  Multiplexer #(.width(32), .enable("false")) multiplexer_5 (
    .in0(Reserved1), .in1({32{1'b0}}), .out(multiplexer_5_out), .sel(\气泡 ));
  Multiplexer #(.width(32), .enable("false")) multiplexer_6 (
    .in0(Reserved2), .in1({32{1'b0}}), .out(multiplexer_6_out), .sel(\气泡 ));
  Multiplexer #(.width(16), .enable("false")) multiplexer_7 (
    .in0({ControlBusIn, MemToReg, RegWrite}), .in1({16{1'b0}}), .out(multiplexer_7_out), .sel(\气泡 ));
  Multiplexer #(.width(5), .enable("false")) multiplexer_8 (
    .in0(WriteReg_num), .in1({5{1'b0}}), .out(multiplexer_8_out), .sel(\气泡 ));
  Multiplexer #(.width(10), .enable("false")) multiplexer_9 (
    .in0(\指令译码信号 ), .in1({10{1'b0}}), .out(multiplexer_9_out), .sel(\气泡 ));
  not not_1 (not_1_out, \EN_低电平有效 );
  Pull_Resistor pull_resistor_4 (.node(\EN_低电平有效 ));
  Register #(.width(32)) u_PC (.D(multiplexer_1_out), .en(not_1_out), .Q(PC_2), .clk(CLK));  // open: clr
  Register #(.width(32)) register_1 (.D(multiplexer_2_out), .en(not_1_out), .Q(AluResult_2), .clk(CLK));  // open: clr
  Register #(.width(32)) register_2 (.D(multiplexer_3_out), .en(not_1_out), .Q(MemData_2), .clk(CLK));  // open: clr
  Register #(.width(32)) register_3 (.D(multiplexer_4_out), .en(not_1_out), .Q(IR_2), .clk(CLK));  // open: clr
  Register #(.width(32)) register_4 (.D(multiplexer_5_out), .en(not_1_out), .Q(Reserved1_2), .clk(CLK));  // open: clr
  Register #(.width(32)) register_5 (.D(multiplexer_6_out), .en(not_1_out), .Q(Reserved2_2), .clk(CLK));  // open: clr
  Register #(.width(16)) register_6 (
    .D(multiplexer_7_out), .en(not_1_out), .Q({ControlBusOut, MemToReg_2, RegWrite_2}), .clk(CLK));  // open: clr
  Register #(.width(5)) register_7 (.D(multiplexer_8_out), .en(not_1_out), .Q(WriteReg_num_2), .clk(CLK));  // open: clr
  Register #(.width(10)) register_8 (.D(multiplexer_9_out), .en(not_1_out), .Q(\指令译码信号_2 ), .clk(CLK));  // open: clr

  // Other names for the same wires on the sheet: ControlBusIn[1:0] = {MemToReg, RegWrite};
  //   ControlBusOut[1:0] = {MemToReg_2, RegWrite_2}

  // Notes on the sheet:
  //   EN_低电平有效: pull=down
  //   保留引脚，自己决定是否使用
  //   PC、IR都应该一致传送，方便调试保留引脚，自己决定是否使用
  //   指令译码信号汇总在一起传输（bne，beq，jal，jalr，ecall，uret等）
  //   分线器已经设置好了，需要用的复制即可
  //   请将控制器输出的所有指令译码信号通过分线器汇总在一起后进行传输，后段需要使用的时候直接用分线器从多位宽线缆引出即可
endmodule
