// Logisim project instruction-coverage.circ as structural Verilog: 6 circuits, main circuit ◇综合指令覆盖测试
module \综合指令覆盖测试  (
  input  IR1,
  input  IR2,
  input  IR3,
  output RegWrite,
  output MemWrite,
  output [31:0] PC,
  output [31:0] IR,
  output [31:0] RDin,
  output [31:0] MDin,
  output [31:0] LedData
);

  wire ALU_SRC, BEQ, BGE, BNE, BR_OP, CLK, clock_1_out, comparator_6_eq, comparator_6_lt, d_ff_1_q, ECALL,
       EQ, GE, GE_FUN, Go, halt, IR1_t, IR2_t, IR3_t, IRA, IRB, IRC, JAL, JALR, JUMP, LED_WE, LH_FUN, LT,
       LUI, MemToReg, nand_1_out, NE, not_1_out, NOT_GO, NOT_PRINT, PRINT, RST, RUN, S_TYPE, TAKE, TAKE0,
       TAKE_EQ, TAKE_GE, TAKE_NE, URET, WAIT;
  wire [3:0] ALU_OP;
  wire [4:0] RA1, RA2;
  wire [12:0] CNT_num;
  wire [15:0] COUNT_NEXT, HALF, HIGH16, LOW16, \总周期数 ;
  wire [31:0] ALU_A, ALU_B, ALU_R, EXEC_RESULT, IMM_B, IMM_B_HALF, IMM_I, IMM_IS, IMM_J, IMM_J_HALF, IMM_S,
       IMM_U, LH_VALUE, LOAD_VALUE, NEXT_PC, NPC0, NPC1, PC4, PC_B, PC_J, PC_JR, R1, WB0;

  Button \u_继续运行  (.out(Go));
  Button _1 (.out(IRA));
  Button _2 (.out(IRB));
  Button _3 (.out(IRC));
  LED led_1 (.in(1'b0));
  LED led_2 (.in(1'b0));
  LED led_3 (.in(1'b0));
  Hex_Digit_Display hex_digit_display_1 (.value(LedData[31:28]));  // open: dp
  Register #(.width(32)) u_PC (.D(NEXT_PC), .en(not_1_out), .Q(PC), .clk(CLK), .clr(RST), .cs(1'b0), .preset(1'b0));
  not not_1 (not_1_out, halt);
  Hex_Digit_Display hex_digit_display_2 (.value(LedData[23:20]));  // open: dp
  Hex_Digit_Display hex_digit_display_3 (.value(LedData[27:24]));  // open: dp
  Hex_Digit_Display hex_digit_display_4 (.value(LedData[19:16]));  // open: dp
  Hex_Digit_Display hex_digit_display_5 (.value(LedData[15:12]));  // open: dp
  // riscv_probe riscv_probe_1: pin names not known; wires that end beside it: IR
  Hex_Digit_Display hex_digit_display_6 (.value(LedData[11:8]));  // open: dp
  Hex_Digit_Display hex_digit_display_7 (.value(LedData[7:4]));  // open: dp
  // Probe on \总周期数 
  ROM #(.addrWidth(10), .dataWidth(32), .Select("high")) rom_1 (.addr(PC[11:2]), .data(IR), .sel(1'b1));
  assign IMM_I = {{20{IR[31]}}, IR[31:20]};  // Bit_Extender bit_extender_1
  assign IMM_S = {{20{IR[31]}}, {IR[31:25], IR[11:7]}};  // Bit_Extender bit_extender_2
  assign IMM_B_HALF = {{20{IR[31]}}, {IR[31], IR[7], IR[30:25], IR[11:8]}};  // Bit_Extender bit_extender_3
  assign IMM_J_HALF = {{12{IR[31]}}, {IR[31], IR[19:12], IR[20], IR[30:21]}};  // Bit_Extender bit_extender_4
  Adder #(.width(32)) adder_1 (.a(PC), .b(32'h4), .out(PC4), .cin(1'b0));  // open: cout
  Adder #(.width(32)) adder_2 (.a(PC), .b(IMM_B), .out(PC_B), .cin(1'b0));  // open: cout
  Adder #(.width(32)) adder_3 (.a(PC), .b(IMM_J), .out(PC_J), .cin(1'b0));  // open: cout
  Hex_Digit_Display hex_digit_display_8 (.value(LedData[3:0]));  // open: dp
  \单周期硬布线控制器  \u_单周期硬布线控制器_1  (
    .Funct({IR[30], IR[25], IR[14:12]}), .OP(IR[6:2]), .ALU_OP(ALU_OP), .MemToReg(MemToReg),
    .MemWrite(MemWrite), .ALU_SRC(ALU_SRC), .RegWrite(RegWrite), .ecall(ECALL), .S_type(S_TYPE), .Jalr(JALR),
    .Beq(BEQ), .JAL(JAL), .Bne(BNE), .in_3(IR[21]), .uret(URET));
  or or_1 (IR1_t, IR1, IRA);
  assign IMM_U = IR & 32'hfffff000;  // AND_Gate and_1, 32 bits wide
  Shifter #(.width(32)) shifter_1 (.in(IMM_B_HALF), .\dist (5'b00001), .out(IMM_B));
  Shifter #(.width(32)) shifter_2 (.in(IMM_J_HALF), .\dist (5'b00001), .out(IMM_J));
  and and_2 (TAKE_EQ, BEQ, EQ);
  not not_2 (NE, EQ);
  assign PC_JR = ALU_R & 32'hfffffffe;  // AND_Gate and_3, 32 bits wide
  or or_2 (IR2_t, IR2, IRB);
  Regifile regifile_1 (
    .Din(RDin), .Clk(CLK), .R1(R1), .R2(MDin), .WE(RegWrite), .W_num(IR[11:7]), .R1_num(RA1), .R2_num(RA2));
  or or_3 (IR3_t, IR3, IRC);
  and and_4 (TAKE_NE, BNE, NE);
  and and_5 (TAKE_GE, BGE, GE);
  ALU alu_1 (
    .X(ALU_A), .Y(ALU_B), .AluOP(ALU_OP), .Equal(EQ), .Result(ALU_R), .out_4(GE), .out_6(LT));  // open: Result_2
  Comparator #(.width(7), .mode("unsigned")) comparator_1 (.a(IR[6:0]), .b(7'b0110111), .eq(LUI));  // open: gt, lt
  Comparator #(.width(3), .mode("unsigned")) comparator_2 (.a(IR[14:12]), .b(3'b001), .eq(LH_FUN));  // open: gt, lt
  Comparator #(.width(3), .mode("unsigned")) comparator_3 (.a(IR[14:12]), .b(3'b101), .eq(GE_FUN));  // open: gt, lt
  Comparator #(.width(7), .mode("unsigned")) comparator_4 (.a(IR[6:0]), .b(7'b1100011), .eq(BR_OP));  // open: gt, lt
  RAM #(.addrWidth(10), .dataWidth(32), .bus("separate"), .Select("high"), .simpleMode("false")) ram_1 (
    .addr(ALU_R[11:2]), .din(MDin), .data({HIGH16, LOW16}), .str(MemWrite), .sel(1'b1), .clk(CLK), .ld(1'b1),
    .clr(1'b0));
  or or_4 (TAKE0, TAKE_EQ, TAKE_NE);
  or or_5 (TAKE, TAKE0, TAKE_GE);
  or or_6 (JUMP, JAL, JALR);
  and and_6 (BGE, GE_FUN, BR_OP);
  Button \u_复位  (.out(RST));
  D_Flip_Flop #(.Pre_Clr_Positions("LEGACY"), .NewFFLayout("false")) d_ff_1 (.Q(d_ff_1_q));  // open: clk, D, Qn, preset, reset
  // Probe on 13'hc
  Multiplexer #(.width(5), .enable("false")) multiplexer_1 (.in0(IR[19:15]), .in1(5'b10001), .out(RA1), .sel(ECALL));
  Multiplexer #(.width(32), .enable("false")) multiplexer_2 (.in0(IMM_I), .in1(IMM_S), .out(IMM_IS), .sel(S_TYPE));
  Multiplexer #(.width(32), .enable("false")) multiplexer_3 (.in0(R1), .in1({32{1'b0}}), .out(ALU_A), .sel(LUI));
  Multiplexer #(.width(32), .enable("false")) multiplexer_4 (.in0(ALU_R), .in1(IMM_U), .out(EXEC_RESULT), .sel(LUI));
  Multiplexer #(.width(32), .enable("false")) multiplexer_5 (.in0(PC4), .in1(PC_B), .out(NPC0), .sel(TAKE));
  Comparator #(.width(32), .mode("unsigned")) comparator_5 (.a(R1), .b(32'h22), .eq(PRINT));  // open: gt, lt
  not not_3 (NOT_PRINT, PRINT);
  not not_4 (NOT_GO, Go);
  Comparator #(.width(13)) comparator_6 (
    .a(CNT_num), .b(13'hc), .eq(comparator_6_eq), .lt(comparator_6_lt));  // open: gt
  Clock clock_1 (.out(clock_1_out));
  Counter #(.width(13), .max('h1fff), .ongoal("stay"), .behavior("old")) counter_1 (
    .count(comparator_6_lt), .Q(CNT_num), .clk(clock_1_out));  // open: load, D, carry, clr, preset
  nand nand_1 (nand_1_out, d_ff_1_q, comparator_6_eq);
  Multiplexer #(.width(32), .enable("false")) multiplexer_6 (.in0(NPC0), .in1(PC_J), .out(NPC1), .sel(JAL));
  and and_7 (LED_WE, PRINT, ECALL);
  and and_8 (WAIT, ECALL, NOT_PRINT);
  assign CLK = nand_1_out ? clock_1_out : 1'bz;  // Controlled_Buffer controlled_buffer_1
  Pull_Resistor #(.pull(1)) pull_resistor_1 (.node(CLK));
  Multiplexer #(.width(5), .enable("false")) multiplexer_7 (.in0(IR[24:20]), .in1(5'b01010), .out(RA2), .sel(ECALL));
  Multiplexer #(.width(32), .enable("false")) multiplexer_8 (.in0(MDin), .in1(IMM_IS), .out(ALU_B), .sel(ALU_SRC));
  Multiplexer #(.width(32), .enable("false")) multiplexer_9 (
    .in0(EXEC_RESULT), .in1(LOAD_VALUE), .out(WB0), .sel(MemToReg));
  Multiplexer #(.width(16), .enable("false")) multiplexer_10 (.in0(LOW16), .in1(HIGH16), .out(HALF), .sel(ALU_R[1]));
  Multiplexer #(.width(32), .enable("false")) multiplexer_11 (.in0(NPC1), .in1(PC_JR), .out(NEXT_PC), .sel(JALR));
  and and_9 (halt, WAIT, NOT_GO);
  not not_5 (RUN, halt);
  Adder #(.width(16)) adder_4 (.a(\总周期数 ), .b(16'h1), .out(COUNT_NEXT), .cin(1'b0));  // open: cout
  Multiplexer #(.width(32), .enable("false")) multiplexer_12 (.in0(WB0), .in1(PC4), .out(RDin), .sel(JUMP));
  assign LH_VALUE = {{16{HALF[15]}}, HALF};  // Bit_Extender bit_extender_5
  Register #(.width(32)) \LED锁存  (.D(MDin), .en(LED_WE), .Q(LedData), .clk(CLK), .clr(RST), .cs(1'b0), .preset(1'b0));
  Register #(.width(16)) \u_执行周期  (
    .D(COUNT_NEXT), .en(RUN), .Q(\总周期数 ), .clk(CLK), .clr(RST), .cs(1'b0), .preset(1'b0));
  Multiplexer #(.width(32), .enable("false")) multiplexer_13 (
    .in0({HIGH16, LOW16}), .in1(LH_VALUE), .out(LOAD_VALUE), .sel(LH_FUN));

  // Other names for the same wires on the sheet: HALF_SEL = ALU_R[1]; DADDR[9:0] = ALU_R[11:2];
  //   B12[11:0] = {IR[31], IR[7], IR[30:25], IR[11:8]}; RD[4:0] = IR[11:7]; S12[11:0] = {IR[31:25], IR[11:7]};
  //   OP7[6:0] = IR[6:0]; OP5[4:0] = IR[6:2]; I12[11:0] = IR[31:20];
  //   J20[19:0] = {IR[31], IR[19:12], IR[20], IR[30:21]}; RS2[4:0] = IR[24:20];
  //   FUN5[4:0] = {IR[30], IR[25], IR[14:12]}; F3[2:0] = IR[14:12]; RS1[4:0] = IR[19:15];
  //   MEM_WORD[31:0] = {HIGH16, LOW16}; IADDR[9:0] = PC[11:2]; R2[31:0] = MDin

  // Notes on the sheet:
  //   中断源
  //   中断等待指示
  //   数码管输出应该用寄存器锁存，否则显示数据只能一闪而过
  //   数码管输出
  //   指令探针
  //   指令存储器
  //   立即数与地址：PC / 数据地址按字节，ROM / RAM 按字寻址
  //   指令字
  //   contents of rom_1 (hex, n*v repeats v):
  //   40000a13 000000b7 00008093 00000137 00110113 000001b7 fff18193 80000237 fff20213 800002b7 00028293
  //   ffff8337 00030313 800083b7 fff38393 12345437 67840413 002084b3 402084b3 0020f4b3 0020e4b3 0020c4b3
  //   0020a4b3 0020b4b3 ff908513 ff90f513 ff90e513 ff90c513 ff90a513 00009593 00109593 00f09593 01f09593
  //   0000d593 0010d593 00f0d593 01f0d593 4000d593 4010d593 40f0d593 41f0d593 004184b3 404184b3 0041f4b3
  //   0041e4b3 0041c4b3 0041a4b3 0041b4b3 ff918513 ff91f513 ff91e513 ff91c513 ff91a513 00019593 00119593
  //   00f19593 01f19593 0001d593 0011d593 00f1d593 01f1d593 4001d593 4011d593 40f1d593 41f1d593 003284b3
  //   403284b3 0032f4b3 0032e4b3 0032c4b3 0032a4b3 0032b4b3 ff928513 ff92f513 ff92e513 ff92c513 ff92a513
  //   00029593 00129593 00f29593 01f29593 0002d593 0012d593 00f2d593 01f2d593 4002d593 4012d593 40f2d593
  //   41f2d593 005204b3 405204b3 005274b3 005264b3 005244b3 005224b3 005234b3 ff920513 ff927513 ff926513
  //   ff924513 ff922513 00021593 00121593 00f21593 01f21593 00025593 00125593 00f25593 01f25593 40025593
  //   40125593 40f25593 41f25593 005284b3 405284b3 0052f4b3 0052e4b3 0052c4b3 0052a4b3 0052b4b3 ff928513
  //   ff92f513 ff92e513 ff92c513 ff92a513 00029593 00129593 00f29593 01f29593 0002d593 0012d593 00f2d593
  //   01f2d593 4002d593 4012d593 40f2d593 41f2d593 006384b3 406384b3 0063f4b3 0063e4b3 0063c4b3 0063a4b3
  //   0063b4b3 ff938513 ff93f513 ff93e513 ff93c513 ff93a513 00039593 00139593 00f39593 01f39593 0003d593
  //   0013d593 00f3d593 01f3d593 4003d593 4013d593 40f3d593 41f3d593 001a2023 000a2603 000a1683 002a1703
  //   002a2223 004a2603 004a1683 006a1703 003a2423 008a2603 008a1683 00aa1703 004a2623 00ca2603 00ca1683
  //   00ea1703 005a2823 010a2603 010a1683 012a1703 006a2a23 014a2603 014a1683 016a1703 007a2c23 018a2603
  //   018a1683 01aa1703 008a2e23 01ca2603 01ca1683 01ea1703 020a0a93 ffaa9783 00208463 00180813 00209463
  //   00180813 0020d463 00180813 00210463 00180813 00211463 00180813 00215463 00180813 00518463 00180813
  //   00519463 00180813 0051d463 00180813 00520463 00180813 00521463 00180813 00525463 00180813 00428463
  //   00180813 00429463 00180813 0042d463 00180813 00528463 00180813 00529463 00180813 0052d463 00180813
  //   00218463 00180813 00219463 00180813 0021d463 00180813 00400913 fff90913 fe095ee3 008000ef 00c0006f
  //   00380813 00008067 3dd00993 00098b67 02180813 9bd20813 40870133 00e38233 006908b3 0113f833 004627b3
  //   005722b3 00c1e233 00d2f4b3 47978493 00d6c2b3 00c23833 00395493 f9d16913 0096e8b3 96d26593 00567233
  //   00f3e7b3 00c8e433 00a3f133 40518233 3086e513 7772e593 41b25293 408887b3 006936b3 b966e613 00f172b3
  //   cd620493 eeb18693 012881b3 e555e593 0042a433 6f22c293 efa8f213 4b07c493 5ed66393 406581b3 00b1e733
  //   0032c1b3 01659293 00942933 00f4f133 49487293 00e123b3 dd414513 00878133 64d20893 d8b1e293 0091f833
  //   0113c3b3 79a7f613 fd64a113 5c41a593 011371b3 a3617913 40d18533 00d845b3 71077113 00b4c8b3 00c69713
  //   87e42793 cab87713 00c49313 00f238b3 01129893 007941b3 00f83133 0115a833 40e4d913 407205b3 e0038213
  //   0067a8b3 01329893 00e20233 41c25313 fc067313 72867593 fdb46313 7113c693 01b59913 01941313 5d84c113
  //   40770233 b2048413 c0410893 e1a72113 37c62713 e1214313 00236433 df192513 00631713 01b65293 26596293
  //   00b8e233 008181b3 40e7d113 00b40133 006164b3 00f723b3 01116233 e3730293 00a80233 d3127493 00d39213
  //   ae82e193 6c670593 00e564b3 00c4b4b3 eb24e393 9be80493 00f548b3 00280233 fef40113 0111c6b3 0028f4b3
  //   00840933 00191693 01029393 73840813 01e21413 40930333 56a4c693 40b68733 00d61713 00350133 c3e3f293
  //   00e937b3 40f708b3 00212233 bb97e593 00890833 f5292493 00766533 0088a6b3 40d1d113 21b86593 00238133
  //   011502b3 01096133 00f706b3 0031e7b3 41040233 00859813 40f388b3 dfd4a413 007322b3 01288333 0061b4b3
  //   01785593 23b17513 0128f633 41f5d393 8653a213 98618113 01123333 20487393 40165313 2bb44213 01273733
  //   00f925b3 00c88433 ee68e313 00f784b3 ea448893 28947693 f171e193 40488233 010882b3 40045493 01118333
  //   40790533 e4a20293 00e28633 e0c6a713 40868233 c0c6e413 79a90513 00830433 00d33333 412106b3 00388933
  //   b2787193 e3592493 01295393 409187b3 00f38633 00976933 00c16133 40a388b3 f9d7e213 38d8c713 b6b4e813
  //   41188133 01c51493 66a6e213 008432b3 d046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
  //   下一条 PC：顺序 / 条件分支 / JAL / JALR（清 bit0）
  //   JAL
  //   JALR
  //   URET
  //   Beq
  //   Bne
  //   MemToReg
  //   MemWrite
  //   AluOP
  //   AluSrcB
  //   RegWrite
  //   数据存储器
  //   为方便自动评测，需要输出PC，IR，寄存器堆写如数据RDin
  //   RAM写使能MemWrite、RAM写入数据MDin等信号
  //   读寄存器 / ALU 输入 / 写回选择
  //   LH：根据地址 bit1 选择半字，16 → 32 位符号扩展
  //   控制位
  //   暂停节拍，不能为0
  //   ECALL：a7=34 锁存 a0；其他调用暂停，Go 继续
  //   戳工具置1进入计数暂停模式，ctrl+k时钟自动运行到对应节拍暂停
  //   ctrl+k关闭时钟连续运行，将控制位置零，进入单步调试模式调试
  //   用这个时钟源需要去掉电路中的其他时钟源
  //   可计数暂停的时钟源
endmodule

// 单周期硬布线控制器
module \单周期硬布线控制器  (
  input  [4:0] OP,
  input  [4:0] Funct,
  input  in_3,
  output [3:0] ALU_OP,
  output uret,
  output MemToReg,
  output ecall,
  output MemWrite,
  output ALU_SRC,
  output RegWrite,
  output S_type,
  output Beq,
  output Bne,
  output Jalr,
  output JAL
);

  wire \控制信号自动生成_1_ecall ;

  \运算控制器自动生成  \u_运算控制器自动生成_1  (
    .OP2(OP[0]), .OP3(OP[1]), .OP4(OP[2]), .OP5(OP[3]), .OP6(OP[4]), .F12(Funct[0]), .F13(Funct[1]),
    .F14(Funct[2]), .F25(Funct[3]), .F30(Funct[4]), .S0(ALU_OP[0]), .S1(ALU_OP[1]), .S2(ALU_OP[2]),
    .S3(ALU_OP[3]));
  \控制信号自动生成  \u_控制信号自动生成_1  (
    .OP2(OP[0]), .MemToReg(MemToReg), .OP3(OP[1]), .MemWrite(MemWrite), .OP4(OP[2]), .ALU_SRC(ALU_SRC),
    .OP5(OP[3]), .RegWrite(RegWrite), .OP6(OP[4]), .ecall(\控制信号自动生成_1_ecall ), .F12(Funct[0]),
    .S_Type(S_type), .F13(Funct[1]), .BEQ(Beq), .F14(Funct[2]), .BNE(Bne), .F25(Funct[3]), .JALR(Jalr),
    .F30(Funct[4]), .JAL(JAL));
  and and_1 (uret, in_3, \控制信号自动生成_1_ecall );
  and and_2 (ecall, ~in_3, \控制信号自动生成_1_ecall );  // AND_Gate

  // Other names for the same wires on the sheet: IR21 = in_3; OP_CODE[4:0] = OP

  // Notes on the sheet:
  //   运算器控制器，根据指令生成运算器功能选择信号
  //   控制信号生成，产生数据通路需要的其他控制信号
endmodule

// 运算器控制器
module \运算控制器自动生成  (
  input  OP2,
  input  OP3,
  input  OP4,
  input  OP5,
  input  OP6,
  input  F12,
  input  F13,
  input  F14,
  input  F25,
  input  F30,
  output S0,
  output S1,
  output S2,
  output S3
);

  wire _ADD_0, _ADD_ALL_0, _ADD_ALL_1, _ADD_ALL_2, _S0_0, _S0_1, _S0_2, _S0_3, _S1_0, _S1_1, _S1_2, _S2_0,
       _S2_1, _S3_0, _S3_1, _S3_2, _SRA_0, _SRL_0, _SUB_0, ADD, ADD_ALL, AND, BR, F0, F1, F2, F3, F4, F5, F6,
       F7, I, J, JR, LD, N30, NSUB, OR, R, RI, SLT, SLTU, SRA, SRL, ST, SUB, SUBBIT, SYS, U, XOR;

  Comparator #(.width(5), .mode("unsigned")) comparator_1 (
    .a({OP6, OP5, OP4, OP3, OP2}), .b(5'b01100), .eq(R));  // open: gt, lt
  Comparator #(.width(5), .mode("unsigned")) comparator_2 (
    .a({OP6, OP5, OP4, OP3, OP2}), .b(5'b00100), .eq(I));  // open: gt, lt
  Comparator #(.width(5), .mode("unsigned")) comparator_3 (
    .a({OP6, OP5, OP4, OP3, OP2}), .b({5{1'b0}}), .eq(LD));  // open: gt, lt
  Comparator #(.width(5), .mode("unsigned")) comparator_4 (
    .a({OP6, OP5, OP4, OP3, OP2}), .b(5'b01000), .eq(ST));  // open: gt, lt
  Comparator #(.width(5), .mode("unsigned")) comparator_5 (
    .a({OP6, OP5, OP4, OP3, OP2}), .b(5'b11000), .eq(BR));  // open: gt, lt
  Comparator #(.width(5), .mode("unsigned")) comparator_6 (
    .a({OP6, OP5, OP4, OP3, OP2}), .b(5'b11001), .eq(JR));  // open: gt, lt
  Comparator #(.width(5), .mode("unsigned")) comparator_7 (
    .a({OP6, OP5, OP4, OP3, OP2}), .b(5'b11011), .eq(J));  // open: gt, lt
  Comparator #(.width(5), .mode("unsigned")) comparator_8 (
    .a({OP6, OP5, OP4, OP3, OP2}), .b(5'b01101), .eq(U));  // open: gt, lt
  Comparator #(.width(5), .mode("unsigned")) comparator_9 (
    .a({OP6, OP5, OP4, OP3, OP2}), .b(5'b11100), .eq(SYS));  // open: gt, lt
  Comparator #(.width(3), .mode("unsigned")) comparator_10 (.a({F14, F13, F12}), .b(3'b000), .eq(F0));  // open: gt, lt
  Comparator #(.width(3), .mode("unsigned")) comparator_11 (.a({F14, F13, F12}), .b(3'b001), .eq(F1));  // open: gt, lt
  Comparator #(.width(3), .mode("unsigned")) comparator_12 (.a({F14, F13, F12}), .b(3'b010), .eq(F2));  // open: gt, lt
  Comparator #(.width(3), .mode("unsigned")) comparator_13 (.a({F14, F13, F12}), .b(3'b011), .eq(F3));  // open: gt, lt
  Comparator #(.width(3), .mode("unsigned")) comparator_14 (.a({F14, F13, F12}), .b(3'b100), .eq(F4));  // open: gt, lt
  Comparator #(.width(3), .mode("unsigned")) comparator_15 (.a({F14, F13, F12}), .b(3'b101), .eq(F5));  // open: gt, lt
  Comparator #(.width(3), .mode("unsigned")) comparator_16 (.a({F14, F13, F12}), .b(3'b110), .eq(F6));  // open: gt, lt
  Comparator #(.width(3), .mode("unsigned")) comparator_17 (.a({F14, F13, F12}), .b(3'b111), .eq(F7));  // open: gt, lt
  not not_1 (N30, F30);
  not not_2 (NSUB, SUBBIT);
  or or_1 (RI, R, I);
  and and_1 (SUBBIT, R, F30);
  and and_2 (_ADD_0, RI, F0);
  and and_3 (ADD, _ADD_0, NSUB);
  and and_4 (_SUB_0, R, F0);
  and and_5 (SUB, _SUB_0, F30);
  and and_6 (SLT, RI, F2);
  and and_7 (SLTU, RI, F3);
  and and_8 (XOR, RI, F4);
  and and_9 (OR, RI, F6);
  and and_10 (AND, RI, F7);
  and and_11 (_SRA_0, RI, F5);
  and and_12 (SRA, _SRA_0, F30);
  and and_13 (_SRL_0, RI, F5);
  and and_14 (SRL, _SRL_0, N30);
  or or_2 (_ADD_ALL_0, ADD, LD);
  or or_3 (_ADD_ALL_1, _ADD_ALL_0, ST);
  or or_4 (_ADD_ALL_2, _ADD_ALL_1, JR);
  or or_5 (ADD_ALL, _ADD_ALL_2, U);
  or or_6 (_S0_0, ADD_ALL, AND);
  or or_7 (_S0_1, _S0_0, XOR);
  or or_8 (_S0_2, _S0_1, SLT);
  or or_9 (_S0_3, _S0_2, SRA);
  or or_10 (S0, _S0_3, BR);
  or or_11 (_S1_0, SUB, AND);
  or or_12 (_S1_1, _S1_0, SLT);
  or or_13 (_S1_2, _S1_1, SRL);
  or or_14 (S1, _S1_2, BR);
  or or_15 (_S2_0, ADD_ALL, SUB);
  or or_16 (_S2_1, _S2_0, AND);
  or or_17 (S2, _S2_1, SLTU);
  or or_18 (_S3_0, OR, XOR);
  or or_19 (_S3_1, _S3_0, SLT);
  or or_20 (_S3_2, _S3_1, SLTU);
  or or_21 (S3, _S3_2, BR);

  // Other names for the same wires on the sheet: FUN3[2:0] = {F14, F13, F12}; OP[4:0] = {OP6, OP5, OP4, OP3, OP2}

  // Notes on the sheet:
  //   ALU 编码：0 SLL / 1 SRA / 2 SRL / 5 ADD / 6 SUB / 7 AND / 8 OR / 9 XOR / 11 SLT / 12 SLTU
endmodule

// 控制信号生成
module \控制信号自动生成  (
  input  OP2,
  input  OP3,
  input  OP4,
  input  OP5,
  input  OP6,
  input  F12,
  input  F13,
  input  F14,
  input  F25,
  input  F30,
  output MemToReg,
  output MemWrite,
  output ALU_SRC,
  output RegWrite,
  output ecall,
  output S_Type,
  output BEQ,
  output BNE,
  output JALR,
  output JAL
);

  wire _ALU_SRC_0, _ALU_SRC_1, _ALU_SRC_2, _RegWrite_0, _RegWrite_1, _RegWrite_2, _RegWrite_3, BR, F0, F1,
       F2, F3, F4, F5, F6, F7, I, J, JR, LD, R, ST, SYS, U;

  Comparator #(.width(5), .mode("unsigned")) comparator_1 (
    .a({OP6, OP5, OP4, OP3, OP2}), .b(5'b01100), .eq(R));  // open: gt, lt
  Comparator #(.width(5), .mode("unsigned")) comparator_2 (
    .a({OP6, OP5, OP4, OP3, OP2}), .b(5'b00100), .eq(I));  // open: gt, lt
  Comparator #(.width(5), .mode("unsigned")) comparator_3 (
    .a({OP6, OP5, OP4, OP3, OP2}), .b({5{1'b0}}), .eq(LD));  // open: gt, lt
  Comparator #(.width(5), .mode("unsigned")) comparator_4 (
    .a({OP6, OP5, OP4, OP3, OP2}), .b(5'b01000), .eq(ST));  // open: gt, lt
  Comparator #(.width(5), .mode("unsigned")) comparator_5 (
    .a({OP6, OP5, OP4, OP3, OP2}), .b(5'b11000), .eq(BR));  // open: gt, lt
  Comparator #(.width(5), .mode("unsigned")) comparator_6 (
    .a({OP6, OP5, OP4, OP3, OP2}), .b(5'b11001), .eq(JR));  // open: gt, lt
  Comparator #(.width(5), .mode("unsigned")) comparator_7 (
    .a({OP6, OP5, OP4, OP3, OP2}), .b(5'b11011), .eq(J));  // open: gt, lt
  Comparator #(.width(5), .mode("unsigned")) comparator_8 (
    .a({OP6, OP5, OP4, OP3, OP2}), .b(5'b01101), .eq(U));  // open: gt, lt
  Comparator #(.width(5), .mode("unsigned")) comparator_9 (
    .a({OP6, OP5, OP4, OP3, OP2}), .b(5'b11100), .eq(SYS));  // open: gt, lt
  Comparator #(.width(3), .mode("unsigned")) comparator_10 (.a({F14, F13, F12}), .b(3'b000), .eq(F0));  // open: gt, lt
  Comparator #(.width(3), .mode("unsigned")) comparator_11 (.a({F14, F13, F12}), .b(3'b001), .eq(F1));  // open: gt, lt
  Comparator #(.width(3), .mode("unsigned")) comparator_12 (.a({F14, F13, F12}), .b(3'b010), .eq(F2));  // open: gt, lt
  Comparator #(.width(3), .mode("unsigned")) comparator_13 (.a({F14, F13, F12}), .b(3'b011), .eq(F3));  // open: gt, lt
  Comparator #(.width(3), .mode("unsigned")) comparator_14 (.a({F14, F13, F12}), .b(3'b100), .eq(F4));  // open: gt, lt
  Comparator #(.width(3), .mode("unsigned")) comparator_15 (.a({F14, F13, F12}), .b(3'b101), .eq(F5));  // open: gt, lt
  Comparator #(.width(3), .mode("unsigned")) comparator_16 (.a({F14, F13, F12}), .b(3'b110), .eq(F6));  // open: gt, lt
  Comparator #(.width(3), .mode("unsigned")) comparator_17 (.a({F14, F13, F12}), .b(3'b111), .eq(F7));  // open: gt, lt
  or or_1 (MemToReg, LD, LD);
  or or_2 (MemWrite, ST, ST);
  or or_3 (S_Type, ST, ST);
  or or_4 (_ALU_SRC_0, I, LD);
  or or_5 (_ALU_SRC_1, _ALU_SRC_0, ST);
  or or_6 (_ALU_SRC_2, _ALU_SRC_1, U);
  or or_7 (ALU_SRC, _ALU_SRC_2, JR);
  or or_8 (_RegWrite_0, R, I);
  or or_9 (_RegWrite_1, _RegWrite_0, LD);
  or or_10 (_RegWrite_2, _RegWrite_1, U);
  or or_11 (_RegWrite_3, _RegWrite_2, J);
  or or_12 (RegWrite, _RegWrite_3, JR);
  or or_13 (ecall, SYS, SYS);
  or or_14 (JALR, JR, JR);
  or or_15 (JAL, J, J);
  and and_1 (BEQ, BR, F0);
  and and_2 (BNE, BR, F1);

  // Other names for the same wires on the sheet: FUN3[2:0] = {F14, F13, F12}; OP[4:0] = {OP6, OP5, OP4, OP3, OP2}

  // Notes on the sheet:
  //   基本控制信号；BGE 与 LH / LUI 扩展选择在主电路
endmodule

// ALU
module ALU (
  input  [31:0] X,
  input  [31:0] Y,
  input  [3:0] AluOP,
  output out_4,
  output Equal,
  output out_6,
  output [31:0] Result,
  output [31:0] Result_2
);

  wire [0:0] comparator_1_lt, comparator_2_lt;
  wire [31:0] adder_1_out, AND_out, divider_1_out, divider_1_rem, multiplier_1_cout, multiplier_1_out,
       NOR_out, OR_out, shifter_1_out, shifter_2_out, shifter_3_out, subtractor_1_out, XOR_out;

  assign AND_out = X & Y;  // AND_Gate AND, 32 bits wide
  assign OR_out = X | Y;  // OR_Gate OR, 32 bits wide
  Shifter #(.width(32)) shifter_1 (.in(X), .\dist (Y[4:0]), .out(shifter_1_out));
  Shifter #(.width(32), .shift("ar")) shifter_2 (.in(X), .\dist (Y[4:0]), .out(shifter_2_out));
  Shifter #(.width(32), .shift("lr")) shifter_3 (.in(X), .\dist (Y[4:0]), .out(shifter_3_out));
  Multiplier #(.width(32)) multiplier_1 (.a(X), .b(Y), .out(multiplier_1_out), .cout(multiplier_1_cout));  // open: cin
  Divider #(.width(32)) divider_1 (.a(X), .b(Y), .out(divider_1_out), .rem(divider_1_rem));  // open: upper
  Adder #(.width(32)) adder_1 (.a(X), .b(Y), .out(adder_1_out));  // open: cin, cout
  Subtractor #(.width(32)) subtractor_1 (.a(X), .b(Y), .out(subtractor_1_out));  // open: bin, bout
  assign XOR_out = X ^ Y;  // XOR_Gate XOR, 32 bits wide
  assign NOR_out = ~(X | Y);  // NOR_Gate NOR, 32 bits wide
  Comparator #(.width(32)) comparator_1 (.a(X), .b(Y), .eq(Equal), .lt(comparator_1_lt[0]));  // open: gt
  Comparator #(.width(32), .mode("unsigned")) comparator_2 (.a(X), .b(Y), .lt(comparator_2_lt[0]));  // open: gt, eq
  Multiplexer #(.select(4), .width(32), .enable("false")) multiplexer_1 (
    .in0(shifter_1_out), .in1(shifter_2_out), .in2(shifter_3_out), .in3(multiplier_1_out),
    .in4(divider_1_out), .in5(adder_1_out), .in6(subtractor_1_out), .in7(AND_out), .in8(OR_out),
    .in9(XOR_out), .in10(NOR_out), .in11({{31{1'b0}}, comparator_1_lt[0]}),
    .in12({{31{1'b0}}, comparator_2_lt[0]}), .in13({32{1'b0}}), .in14({32{1'b0}}), .in15({32{1'b0}}),
    .out(Result), .sel(AluOP));
  Multiplexer #(.select(4), .width(32), .enable("false")) multiplexer_2 (
    .in0({32{1'b0}}), .in1({32{1'b0}}), .in2({32{1'b0}}), .in3(multiplier_1_cout), .in4(divider_1_rem),
    .in5({32{1'b0}}), .in6({32{1'b0}}), .in7({32{1'b0}}), .in8({32{1'b0}}), .in9({32{1'b0}}),
    .in10({32{1'b0}}), .in11({32{1'b0}}), .in12({32{1'b0}}), .in13({32{1'b0}}), .in14({32{1'b0}}),
    .in15({32{1'b0}}), .out(Result_2), .sel(AluOP));
  Multiplexer #(.select(4), .enable("false")) multiplexer_3 (
    .in0(1'b0), .in1(1'b0), .in2(1'b0), .in3(1'b0), .in4(1'b0), .in5(1'b0), .in6(1'b0), .in7(1'b0),
    .in8(1'b0), .in9(1'b0), .in10(1'b0), .in11(comparator_1_lt[0]), .in12(comparator_2_lt[0]), .in13(1'b0),
    .in14(1'b0), .in15(1'b0), .out(out_6), .sel(AluOP));
  not not_1 (out_4, out_6);

  // Other names for the same wires on the sheet: Result2[31:0] = Result_2; S[3:0] = AluOP; tunnel = out_6;
  //   tunnel_t = out_4

  // Notes on the sheet:
  //   不要改变此引脚区域内容，也不要改变ALU封装形式
  //   输入引脚
  //   输出引脚
endmodule

module Regifile (
  input  [31:0] Din,
  input  Clk,
  input  WE,
  input  [4:0] R1_num,
  input  [4:0] W_num,
  input  [4:0] R2_num,
  output [31:0] R1,
  output [31:0] R2
);

  // register_file register_file_1: pin names not known; wires that end beside it: Din, Clk, WE, W_num, R1_num, R2_num, R1, R2
endmodule
