// Logisim project nested-interrupt.circ as structural Verilog: 6 circuits, main circuit ◇单周期+多级中断
module \单周期_多级中断  (
  input  IR1,
  input  IR2,
  input  IR3,
  output RegWrite,
  output MemWrite,
  output [31:0] PC,
  output [31:0] IR,
  output [31:0] RDin,
  output [31:0] MDin,
  output [31:0] LedData
);

  wire ALU_SRC, BEQ, BGE, BNE, BR_OP, CLK, clock_1_out, comparator_15_eq, comparator_15_lt, d_ff_1_q, ECALL,
       EQ, GE, GE_FUN, Go, halt, IR1_t, IR2_t, IR3_t, IRA, IRB, IRC, IRQ_Accept, IRQ_Accept_0, IRQ_Accept_1,
       IRQ_Accept_2, IRQ_Accept_3, IRQ_Ack1, IRQ_Ack2, IRQ_Ack3, IRQ_AckPulse1, IRQ_AckPulse2, IRQ_AckPulse3,
       IRQ_Active0, IRQ_Active1, IRQ_Active2, IRQ_Active3, IRQ_Any, IRQ_Any_0, IRQ_Below2, IRQ_Below3,
       IRQ_Capture1, IRQ_Capture2, IRQ_Capture3, IRQ_Clear1, IRQ_Clear2, IRQ_Clear3, IRQ_Close, IRQ_Disabled,
       IRQ_DisabledNext, IRQ_DisabledOr, IRQ_DisabledOr_0, IRQ_Eligible1, IRQ_Eligible2, IRQ_Eligible3,
       IRQ_Empty, IRQ_EnableNow, IRQ_Full, IRQ_IE, IRQ_InISR, IRQ_NotAck1, IRQ_NotAck2, IRQ_NotAck3,
       IRQ_NotClose, IRQ_NotEnable, IRQ_NotReturn, IRQ_Open, IRQ_Pending1, IRQ_Pending2, IRQ_Pending3,
       IRQ_PendingNext1, IRQ_PendingNext2, IRQ_PendingNext3, IRQ_Return, IRQ_Space, IRQ_StackEN,
       IRQ_SystemRaw, IRQ_Uret, IRQ_UretRaw, JAL, JALR, JUMP, LED_WE, LH_FUN, LT, LUI, MemToReg, nand_1_out,
       NE, not_1_out, NOT_GO, NOT_PRINT, PRINT, RST, RUN, S_TYPE, TAKE, TAKE0, TAKE_EQ, TAKE_GE, TAKE_NE, W1,
       W2, W3, WAIT;
  wire [1:0] IRQ_Active, IRQ_ActiveNext, IRQ_Delta, IRQ_Depth, IRQ_DepthNext, IRQ_Prev1, IRQ_Prev2,
       IRQ_Prev3, IRQ_PrevNext1, IRQ_PrevNext2, IRQ_PrevNext3, IRQ_Selected, IRQ_Selected12;
  wire [3:0] ALU_OP;
  wire [4:0] RA1, RA2;
  wire [12:0] CNT_num;
  wire [15:0] COUNT_NEXT, HALF, HIGH16, LOW16, \总周期数 ;
  wire [31:0] ALU_A, ALU_B, ALU_R, EXEC_RESULT, IMM_B, IMM_B_HALF, IMM_I, IMM_IS, IMM_J, IMM_J_HALF, IMM_S,
       IMM_U, IRQ_EPC, IRQ_EPC2, IRQ_EPC3, IRQ_EPCNext1, IRQ_EPCNext2, IRQ_EPCNext3, IRQ_NormalNext,
       IRQ_ReturnNext, IRQ_Vector, IRQ_Vector12, LH_VALUE, LOAD_VALUE, NEXT_PC, NPC0, NPC1, PC4, PC_B, PC_J,
       PC_JR, R1, WB0;

  Button \u_继续运行  (.out(Go));
  Button _1 (.out(IRA));
  Button _2 (.out(IRB));
  Button _3 (.out(IRC));
  LED led_1 (.in(W1));
  LED led_2 (.in(W2));
  LED led_3 (.in(W3));
  Hex_Digit_Display hex_digit_display_1 (.value(LedData[31:28]));  // open: dp
  Register #(.width(32)) u_PC (.D(NEXT_PC), .en(not_1_out), .Q(PC), .clk(CLK), .clr(RST), .cs(1'b0), .preset(1'b0));
  not not_1 (not_1_out, halt);
  Hex_Digit_Display hex_digit_display_2 (.value(LedData[23:20]));  // open: dp
  Hex_Digit_Display hex_digit_display_3 (.value(LedData[27:24]));  // open: dp
  Hex_Digit_Display hex_digit_display_4 (.value(LedData[15:12]));  // open: dp
  Hex_Digit_Display hex_digit_display_5 (.value(LedData[19:16]));  // open: dp
  // riscv_probe riscv_probe_1: pin names not known; wires that end beside it: IR
  Register #(.width(1)) register_1 (
    .D(1'b1), .en(1'b1), .Q(IRQ_Capture1), .clk(IR1_t), .clr(IRQ_Clear1), .cs(1'b0), .preset(1'b0));
  Comparator #(.width(2), .mode("unsigned")) comparator_1 (
    .a(IRQ_Active), .b(2'b01), .eq(IRQ_Active1));  // open: gt, lt
  Register #(.width(1)) register_2 (
    .D(1'b1), .en(1'b1), .Q(IRQ_Capture2), .clk(IR2_t), .clr(IRQ_Clear2), .cs(1'b0), .preset(1'b0));
  Comparator #(.width(2), .mode("unsigned")) comparator_2 (
    .a(IRQ_Active), .b(2'b10), .eq(IRQ_Active2));  // open: gt, lt
  Register #(.width(1)) register_3 (
    .D(1'b1), .en(1'b1), .Q(IRQ_Capture3), .clk(IR3_t), .clr(IRQ_Clear3), .cs(1'b0), .preset(1'b0));
  Comparator #(.width(2), .mode("unsigned")) comparator_3 (
    .a(IRQ_Active), .b(2'b11), .eq(IRQ_Active3));  // open: gt, lt
  Hex_Digit_Display hex_digit_display_6 (.value(LedData[7:4]));  // open: dp
  Hex_Digit_Display hex_digit_display_7 (.value(LedData[11:8]));  // open: dp
  // Probe on \总周期数 
  ROM #(.addrWidth(10), .dataWidth(32), .Select("high")) rom_1 (.addr(PC[11:2]), .data(IR), .sel(1'b1));
  assign IMM_I = {{20{IR[31]}}, IR[31:20]};  // Bit_Extender bit_extender_1
  assign IMM_S = {{20{IR[31]}}, {IR[31:25], IR[11:7]}};  // Bit_Extender bit_extender_2
  assign IMM_B_HALF = {{20{IR[31]}}, {IR[31], IR[7], IR[30:25], IR[11:8]}};  // Bit_Extender bit_extender_3
  assign IMM_J_HALF = {{12{IR[31]}}, {IR[31], IR[19:12], IR[20], IR[30:21]}};  // Bit_Extender bit_extender_4
  Adder #(.width(32)) adder_1 (.a(PC), .b(32'h4), .out(PC4), .cin(1'b0));  // open: cout
  Adder #(.width(32)) adder_2 (.a(PC), .b(IMM_B), .out(PC_B), .cin(1'b0));  // open: cout
  Adder #(.width(32)) adder_3 (.a(PC), .b(IMM_J), .out(PC_J), .cin(1'b0));  // open: cout
  Comparator #(.width(32), .mode("unsigned")) comparator_4 (.a(IR), .b(32'h73), .eq(ECALL));  // open: gt, lt
  Comparator #(.width(32), .mode("unsigned")) comparator_5 (.a(IR), .b(32'h200073), .eq(IRQ_Uret));  // open: gt, lt
  Comparator #(.width(32), .mode("unsigned")) comparator_6 (.a(IR), .b(32'h40e073), .eq(IRQ_Open));  // open: gt, lt
  Comparator #(.width(32), .mode("unsigned")) comparator_7 (.a(IR), .b(32'h40f073), .eq(IRQ_Close));  // open: gt, lt
  Multiplexer #(.width(32), .select(1), .enable("false")) multiplexer_1 (
    .in0(IRQ_EPC2), .in1(IRQ_NormalNext), .out(IRQ_EPCNext1), .sel(IRQ_Accept));
  Multiplexer #(.width(32), .select(1), .enable("false")) multiplexer_2 (
    .in0(IRQ_EPC3), .in1(IRQ_EPC), .out(IRQ_EPCNext2), .sel(IRQ_Accept));
  Multiplexer #(.width(32), .select(1), .enable("false")) multiplexer_3 (
    .in0({32{1'b0}}), .in1(IRQ_EPC2), .out(IRQ_EPCNext3), .sel(IRQ_Accept));
  Hex_Digit_Display hex_digit_display_8 (.value(LedData[3:0]));  // open: dp
  \单周期硬布线控制器  \u_单周期硬布线控制器_1  (
    .Funct({IR[30], IR[25], IR[14:12]}), .OP(IR[6:2]), .ALU_OP(ALU_OP), .MemToReg(MemToReg),
    .MemWrite(MemWrite), .ALU_SRC(ALU_SRC), .RegWrite(RegWrite), .ecall(IRQ_SystemRaw), .S_type(S_TYPE),
    .Jalr(JALR), .Beq(BEQ), .JAL(JAL), .Bne(BNE), .in_3(IR[21]), .uret(IRQ_UretRaw));
  or or_1 (IR1_t, IR1, IRA);
  assign IMM_U = IR & 32'hfffff000;  // AND_Gate and_1, 32 bits wide
  Shifter #(.width(32)) shifter_1 (.in(IMM_B_HALF), .\dist (5'b00001), .out(IMM_B));
  Shifter #(.width(32)) shifter_2 (.in(IMM_J_HALF), .\dist (5'b00001), .out(IMM_J));
  and and_2 (TAKE_EQ, BEQ, EQ);
  not not_2 (NE, EQ);
  assign PC_JR = ALU_R & 32'hfffffffe;  // AND_Gate and_3, 32 bits wide
  and and_4 (IRQ_Ack1, IRQ_Active1, IRQ_Return);
  and and_5 (IRQ_Ack2, IRQ_Active2, IRQ_Return);
  and and_6 (IRQ_Ack3, IRQ_Active3, IRQ_Return);
  or or_2 (IR2_t, IR2, IRB);
  Regifile regifile_1 (
    .Din(RDin), .Clk(CLK), .R1(R1), .R2(MDin), .WE(RegWrite), .W_num(IR[11:7]), .R1_num(RA1), .R2_num(RA2));
  Comparator #(.width(2), .mode("unsigned")) comparator_8 (.a(IRQ_Depth), .b(2'b00), .eq(IRQ_Empty));  // open: gt, lt
  Comparator #(.width(2), .mode("unsigned")) comparator_9 (.a(IRQ_Depth), .b(2'b11), .eq(IRQ_Full));  // open: gt, lt
  not not_3 (IRQ_IE, IRQ_Disabled);
  or or_3 (W1, IRQ_Capture1, IRQ_Pending1);
  or or_4 (W2, IRQ_Capture2, IRQ_Pending2);
  or or_5 (W3, IRQ_Capture3, IRQ_Pending3);
  Register #(.width(32)) register_4 (
    .D(IRQ_EPCNext1), .en(IRQ_StackEN), .Q(IRQ_EPC), .clk(CLK), .clr(RST), .cs(1'b0), .preset(1'b0));
  Register #(.width(32)) register_5 (
    .D(IRQ_EPCNext2), .en(IRQ_StackEN), .Q(IRQ_EPC2), .clk(CLK), .clr(RST), .cs(1'b0), .preset(1'b0));
  Register #(.width(32)) register_6 (
    .D(IRQ_EPCNext3), .en(IRQ_StackEN), .Q(IRQ_EPC3), .clk(CLK), .clr(RST), .cs(1'b0), .preset(1'b0));
  or or_6 (IR3_t, IR3, IRC);
  and and_7 (TAKE_NE, BNE, NE);
  and and_8 (TAKE_GE, BGE, GE);
  or or_7 (IRQ_Clear1, IRQ_AckPulse1, RST);
  Register #(.width(1)) register_7 (
    .D(IRQ_Ack1), .en(1'b1), .Q(IRQ_AckPulse1), .clk(CLK), .clr(RST), .cs(1'b0), .preset(1'b0));
  or or_8 (IRQ_Clear2, IRQ_AckPulse2, RST);
  Register #(.width(1)) register_8 (
    .D(IRQ_Ack2), .en(1'b1), .Q(IRQ_AckPulse2), .clk(CLK), .clr(RST), .cs(1'b0), .preset(1'b0));
  or or_9 (IRQ_Clear3, IRQ_AckPulse3, RST);
  Register #(.width(1)) register_9 (
    .D(IRQ_Ack3), .en(1'b1), .Q(IRQ_AckPulse3), .clk(CLK), .clr(RST), .cs(1'b0), .preset(1'b0));
  ALU alu_1 (
    .X(ALU_A), .Y(ALU_B), .AluOP(ALU_OP), .Equal(EQ), .Result(ALU_R), .out_4(GE), .out_6(LT));  // open: Result_2
  Comparator #(.width(7), .mode("unsigned")) comparator_10 (.a(IR[6:0]), .b(7'b0110111), .eq(LUI));  // open: gt, lt
  Comparator #(.width(3), .mode("unsigned")) comparator_11 (.a(IR[14:12]), .b(3'b001), .eq(LH_FUN));  // open: gt, lt
  Comparator #(.width(3), .mode("unsigned")) comparator_12 (.a(IR[14:12]), .b(3'b101), .eq(GE_FUN));  // open: gt, lt
  Comparator #(.width(7), .mode("unsigned")) comparator_13 (.a(IR[6:0]), .b(7'b1100011), .eq(BR_OP));  // open: gt, lt
  not not_4 (IRQ_InISR, IRQ_Empty);
  not not_5 (IRQ_Space, IRQ_Full);
  not not_6 (IRQ_NotAck1, IRQ_Ack1);
  not not_7 (IRQ_NotAck2, IRQ_Ack2);
  not not_8 (IRQ_NotAck3, IRQ_Ack3);
  not not_9 (IRQ_NotClose, IRQ_Close);
  RAM #(.addrWidth(10), .dataWidth(32), .bus("separate"), .Select("high"), .simpleMode("false")) ram_1 (
    .addr(ALU_R[11:2]), .din(MDin), .data({HIGH16, LOW16}), .str(MemWrite), .sel(1'b1), .clk(CLK), .ld(1'b1),
    .clr(1'b0));
  or or_10 (TAKE0, TAKE_EQ, TAKE_NE);
  or or_11 (TAKE, TAKE0, TAKE_GE);
  or or_12 (JUMP, JAL, JALR);
  and and_9 (BGE, GE_FUN, BR_OP);
  Multiplexer #(.width(2), .select(1), .enable("false")) multiplexer_4 (
    .in0(IRQ_Prev2), .in1(IRQ_Active), .out(IRQ_PrevNext1), .sel(IRQ_Accept));
  Multiplexer #(.width(2), .select(1), .enable("false")) multiplexer_5 (
    .in0(IRQ_Prev3), .in1(IRQ_Prev1), .out(IRQ_PrevNext2), .sel(IRQ_Accept));
  Multiplexer #(.width(2), .select(1), .enable("false")) multiplexer_6 (
    .in0(2'b00), .in1(IRQ_Prev2), .out(IRQ_PrevNext3), .sel(IRQ_Accept));
  Button \u_复位  (.out(RST));
  and and_10 (IRQ_Return, IRQ_Uret, IRQ_InISR);
  and and_11 (IRQ_PendingNext1, W1, IRQ_NotAck1);
  and and_12 (IRQ_PendingNext2, W2, IRQ_NotAck2);
  and and_13 (IRQ_PendingNext3, W3, IRQ_NotAck3);
  D_Flip_Flop #(.Pre_Clr_Positions("LEGACY"), .NewFFLayout("false")) d_ff_1 (.Q(d_ff_1_q));  // open: clk, D, Qn, preset, reset
  // Probe on 13'hc
  // Probe on IRQ_IE
  Multiplexer #(.width(5), .enable("false")) multiplexer_7 (.in0(IR[19:15]), .in1(5'b10001), .out(RA1), .sel(ECALL));
  Multiplexer #(.width(32), .enable("false")) multiplexer_8 (.in0(IMM_I), .in1(IMM_S), .out(IMM_IS), .sel(S_TYPE));
  Multiplexer #(.width(32), .enable("false")) multiplexer_9 (.in0(R1), .in1({32{1'b0}}), .out(ALU_A), .sel(LUI));
  Multiplexer #(.width(32), .enable("false")) multiplexer_10 (.in0(ALU_R), .in1(IMM_U), .out(EXEC_RESULT), .sel(LUI));
  Multiplexer #(.width(32), .enable("false")) multiplexer_11 (.in0(PC4), .in1(PC_B), .out(NPC0), .sel(TAKE));
  Comparator #(.width(32), .mode("unsigned")) comparator_14 (.a(R1), .b(32'h22), .eq(PRINT));  // open: gt, lt
  not not_10 (NOT_PRINT, PRINT);
  not not_11 (NOT_GO, Go);
  Comparator #(.width(13)) comparator_15 (
    .a(CNT_num), .b(13'hc), .eq(comparator_15_eq), .lt(comparator_15_lt));  // open: gt
  Clock clock_1 (.out(clock_1_out));
  not not_12 (IRQ_NotReturn, IRQ_Return);
  Counter #(.width(13), .max('h1fff), .ongoal("stay"), .behavior("old")) counter_1 (
    .count(comparator_15_lt), .Q(CNT_num), .clk(clock_1_out));  // open: load, D, carry, clr, preset
  Register #(.width(1)) register_10 (
    .D(IRQ_PendingNext1), .en(1'b1), .Q(IRQ_Pending1), .clk(CLK), .clr(RST), .cs(1'b0), .preset(1'b0));
  Register #(.width(1)) register_11 (
    .D(IRQ_PendingNext2), .en(1'b1), .Q(IRQ_Pending2), .clk(CLK), .clr(RST), .cs(1'b0), .preset(1'b0));
  Register #(.width(1)) register_12 (
    .D(IRQ_PendingNext3), .en(1'b1), .Q(IRQ_Pending3), .clk(CLK), .clr(RST), .cs(1'b0), .preset(1'b0));
  Register #(.width(2)) register_13 (
    .D(IRQ_PrevNext1), .en(IRQ_StackEN), .Q(IRQ_Prev1), .clk(CLK), .clr(RST), .cs(1'b0), .preset(1'b0));
  Register #(.width(2)) register_14 (
    .D(IRQ_PrevNext2), .en(IRQ_StackEN), .Q(IRQ_Prev2), .clk(CLK), .clr(RST), .cs(1'b0), .preset(1'b0));
  Register #(.width(2)) register_15 (
    .D(IRQ_PrevNext3), .en(IRQ_StackEN), .Q(IRQ_Prev3), .clk(CLK), .clr(RST), .cs(1'b0), .preset(1'b0));
  nand nand_1 (nand_1_out, d_ff_1_q, comparator_15_eq);
  Multiplexer #(.width(32), .enable("false")) multiplexer_12 (.in0(NPC0), .in1(PC_J), .out(NPC1), .sel(JAL));
  and and_14 (LED_WE, PRINT, ECALL);
  and and_15 (WAIT, ECALL, NOT_PRINT);
  assign CLK = nand_1_out ? clock_1_out : 1'bz;  // Controlled_Buffer controlled_buffer_1
  Pull_Resistor #(.pull(1)) pull_resistor_1 (.node(CLK));
  // Probe on IRQ_Active
  Multiplexer #(.width(5), .enable("false")) multiplexer_13 (.in0(IR[24:20]), .in1(5'b01010), .out(RA2), .sel(ECALL));
  Multiplexer #(.width(32), .enable("false")) multiplexer_14 (.in0(MDin), .in1(IMM_IS), .out(ALU_B), .sel(ALU_SRC));
  Multiplexer #(.width(32), .enable("false")) multiplexer_15 (
    .in0(EXEC_RESULT), .in1(LOAD_VALUE), .out(WB0), .sel(MemToReg));
  Multiplexer #(.width(16), .enable("false")) multiplexer_16 (.in0(LOW16), .in1(HIGH16), .out(HALF), .sel(ALU_R[1]));
  Comparator #(.width(2), .mode("unsigned")) comparator_16 (
    .a(IRQ_Active), .b(2'b00), .eq(IRQ_Active0));  // open: gt, lt
  not not_13 (IRQ_Below3, IRQ_Active3);
  or or_13 (IRQ_Any_0, IRQ_Eligible1, IRQ_Eligible2);
  and and_16 (IRQ_Accept_0, IRQ_Any, IRQ_IE);
  or or_14 (IRQ_EnableNow, IRQ_Return, IRQ_Open);
  Multiplexer #(.width(32), .enable("false")) multiplexer_17 (
    .in0(NPC1), .in1(PC_JR), .out(IRQ_NormalNext), .sel(JALR));
  and and_17 (halt, WAIT, NOT_GO);
  not not_14 (RUN, halt);
  Adder #(.width(16)) adder_4 (.a(\总周期数 ), .b(16'h1), .out(COUNT_NEXT), .cin(1'b0));  // open: cout
  or or_15 (IRQ_StackEN, IRQ_Accept, IRQ_Return);
  // Probe on IRQ_EPC
  Multiplexer #(.width(32), .enable("false")) multiplexer_18 (.in0(WB0), .in1(PC4), .out(RDin), .sel(JUMP));
  assign LH_VALUE = {{16{HALF[15]}}, HALF};  // Bit_Extender bit_extender_5
  Register #(.width(32)) \LED锁存  (.D(MDin), .en(LED_WE), .Q(LedData), .clk(CLK), .clr(RST), .cs(1'b0), .preset(1'b0));
  Register #(.width(16)) \u_执行周期  (
    .D(COUNT_NEXT), .en(RUN), .Q(\总周期数 ), .clk(CLK), .clr(RST), .cs(1'b0), .preset(1'b0));
  or or_16 (IRQ_Below2, IRQ_Active0, IRQ_Active1);
  or or_17 (IRQ_Any, IRQ_Any_0, IRQ_Eligible3);
  and and_18 (IRQ_Accept_1, IRQ_Accept_0, RUN);
  not not_15 (IRQ_NotEnable, IRQ_EnableNow);
  // Probe on IRQ_Accept
  Multiplexer #(.width(32), .enable("false")) multiplexer_19 (
    .in0({HIGH16, LOW16}), .in1(LH_VALUE), .out(LOAD_VALUE), .sel(LH_FUN));
  Multiplexer #(.width(2), .select(1), .enable("false")) multiplexer_20 (
    .in0(2'b11), .in1(2'b01), .out(IRQ_Delta), .sel(IRQ_Accept));
  Multiplexer #(.width(32), .select(1), .enable("false")) multiplexer_21 (
    .in0(IRQ_NormalNext), .in1(IRQ_EPC), .out(IRQ_ReturnNext), .sel(IRQ_Return));
  and and_19 (IRQ_Accept_2, IRQ_Accept_1, IRQ_NotReturn);
  or or_18 (IRQ_DisabledOr_0, IRQ_Disabled, IRQ_Accept);
  and and_20 (IRQ_Eligible1, IRQ_Pending1, IRQ_Active0);
  and and_21 (IRQ_Eligible2, IRQ_Pending2, IRQ_Below2);
  and and_22 (IRQ_Eligible3, IRQ_Pending3, IRQ_Below3);
  // Probe on IRQ_Depth
  Multiplexer #(.width(32), .select(1), .enable("false")) multiplexer_22 (
    .in0(32'h30ac), .in1(32'h3158), .out(IRQ_Vector12), .sel(IRQ_Eligible2));
  Multiplexer #(.width(2), .select(1), .enable("false")) multiplexer_23 (
    .in0(2'b01), .in1(2'b10), .out(IRQ_Selected12), .sel(IRQ_Eligible2));
  Multiplexer #(.width(2), .select(1), .enable("false")) multiplexer_24 (
    .in0(IRQ_Prev1), .in1(IRQ_Selected), .out(IRQ_ActiveNext), .sel(IRQ_Accept));
  and and_23 (IRQ_Accept_3, IRQ_Accept_2, IRQ_NotClose);
  Adder #(.width(2)) adder_5 (.a(IRQ_Depth), .b(IRQ_Delta), .out(IRQ_DepthNext), .cin(1'b0));  // open: cout
  or or_19 (IRQ_DisabledOr, IRQ_DisabledOr_0, IRQ_Close);
  Multiplexer #(.width(32), .select(1), .enable("false")) multiplexer_25 (
    .in0(IRQ_ReturnNext), .in1(IRQ_Vector), .out(NEXT_PC), .sel(IRQ_Accept));
  and and_24 (IRQ_Accept, IRQ_Accept_3, IRQ_Space);
  and and_25 (IRQ_DisabledNext, IRQ_DisabledOr, IRQ_NotEnable);
  Multiplexer #(.width(32), .select(1), .enable("false")) multiplexer_26 (
    .in0(IRQ_Vector12), .in1(32'h3204), .out(IRQ_Vector), .sel(IRQ_Eligible3));
  Multiplexer #(.width(2), .select(1), .enable("false")) multiplexer_27 (
    .in0(IRQ_Selected12), .in1(2'b11), .out(IRQ_Selected), .sel(IRQ_Eligible3));
  Register #(.width(2)) register_16 (
    .D(IRQ_ActiveNext), .en(IRQ_StackEN), .Q(IRQ_Active), .clk(CLK), .clr(RST), .cs(1'b0), .preset(1'b0));
  Register #(.width(2)) register_17 (
    .D(IRQ_DepthNext), .en(IRQ_StackEN), .Q(IRQ_Depth), .clk(CLK), .clr(RST), .cs(1'b0), .preset(1'b0));
  Register #(.width(1)) register_18 (
    .D(IRQ_DisabledNext), .en(RUN), .Q(IRQ_Disabled), .clk(CLK), .clr(RST), .cs(1'b0), .preset(1'b0));

  // Other names for the same wires on the sheet: HALF_SEL = ALU_R[1]; DADDR[9:0] = ALU_R[11:2];
  //   B12[11:0] = {IR[31], IR[7], IR[30:25], IR[11:8]}; RD[4:0] = IR[11:7]; S12[11:0] = {IR[31:25], IR[11:7]};
  //   OP7[6:0] = IR[6:0]; OP5[4:0] = IR[6:2]; IRQ_EPC1[31:0] = IRQ_EPC; I12[11:0] = IR[31:20];
  //   J20[19:0] = {IR[31], IR[19:12], IR[20], IR[30:21]}; RS2[4:0] = IR[24:20];
  //   FUN5[4:0] = {IR[30], IR[25], IR[14:12]}; F3[2:0] = IR[14:12]; RS1[4:0] = IR[19:15];
  //   MEM_WORD[31:0] = {HIGH16, LOW16}; IADDR[9:0] = PC[11:2]; R2[31:0] = MDin

  // Notes on the sheet:
  //   中断源
  //   中断等待指示
  //   总复位信号应将除ROM以外所有存储组件全部清零
  //   请求1：捕获 / 等待 / 仅在本层返回时清除
  //   请求2：捕获 / 等待 / 仅在本层返回时清除
  //   请求3：捕获 / 等待 / 仅在本层返回时清除
  //   数码管输出
  //   指令探针
  //   指令存储器
  //   立即数与地址：PC / 数据地址按字节，ROM / RAM 按字寻址
  //   按键1捕获
  //   按键2捕获
  //   按键3捕获
  //   数码管输出应该用寄存器锁存，否则显示数据只能一闪而过
  //   指令字
  //   contents of rom_1 (hex, n*v repeats v):
  //   7d000113 00100413 01f41993 41f9d993 00000433 00c00913 00800b13 00140413 00f47413 00800293 00100313
  //   00499993 0089e9b3 01300533 02200893 00000073 406282b3 fe0294e3 00140413 00f00f93 01f47433 01c41413
  //   00800293 00100313 0049d993 0089e9b3 01300533 02200893 00000073 406282b3 fe0294e3 01c45413 406b0b33
  //   000b0463 f95ff06f 000002b3 fff2c293 01029293 fff2e293 00500533 02200893 00000073 f5dff06f 2540006f
  //   00000013 00000013 00000013 00000013 00000013 00000013 00000013 00000013 00000013 00000013 00000013
  //   00000013 00000013 00000013 00000013 00000013 00000013 00000013 00000013 00000013 00000013 00000013
  //   00000013 00000013 00000013 00000013 00000013 00000013 00000013 00000013 00000013 00000013 00000013
  //   00000013 00000013 00000013 00000013 00000013 00000013 00000013 00000013 00000013 2dc0006f 00000013
  //   00000013 00000013 00000013 00000013 00000013 00000013 00000013 00000013 00000013 00000013 00000013
  //   00000013 00000013 00000013 00000013 00000013 00000013 00000013 00000013 00000013 00000013 00000013
  //   00000013 00000013 00000013 00000013 00000013 00000013 00000013 00000013 00000013 00000013 00000013
  //   00000013 00000013 00000013 00000013 00000013 00000013 00000013 00000013 3780006f 00000013 00000013
  //   00000013 00000013 00000013 00000013 00000013 00000013 00000013 00000013 00000013 00000013 00000013
  //   00000013 00000013 00000013 00000013 00000013 00000013 00000013 00000013 00000013 00000013 00000013
  //   00000013 00000013 00000013 00000013 00000013 00000013 00000013 00000013 00000013 00000013 00000013
  //   00000013 00000013 00000013 00000013 00000013 00000013 00000013 00000013 00000013 00000013 00000013
  //   00000013 00000013 00000013 00000013 00000013 00000013 00000013 00000013 00000013 00000013 00000013
  //   00000013 00000013 00000013 00000013 00000013 01112023 00410113 00a12023 00410113 00812023 00410113
  //   01312023 00410113 01412023 00410113 01512023 00410113 01612023 00410113 00512023 00410113 00612023
  //   00410113 01c12023 00410113 00912023 00410113 01212023 00410113 0040e073 00100b13 00300a13 00100a93
  //   01600433 00441413 014469b3 01300533 02200893 00000073 fe0416e3 415a0a33 fe0a10e3 fff00293 07700493
  //   00849493 07748493 00900533 02200893 00000073 01000e13 0054c4b3 00900533 02200893 00000073 fffe0e13
  //   fe0e16e3 0040f073 ffc10113 00012903 ffc10113 00012483 ffc10113 00012e03 ffc10113 00012303 ffc10113
  //   00012283 ffc10113 00012b03 ffc10113 00012a83 ffc10113 00012a03 ffc10113 00012983 ffc10113 00012403
  //   ffc10113 00012503 ffc10113 00012883 00200073 01112023 00410113 00a12023 00410113 00812023 00410113
  //   01312023 00410113 01412023 00410113 01512023 00410113 01612023 00410113 00512023 00410113 00612023
  //   00410113 01c12023 00410113 00912023 00410113 01212023 00410113 0040e073 00200b13 00300a13 00100a93
  //   01600433 00441413 014469b3 01300533 02200893 00000073 fe0416e3 415a0a33 fe0a10e3 00800e13 fedc04b7
  //   fff00413 01045413 0084e4b3 00900533 02200893 00000073 0ba984b7 00900533 00000073 076544b7 00900533
  //   00000073 032104b7 00900533 00000073 fffe0e13 fa0e1ee3 0040f073 ffc10113 00012903 ffc10113 00012483
  //   ffc10113 00012e03 ffc10113 00012303 ffc10113 00012283 ffc10113 00012b03 ffc10113 00012a83 ffc10113
  //   00012a03 ffc10113 00012983 ffc10113 00012403 ffc10113 00012503 ffc10113 00012883 00200073 01112023
  //   00410113 00a12023 00410113 00812023 00410113 01312023 00410113 01412023 00410113 01512023 00410113
  //   01612023 00410113 00512023 00410113 00612023 00410113 01c12023 00410113 00912023 00410113 01212023
  //   00410113 0040e073 00300b13 00300a13 00100a93 01600433 00441413 014469b3 01300533 02200893 00000073
  //   fe0416e3 415a0a33 fe0a10e3 40000313 01000e13 08400493 00849493 08348493 00400913 00891913 00490913
  //   00849493 08248493 00849493 08148493 00891913 00490913 00891913 00490913 00932023 012484b3 00430313
  //   fffe0e13 fe0e18e3 02000e13 40000313 00031483 00900533 02200893 00000073 00230313 fffe0e13 fe0e14e3
  //   0040f073 ffc10113 00012903 ffc10113 00012483 ffc10113 00012e03 ffc10113 00012303 ffc10113 00012283
  //   ffc10113 00012b03 ffc10113 00012a83 ffc10113 00012a03 ffc10113 00012983 ffc10113 00012403 ffc10113
  //   00012503 ffc10113 00012883 00200073
  //   下一条 PC：顺序 / 条件分支 / JAL / JALR（清 bit0）
  //   JAL
  //   JALR
  //   URET
  //   Beq
  //   Bne
  //   MemToReg
  //   MemWrite
  //   AluOP
  //   AluSrcB
  //   RegWrite
  //   多级中断：关中断保护现场，开中断后仅响应更高优先级；返回自动开中断
  //   EPC 硬件堆栈：压栈保存真实下一PC及上一层优先级；弹栈恢复；最多三层
  //   EPC栈第1层
  //   EPC栈第2层
  //   EPC栈第3层
  //   返回1清除脉冲
  //   返回2清除脉冲
  //   返回3清除脉冲
  //   数据存储器
  //   为方便自动评测，需要输出PC，IR，寄存器堆写如数据RDin
  //   RAM写使能MemWrite、RAM写入数据MDin等信号
  //   读寄存器 / ALU 输入 / 写回选择
  //   LH：根据地址 bit1 选择半字，16 → 32 位符号扩展
  //   控制位
  //   暂停节拍，不能为0
  //   ECALL：a7=34 锁存 a0；其他调用暂停，Go 继续
  //   戳工具置1进入计数暂停模式，ctrl+k时钟自动运行到对应节拍暂停
  //   ctrl+k关闭时钟连续运行，将控制位置零，进入单步调试模式调试
  //   用这个时钟源需要去掉电路中的其他时钟源
  //   IR1等待
  //   IR2等待
  //   IR3等待
  //   优先级栈第1层
  //   优先级栈第2层
  //   优先级栈第3层
  //   中断状态：IE / 当前服务号 / EPC / 同拍响应
  //   可计数暂停的时钟源
  //   控制优先级：复位 > 暂停保持 > 返回 / 关中断 > 中断响应 > 普通执行
  //   EPC 保留完整32位地址；仅ROM取址映射；返回不响应新中断，不增加隐指令周期
  //   当前服务优先级
  //   硬件栈深度 0..3
  //   中断禁止位：复位0 / 入口1 / 软件开关
endmodule

// 单周期硬布线控制器
module \单周期硬布线控制器  (
  input  [4:0] OP,
  input  [4:0] Funct,
  input  in_3,
  output [3:0] ALU_OP,
  output uret,
  output MemToReg,
  output ecall,
  output MemWrite,
  output ALU_SRC,
  output RegWrite,
  output S_type,
  output Beq,
  output Bne,
  output Jalr,
  output JAL
);

  wire \控制信号自动生成_1_ecall ;

  \运算控制器自动生成  \u_运算控制器自动生成_1  (
    .OP2(OP[0]), .OP3(OP[1]), .OP4(OP[2]), .OP5(OP[3]), .OP6(OP[4]), .F12(Funct[0]), .F13(Funct[1]),
    .F14(Funct[2]), .F25(Funct[3]), .F30(Funct[4]), .S0(ALU_OP[0]), .S1(ALU_OP[1]), .S2(ALU_OP[2]),
    .S3(ALU_OP[3]));
  \控制信号自动生成  \u_控制信号自动生成_1  (
    .OP2(OP[0]), .MemToReg(MemToReg), .OP3(OP[1]), .MemWrite(MemWrite), .OP4(OP[2]), .ALU_SRC(ALU_SRC),
    .OP5(OP[3]), .RegWrite(RegWrite), .OP6(OP[4]), .ecall(\控制信号自动生成_1_ecall ), .F12(Funct[0]),
    .S_Type(S_type), .F13(Funct[1]), .BEQ(Beq), .F14(Funct[2]), .BNE(Bne), .F25(Funct[3]), .JALR(Jalr),
    .F30(Funct[4]), .JAL(JAL));
  and and_1 (uret, in_3, \控制信号自动生成_1_ecall );
  and and_2 (ecall, ~in_3, \控制信号自动生成_1_ecall );  // AND_Gate

  // Other names for the same wires on the sheet: IR21 = in_3; OP_CODE[4:0] = OP

  // Notes on the sheet:
  //   运算器控制器，根据指令生成运算器功能选择信号
  //   控制信号生成，产生数据通路需要的其他控制信号
endmodule

// 运算器控制器
module \运算控制器自动生成  (
  input  OP2,
  input  OP3,
  input  OP4,
  input  OP5,
  input  OP6,
  input  F12,
  input  F13,
  input  F14,
  input  F25,
  input  F30,
  output S0,
  output S1,
  output S2,
  output S3
);

  wire _ADD_0, _ADD_ALL_0, _ADD_ALL_1, _ADD_ALL_2, _S0_0, _S0_1, _S0_2, _S0_3, _S1_0, _S1_1, _S1_2, _S2_0,
       _S2_1, _S3_0, _S3_1, _S3_2, _SRA_0, _SRL_0, _SUB_0, ADD, ADD_ALL, AND, BR, F0, F1, F2, F3, F4, F5, F6,
       F7, I, J, JR, LD, N30, NSUB, OR, R, RI, SLT, SLTU, SRA, SRL, ST, SUB, SUBBIT, SYS, U, XOR;

  Comparator #(.width(5), .mode("unsigned")) comparator_1 (
    .a({OP6, OP5, OP4, OP3, OP2}), .b(5'b01100), .eq(R));  // open: gt, lt
  Comparator #(.width(5), .mode("unsigned")) comparator_2 (
    .a({OP6, OP5, OP4, OP3, OP2}), .b(5'b00100), .eq(I));  // open: gt, lt
  Comparator #(.width(5), .mode("unsigned")) comparator_3 (
    .a({OP6, OP5, OP4, OP3, OP2}), .b({5{1'b0}}), .eq(LD));  // open: gt, lt
  Comparator #(.width(5), .mode("unsigned")) comparator_4 (
    .a({OP6, OP5, OP4, OP3, OP2}), .b(5'b01000), .eq(ST));  // open: gt, lt
  Comparator #(.width(5), .mode("unsigned")) comparator_5 (
    .a({OP6, OP5, OP4, OP3, OP2}), .b(5'b11000), .eq(BR));  // open: gt, lt
  Comparator #(.width(5), .mode("unsigned")) comparator_6 (
    .a({OP6, OP5, OP4, OP3, OP2}), .b(5'b11001), .eq(JR));  // open: gt, lt
  Comparator #(.width(5), .mode("unsigned")) comparator_7 (
    .a({OP6, OP5, OP4, OP3, OP2}), .b(5'b11011), .eq(J));  // open: gt, lt
  Comparator #(.width(5), .mode("unsigned")) comparator_8 (
    .a({OP6, OP5, OP4, OP3, OP2}), .b(5'b01101), .eq(U));  // open: gt, lt
  Comparator #(.width(5), .mode("unsigned")) comparator_9 (
    .a({OP6, OP5, OP4, OP3, OP2}), .b(5'b11100), .eq(SYS));  // open: gt, lt
  Comparator #(.width(3), .mode("unsigned")) comparator_10 (.a({F14, F13, F12}), .b(3'b000), .eq(F0));  // open: gt, lt
  Comparator #(.width(3), .mode("unsigned")) comparator_11 (.a({F14, F13, F12}), .b(3'b001), .eq(F1));  // open: gt, lt
  Comparator #(.width(3), .mode("unsigned")) comparator_12 (.a({F14, F13, F12}), .b(3'b010), .eq(F2));  // open: gt, lt
  Comparator #(.width(3), .mode("unsigned")) comparator_13 (.a({F14, F13, F12}), .b(3'b011), .eq(F3));  // open: gt, lt
  Comparator #(.width(3), .mode("unsigned")) comparator_14 (.a({F14, F13, F12}), .b(3'b100), .eq(F4));  // open: gt, lt
  Comparator #(.width(3), .mode("unsigned")) comparator_15 (.a({F14, F13, F12}), .b(3'b101), .eq(F5));  // open: gt, lt
  Comparator #(.width(3), .mode("unsigned")) comparator_16 (.a({F14, F13, F12}), .b(3'b110), .eq(F6));  // open: gt, lt
  Comparator #(.width(3), .mode("unsigned")) comparator_17 (.a({F14, F13, F12}), .b(3'b111), .eq(F7));  // open: gt, lt
  not not_1 (N30, F30);
  not not_2 (NSUB, SUBBIT);
  or or_1 (RI, R, I);
  and and_1 (SUBBIT, R, F30);
  and and_2 (_ADD_0, RI, F0);
  and and_3 (ADD, _ADD_0, NSUB);
  and and_4 (_SUB_0, R, F0);
  and and_5 (SUB, _SUB_0, F30);
  and and_6 (SLT, RI, F2);
  and and_7 (SLTU, RI, F3);
  and and_8 (XOR, RI, F4);
  and and_9 (OR, RI, F6);
  and and_10 (AND, RI, F7);
  and and_11 (_SRA_0, RI, F5);
  and and_12 (SRA, _SRA_0, F30);
  and and_13 (_SRL_0, RI, F5);
  and and_14 (SRL, _SRL_0, N30);
  or or_2 (_ADD_ALL_0, ADD, LD);
  or or_3 (_ADD_ALL_1, _ADD_ALL_0, ST);
  or or_4 (_ADD_ALL_2, _ADD_ALL_1, JR);
  or or_5 (ADD_ALL, _ADD_ALL_2, U);
  or or_6 (_S0_0, ADD_ALL, AND);
  or or_7 (_S0_1, _S0_0, XOR);
  or or_8 (_S0_2, _S0_1, SLT);
  or or_9 (_S0_3, _S0_2, SRA);
  or or_10 (S0, _S0_3, BR);
  or or_11 (_S1_0, SUB, AND);
  or or_12 (_S1_1, _S1_0, SLT);
  or or_13 (_S1_2, _S1_1, SRL);
  or or_14 (S1, _S1_2, BR);
  or or_15 (_S2_0, ADD_ALL, SUB);
  or or_16 (_S2_1, _S2_0, AND);
  or or_17 (S2, _S2_1, SLTU);
  or or_18 (_S3_0, OR, XOR);
  or or_19 (_S3_1, _S3_0, SLT);
  or or_20 (_S3_2, _S3_1, SLTU);
  or or_21 (S3, _S3_2, BR);

  // Other names for the same wires on the sheet: FUN3[2:0] = {F14, F13, F12}; OP[4:0] = {OP6, OP5, OP4, OP3, OP2}

  // Notes on the sheet:
  //   ALU 编码：0 SLL / 1 SRA / 2 SRL / 5 ADD / 6 SUB / 7 AND / 8 OR / 9 XOR / 11 SLT / 12 SLTU
endmodule

// 控制信号生成
module \控制信号自动生成  (
  input  OP2,
  input  OP3,
  input  OP4,
  input  OP5,
  input  OP6,
  input  F12,
  input  F13,
  input  F14,
  input  F25,
  input  F30,
  output MemToReg,
  output MemWrite,
  output ALU_SRC,
  output RegWrite,
  output ecall,
  output S_Type,
  output BEQ,
  output BNE,
  output JALR,
  output JAL
);

  wire _ALU_SRC_0, _ALU_SRC_1, _ALU_SRC_2, _RegWrite_0, _RegWrite_1, _RegWrite_2, _RegWrite_3, BR, F0, F1,
       F2, F3, F4, F5, F6, F7, I, J, JR, LD, R, ST, SYS, U;

  Comparator #(.width(5), .mode("unsigned")) comparator_1 (
    .a({OP6, OP5, OP4, OP3, OP2}), .b(5'b01100), .eq(R));  // open: gt, lt
  Comparator #(.width(5), .mode("unsigned")) comparator_2 (
    .a({OP6, OP5, OP4, OP3, OP2}), .b(5'b00100), .eq(I));  // open: gt, lt
  Comparator #(.width(5), .mode("unsigned")) comparator_3 (
    .a({OP6, OP5, OP4, OP3, OP2}), .b({5{1'b0}}), .eq(LD));  // open: gt, lt
  Comparator #(.width(5), .mode("unsigned")) comparator_4 (
    .a({OP6, OP5, OP4, OP3, OP2}), .b(5'b01000), .eq(ST));  // open: gt, lt
  Comparator #(.width(5), .mode("unsigned")) comparator_5 (
    .a({OP6, OP5, OP4, OP3, OP2}), .b(5'b11000), .eq(BR));  // open: gt, lt
  Comparator #(.width(5), .mode("unsigned")) comparator_6 (
    .a({OP6, OP5, OP4, OP3, OP2}), .b(5'b11001), .eq(JR));  // open: gt, lt
  Comparator #(.width(5), .mode("unsigned")) comparator_7 (
    .a({OP6, OP5, OP4, OP3, OP2}), .b(5'b11011), .eq(J));  // open: gt, lt
  Comparator #(.width(5), .mode("unsigned")) comparator_8 (
    .a({OP6, OP5, OP4, OP3, OP2}), .b(5'b01101), .eq(U));  // open: gt, lt
  Comparator #(.width(5), .mode("unsigned")) comparator_9 (
    .a({OP6, OP5, OP4, OP3, OP2}), .b(5'b11100), .eq(SYS));  // open: gt, lt
  Comparator #(.width(3), .mode("unsigned")) comparator_10 (.a({F14, F13, F12}), .b(3'b000), .eq(F0));  // open: gt, lt
  Comparator #(.width(3), .mode("unsigned")) comparator_11 (.a({F14, F13, F12}), .b(3'b001), .eq(F1));  // open: gt, lt
  Comparator #(.width(3), .mode("unsigned")) comparator_12 (.a({F14, F13, F12}), .b(3'b010), .eq(F2));  // open: gt, lt
  Comparator #(.width(3), .mode("unsigned")) comparator_13 (.a({F14, F13, F12}), .b(3'b011), .eq(F3));  // open: gt, lt
  Comparator #(.width(3), .mode("unsigned")) comparator_14 (.a({F14, F13, F12}), .b(3'b100), .eq(F4));  // open: gt, lt
  Comparator #(.width(3), .mode("unsigned")) comparator_15 (.a({F14, F13, F12}), .b(3'b101), .eq(F5));  // open: gt, lt
  Comparator #(.width(3), .mode("unsigned")) comparator_16 (.a({F14, F13, F12}), .b(3'b110), .eq(F6));  // open: gt, lt
  Comparator #(.width(3), .mode("unsigned")) comparator_17 (.a({F14, F13, F12}), .b(3'b111), .eq(F7));  // open: gt, lt
  or or_1 (MemToReg, LD, LD);
  or or_2 (MemWrite, ST, ST);
  or or_3 (S_Type, ST, ST);
  or or_4 (_ALU_SRC_0, I, LD);
  or or_5 (_ALU_SRC_1, _ALU_SRC_0, ST);
  or or_6 (_ALU_SRC_2, _ALU_SRC_1, U);
  or or_7 (ALU_SRC, _ALU_SRC_2, JR);
  or or_8 (_RegWrite_0, R, I);
  or or_9 (_RegWrite_1, _RegWrite_0, LD);
  or or_10 (_RegWrite_2, _RegWrite_1, U);
  or or_11 (_RegWrite_3, _RegWrite_2, J);
  or or_12 (RegWrite, _RegWrite_3, JR);
  or or_13 (ecall, SYS, SYS);
  or or_14 (JALR, JR, JR);
  or or_15 (JAL, J, J);
  and and_1 (BEQ, BR, F0);
  and and_2 (BNE, BR, F1);

  // Other names for the same wires on the sheet: FUN3[2:0] = {F14, F13, F12}; OP[4:0] = {OP6, OP5, OP4, OP3, OP2}

  // Notes on the sheet:
  //   基本控制信号；BGE 与 LH / LUI 扩展选择在主电路
endmodule

// ALU
module ALU (
  input  [31:0] X,
  input  [31:0] Y,
  input  [3:0] AluOP,
  output out_4,
  output Equal,
  output out_6,
  output [31:0] Result,
  output [31:0] Result_2
);

  wire [0:0] comparator_1_lt, comparator_2_lt;
  wire [31:0] adder_1_out, AND_out, divider_1_out, divider_1_rem, multiplier_1_cout, multiplier_1_out,
       NOR_out, OR_out, shifter_1_out, shifter_2_out, shifter_3_out, subtractor_1_out, XOR_out;

  assign AND_out = X & Y;  // AND_Gate AND, 32 bits wide
  assign OR_out = X | Y;  // OR_Gate OR, 32 bits wide
  Shifter #(.width(32)) shifter_1 (.in(X), .\dist (Y[4:0]), .out(shifter_1_out));
  Shifter #(.width(32), .shift("ar")) shifter_2 (.in(X), .\dist (Y[4:0]), .out(shifter_2_out));
  Shifter #(.width(32), .shift("lr")) shifter_3 (.in(X), .\dist (Y[4:0]), .out(shifter_3_out));
  Multiplier #(.width(32)) multiplier_1 (.a(X), .b(Y), .out(multiplier_1_out), .cout(multiplier_1_cout));  // open: cin
  Divider #(.width(32)) divider_1 (.a(X), .b(Y), .out(divider_1_out), .rem(divider_1_rem));  // open: upper
  Adder #(.width(32)) adder_1 (.a(X), .b(Y), .out(adder_1_out));  // open: cin, cout
  Subtractor #(.width(32)) subtractor_1 (.a(X), .b(Y), .out(subtractor_1_out));  // open: bin, bout
  assign XOR_out = X ^ Y;  // XOR_Gate XOR, 32 bits wide
  assign NOR_out = ~(X | Y);  // NOR_Gate NOR, 32 bits wide
  Comparator #(.width(32)) comparator_1 (.a(X), .b(Y), .eq(Equal), .lt(comparator_1_lt[0]));  // open: gt
  Comparator #(.width(32), .mode("unsigned")) comparator_2 (.a(X), .b(Y), .lt(comparator_2_lt[0]));  // open: gt, eq
  Multiplexer #(.select(4), .width(32), .enable("false")) multiplexer_1 (
    .in0(shifter_1_out), .in1(shifter_2_out), .in2(shifter_3_out), .in3(multiplier_1_out),
    .in4(divider_1_out), .in5(adder_1_out), .in6(subtractor_1_out), .in7(AND_out), .in8(OR_out),
    .in9(XOR_out), .in10(NOR_out), .in11({{31{1'b0}}, comparator_1_lt[0]}),
    .in12({{31{1'b0}}, comparator_2_lt[0]}), .in13({32{1'b0}}), .in14({32{1'b0}}), .in15({32{1'b0}}),
    .out(Result), .sel(AluOP));
  Multiplexer #(.select(4), .width(32), .enable("false")) multiplexer_2 (
    .in0({32{1'b0}}), .in1({32{1'b0}}), .in2({32{1'b0}}), .in3(multiplier_1_cout), .in4(divider_1_rem),
    .in5({32{1'b0}}), .in6({32{1'b0}}), .in7({32{1'b0}}), .in8({32{1'b0}}), .in9({32{1'b0}}),
    .in10({32{1'b0}}), .in11({32{1'b0}}), .in12({32{1'b0}}), .in13({32{1'b0}}), .in14({32{1'b0}}),
    .in15({32{1'b0}}), .out(Result_2), .sel(AluOP));
  Multiplexer #(.select(4), .enable("false")) multiplexer_3 (
    .in0(1'b0), .in1(1'b0), .in2(1'b0), .in3(1'b0), .in4(1'b0), .in5(1'b0), .in6(1'b0), .in7(1'b0),
    .in8(1'b0), .in9(1'b0), .in10(1'b0), .in11(comparator_1_lt[0]), .in12(comparator_2_lt[0]), .in13(1'b0),
    .in14(1'b0), .in15(1'b0), .out(out_6), .sel(AluOP));
  not not_1 (out_4, out_6);

  // Other names for the same wires on the sheet: Result2[31:0] = Result_2; S[3:0] = AluOP; tunnel = out_6;
  //   tunnel_t = out_4

  // Notes on the sheet:
  //   不要改变此引脚区域内容，也不要改变ALU封装形式
  //   输入引脚
  //   输出引脚
endmodule

module Regifile (
  input  [31:0] Din,
  input  Clk,
  input  WE,
  input  [4:0] R1_num,
  input  [4:0] W_num,
  input  [4:0] R2_num,
  output [31:0] R1,
  output [31:0] R2
);

  // register_file register_file_1: pin names not known; wires that end beside it: Din, Clk, WE, W_num, R1_num, R2_num, R1, R2
endmodule
