// Logisim project pipeline-interrupt.circ as structural Verilog: 10 circuits, main circuit ◇流水多级中断
module \流水多级中断  (
  output RegWrite,
  output MemWrite,
  output [31:0] IF_PC,
  output [31:0] ID_PC,
  output [31:0] EX_PC,
  output [31:0] M_PC,
  output [31:0] WB_PC,
  output [31:0] RDin,
  output [31:0] MDin,
  output [31:0] LedData
);

  wire CLK, clock_1_out, comparator_6_eq, comparator_6_lt, Count_Branch, Count_Branch_BeforeIRQ,
       Count_Branch_BeforeStopFix, Count_BranchSuccess, Count_BranchSuccess_BeforeIRQ,
       Count_BranchSuccess_BeforeStopFix, Count_Data, Count_Data_0, Count_Data_1, Count_Data_BeforeIRQ,
       Count_Data_BeforeStopFix, Count_Jump, Count_Jump_BeforeIRQ, Count_Jump_BeforeStopFix, Count_LoadUse,
       Count_LoadUse_0, Count_LoadUse_1, Count_LoadUse_BeforeIRQ, Count_LoadUse_BeforeStopFix,
       Count_Redirect, Count_Redirect_BeforeIRQ, Count_Redirect_BeforeStopFix, Count_System, Count_System_0,
       d_ff_1_q, ECALL, EX_ALUSRC, EX_BEQ, EX_BGE, EX_BNE, EX_Branch, EX_Branch_0, EX_EQ, EX_GE, EX_Hazard,
       EX_Hazard1, EX_Hazard1_0, EX_Hazard2, EX_Hazard2_0, EX_Jump, EX_Match1, EX_Match2, EX_MemToReg,
       EX_MemWrite, EX_NE, EX_NotTake, EX_Producer, EX_RDNonzero, EX_RDZero, EX_RegWrite, EX_Take, EX_Take0,
       EX_TakeBR, EX_TakeEQ, EX_TakeGE, EX_TakeNE, FWD_MEM1, FWD_MEM2, FWD_MEMMatch1, FWD_MEMMatch2, FWD_WB1,
       FWD_WB2, FWD_WBMatch1, FWD_WBMatch2, Go, Go_NoRise, Go_NotPrevious, Go_Previous, Go_Rise, halt,
       ID_AllRAW, ID_ALUSRC, ID_BEQ, ID_BGE, ID_BImm_p2, ID_BImm_p3, ID_BNE, ID_BR, ID_DataStall,
       ID_DataStall_0, ID_FGE, ID_Flush, ID_Flush_0, ID_Flush_1, ID_Flush_BeforeIRQ, ID_Flush_BeforeStopFix,
       ID_IsBranch, ID_IsI, ID_IsJR, ID_IsLoad, ID_IsR, ID_IsStore, ID_MemToReg, ID_MemWrite, ID_MemWriteRaw,
       ID_Ready, ID_RegWrite, ID_ST, ID_SystemOpcode, ID_URET, ID_Use1, ID_Use1Raw, ID_Use1Raw_0,
       ID_Use1Raw_1, ID_Use1Raw_2, ID_Use1Raw_3, ID_Use1Raw_4, ID_Use2, ID_Use2Raw, ID_Use2Raw_0,
       ID_Use2Raw_1, ID_Valid, ID_WriteRaw, IF_Advance, IF_Enable, IF_Enable_BeforeIRQ,
       IF_Enable_BeforeStopFix, IF_Flush, IF_Flush_BeforeIRQ, IF_Flush_BeforeStopFix, IF_Flush_Part0,
       IF_Hold, IF_Hold_BeforeIRQ, IF_Hold_BeforeStopFix, IF_Kill, IF_NotKill, IF_Stall, IF_Stall_0, IF_Wait,
       IF_Want, IR1, IR2, IR3, IRQ_Accept, IRQ_Accept_0, IRQ_Accept_1, IRQ_Accept_2, IRQ_Accept_3, IRQ_Ack1,
       IRQ_Ack2, IRQ_Ack3, IRQ_AckPulse1, IRQ_AckPulse2, IRQ_AckPulse3, IRQ_Active0, IRQ_Active1,
       IRQ_Active2, IRQ_Active3, IRQ_Any, IRQ_Any_0, IRQ_Below2, IRQ_Below3, IRQ_Capture1, IRQ_Capture2,
       IRQ_Capture3, IRQ_Clear1, IRQ_Clear2, IRQ_Clear3, IRQ_Close, IRQ_Disabled, IRQ_DisabledNext,
       IRQ_DisabledOr, IRQ_DisabledOr_0, IRQ_Drain, IRQ_DrainCycle, IRQ_Eligible1, IRQ_Eligible2,
       IRQ_Eligible3, IRQ_Empty, IRQ_EmptyEX, IRQ_EmptyID, IRQ_EmptyMEM, IRQ_EmptyWB, IRQ_EnableNow,
       IRQ_FlowFlush, IRQ_Full, IRQ_IE, IRQ_InISR, IRQ_NoFlowFlush, IRQ_NoReturn, IRQ_NormalPCEnable,
       IRQ_NotAccept, IRQ_NotAck1, IRQ_NotAck2, IRQ_NotAck3, IRQ_NotClose, IRQ_NotDrain, IRQ_NotEnable,
       IRQ_NotReturn, IRQ_Open, IRQ_PCAllowed, IRQ_Pending1, IRQ_Pending2, IRQ_Pending3, IRQ_PendingNext1,
       IRQ_PendingNext2, IRQ_PendingNext3, IRQ_PipelineEmpty, IRQ_PipelineEmpty_Part0,
       IRQ_PipelineEmpty_Part1, IRQ_Return, IRQ_ReturnDecoded, IRQ_Space, IRQ_StackEN, IRQ_Uret, LED_WE,
       MEM_Forwardable, MEM_HalfSel, MEM_Hazard, MEM_Hazard1, MEM_Hazard1_0, MEM_Hazard2, MEM_Hazard2_0,
       MEM_Match1, MEM_Match2, MEM_MemToReg, MEM_NotLoad, MEM_Producer, MEM_RDNonzero, MEM_RDZero,
       MEM_RegWrite, MEM_WriteLive, MemWrite_BeforeIRQ, MemWrite_BeforeStopFix, nand_1_out, NotGo,
       PAUSE_HOLD, Pause_Keep, PAUSE_NEXT, PAUSE_NEXT_BeforeIRQ, RST, RUN, SYS_Busy, SYS_Busy_0,
       SYS_Busy_BeforeStopFix, SYS_Issue, SYS_Issue_0, SYS_Issue_1, SYS_Issue_2, SYS_Issue_BeforeStopFix,
       SYS_Ready, W1, W2, W3, WB_HaltEvent, WB_Hazard, WB_Hazard1, WB_Hazard1_0, WB_Hazard2, WB_Hazard2_0,
       WB_Match1, WB_Match2, WB_MemToReg, WB_NoStop, WB_NotPrint, WB_Print, WB_PrintRaw, WB_Producer,
       WB_RDNonzero, WB_RDZero, WB_StopFlush, WB_StopFlush_BeforeIRQ, WB_Wait, WB_WriteLive;
  wire [1:0] IRQ_Active, IRQ_ActiveNext, IRQ_Delta, IRQ_Depth, IRQ_DepthNext, IRQ_Prev1, IRQ_Prev2,
       IRQ_Prev3, IRQ_PrevNext1, IRQ_PrevNext2, IRQ_PrevNext3, IRQ_Selected, IRQ_Selected12;
  wire [2:0] ID_F3;
  wire [3:0] EX_ALUOP, ID_ALUOP, ID_BImm_p0;
  wire [4:0] EX_RA1, EX_RA2, EX_RD, ID_I12, ID_RA1, ID_RA2, MEM_RD, WB_RD;
  wire [5:0] ID_BImm_p1;
  wire [7:2] ID_CtrlRaw;
  wire [9:0] ID_Ctrl, MEM_Ctrl, WB_Ctrl;
  wire [9:2] EX_Ctrl;
  wire [12:0] CNT_num;
  wire [15:0] COUNT_NEXT, \LoadUse次数 , \LoadUse次数_Next , MEM_Half, MEM_High16, MEM_Low16, \中断响应次数 ,
       \中断响应次数_Next , \中断排空周期 , \中断排空周期_Next , \中断返回次数 , \中断返回次数_Next , \分支气泡数 , \分支气泡数_Next , \总周期数 ,
       \插入气泡数 , \数据气泡数 , \数据气泡数_Next , \无条件分支数 , \无条件分支数_Next , \条件分支成功数 , \条件分支成功数_Next , \条件分支次数 ,
       \条件分支次数_Next , \系统等待周期 , \系统等待周期_Next ;
  wire [19:0] ID_IR;
  wire [23:0] DADDR;
  wire [31:0] EX_ALU, EX_B, EX_BImm, EX_BTarget, EX_Imm, EX_IR, EX_JImm, EX_JRTarget, EX_JTarget, EX_PC4,
       EX_R1, EX_R2, EX_Raw1, EX_Raw2, EX_Res0, EX_Result, EX_Target, EX_Target0, FWD_Older1, FWD_Older2,
       ID_BImm, ID_BImm_half, ID_Bypass1, ID_Bypass2, ID_IImm, ID_Imm, ID_ImmIS, ID_JImm, ID_JImm_half,
       ID_R1, ID_R2, ID_SImm, ID_UImm, IF_BufferedIR, IF_BufferedPC, IF_IR, IF_PC4, IRQ_ControllerNext,
       IRQ_EPC, IRQ_EPC2, IRQ_EPC3, IRQ_EPCNext1, IRQ_EPCNext2, IRQ_EPCNext3, IRQ_ReturnNext, IRQ_Vector,
       IRQ_Vector12, MEM_IR, MEM_Load, MEM_PC4, MEM_R1, MEM_Result, MEM_SignedHalf, NEXT_PC,
       NEXT_PC_BeforeIRQ, NEXT_PC_BeforeStopFix, WB_IR, WB_Load, WB_PC4, WB_R1, WB_R2, WB_Result;

  // Probe on \总周期数 
  Button \u_总复位  (.out(RST));
  Button _1 (.out(IR1));
  Button _2 (.out(IR2));
  Button _3 (.out(IR3));
  // Probe on \总周期数 
  Button \u_继续运行  (.out(Go));
  LED led_1 (.in(W1));
  LED led_2 (.in(W2));
  LED led_3 (.in(W3));
  // Probe on IF_PC[19:0]
  // riscv_probe riscv_probe_1: pin names not known; wires that end beside it: IF_IR
  Register #(.width(32)) PC (.D(NEXT_PC), .en(IF_Enable), .Q(IF_PC), .clk(CLK), .clr(RST), .cs(1'b0), .preset(1'b0));
  Hex_Digit_Display hex_digit_display_1 (.value(LedData[31:28]));  // open: dp
  Hex_Digit_Display hex_digit_display_2 (.value(LedData[27:24]));  // open: dp
  Hex_Digit_Display hex_digit_display_3 (.value(LedData[23:20]));  // open: dp
  // Probe on ID_PC[19:0]
  // riscv_probe riscv_probe_2: pin names not known; wires that end beside it: {ID_BImm_p3, ID_BImm_p1, ID_I12, ID_IR[19:15], ID_F3, ID_BImm_p0, ID_BImm_p2, ID_IR[6:0]}
  Comparator #(.width(2), .mode("unsigned")) comparator_1 (.a(ID_IR[1:0]), .b(2'b11), .eq(ID_Valid));  // open: gt, lt
  and and_1 (ID_RegWrite, ID_WriteRaw, ID_Valid);
  Hex_Digit_Display hex_digit_display_4 (.value(LedData[19:16]));  // open: dp
  Adder #(.width(32)) adder_1 (.a(IF_PC), .b(32'h4), .out(IF_PC4), .cin(1'b0));  // open: cout
  Multiplexer #(.width(32), .enable("false")) multiplexer_1 (
    .in0(IF_PC4), .in1(EX_Target), .out(NEXT_PC_BeforeStopFix), .sel(EX_Take));
  Multiplexer #(.width(32), .enable("false")) multiplexer_2 (
    .in0(IF_IR), .in1({32{1'b0}}), .out(IF_BufferedIR), .sel(IF_Flush));
  Multiplexer #(.width(32), .enable("false")) multiplexer_3 (
    .in0(IF_PC), .in1({32{1'b0}}), .out(IF_BufferedPC), .sel(IF_Flush));
  Hex_Digit_Display hex_digit_display_5 (.value(LedData[15:12]));  // open: dp
  Hex_Digit_Display hex_digit_display_6 (.value(LedData[11:8]));  // open: dp
  ROM #(.addrWidth(20), .dataWidth(32), .Select("high")) rom_1 (.addr(IF_PC[21:2]), .data(IF_IR), .sel(1'b1));
  Hex_Digit_Display hex_digit_display_7 (.value(LedData[7:4]));  // open: dp
  // Probe on EX_PC[19:0]
  // riscv_probe riscv_probe_3: pin names not known; wires that end beside it: EX_IR
  Hex_Digit_Display hex_digit_display_8 (.value(LedData[3:0]));  // open: dp
  IF_ID if_id_1 (
    .PredictJump(1'b0), .IR(IF_BufferedIR), .\气泡 (1'b0),
    .IR_2({ID_BImm_p3, ID_BImm_p1, ID_I12, ID_IR[19:15], ID_F3, ID_BImm_p0, ID_BImm_p2, ID_IR[6:0]}),
    .\EN_低电平有效 (IF_Hold), .CLK(CLK), .PC_2(ID_PC), .PC(IF_BufferedPC),
    .IR_3({ID_BImm_p3, ID_BImm_p1, ID_I12, ID_IR[19:15], ID_F3, ID_BImm_p0, ID_BImm_p2, ID_IR[6:0]}));  // open: PredictJump_2
  // riscv_probe riscv_probe_4: pin names not known; wires that end beside it: MEM_IR
  // Probe on \总周期数 
  // Probe on M_PC[19:0]
  // Probe on \总周期数 
  // Probe on \无条件分支数 
  // Probe on \条件分支成功数 
  // Probe on \插入气泡数 
  // Probe on \LoadUse次数 
  \单周期硬布线控制器  \u_单周期硬布线控制器_1  (
    .Funct({ID_BImm_p1[5], ID_BImm_p1[0], ID_F3}), .OP(ID_IR[6:2]), .ALU_OP(ID_ALUOP),
    .MemToReg(ID_MemToReg), .MemWrite(ID_MemWriteRaw), .ALU_SRC(ID_ALUSRC), .RegWrite(ID_WriteRaw),
    .ecall(ID_SystemOpcode), .S_type(ID_ST), .Jalr(ID_CtrlRaw[3]), .Beq(ID_BEQ), .JAL(ID_CtrlRaw[2]),
    .Bne(ID_BNE), .in_3(ID_I12[1]), .uret(ID_URET));
  // Probe on WB_PC[19:0]
  // riscv_probe riscv_probe_5: pin names not known; wires that end beside it: WB_IR
  // Probe on IF_PC[11:0]
  Regifile regifile_1 (
    .Din(RDin), .Clk(CLK), .R1(ID_R1), .R2(ID_R2), .WE(RegWrite), .W_num(WB_RD), .R1_num(ID_RA1),
    .R2_num(ID_RA2));
  assign ID_IImm = {{20{ID_BImm_p3}}, {ID_BImm_p3, ID_BImm_p1, ID_I12}};  // Bit_Extender bit_extender_1
  assign ID_SImm = {{20{ID_BImm_p3}}, {ID_BImm_p3, ID_BImm_p1, ID_BImm_p0, ID_BImm_p2}};  // Bit_Extender bit_extender_2
  Multiplexer #(.width(32), .enable("false")) multiplexer_4 (.in0(ID_IImm), .in1(ID_SImm), .out(ID_ImmIS), .sel(ID_ST));
  assign ID_UImm = {ID_BImm_p3, ID_BImm_p1, ID_I12, ID_IR[19:15], ID_F3, ID_BImm_p0, ID_BImm_p2, ID_IR[6:0]} & 32'hfffff000;  // AND_Gate and_2, 32 bits wide
  Multiplexer #(.width(32), .enable("false")) multiplexer_5 (
    .in0(ID_ImmIS), .in1(ID_UImm), .out(ID_Imm), .sel(ID_CtrlRaw[6]));
  Comparator #(.width(7), .mode("unsigned")) comparator_2 (
    .a(ID_IR[6:0]), .b(7'b0110111), .eq(ID_CtrlRaw[6]));  // open: gt, lt
  Comparator #(.width(3), .mode("unsigned")) comparator_3 (.a(ID_F3), .b(3'b001), .eq(ID_CtrlRaw[7]));  // open: gt, lt
  Comparator #(.width(7), .mode("unsigned")) comparator_4 (.a(ID_IR[6:0]), .b(7'b1100011), .eq(ID_BR));  // open: gt, lt
  Comparator #(.width(3), .mode("unsigned")) comparator_5 (.a(ID_F3), .b(3'b101), .eq(ID_FGE));  // open: gt, lt
  and and_3 (ID_BGE, ID_BR, ID_FGE);
  Multiplexer #(.width(5), .enable("false")) multiplexer_6 (
    .in0(ID_IR[19:15]), .in1(5'b10001), .out(ID_RA1), .sel(ID_CtrlRaw[4]));
  Multiplexer #(.width(5), .enable("false")) multiplexer_7 (
    .in0(ID_I12), .in1(5'b01010), .out(ID_RA2), .sel(ID_CtrlRaw[4]));
  Multiplexer #(.width(10), .enable("false")) multiplexer_8 (
    .in0({10{1'b0}}), .in1({2'b00, ID_CtrlRaw[7:6], ID_BGE, ID_CtrlRaw[4:2], ID_BNE, ID_BEQ}), .out(ID_Ctrl),
    .sel(ID_Valid));
  // Probe on ID_PC[11:0]
  assign ID_BImm_half = {{20{ID_BImm_p3}}, {ID_BImm_p3, ID_BImm_p2, ID_BImm_p1, ID_BImm_p0}};  // Bit_Extender bit_extender_3
  Shifter #(.width(32)) shifter_1 (.in(ID_BImm_half), .\dist (5'b00001), .out(ID_BImm));
  assign ID_JImm_half = {{12{ID_BImm_p3}}, {ID_BImm_p3, ID_IR[19:15], ID_F3, ID_I12[0], ID_BImm_p1, ID_I12[4:1]}};  // Bit_Extender bit_extender_4
  Shifter #(.width(32)) shifter_2 (.in(ID_JImm_half), .\dist (5'b00001), .out(ID_JImm));
  // Probe on EX_PC[11:0]
  D_Flip_Flop #(.Pre_Clr_Positions("LEGACY"), .NewFFLayout("false")) d_ff_1 (.Q(d_ff_1_q));  // open: clk, D, Qn, preset, reset
  // Probe on M_PC[11:0]
  // Probe on 13'hc
  // Probe on WB_PC[11:0]
  Clock clock_1 (.out(clock_1_out));
  ID_EX id_ex_1 (
    .PC(ID_PC), .RS1(ID_Bypass1), .RS2(ID_Bypass2),
    .IR({ID_BImm_p3, ID_BImm_p1, ID_I12, ID_IR[19:15], ID_F3, ID_BImm_p0, ID_BImm_p2, ID_IR[6:0]}),
    .WriteReg_num({ID_BImm_p0, ID_BImm_p2}), .ALUOP(ID_ALUOP), .\气泡 (ID_Flush), .PC_2(EX_PC),
    .RS1_2(EX_Raw1), .RS2_2(EX_Raw2), .IR_2(EX_IR), .RegWrite_2(EX_RegWrite), .MemToReg_2(EX_MemToReg),
    .MemWrite_2(EX_MemWrite), .ALuSrc_2(EX_ALUSRC), .WriteReg_num_2(EX_RD), .RegWrite(ID_RegWrite),
    .MemToReg(ID_MemToReg), .MemWrite(ID_MemWrite), .ALuSrc(ID_ALUSRC), .ALUOP_2(EX_ALUOP),
    .\EN_低电平有效 (halt), .CLK(CLK), .Reserved1_2(EX_BImm), .Reserved1(ID_BImm), .Imm32_2(EX_Imm),
    .Imm32(ID_Imm), .rs2Fwd(2'b00), .rs1Fwd(2'b00), .PredictJump(1'b0), .\指令译码信号 (ID_Ctrl),
    .\指令译码信号_2 ({EX_Ctrl[9:6], EX_BGE, EX_Ctrl[4:2], EX_BNE, EX_BEQ}), .Reserved2(ID_JImm),
    .Reserved2_2(EX_JImm));  // open: rs2Fwd_2, rs1Fwd_2, PredictJump_2
  Comparator #(.width(13)) comparator_6 (
    .a(CNT_num), .b(13'hc), .eq(comparator_6_eq), .lt(comparator_6_lt));  // open: gt
  nand nand_1 (nand_1_out, d_ff_1_q, comparator_6_eq);
  Counter #(.width(13), .max('h1fff), .ongoal("stay"), .behavior("old")) counter_1 (
    .count(comparator_6_lt), .Q(CNT_num), .clk(clock_1_out));  // open: load, D, carry, clr, preset
  assign CLK = nand_1_out ? clock_1_out : 1'bz;  // Controlled_Buffer controlled_buffer_1
  ALU alu_1 (
    .X(EX_R1), .Y(EX_B), .AluOP(EX_ALUOP), .Equal(EX_EQ), .Result(EX_ALU), .out_4(EX_GE));  // open: Result_2, out_6
  Pull_Resistor #(.pull(1)) pull_resistor_1 (.node(CLK));
  Multiplexer #(.width(32), .enable("false")) multiplexer_9 (.in0(EX_R2), .in1(EX_Imm), .out(EX_B), .sel(EX_ALUSRC));
  Multiplexer #(.width(32), .enable("false")) multiplexer_10 (
    .in0(EX_ALU), .in1(EX_Imm), .out(EX_Res0), .sel(EX_Ctrl[6]));
  Adder #(.width(32)) adder_2 (.a(EX_PC), .b(32'h4), .out(EX_PC4), .cin(1'b0));  // open: cout
  or or_1 (EX_Jump, EX_Ctrl[2], EX_Ctrl[3]);
  Multiplexer #(.width(32), .enable("false")) multiplexer_11 (
    .in0(EX_Res0), .in1(EX_PC4), .out(EX_Result), .sel(EX_Jump));
  Adder #(.width(32)) adder_3 (.a(EX_PC), .b(EX_BImm), .out(EX_BTarget), .cin(1'b0));  // open: cout
  Adder #(.width(32)) adder_4 (.a(EX_PC), .b(EX_JImm), .out(EX_JTarget), .cin(1'b0));  // open: cout
  assign EX_JRTarget = EX_ALU & 32'hfffffffe;  // AND_Gate and_4, 32 bits wide
  and and_5 (EX_TakeEQ, EX_BEQ, EX_EQ);
  not not_1 (EX_NE, EX_EQ);
  and and_6 (EX_TakeNE, EX_BNE, EX_NE);
  and and_7 (EX_TakeGE, EX_BGE, EX_GE);
  or or_2 (EX_Take0, EX_TakeEQ, EX_TakeNE);
  or or_3 (EX_TakeBR, EX_Take0, EX_TakeGE);
  or or_4 (EX_Take, EX_TakeBR, EX_Jump);
  Multiplexer #(.width(32), .enable("false")) multiplexer_12 (
    .in0(EX_BTarget), .in1(EX_JTarget), .out(EX_Target0), .sel(EX_Ctrl[2]));
  Multiplexer #(.width(32), .enable("false")) multiplexer_13 (
    .in0(EX_Target0), .in1(EX_JRTarget), .out(EX_Target), .sel(EX_Ctrl[3]));
  // Probe on IRQ_IE
  EX_MEM ex_mem_1 (
    .PC(EX_PC), .IR(EX_IR), .WriteReg_num(EX_RD), .\气泡 (WB_StopFlush), .PC_2(M_PC), .IR_2(MEM_IR),
    .RegWrite_2(MEM_RegWrite), .MemToReg_2(MEM_MemToReg), .MemWrite_2(MEM_WriteLive),
    .WriteReg_num_2(MEM_RD), .RegWrite(EX_RegWrite), .MemToReg(EX_MemToReg), .MemWrite(EX_MemWrite),
    .\EN_低电平有效 (halt), .CLK(CLK), .Reserved1_2(MEM_R1), .Reserved1(EX_R1),
    .\指令译码信号 ({EX_Ctrl[9:6], EX_BGE, EX_Ctrl[4:2], EX_BNE, EX_BEQ}), .\指令译码信号_2 (MEM_Ctrl),
    .Reserved2(EX_PC4), .Reserved2_2(MEM_PC4), .WriteData(EX_R2), .WriteData_2(MDin), .AluResult(EX_Result),
    .AluResult_2({MEM_Result[31:26], DADDR, MEM_HalfSel, MEM_Result[0]}));
  // Probe on \中断响应次数 
  // Probe on IRQ_Active
  RAM #(.addrWidth(24), .dataWidth(32), .bus("separate"), .Select("high"), .simpleMode("false")) ram_1 (
    .addr(DADDR), .din(MDin), .data({MEM_High16, MEM_Low16}), .str(MemWrite), .sel(1'b1), .clk(CLK),
    .clr(1'b0));  // open: ld
  Multiplexer #(.width(16), .enable("false")) multiplexer_14 (
    .in0(MEM_Low16), .in1(MEM_High16), .out(MEM_Half), .sel(MEM_HalfSel));
  assign MEM_SignedHalf = {{16{MEM_Half[15]}}, MEM_Half};  // Bit_Extender bit_extender_5
  Multiplexer #(.width(32), .enable("false")) multiplexer_15 (
    .in0({MEM_High16, MEM_Low16}), .in1(MEM_SignedHalf), .out(MEM_Load), .sel(MEM_Ctrl[7]));
  MEM_WB mem_wb_1 (
    .PC(M_PC), .IR(MEM_IR), .WriteReg_num(MEM_RD), .\气泡 (WB_StopFlush), .PC_2(WB_PC), .IR_2(WB_IR),
    .RegWrite_2(WB_WriteLive), .MemToReg_2(WB_MemToReg), .WriteReg_num_2(WB_RD), .RegWrite(MEM_RegWrite),
    .MemToReg(MEM_MemToReg), .\EN_低电平有效 (halt), .CLK(CLK), .Reserved1_2(WB_R1), .Reserved1(MEM_R1),
    .\指令译码信号 (MEM_Ctrl), .\指令译码信号_2 (WB_Ctrl), .Reserved2(MDin), .Reserved2_2(WB_R2), .MemData(MEM_Load),
    .MemData_2(WB_Load), .AluResult({MEM_Result[31:26], DADDR, MEM_HalfSel, MEM_Result[0]}),
    .AluResult_2(WB_Result));
  // Probe on \中断返回次数 
  // Probe on IRQ_Depth
  Multiplexer #(.width(32), .enable("false")) multiplexer_16 (
    .in0(WB_Result), .in1(WB_Load), .out(RDin), .sel(WB_MemToReg));
  Comparator #(.width(32), .mode("unsigned")) comparator_7 (.a(WB_R1), .b(32'h22), .eq(WB_Print));  // open: gt, lt
  and and_8 (WB_PrintRaw, WB_Ctrl[4], WB_Print);
  not not_2 (WB_NotPrint, WB_Print);
  and and_9 (WB_Wait, WB_Ctrl[4], WB_NotPrint);
  Register #(.width(32)) \ECALL显示锁存  (
    .D(WB_R2), .en(LED_WE), .Q(LedData), .clk(CLK), .clr(RST), .cs(1'b0), .preset(1'b0));
  Register #(.width(16)) \u_流水周期  (
    .D(COUNT_NEXT), .en(RUN), .Q(\总周期数 ), .clk(CLK), .clr(RST), .cs(1'b0), .preset(1'b0));
  Adder #(.width(16)) adder_5 (.a(\总周期数 ), .b(16'h1), .out(COUNT_NEXT), .cin(1'b0));  // open: cout
  Register #(.width(1)) \ECALL暂停状态  (
    .D(PAUSE_NEXT), .en(1'b1), .Q(halt), .clk(CLK), .clr(RST), .cs(1'b0), .preset(1'b0));
  // Probe on IRQ_EPC
  // Probe on \中断排空周期 
  // Probe on IRQ_Drain
  and and_10 (RegWrite, WB_WriteLive, RUN);
  and and_11 (MemWrite_BeforeStopFix, MEM_WriteLive, RUN);
  Comparator #(.width(7), .mode("unsigned")) comparator_8 (
    .a(ID_IR[6:0]), .b(7'b0110011), .eq(ID_IsR));  // open: gt, lt
  Comparator #(.width(7), .mode("unsigned")) comparator_9 (
    .a(ID_IR[6:0]), .b(7'b0010011), .eq(ID_IsI));  // open: gt, lt
  Comparator #(.width(7), .mode("unsigned")) comparator_10 (
    .a(ID_IR[6:0]), .b(7'b0000011), .eq(ID_IsLoad));  // open: gt, lt
  Comparator #(.width(7), .mode("unsigned")) comparator_11 (
    .a(ID_IR[6:0]), .b(7'b0100011), .eq(ID_IsStore));  // open: gt, lt
  Comparator #(.width(7), .mode("unsigned")) comparator_12 (
    .a(ID_IR[6:0]), .b(7'b1100011), .eq(ID_IsBranch));  // open: gt, lt
  Comparator #(.width(7), .mode("unsigned")) comparator_13 (
    .a(ID_IR[6:0]), .b(7'b1100111), .eq(ID_IsJR));  // open: gt, lt
  or or_5 (ID_Use1Raw_0, ID_IsR, ID_IsI);
  or or_6 (ID_Use1Raw_1, ID_Use1Raw_0, ID_IsLoad);
  or or_7 (ID_Use1Raw_2, ID_Use1Raw_1, ID_IsStore);
  or or_8 (ID_Use1Raw_3, ID_Use1Raw_2, ID_IsBranch);
  or or_9 (ID_Use1Raw_4, ID_Use1Raw_3, ID_IsJR);
  or or_10 (ID_Use1Raw, ID_Use1Raw_4, ID_CtrlRaw[4]);
  or or_11 (ID_Use2Raw_0, ID_IsR, ID_IsStore);
  or or_12 (ID_Use2Raw_1, ID_Use2Raw_0, ID_IsBranch);
  or or_13 (ID_Use2Raw, ID_Use2Raw_1, ID_CtrlRaw[4]);
  and and_12 (ID_Use1, ID_Valid, ID_Use1Raw);
  and and_13 (ID_Use2, ID_Valid, ID_Use2Raw);
  and and_14 (ID_MemWrite, ID_MemWriteRaw, ID_Valid);
  Comparator #(.width(5), .mode("unsigned")) comparator_14 (.a(EX_RD), .b({5{1'b0}}), .eq(EX_RDZero));  // open: gt, lt
  not not_3 (EX_RDNonzero, EX_RDZero);
  and and_15 (EX_Producer, EX_RegWrite, EX_RDNonzero);
  Comparator #(.width(5), .mode("unsigned")) comparator_15 (.a(ID_RA1), .b(EX_RD), .eq(EX_Match1));  // open: gt, lt
  Register #(.width(16)) \u_数据气泡数  (
    .D(\数据气泡数_Next ), .en(Count_Data), .Q(\数据气泡数 ), .clk(CLK), .clr(RST), .cs(1'b0), .preset(1'b0));
  Adder #(.width(16)) adder_6 (.a(\数据气泡数 ), .b(16'h1), .out(\数据气泡数_Next ), .cin(1'b0));  // open: cout
  Adder #(.width(16)) adder_7 (.a(\数据气泡数 ), .b(\分支气泡数 ), .out(\插入气泡数 ), .cin(1'b0));  // open: cout
  and and_16 (EX_Hazard1_0, EX_Match1, ID_Use1);
  and and_17 (EX_Hazard1, EX_Hazard1_0, EX_Producer);
  Comparator #(.width(5), .mode("unsigned")) comparator_16 (.a(ID_RA2), .b(EX_RD), .eq(EX_Match2));  // open: gt, lt
  and and_18 (EX_Hazard2_0, EX_Match2, ID_Use2);
  and and_19 (EX_Hazard2, EX_Hazard2_0, EX_Producer);
  or or_14 (EX_Hazard, EX_Hazard1, EX_Hazard2);
  Comparator #(.width(5), .mode("unsigned")) comparator_17 (
    .a(MEM_RD), .b({5{1'b0}}), .eq(MEM_RDZero));  // open: gt, lt
  not not_4 (MEM_RDNonzero, MEM_RDZero);
  and and_20 (MEM_Producer, MEM_RegWrite, MEM_RDNonzero);
  Comparator #(.width(5), .mode("unsigned")) comparator_18 (.a(ID_RA1), .b(MEM_RD), .eq(MEM_Match1));  // open: gt, lt
  and and_21 (MEM_Hazard1_0, MEM_Match1, ID_Use1);
  and and_22 (MEM_Hazard1, MEM_Hazard1_0, MEM_Producer);
  Comparator #(.width(5), .mode("unsigned")) comparator_19 (.a(ID_RA2), .b(MEM_RD), .eq(MEM_Match2));  // open: gt, lt
  and and_23 (MEM_Hazard2_0, MEM_Match2, ID_Use2);
  and and_24 (MEM_Hazard2, MEM_Hazard2_0, MEM_Producer);
  or or_15 (MEM_Hazard, MEM_Hazard1, MEM_Hazard2);
  Comparator #(.width(5), .mode("unsigned")) comparator_20 (.a(WB_RD), .b({5{1'b0}}), .eq(WB_RDZero));  // open: gt, lt
  not not_5 (WB_RDNonzero, WB_RDZero);
  and and_25 (WB_Producer, WB_WriteLive, WB_RDNonzero);
  Comparator #(.width(5), .mode("unsigned")) comparator_21 (.a(ID_RA1), .b(WB_RD), .eq(WB_Match1));  // open: gt, lt
  and and_26 (WB_Hazard1_0, WB_Match1, ID_Use1);
  and and_27 (WB_Hazard1, WB_Hazard1_0, WB_Producer);
  Comparator #(.width(5), .mode("unsigned")) comparator_22 (.a(ID_RA2), .b(WB_RD), .eq(WB_Match2));  // open: gt, lt
  and and_28 (WB_Hazard2_0, WB_Match2, ID_Use2);
  Register #(.width(16)) \u_分支气泡数  (
    .D(\分支气泡数_Next ), .en(Count_Redirect), .Q(\分支气泡数 ), .clk(CLK), .clr(RST), .cs(1'b0), .preset(1'b0));
  Adder #(.width(16)) adder_8 (.a(\分支气泡数 ), .b(16'h2), .out(\分支气泡数_Next ), .cin(1'b0));  // open: cout
  and and_29 (WB_Hazard2, WB_Hazard2_0, WB_Producer);
  or or_16 (WB_Hazard, WB_Hazard1, WB_Hazard2);
  or or_17 (ID_DataStall_0, EX_Hazard, MEM_Hazard);
  or or_18 (ID_AllRAW, ID_DataStall_0, WB_Hazard);
  and and_30 (ID_DataStall, EX_Hazard, EX_MemToReg);
  or or_19 (SYS_Busy_0, EX_Ctrl[4], MEM_Ctrl[4]);
  or or_20 (SYS_Busy_BeforeStopFix, SYS_Busy_0, WB_Ctrl[4]);
  not not_6 (ID_Ready, ID_DataStall);
  not not_7 (SYS_Ready, SYS_Busy);
  not not_8 (EX_NotTake, EX_Take);
  and and_31 (SYS_Issue_0, ID_CtrlRaw[4], ID_Valid);
  and and_32 (SYS_Issue_1, SYS_Issue_0, ID_Ready);
  and and_33 (SYS_Issue_2, SYS_Issue_1, SYS_Ready);
  and and_34 (SYS_Issue_BeforeStopFix, SYS_Issue_2, EX_NotTake);
  or or_21 (IF_Stall_0, ID_DataStall, SYS_Busy);
  or or_22 (IF_Stall, IF_Stall_0, SYS_Issue);
  not not_9 (IF_Advance, IF_Stall);
  or or_23 (IF_Want, IF_Advance, EX_Take);
  not not_10 (RUN, halt);
  and and_35 (IF_Enable_BeforeStopFix, IF_Want, RUN);
  or or_24 (IF_Kill, EX_Take, SYS_Issue);
  not not_11 (IF_NotKill, IF_Kill);
  and and_36 (IF_Wait, IF_Stall, IF_NotKill);
  or or_25 (IF_Hold_BeforeStopFix, IF_Wait, halt);
  Register #(.width(16)) \u_LoadUse次数  (
    .D(\LoadUse次数_Next ), .en(Count_LoadUse), .Q(\LoadUse次数 ), .clk(CLK), .clr(RST), .cs(1'b0), .preset(1'b0));
  Adder #(.width(16)) adder_9 (.a(\LoadUse次数 ), .b(16'h1), .out(\LoadUse次数_Next ), .cin(1'b0));  // open: cout
  or or_26 (IF_Flush_BeforeStopFix, RST, IF_Kill);
  or or_27 (ID_Flush_0, RST, EX_Take);
  or or_28 (ID_Flush_1, ID_Flush_0, ID_DataStall);
  or or_29 (ID_Flush_BeforeStopFix, ID_Flush_1, SYS_Busy);
  and and_37 (WB_HaltEvent, WB_Wait, RUN);
  or or_30 (PAUSE_HOLD, halt, WB_HaltEvent);
  not not_12 (NotGo, Go);
  and and_38 (PAUSE_NEXT_BeforeIRQ, PAUSE_HOLD, NotGo);
  and and_39 (LED_WE, WB_PrintRaw, RUN);
  and and_40 (Count_Data_0, ID_DataStall, EX_NotTake);
  and and_41 (Count_Data_1, Count_Data_0, SYS_Ready);
  and and_42 (Count_Data_BeforeStopFix, Count_Data_1, RUN);
  and and_43 (Count_LoadUse_0, ID_DataStall, EX_NotTake);
  and and_44 (Count_LoadUse_1, Count_LoadUse_0, SYS_Ready);
  and and_45 (Count_LoadUse_BeforeStopFix, Count_LoadUse_1, RUN);
  and and_46 (Count_Redirect_BeforeStopFix, EX_Take, RUN);
  and and_47 (Count_BranchSuccess_BeforeStopFix, EX_TakeBR, RUN);
  or or_31 (EX_Branch_0, EX_BEQ, EX_BNE);
  or or_32 (EX_Branch, EX_Branch_0, EX_BGE);
  and and_48 (Count_Branch_BeforeStopFix, EX_Branch, RUN);
  and and_49 (Count_Jump_BeforeStopFix, EX_Jump, RUN);
  and and_50 (Count_System_0, SYS_Busy, EX_NotTake);
  and and_51 (Count_System, Count_System_0, RUN);
  Register #(.width(16)) \u_条件分支次数  (
    .D(\条件分支次数_Next ), .en(Count_Branch), .Q(\条件分支次数 ), .clk(CLK), .clr(RST), .cs(1'b0), .preset(1'b0));
  Adder #(.width(16)) adder_10 (.a(\条件分支次数 ), .b(16'h1), .out(\条件分支次数_Next ), .cin(1'b0));  // open: cout
  Register #(.width(16)) \u_条件分支成功数  (
    .D(\条件分支成功数_Next ), .en(Count_BranchSuccess), .Q(\条件分支成功数 ), .clk(CLK), .clr(RST), .cs(1'b0),
    .preset(1'b0));
  Adder #(.width(16)) adder_11 (.a(\条件分支成功数 ), .b(16'h1), .out(\条件分支成功数_Next ), .cin(1'b0));  // open: cout
  Multiplexer #(.width(32), .select(1), .enable("false")) multiplexer_17 (
    .in0(ID_R1), .in1(RDin), .out(ID_Bypass1), .sel(WB_Hazard1));
  Multiplexer #(.width(32), .select(1), .enable("false")) multiplexer_18 (
    .in0(ID_R2), .in1(RDin), .out(ID_Bypass2), .sel(WB_Hazard2));
  not not_13 (MEM_NotLoad, MEM_MemToReg);
  and and_52 (MEM_Forwardable, MEM_Producer, MEM_NotLoad);
  Comparator #(.width(5), .mode("unsigned")) comparator_23 (
    .a(EX_RA1), .b(MEM_RD), .eq(FWD_MEMMatch1));  // open: gt, lt
  and and_53 (FWD_MEM1, FWD_MEMMatch1, MEM_Forwardable);
  Comparator #(.width(5), .mode("unsigned")) comparator_24 (.a(EX_RA1), .b(WB_RD), .eq(FWD_WBMatch1));  // open: gt, lt
  and and_54 (FWD_WB1, FWD_WBMatch1, WB_Producer);
  Comparator #(.width(5), .mode("unsigned")) comparator_25 (
    .a(EX_RA2), .b(MEM_RD), .eq(FWD_MEMMatch2));  // open: gt, lt
  and and_55 (FWD_MEM2, FWD_MEMMatch2, MEM_Forwardable);
  Comparator #(.width(5), .mode("unsigned")) comparator_26 (.a(EX_RA2), .b(WB_RD), .eq(FWD_WBMatch2));  // open: gt, lt
  and and_56 (FWD_WB2, FWD_WBMatch2, WB_Producer);
  Register #(.width(16)) \u_无条件分支数  (
    .D(\无条件分支数_Next ), .en(Count_Jump), .Q(\无条件分支数 ), .clk(CLK), .clr(RST), .cs(1'b0), .preset(1'b0));
  Adder #(.width(16)) adder_12 (.a(\无条件分支数 ), .b(16'h1), .out(\无条件分支数_Next ), .cin(1'b0));  // open: cout
  Multiplexer #(.width(5), .select(1), .enable("false")) multiplexer_19 (
    .in0(EX_IR[19:15]), .in1(5'b10001), .out(EX_RA1), .sel(EX_Ctrl[4]));
  Multiplexer #(.width(5), .select(1), .enable("false")) multiplexer_20 (
    .in0(EX_IR[24:20]), .in1(5'b01010), .out(EX_RA2), .sel(EX_Ctrl[4]));
  Register #(.width(16)) \u_系统等待周期  (
    .D(\系统等待周期_Next ), .en(Count_System), .Q(\系统等待周期 ), .clk(CLK), .clr(RST), .cs(1'b0), .preset(1'b0));
  Adder #(.width(16)) adder_13 (.a(\系统等待周期 ), .b(16'h1), .out(\系统等待周期_Next ), .cin(1'b0));  // open: cout
  Multiplexer #(.width(32), .select(1), .enable("false")) multiplexer_21 (
    .in0(EX_Raw1), .in1(RDin), .out(FWD_Older1), .sel(FWD_WB1));
  Multiplexer #(.width(32), .select(1), .enable("false")) multiplexer_22 (
    .in0(EX_Raw2), .in1(RDin), .out(FWD_Older2), .sel(FWD_WB2));
  Multiplexer #(.width(32), .select(1), .enable("false")) multiplexer_23 (
    .in0(FWD_Older1), .in1({MEM_Result[31:26], DADDR, MEM_HalfSel, MEM_Result[0]}), .out(EX_R1),
    .sel(FWD_MEM1));
  Multiplexer #(.width(32), .select(1), .enable("false")) multiplexer_24 (
    .in0(FWD_Older2), .in1({MEM_Result[31:26], DADDR, MEM_HalfSel, MEM_Result[0]}), .out(EX_R2),
    .sel(FWD_MEM2));
  or or_33 (SYS_Issue, 1'b0, 1'b0);
  or or_34 (SYS_Busy, 1'b0, 1'b0);
  not not_14 (WB_NoStop, WB_HaltEvent);
  and and_57 (MemWrite_BeforeIRQ, MemWrite_BeforeStopFix, WB_NoStop);
  Multiplexer #(.width(32), .select(1), .enable("false")) multiplexer_25 (
    .in0(NEXT_PC_BeforeStopFix), .in1(WB_PC4), .out(NEXT_PC_BeforeIRQ), .sel(WB_HaltEvent));
  or or_35 (IF_Enable_BeforeIRQ, IF_Enable_BeforeStopFix, WB_HaltEvent);
  or or_36 (IF_Flush_BeforeIRQ, IF_Flush_BeforeStopFix, WB_HaltEvent);
  or or_37 (ID_Flush_BeforeIRQ, ID_Flush_BeforeStopFix, WB_HaltEvent);
  and and_58 (IF_Hold_BeforeIRQ, IF_Hold_BeforeStopFix, WB_NoStop);
  or or_38 (WB_StopFlush_BeforeIRQ, RST, WB_HaltEvent);
  and and_59 (Count_Data_BeforeIRQ, Count_Data_BeforeStopFix, WB_NoStop);
  and and_60 (Count_LoadUse_BeforeIRQ, Count_LoadUse_BeforeStopFix, WB_NoStop);
  and and_61 (Count_Redirect_BeforeIRQ, Count_Redirect_BeforeStopFix, WB_NoStop);
  and and_62 (Count_BranchSuccess_BeforeIRQ, Count_BranchSuccess_BeforeStopFix, WB_NoStop);
  and and_63 (Count_Branch_BeforeIRQ, Count_Branch_BeforeStopFix, WB_NoStop);
  and and_64 (Count_Jump_BeforeIRQ, Count_Jump_BeforeStopFix, WB_NoStop);
  Adder #(.width(32)) adder_14 (.a(WB_PC), .b(32'h4), .out(WB_PC4), .cin(1'b0));  // open: cout
  Comparator #(.width(32), .mode("unsigned")) comparator_27 (
    .a({ID_BImm_p3, ID_BImm_p1, ID_I12, ID_IR[19:15], ID_F3, ID_BImm_p0, ID_BImm_p2, ID_IR[6:0]}),
    .b(32'h73), .eq(ID_CtrlRaw[4]));  // open: gt, lt
  Comparator #(.width(32), .mode("unsigned")) comparator_28 (
    .a({ID_BImm_p3, ID_BImm_p1, ID_I12, ID_IR[19:15], ID_F3, ID_BImm_p0, ID_BImm_p2, ID_IR[6:0]}),
    .b({32{1'b0}}), .eq(IRQ_EmptyID));  // open: gt, lt
  and and_65 (IRQ_PipelineEmpty_Part0, IRQ_EmptyID, IRQ_EmptyEX);
  or or_39 (IRQ_FlowFlush, IRQ_Accept, IRQ_Return);
  not not_15 (IRQ_NotDrain, IRQ_Drain);
  or or_40 (IF_Flush_Part0, IF_Flush_BeforeIRQ, IRQ_Drain);
  or or_41 (ID_Flush, ID_Flush_BeforeIRQ, IRQ_FlowFlush);
  and and_66 (MemWrite, MemWrite_BeforeIRQ, IRQ_NoReturn);
  and and_67 (Count_Data, Count_Data_BeforeIRQ, IRQ_NoReturn);
  and and_68 (Count_BranchSuccess, Count_BranchSuccess_BeforeIRQ, IRQ_NoReturn);
  Register #(.width(1), .trigger("rising"), .Select("low")) u_Go_Previous (
    .D(Go), .en(1'b1), .Q(Go_Previous), .clk(CLK), .clr(RST), .cs(1'b0), .preset(1'b0));
  not not_16 (Go_NoRise, Go_Rise);
  not not_17 (IRQ_NotAccept, IRQ_Accept);
  Register #(.width(16), .trigger("rising"), .Select("low")) \u_中断响应次数_2  (
    .D(\中断响应次数_Next ), .en(IRQ_Accept), .Q(\中断响应次数 ), .clk(CLK), .clr(RST), .cs(1'b0), .preset(1'b0));
  Adder #(.width(16)) adder_15 (.a(\中断响应次数 ), .b(16'h1), .out(\中断响应次数_Next ), .cin(1'b0));  // open: cout
  and and_69 (IRQ_PipelineEmpty_Part1, IRQ_PipelineEmpty_Part0, IRQ_EmptyMEM);
  or or_42 (IF_Flush, IF_Flush_Part0, IRQ_FlowFlush);
  and and_70 (IRQ_Return, IRQ_ReturnDecoded, RUN);
  Comparator #(.width(32), .mode("unsigned")) comparator_29 (
    .a(EX_IR), .b({32{1'b0}}), .eq(IRQ_EmptyEX));  // open: gt, lt
  and and_71 (IRQ_Accept, IRQ_Drain, IRQ_PipelineEmpty);
  not not_18 (IRQ_NoFlowFlush, IRQ_FlowFlush);
  or or_43 (IRQ_PCAllowed, IRQ_NotDrain, EX_Take);
  or or_44 (WB_StopFlush, WB_StopFlush_BeforeIRQ, IRQ_FlowFlush);
  not not_19 (Go_NotPrevious, Go_Previous);
  and and_72 (Pause_Keep, halt, Go_NoRise);
  and and_73 (IRQ_DrainCycle, IRQ_Drain, IRQ_NotAccept);
  Register #(.width(1)) register_1 (
    .D(1'b1), .en(1'b1), .Q(IRQ_Capture1), .clk(IR1), .clr(IRQ_Clear1), .cs(1'b0), .preset(1'b0));
  Comparator #(.width(2), .mode("unsigned")) comparator_30 (
    .a(IRQ_Active), .b(2'b01), .eq(IRQ_Active1));  // open: gt, lt
  Register #(.width(1)) register_2 (
    .D(1'b1), .en(1'b1), .Q(IRQ_Capture2), .clk(IR2), .clr(IRQ_Clear2), .cs(1'b0), .preset(1'b0));
  Comparator #(.width(2), .mode("unsigned")) comparator_31 (
    .a(IRQ_Active), .b(2'b10), .eq(IRQ_Active2));  // open: gt, lt
  Register #(.width(1)) register_3 (
    .D(1'b1), .en(1'b1), .Q(IRQ_Capture3), .clk(IR3), .clr(IRQ_Clear3), .cs(1'b0), .preset(1'b0));
  Comparator #(.width(2), .mode("unsigned")) comparator_32 (
    .a(IRQ_Active), .b(2'b11), .eq(IRQ_Active3));  // open: gt, lt
  and and_74 (Count_LoadUse, Count_LoadUse_BeforeIRQ, IRQ_NoReturn);
  and and_75 (Count_Branch, Count_Branch_BeforeIRQ, IRQ_NoReturn);
  Comparator #(.width(32), .mode("unsigned")) comparator_33 (.a(WB_IR), .b(32'h73), .eq(ECALL));  // open: gt, lt
  Comparator #(.width(32), .mode("unsigned")) comparator_34 (.a(WB_IR), .b(32'h200073), .eq(IRQ_Uret));  // open: gt, lt
  Comparator #(.width(32), .mode("unsigned")) comparator_35 (.a(WB_IR), .b(32'h40e073), .eq(IRQ_Open));  // open: gt, lt
  Comparator #(.width(32), .mode("unsigned")) comparator_36 (
    .a(WB_IR), .b(32'h40f073), .eq(IRQ_Close));  // open: gt, lt
  Multiplexer #(.width(32), .select(1), .enable("false")) multiplexer_26 (
    .in0(IRQ_EPC2), .in1(IF_PC), .out(IRQ_EPCNext1), .sel(IRQ_Accept));
  Multiplexer #(.width(32), .select(1), .enable("false")) multiplexer_27 (
    .in0(IRQ_EPC3), .in1(IRQ_EPC), .out(IRQ_EPCNext2), .sel(IRQ_Accept));
  Multiplexer #(.width(32), .select(1), .enable("false")) multiplexer_28 (
    .in0({32{1'b0}}), .in1(IRQ_EPC2), .out(IRQ_EPCNext3), .sel(IRQ_Accept));
  Register #(.width(16), .trigger("rising"), .Select("low")) \u_中断返回次数_2  (
    .D(\中断返回次数_Next ), .en(IRQ_Return), .Q(\中断返回次数 ), .clk(CLK), .clr(RST), .cs(1'b0), .preset(1'b0));
  Adder #(.width(16)) adder_16 (.a(\中断返回次数 ), .b(16'h1), .out(\中断返回次数_Next ), .cin(1'b0));  // open: cout
  and and_76 (IRQ_PipelineEmpty, IRQ_PipelineEmpty_Part1, IRQ_EmptyWB);
  Comparator #(.width(32), .mode("unsigned")) comparator_37 (
    .a(MEM_IR), .b({32{1'b0}}), .eq(IRQ_EmptyMEM));  // open: gt, lt
  and and_77 (IRQ_Ack1, IRQ_Active1, IRQ_Return);
  and and_78 (IRQ_Ack2, IRQ_Active2, IRQ_Return);
  and and_79 (IRQ_Ack3, IRQ_Active3, IRQ_Return);
  not not_20 (IRQ_NoReturn, IRQ_Return);
  and and_80 (IRQ_NormalPCEnable, IF_Enable_BeforeIRQ, IRQ_PCAllowed);
  and and_81 (IF_Hold, IF_Hold_BeforeIRQ, IRQ_NoFlowFlush);
  Multiplexer #(.width(32), .select(1), .enable("false")) multiplexer_29 (
    .in0(NEXT_PC_BeforeIRQ), .in1(IRQ_ControllerNext), .out(NEXT_PC), .sel(IRQ_FlowFlush));
  and and_82 (Go_Rise, Go, Go_NotPrevious);
  or or_45 (PAUSE_NEXT, Pause_Keep, WB_HaltEvent);
  or or_46 (W1, IRQ_Capture1, IRQ_Pending1);
  or or_47 (W2, IRQ_Capture2, IRQ_Pending2);
  or or_48 (W3, IRQ_Capture3, IRQ_Pending3);
  Comparator #(.width(2), .mode("unsigned")) comparator_38 (.a(IRQ_Depth), .b(2'b00), .eq(IRQ_Empty));  // open: gt, lt
  Comparator #(.width(2), .mode("unsigned")) comparator_39 (.a(IRQ_Depth), .b(2'b11), .eq(IRQ_Full));  // open: gt, lt
  not not_21 (IRQ_IE, IRQ_Disabled);
  Register #(.width(32)) register_4 (
    .D(IRQ_EPCNext1), .en(IRQ_StackEN), .Q(IRQ_EPC), .clk(CLK), .clr(RST), .cs(1'b0), .preset(1'b0));
  Register #(.width(32)) register_5 (
    .D(IRQ_EPCNext2), .en(IRQ_StackEN), .Q(IRQ_EPC2), .clk(CLK), .clr(RST), .cs(1'b0), .preset(1'b0));
  Register #(.width(32)) register_6 (
    .D(IRQ_EPCNext3), .en(IRQ_StackEN), .Q(IRQ_EPC3), .clk(CLK), .clr(RST), .cs(1'b0), .preset(1'b0));
  and and_83 (Count_Redirect, Count_Redirect_BeforeIRQ, IRQ_NoReturn);
  and and_84 (Count_Jump, Count_Jump_BeforeIRQ, IRQ_NoReturn);
  or or_49 (IRQ_Clear1, IRQ_AckPulse1, RST);
  Register #(.width(1)) register_7 (
    .D(IRQ_Ack1), .en(1'b1), .Q(IRQ_AckPulse1), .clk(CLK), .clr(RST), .cs(1'b0), .preset(1'b0));
  or or_50 (IRQ_Clear2, IRQ_AckPulse2, RST);
  Register #(.width(1)) register_8 (
    .D(IRQ_Ack2), .en(1'b1), .Q(IRQ_AckPulse2), .clk(CLK), .clr(RST), .cs(1'b0), .preset(1'b0));
  or or_51 (IRQ_Clear3, IRQ_AckPulse3, RST);
  Register #(.width(1)) register_9 (
    .D(IRQ_Ack3), .en(1'b1), .Q(IRQ_AckPulse3), .clk(CLK), .clr(RST), .cs(1'b0), .preset(1'b0));
  not not_22 (IRQ_InISR, IRQ_Empty);
  not not_23 (IRQ_Space, IRQ_Full);
  not not_24 (IRQ_NotAck1, IRQ_Ack1);
  not not_25 (IRQ_NotAck2, IRQ_Ack2);
  not not_26 (IRQ_NotAck3, IRQ_Ack3);
  Comparator #(.width(32), .mode("unsigned")) comparator_40 (
    .a(WB_IR), .b({32{1'b0}}), .eq(IRQ_EmptyWB));  // open: gt, lt
  not not_27 (IRQ_NotClose, IRQ_Close);
  Register #(.width(16), .trigger("rising"), .Select("low")) \u_中断排空周期_2  (
    .D(\中断排空周期_Next ), .en(IRQ_DrainCycle), .Q(\中断排空周期 ), .clk(CLK), .clr(RST), .cs(1'b0), .preset(1'b0));
  Adder #(.width(16)) adder_17 (.a(\中断排空周期 ), .b(16'h1), .out(\中断排空周期_Next ), .cin(1'b0));  // open: cout
  or or_52 (IF_Enable, IRQ_NormalPCEnable, IRQ_FlowFlush);
  Multiplexer #(.width(2), .select(1), .enable("false")) multiplexer_30 (
    .in0(IRQ_Prev2), .in1(IRQ_Active), .out(IRQ_PrevNext1), .sel(IRQ_Accept));
  Multiplexer #(.width(2), .select(1), .enable("false")) multiplexer_31 (
    .in0(IRQ_Prev3), .in1(IRQ_Prev1), .out(IRQ_PrevNext2), .sel(IRQ_Accept));
  Multiplexer #(.width(2), .select(1), .enable("false")) multiplexer_32 (
    .in0(2'b00), .in1(IRQ_Prev2), .out(IRQ_PrevNext3), .sel(IRQ_Accept));
  and and_85 (IRQ_ReturnDecoded, IRQ_Uret, IRQ_InISR);
  and and_86 (IRQ_PendingNext1, W1, IRQ_NotAck1);
  and and_87 (IRQ_PendingNext2, W2, IRQ_NotAck2);
  and and_88 (IRQ_PendingNext3, W3, IRQ_NotAck3);
  not not_28 (IRQ_NotReturn, IRQ_Return);
  Register #(.width(1)) register_10 (
    .D(IRQ_PendingNext1), .en(1'b1), .Q(IRQ_Pending1), .clk(CLK), .clr(RST), .cs(1'b0), .preset(1'b0));
  Register #(.width(1)) register_11 (
    .D(IRQ_PendingNext2), .en(1'b1), .Q(IRQ_Pending2), .clk(CLK), .clr(RST), .cs(1'b0), .preset(1'b0));
  Register #(.width(1)) register_12 (
    .D(IRQ_PendingNext3), .en(1'b1), .Q(IRQ_Pending3), .clk(CLK), .clr(RST), .cs(1'b0), .preset(1'b0));
  Register #(.width(2)) register_13 (
    .D(IRQ_PrevNext1), .en(IRQ_StackEN), .Q(IRQ_Prev1), .clk(CLK), .clr(RST), .cs(1'b0), .preset(1'b0));
  Register #(.width(2)) register_14 (
    .D(IRQ_PrevNext2), .en(IRQ_StackEN), .Q(IRQ_Prev2), .clk(CLK), .clr(RST), .cs(1'b0), .preset(1'b0));
  Register #(.width(2)) register_15 (
    .D(IRQ_PrevNext3), .en(IRQ_StackEN), .Q(IRQ_Prev3), .clk(CLK), .clr(RST), .cs(1'b0), .preset(1'b0));
  Comparator #(.width(2), .mode("unsigned")) comparator_41 (
    .a(IRQ_Active), .b(2'b00), .eq(IRQ_Active0));  // open: gt, lt
  not not_29 (IRQ_Below3, IRQ_Active3);
  or or_53 (IRQ_Any_0, IRQ_Eligible1, IRQ_Eligible2);
  and and_89 (IRQ_Accept_0, IRQ_Any, IRQ_IE);
  or or_54 (IRQ_EnableNow, IRQ_Return, IRQ_Open);
  or or_55 (IRQ_StackEN, IRQ_Accept, IRQ_Return);
  or or_56 (IRQ_Below2, IRQ_Active0, IRQ_Active1);
  or or_57 (IRQ_Any, IRQ_Any_0, IRQ_Eligible3);
  and and_90 (IRQ_Accept_1, IRQ_Accept_0, RUN);
  not not_30 (IRQ_NotEnable, IRQ_EnableNow);
  Multiplexer #(.width(2), .select(1), .enable("false")) multiplexer_33 (
    .in0(2'b11), .in1(2'b01), .out(IRQ_Delta), .sel(IRQ_Accept));
  Multiplexer #(.width(32), .select(1), .enable("false")) multiplexer_34 (
    .in0(IF_PC), .in1(IRQ_EPC), .out(IRQ_ReturnNext), .sel(IRQ_Return));
  and and_91 (IRQ_Accept_2, IRQ_Accept_1, IRQ_NotReturn);
  or or_58 (IRQ_DisabledOr_0, IRQ_Disabled, IRQ_Accept);
  and and_92 (IRQ_Eligible1, IRQ_Pending1, IRQ_Active0);
  and and_93 (IRQ_Eligible2, IRQ_Pending2, IRQ_Below2);
  and and_94 (IRQ_Eligible3, IRQ_Pending3, IRQ_Below3);
  Multiplexer #(.width(32), .select(1), .enable("false")) multiplexer_35 (
    .in0(32'h30ac), .in1(32'h3158), .out(IRQ_Vector12), .sel(IRQ_Eligible2));
  Multiplexer #(.width(2), .select(1), .enable("false")) multiplexer_36 (
    .in0(2'b01), .in1(2'b10), .out(IRQ_Selected12), .sel(IRQ_Eligible2));
  Multiplexer #(.width(2), .select(1), .enable("false")) multiplexer_37 (
    .in0(IRQ_Prev1), .in1(IRQ_Selected), .out(IRQ_ActiveNext), .sel(IRQ_Accept));
  and and_95 (IRQ_Accept_3, IRQ_Accept_2, IRQ_NotClose);
  Adder #(.width(2)) adder_18 (.a(IRQ_Depth), .b(IRQ_Delta), .out(IRQ_DepthNext), .cin(1'b0));  // open: cout
  or or_59 (IRQ_DisabledOr, IRQ_DisabledOr_0, IRQ_Close);
  Multiplexer #(.width(32), .select(1), .enable("false")) multiplexer_38 (
    .in0(IRQ_ReturnNext), .in1(IRQ_Vector), .out(IRQ_ControllerNext), .sel(IRQ_Accept));
  and and_96 (IRQ_Drain, IRQ_Accept_3, IRQ_Space);
  Multiplexer #(.width(32), .select(1), .enable("false")) multiplexer_39 (
    .in0(IRQ_Vector12), .in1(32'h3204), .out(IRQ_Vector), .sel(IRQ_Eligible3));
  Multiplexer #(.width(2), .select(1), .enable("false")) multiplexer_40 (
    .in0(IRQ_Selected12), .in1(2'b11), .out(IRQ_Selected), .sel(IRQ_Eligible3));
  Register #(.width(2)) register_16 (
    .D(IRQ_ActiveNext), .en(IRQ_StackEN), .Q(IRQ_Active), .clk(CLK), .clr(RST), .cs(1'b0), .preset(1'b0));
  and and_97 (IRQ_DisabledNext, IRQ_DisabledOr, IRQ_NotEnable);
  Register #(.width(2)) register_17 (
    .D(IRQ_DepthNext), .en(IRQ_StackEN), .Q(IRQ_Depth), .clk(CLK), .clr(RST), .cs(1'b0), .preset(1'b0));
  Register #(.width(1)) register_18 (
    .D(IRQ_DisabledNext), .en(RUN), .Q(IRQ_Disabled), .clk(CLK), .clr(RST), .cs(1'b0), .preset(1'b0));

  // Other names for the same wires on the sheet: EX_Ctrl (some bits) = {EX_BGE, EX_BNE, EX_BEQ}; EX_JAL = EX_Ctrl[2];
  //   EX_JALR = EX_Ctrl[3]; EX_ECALL = EX_Ctrl[4]; EX_LUI = EX_Ctrl[6]; EX_LH = EX_Ctrl[7];
  //   EX_RS1[4:0] = EX_IR[19:15]; EX_RS2[4:0] = EX_IR[24:20]; PAUSED = halt;
  //   ID_BImm_raw[11:0] = {ID_BImm_p3, ID_BImm_p2, ID_BImm_p1, ID_BImm_p0};
  //   ID_IR (some bits) = {ID_BImm_p3, ID_BImm_p1, ID_I12, ID_F3, ID_BImm_p0, ID_BImm_p2};
  //   ID_RD[4:0] = {ID_BImm_p0, ID_BImm_p2}; ID_S12[11:0] = {ID_BImm_p3, ID_BImm_p1, ID_BImm_p0, ID_BImm_p2};
  //   ID_CtrlRaw (some bits) = {ID_BGE, ID_BNE, ID_BEQ}; ID_JAL = ID_CtrlRaw[2]; ID_JALR = ID_CtrlRaw[3];
  //   ID_ECALL = ID_CtrlRaw[4]; ID_LUI = ID_CtrlRaw[6]; ID_LH = ID_CtrlRaw[7]; ID_Low2[1:0] = ID_IR[1:0];
  //   ID_OP7[6:0] = ID_IR[6:0]; ID_OP5[4:0] = ID_IR[6:2]; ID_IR21 = ID_I12[1];
  //   ID_JImm_p0[9:0] = {ID_BImm_p1, ID_I12[4:1]};
  //   ID_JImm_raw[19:0] = {ID_BImm_p3, ID_IR[19:15], ID_F3, ID_I12[0], ID_BImm_p1, ID_I12[4:1]}; ID_RS2[4:0] = ID_I12;
  //   ID_FUN5[4:0] = {ID_BImm_p1[5], ID_BImm_p1[0], ID_F3}; ID_I12[11:5] = {ID_BImm_p3, ID_BImm_p1};
  //   ID_JImm_p1 = ID_I12[0]; ID_JImm_p2[7:0] = {ID_IR[19:15], ID_F3}; ID_RS1[4:0] = ID_IR[19:15];
  //   ID_JImm_p3 = ID_BImm_p3; ID_LoadUse = ID_DataStall; IRQ_EPC1[31:0] = IRQ_EPC; IRQ_NormalNext[31:0] = IF_PC;
  //   IADDR[19:0] = IF_PC[21:2]; IRQ_Ready = IRQ_Drain; LoadUse气泡[15:0] = \LoadUse次数 ; MEM_ECALL = MEM_Ctrl[4];
  //   MEM_LH = MEM_Ctrl[7]; MEM_PC[31:0] = M_PC; MEM_Result[25:1] = {DADDR, MEM_HalfSel};
  //   MEM_Word[31:0] = {MEM_High16, MEM_Low16}; RAW_CLK = CLK; WB_ECALL = WB_Ctrl[4]

  // Notes on the sheet:
  //   中断源
  //   时空图监测，可删除
  //   中断等待指示
  //   IF：顺序与 EX 分支反馈
  //   Load-Use：保持前端，清空 ID-EX 一周期
  //   EX 转移优先：清空两级，无延迟槽
  //   ECALL 正常流动；WB 暂停取消年轻指令，Go 从下一条重取
  //   IF-ID 原气泡零源断开：外置清零，封装不变
  //   数码管输出
  //   contents of rom_1 (hex, n*v repeats v):
  //   7d000113 00100413 01f41993 41f9d993 00000433 00c00913 00800b13 00140413 00f47413 00800293 00100313
  //   00499993 0089e9b3 01300533 02200893 00000073 406282b3 fe0294e3 00140413 00f00f93 01f47433 01c41413
  //   00800293 00100313 0049d993 0089e9b3 01300533 02200893 00000073 406282b3 fe0294e3 01c45413 406b0b33
  //   000b0463 f95ff06f 000002b3 fff2c293 01029293 fff2e293 00500533 02200893 00000073 f5dff06f 00000000
  //   00000000 00000000 00000000 00000000 00000000 00000000 00000000 00000000 00000000 00000000 00000000
  //   00000000 00000000 00000000 00000000 00000000 00000000 00000000 00000000 00000000 00000000 00000000
  //   00000000 00000000 00000000 00000000 00000000 00000000 00000000 00000000 00000000 00000000 00000000
  //   00000000 00000000 00000000 00000000 00000000 00000000 00000000 00000000 00000000 00000000 00000000
  //   00000000 00000000 00000000 00000000 00000000 00000000 00000000 00000000 00000000 00000000 00000000
  //   00000000 00000000 00000000 00000000 00000000 00000000 00000000 00000000 00000000 00000000 00000000
  //   00000000 00000000 00000000 00000000 00000000 00000000 00000000 00000000 00000000 00000000 00000000
  //   00000000 00000000 00000000 00000000 00000000 00000000 00000000 00000000 00000000 00000000 00000000
  //   00000000 00000000 00000000 00000000 00000000 00000000 00000000 00000000 00000000 00000000 00000000
  //   00000000 00000000 00000000 00000000 00000000 00000000 00000000 00000000 00000000 00000000 00000000
  //   00000000 00000000 00000000 00000000 00000000 00000000 00000000 00000000 00000000 00000000 00000000
  //   00000000 00000000 00000000 00000000 00000000 00000000 00000000 00000000 00000000 00000000 00000000
  //   00000000 00000000 00000000 00000000 00000000 00000000 00000000 00000000 00000000 00000000 00000000
  //   00000000 00000000 00000000 00000000 00000000 00000000 00000000 00000000 00000000 00000000 00000000
  //   00000000 00000000 00000000 00000000 00000000 00000000 00000000 00000000 00000000 00000000 00000000
  //   00000000 00000000 00000000 00000000 00000000 00000000 00000000 00000000 00000000 00000000 00000000
  //   00000000 00000000 00000000 00000000 00000000 00000000 00000000 00000000 00000000 00000000 00000000
  //   00000000 00000000 00000000 00000000 00000000 00000000 00000000 00000000 00000000 00000000 00000000
  //   00000000 00000000 00000000 00000000 00000000 00000000 00000000 00000000 00000000 00000000 00000000
  //   00000000 00000000 00000000 00000000 00000000 00000000 00000000 00000000 00000000 00000000 00000000
  //   00000000 00000000 00000000 00000000 00000000 00000000 00000000 00000000 00000000 00000000 00000000
  //   00000000 00000000 00000000 00000000 00000000 00000000 00000000 00000000 00000000 00000000 00000000
  //   00000000 00000000 00000000 00000000 00000000 00000000 00000000 00000000 00000000 00000000 00000000
  //   00000000 00000000 00000000 00000000 00000000 00000000 00000000 00000000 00000000 00000000 00000000
  //   00000000 00000000 00000000 00000000 00000000 00000000 00000000 00000000 00000000 00000000 00000000
  //   00000000 00000000 00000000 00000000 00000000 00000000 00000000 00000000 00000000 00000000 00000000
  //   00000000 00000000 00000000 00000000 00000000 00000000 00000000 00000000 00000000 00000000 00000000
  //   00000000 00000000 00000000 00000000 00000000 00000000 00000000 00000000 00000000 00000000 00000000
  //   00000000 00000000 00000000 00000000 00000000 00000000 00000000 00000000 00000000 00000000 00000000
  //   00000000 00000000 00000000 00000000 00000000 00000000 00000000 00000000 00000000 00000000 00000000
  //   00000000 00000000 00000000 00000000 00000000 00000000 00000000 00000000 00000000 00000000 00000000
  //   00000000 00000000 00000000 00000000 00000000 00000000 00000000 00000000 00000000 00000000 00000000
  //   00000000 00000000 00000000 00000000 00000000 00000000 00000000 00000000 00000000 00000000 00000000
  //   00000000 00000000 00000000 00000000 00000000 00000000 00000000 00000000 00000000 00000000 00000000
  //   00000000 00000000 00000000 00000000 00000000 00000000 00000000 00000000 00000000 00000000 00000000
  //   00000000 00000000 00000000 00000000 00000000 00000000 00000000 00000000 00000000 00000000 00000000
  //   00000000 00000000 00000000 00000000 0000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
  //   ID：立即数、控制信号
  //   控制位
  //   暂停节拍，不能为0
  //   流水调试日志用
  //   用这个时钟源需要去掉电路中的其他时钟源
  //   戳工具置1进入计数暂停模式，ctrl+k时钟自动运行到对应节拍暂停
  //   ctrl+k关闭时钟连续运行，将控制位置零，进入单步调试模式调试
  //   可计数暂停的时钟源
  //   EX：执行与分支
  //   为方便自动评测，需要输出流水线各段保存的PC值，注意是PC不是PC+4，另外ID段寄存器写入信息，Mem段内存写入信息也要输出
  //   MEM：访存与 LH
  //   流水多级中断：IE / 服务号 / 嵌套深度 / 栈顶EPC / 排空
  //   Ctrl+R 全复位 / Ctrl+K 自动运行
  //   WB：写回与 ECALL
  //   气泡冲突检测：真实源寄存器 / x0 排除 / EX → MEM → WB
  //   气泡总数 = 数据停顿 + 2 × 已执行转移；系统等待单列
  //   数据重定向：MEM 非 load 结果优先；WB 实际写回次之
  //   MEM load 地址禁止转发；Load-Use 在 ID 停顿 1 周期
  //   ALU / 分支 / JALR / Store / ECALL 共用修正后的 R1、R2
  //   WB 暂停边界：前端不提前排空；取消年轻副作用并保存续行 PC
  //   请求1：捕获 / 等待 / 仅在本层返回时清除
  //   请求2：捕获 / 等待 / 仅在本层返回时清除
  //   请求3：捕获 / 等待 / 仅在本层返回时清除
  //   按键1捕获
  //   按键2捕获
  //   按键3捕获
  //   IRQ：停取指、排空四级、保存 IF.PC；EX 分支仍可纠正排空期间的断点
  //   URET 在 WB 弹栈，取消年轻指令及 MEM 存储；CSR 开关中断在 WB 生效
  //   多级中断：关中断保护现场，开中断后仅响应更高优先级；返回自动开中断
  //   EPC栈第1层
  //   EPC栈第2层
  //   EPC栈第3层
  //   EPC 硬件堆栈：压栈保存真实下一PC及上一层优先级；弹栈恢复；最多三层
  //   返回1清除脉冲
  //   返回2清除脉冲
  //   返回3清除脉冲
  //   IR1等待
  //   IR2等待
  //   IR3等待
  //   优先级栈第1层
  //   优先级栈第2层
  //   优先级栈第3层
  //   控制优先级：复位 > 暂停保持 > 返回 / 关中断 > 中断响应 > 普通执行
  //   返回同拍不响应新中断；排空后响应，EPC 保存完整32位实际续行地址
  //   当前服务优先级
  //   硬件栈深度 0..3
  //   中断禁止位：复位0 / 入口1 / 软件开关
endmodule

// 单周期硬布线控制器
module \单周期硬布线控制器  (
  input  [4:0] OP,
  input  [4:0] Funct,
  input  in_3,
  output [3:0] ALU_OP,
  output uret,
  output MemToReg,
  output ecall,
  output MemWrite,
  output ALU_SRC,
  output RegWrite,
  output S_type,
  output Beq,
  output Bne,
  output Jalr,
  output JAL
);

  wire \控制信号自动生成_1_ecall ;

  \运算控制器自动生成  \u_运算控制器自动生成_1  (
    .S1(ALU_OP[1]), .OP3(OP[1]), .S2(ALU_OP[2]), .OP5(OP[3]), .F12(Funct[0]), .OP6(OP[4]), .S0(ALU_OP[0]),
    .F30(Funct[4]), .OP4(OP[2]), .S3(ALU_OP[3]), .F25(Funct[3]), .OP2(OP[0]), .F13(Funct[1]), .F14(Funct[2]));
  \控制信号自动生成  \u_控制信号自动生成_1  (
    .OP2(OP[0]), .MemToReg(MemToReg), .OP3(OP[1]), .MemWrite(MemWrite), .OP4(OP[2]), .ALU_SRC(ALU_SRC),
    .OP5(OP[3]), .RegWrite(RegWrite), .OP6(OP[4]), .ecall(\控制信号自动生成_1_ecall ), .F12(Funct[0]),
    .S_Type(S_type), .F13(Funct[1]), .BEQ(Beq), .F14(Funct[2]), .BNE(Bne), .F25(Funct[3]), .JALR(Jalr),
    .F30(Funct[4]), .JAL(JAL));
  and and_1 (uret, in_3, \控制信号自动生成_1_ecall );
  and and_2 (ecall, ~in_3, \控制信号自动生成_1_ecall );  // AND_Gate

  // Other names for the same wires on the sheet: IR21 = in_3; OP_CODE[4:0] = OP

  // Notes on the sheet:
  //   运算器控制器，根据指令生成运算器功能选择信号
  //   控制信号生成，产生数据通路需要的其他控制信号
endmodule

// 运算器控制器
module \运算控制器自动生成  (
  input  OP2,
  input  OP3,
  input  OP4,
  input  OP5,
  input  OP6,
  input  F12,
  input  F13,
  input  F14,
  input  F25,
  input  F30,
  output S0,
  output S1,
  output S2,
  output S3
);

  wire _ADD_0, _ADD_ALL_0, _ADD_ALL_1, _ADD_ALL_2, _S0_0, _S0_1, _S0_2, _S0_3, _S1_0, _S1_1, _S1_2, _S2_0,
       _S2_1, _S3_0, _S3_1, _S3_2, _SRA_0, _SRL_0, _SUB_0, ADD, ADD_ALL, AND, BR, F0, F1, F2, F3, F4, F5, F6,
       F7, I, J, JR, LD, N30, NSUB, OR, R, RI, SLT, SLTU, SRA, SRL, ST, SUB, SUBBIT, SYS, U, XOR;

  Comparator #(.width(5), .mode("unsigned")) comparator_1 (
    .a({OP6, OP5, OP4, OP3, OP2}), .b(5'b01100), .eq(R));  // open: gt, lt
  Comparator #(.width(5), .mode("unsigned")) comparator_2 (
    .a({OP6, OP5, OP4, OP3, OP2}), .b(5'b00100), .eq(I));  // open: gt, lt
  Comparator #(.width(5), .mode("unsigned")) comparator_3 (
    .a({OP6, OP5, OP4, OP3, OP2}), .b({5{1'b0}}), .eq(LD));  // open: gt, lt
  Comparator #(.width(5), .mode("unsigned")) comparator_4 (
    .a({OP6, OP5, OP4, OP3, OP2}), .b(5'b01000), .eq(ST));  // open: gt, lt
  Comparator #(.width(5), .mode("unsigned")) comparator_5 (
    .a({OP6, OP5, OP4, OP3, OP2}), .b(5'b11000), .eq(BR));  // open: gt, lt
  Comparator #(.width(5), .mode("unsigned")) comparator_6 (
    .a({OP6, OP5, OP4, OP3, OP2}), .b(5'b11001), .eq(JR));  // open: gt, lt
  Comparator #(.width(5), .mode("unsigned")) comparator_7 (
    .a({OP6, OP5, OP4, OP3, OP2}), .b(5'b11011), .eq(J));  // open: gt, lt
  Comparator #(.width(5), .mode("unsigned")) comparator_8 (
    .a({OP6, OP5, OP4, OP3, OP2}), .b(5'b01101), .eq(U));  // open: gt, lt
  Comparator #(.width(5), .mode("unsigned")) comparator_9 (
    .a({OP6, OP5, OP4, OP3, OP2}), .b(5'b11100), .eq(SYS));  // open: gt, lt
  Comparator #(.width(3), .mode("unsigned")) comparator_10 (.a({F14, F13, F12}), .b(3'b000), .eq(F0));  // open: gt, lt
  Comparator #(.width(3), .mode("unsigned")) comparator_11 (.a({F14, F13, F12}), .b(3'b001), .eq(F1));  // open: gt, lt
  Comparator #(.width(3), .mode("unsigned")) comparator_12 (.a({F14, F13, F12}), .b(3'b010), .eq(F2));  // open: gt, lt
  Comparator #(.width(3), .mode("unsigned")) comparator_13 (.a({F14, F13, F12}), .b(3'b011), .eq(F3));  // open: gt, lt
  Comparator #(.width(3), .mode("unsigned")) comparator_14 (.a({F14, F13, F12}), .b(3'b100), .eq(F4));  // open: gt, lt
  Comparator #(.width(3), .mode("unsigned")) comparator_15 (.a({F14, F13, F12}), .b(3'b101), .eq(F5));  // open: gt, lt
  Comparator #(.width(3), .mode("unsigned")) comparator_16 (.a({F14, F13, F12}), .b(3'b110), .eq(F6));  // open: gt, lt
  Comparator #(.width(3), .mode("unsigned")) comparator_17 (.a({F14, F13, F12}), .b(3'b111), .eq(F7));  // open: gt, lt
  not not_1 (N30, F30);
  not not_2 (NSUB, SUBBIT);
  or or_1 (RI, R, I);
  and and_1 (SUBBIT, R, F30);
  and and_2 (_ADD_0, RI, F0);
  and and_3 (ADD, _ADD_0, NSUB);
  and and_4 (_SUB_0, R, F0);
  and and_5 (SUB, _SUB_0, F30);
  and and_6 (SLT, RI, F2);
  and and_7 (SLTU, RI, F3);
  and and_8 (XOR, RI, F4);
  and and_9 (OR, RI, F6);
  and and_10 (AND, RI, F7);
  and and_11 (_SRA_0, RI, F5);
  and and_12 (SRA, _SRA_0, F30);
  and and_13 (_SRL_0, RI, F5);
  and and_14 (SRL, _SRL_0, N30);
  or or_2 (_ADD_ALL_0, ADD, LD);
  or or_3 (_ADD_ALL_1, _ADD_ALL_0, ST);
  or or_4 (_ADD_ALL_2, _ADD_ALL_1, JR);
  or or_5 (ADD_ALL, _ADD_ALL_2, U);
  or or_6 (_S0_0, ADD_ALL, AND);
  or or_7 (_S0_1, _S0_0, XOR);
  or or_8 (_S0_2, _S0_1, SLT);
  or or_9 (_S0_3, _S0_2, SRA);
  or or_10 (S0, _S0_3, BR);
  or or_11 (_S1_0, SUB, AND);
  or or_12 (_S1_1, _S1_0, SLT);
  or or_13 (_S1_2, _S1_1, SRL);
  or or_14 (S1, _S1_2, BR);
  or or_15 (_S2_0, ADD_ALL, SUB);
  or or_16 (_S2_1, _S2_0, AND);
  or or_17 (S2, _S2_1, SLTU);
  or or_18 (_S3_0, OR, XOR);
  or or_19 (_S3_1, _S3_0, SLT);
  or or_20 (_S3_2, _S3_1, SLTU);
  or or_21 (S3, _S3_2, BR);

  // Other names for the same wires on the sheet: FUN3[2:0] = {F14, F13, F12}; OP[4:0] = {OP6, OP5, OP4, OP3, OP2}

  // Notes on the sheet:
  //   ALU 编码：0 SLL / 1 SRA / 2 SRL / 5 ADD / 6 SUB / 7 AND / 8 OR / 9 XOR / 11 SLT / 12 SLTU
endmodule

// 控制信号生成
module \控制信号自动生成  (
  input  OP2,
  input  OP3,
  input  OP4,
  input  OP5,
  input  OP6,
  input  F12,
  input  F13,
  input  F14,
  input  F25,
  input  F30,
  output MemToReg,
  output MemWrite,
  output ALU_SRC,
  output RegWrite,
  output ecall,
  output S_Type,
  output BEQ,
  output BNE,
  output JALR,
  output JAL
);

  wire _ALU_SRC_0, _ALU_SRC_1, _ALU_SRC_2, _RegWrite_0, _RegWrite_1, _RegWrite_2, _RegWrite_3, BR, F0, F1,
       F2, F3, F4, F5, F6, F7, I, J, JR, LD, R, ST, SYS, U;

  Comparator #(.width(5), .mode("unsigned")) comparator_1 (
    .a({OP6, OP5, OP4, OP3, OP2}), .b(5'b01100), .eq(R));  // open: gt, lt
  Comparator #(.width(5), .mode("unsigned")) comparator_2 (
    .a({OP6, OP5, OP4, OP3, OP2}), .b(5'b00100), .eq(I));  // open: gt, lt
  Comparator #(.width(5), .mode("unsigned")) comparator_3 (
    .a({OP6, OP5, OP4, OP3, OP2}), .b({5{1'b0}}), .eq(LD));  // open: gt, lt
  Comparator #(.width(5), .mode("unsigned")) comparator_4 (
    .a({OP6, OP5, OP4, OP3, OP2}), .b(5'b01000), .eq(ST));  // open: gt, lt
  Comparator #(.width(5), .mode("unsigned")) comparator_5 (
    .a({OP6, OP5, OP4, OP3, OP2}), .b(5'b11000), .eq(BR));  // open: gt, lt
  Comparator #(.width(5), .mode("unsigned")) comparator_6 (
    .a({OP6, OP5, OP4, OP3, OP2}), .b(5'b11001), .eq(JR));  // open: gt, lt
  Comparator #(.width(5), .mode("unsigned")) comparator_7 (
    .a({OP6, OP5, OP4, OP3, OP2}), .b(5'b11011), .eq(J));  // open: gt, lt
  Comparator #(.width(5), .mode("unsigned")) comparator_8 (
    .a({OP6, OP5, OP4, OP3, OP2}), .b(5'b01101), .eq(U));  // open: gt, lt
  Comparator #(.width(5), .mode("unsigned")) comparator_9 (
    .a({OP6, OP5, OP4, OP3, OP2}), .b(5'b11100), .eq(SYS));  // open: gt, lt
  Comparator #(.width(3), .mode("unsigned")) comparator_10 (.a({F14, F13, F12}), .b(3'b000), .eq(F0));  // open: gt, lt
  Comparator #(.width(3), .mode("unsigned")) comparator_11 (.a({F14, F13, F12}), .b(3'b001), .eq(F1));  // open: gt, lt
  Comparator #(.width(3), .mode("unsigned")) comparator_12 (.a({F14, F13, F12}), .b(3'b010), .eq(F2));  // open: gt, lt
  Comparator #(.width(3), .mode("unsigned")) comparator_13 (.a({F14, F13, F12}), .b(3'b011), .eq(F3));  // open: gt, lt
  Comparator #(.width(3), .mode("unsigned")) comparator_14 (.a({F14, F13, F12}), .b(3'b100), .eq(F4));  // open: gt, lt
  Comparator #(.width(3), .mode("unsigned")) comparator_15 (.a({F14, F13, F12}), .b(3'b101), .eq(F5));  // open: gt, lt
  Comparator #(.width(3), .mode("unsigned")) comparator_16 (.a({F14, F13, F12}), .b(3'b110), .eq(F6));  // open: gt, lt
  Comparator #(.width(3), .mode("unsigned")) comparator_17 (.a({F14, F13, F12}), .b(3'b111), .eq(F7));  // open: gt, lt
  or or_1 (MemToReg, LD, LD);
  or or_2 (MemWrite, ST, ST);
  or or_3 (S_Type, ST, ST);
  or or_4 (_ALU_SRC_0, I, LD);
  or or_5 (_ALU_SRC_1, _ALU_SRC_0, ST);
  or or_6 (_ALU_SRC_2, _ALU_SRC_1, U);
  or or_7 (ALU_SRC, _ALU_SRC_2, JR);
  or or_8 (_RegWrite_0, R, I);
  or or_9 (_RegWrite_1, _RegWrite_0, LD);
  or or_10 (_RegWrite_2, _RegWrite_1, U);
  or or_11 (_RegWrite_3, _RegWrite_2, J);
  or or_12 (RegWrite, _RegWrite_3, JR);
  or or_13 (ecall, SYS, SYS);
  or or_14 (JALR, JR, JR);
  or or_15 (JAL, J, J);
  and and_1 (BEQ, BR, F0);
  and and_2 (BNE, BR, F1);

  // Other names for the same wires on the sheet: FUN3[2:0] = {F14, F13, F12}; OP[4:0] = {OP6, OP5, OP4, OP3, OP2}

  // Notes on the sheet:
  //   基本控制信号；BGE 与 LH / LUI 扩展选择在主电路
endmodule

// ALU
module ALU (
  input  [31:0] X,
  input  [31:0] Y,
  input  [3:0] AluOP,
  output out_4,
  output Equal,
  output out_6,
  output [31:0] Result,
  output [31:0] Result_2
);

  wire [0:0] comparator_1_lt, comparator_2_lt;
  wire [31:0] adder_1_out, AND_out, divider_1_out, divider_1_rem, multiplier_1_cout, multiplier_1_out,
       NOR_out, OR_out, shifter_1_out, shifter_2_out, shifter_3_out, subtractor_1_out, XOR_out;

  assign AND_out = X & Y;  // AND_Gate AND, 32 bits wide
  assign OR_out = X | Y;  // OR_Gate OR, 32 bits wide
  Shifter #(.width(32)) shifter_1 (.in(X), .\dist (Y[4:0]), .out(shifter_1_out));
  Shifter #(.width(32), .shift("ar")) shifter_2 (.in(X), .\dist (Y[4:0]), .out(shifter_2_out));
  Shifter #(.width(32), .shift("lr")) shifter_3 (.in(X), .\dist (Y[4:0]), .out(shifter_3_out));
  Multiplier #(.width(32)) multiplier_1 (.a(X), .b(Y), .out(multiplier_1_out), .cout(multiplier_1_cout));  // open: cin
  Divider #(.width(32)) divider_1 (.a(X), .b(Y), .out(divider_1_out), .rem(divider_1_rem));  // open: upper
  Adder #(.width(32)) adder_1 (.a(X), .b(Y), .out(adder_1_out));  // open: cin, cout
  Subtractor #(.width(32)) subtractor_1 (.a(X), .b(Y), .out(subtractor_1_out));  // open: bin, bout
  assign XOR_out = X ^ Y;  // XOR_Gate XOR, 32 bits wide
  assign NOR_out = ~(X | Y);  // NOR_Gate NOR, 32 bits wide
  Comparator #(.width(32)) comparator_1 (.a(X), .b(Y), .eq(Equal), .lt(comparator_1_lt[0]));  // open: gt
  Comparator #(.width(32), .mode("unsigned")) comparator_2 (.a(X), .b(Y), .lt(comparator_2_lt[0]));  // open: gt, eq
  Multiplexer #(.select(4), .width(32), .enable("false")) multiplexer_1 (
    .in0(shifter_1_out), .in1(shifter_2_out), .in2(shifter_3_out), .in3(multiplier_1_out),
    .in4(divider_1_out), .in5(adder_1_out), .in6(subtractor_1_out), .in7(AND_out), .in8(OR_out),
    .in9(XOR_out), .in10(NOR_out), .in11({{31{1'b0}}, comparator_1_lt[0]}),
    .in12({{31{1'b0}}, comparator_2_lt[0]}), .in13({32{1'b0}}), .in14({32{1'b0}}), .in15({32{1'b0}}),
    .out(Result), .sel(AluOP));
  Multiplexer #(.select(4), .width(32), .enable("false")) multiplexer_2 (
    .in0({32{1'b0}}), .in1({32{1'b0}}), .in2({32{1'b0}}), .in3(multiplier_1_cout), .in4(divider_1_rem),
    .in5({32{1'b0}}), .in6({32{1'b0}}), .in7({32{1'b0}}), .in8({32{1'b0}}), .in9({32{1'b0}}),
    .in10({32{1'b0}}), .in11({32{1'b0}}), .in12({32{1'b0}}), .in13({32{1'b0}}), .in14({32{1'b0}}),
    .in15({32{1'b0}}), .out(Result_2), .sel(AluOP));
  Multiplexer #(.select(4), .enable("false")) multiplexer_3 (
    .in0(1'b0), .in1(1'b0), .in2(1'b0), .in3(1'b0), .in4(1'b0), .in5(1'b0), .in6(1'b0), .in7(1'b0),
    .in8(1'b0), .in9(1'b0), .in10(1'b0), .in11(comparator_1_lt[0]), .in12(comparator_2_lt[0]), .in13(1'b0),
    .in14(1'b0), .in15(1'b0), .out(out_6), .sel(AluOP));
  not not_1 (out_4, out_6);

  // Other names for the same wires on the sheet: Result2[31:0] = Result_2; S[3:0] = AluOP; tunnel = out_6;
  //   tunnel_t = out_4

  // Notes on the sheet:
  //   不要改变此引脚区域内容，也不要改变ALU封装形式
  //   输入引脚
  //   输出引脚
endmodule

module Regifile (
  input  [31:0] Din,
  input  Clk,
  input  WE,
  input  [4:0] R1_num,
  input  [4:0] W_num,
  input  [4:0] R2_num,
  output [31:0] R1,
  output [31:0] R2
);

  // register_file register_file_1: pin names not known; wires that end beside it: Din, Clk, WE, W_num, R1_num, R2_num, R1, R2
endmodule

// IF / ID
module IF_ID (
  input  PredictJump,
  input  [31:0] IR,
  input  [31:0] PC,
  input  \气泡 ,
  input  \EN_低电平有效 ,
  input  CLK,
  output PredictJump_2,
  output [31:0] IR_2,
  output [31:0] PC_2,
  output [31:0] IR_3
);

  wire multiplexer_1_out, not_1_out, pull_resistor_3_node;
  wire [31:0] multiplexer_2_out, multiplexer_3_out, undriven;

  Pull_Resistor pull_resistor_1 (.node(\气泡 ));
  Multiplexer #(.enable("false")) multiplexer_1 (.in0(PredictJump), .in1(1'b0), .out(multiplexer_1_out), .sel(\气泡 ));
  Multiplexer #(.width(32), .enable("false")) multiplexer_2 (
    .in0(IR), .in1(undriven), .out(multiplexer_2_out), .sel(\气泡 ));
  Multiplexer #(.width(32), .enable("false")) multiplexer_3 (
    .in0(PC), .in1(undriven), .out(multiplexer_3_out), .sel(\气泡 ));
  Pull_Resistor pull_resistor_2 (.node(\EN_低电平有效 ));
  Pull_Resistor pull_resistor_3 (.node(pull_resistor_3_node));
  not not_1 (not_1_out, \EN_低电平有效 );
  Register #(.width(1)) u_PredictJump (
    .D(multiplexer_1_out), .en(not_1_out), .Q(PredictJump_2), .clk(CLK));  // open: clr
  Register #(.width(32)) u_IR (.D(multiplexer_2_out), .en(not_1_out), .Q(IR_2), .clk(CLK));  // open: clr
  Register #(.width(32)) u_PC (.D(multiplexer_3_out), .en(not_1_out), .Q(PC_2), .clk(CLK));  // open: clr

  assign IR_3 = IR_2;

  // Notes on the sheet:
  //   气泡: pull=down
endmodule

// ID / EX
module ID_EX (
  input  [31:0] PC,
  input  [31:0] RS1,
  input  [31:0] RS2,
  input  RegWrite,
  input  MemToReg,
  input  MemWrite,
  input  ALuSrc,
  input  [31:0] Imm32,
  input  [1:0] rs2Fwd,
  input  [1:0] rs1Fwd,
  input  PredictJump,
  input  [31:0] IR,
  input  [31:0] Reserved1,
  input  [31:0] Reserved2,
  input  [4:0] WriteReg_num,
  input  [3:0] ALUOP,
  input  [9:0] \指令译码信号 ,
  input  \气泡 ,
  input  \EN_低电平有效 ,
  input  CLK,
  output [31:0] PC_2,
  output [31:0] RS1_2,
  output [31:0] RS2_2,
  output [31:0] Imm32_2,
  output [31:0] IR_2,
  output RegWrite_2,
  output MemToReg_2,
  output MemWrite_2,
  output ALuSrc_2,
  output [1:0] rs2Fwd_2,
  output [31:0] Reserved1_2,
  output [1:0] rs1Fwd_2,
  output PredictJump_2,
  output [31:0] Reserved2_2,
  output [4:0] WriteReg_num_2,
  output [3:0] ALUOP_2,
  output [9:0] \指令译码信号_2 
);

  wire not_1_out;
  wire [3:0] multiplexer_10_out;
  wire [4:0] multiplexer_9_out;
  wire [9:0] multiplexer_11_out;
  wire [15:0] multiplexer_8_out;
  wire [15:9] ControlBusIn, ControlBusOut;
  wire [31:0] multiplexer_1_out, multiplexer_2_out, multiplexer_3_out, multiplexer_4_out, multiplexer_5_out,
       multiplexer_6_out, multiplexer_7_out;

  Pull_Resistor pull_resistor_1 (.node({ControlBusIn, PredictJump, rs1Fwd, rs2Fwd, ALuSrc, MemWrite, MemToReg, RegWrite}));
  Pull_Resistor pull_resistor_2 (.node(\指令译码信号 ));
  Pull_Resistor pull_resistor_3 (.node(\气泡 ));
  Multiplexer #(.width(32), .enable("false")) multiplexer_1 (
    .in0(PC), .in1({32{1'b0}}), .out(multiplexer_1_out), .sel(\气泡 ));
  Multiplexer #(.width(32), .enable("false")) multiplexer_2 (
    .in0(RS1), .in1({32{1'b0}}), .out(multiplexer_2_out), .sel(\气泡 ));
  Multiplexer #(.width(32), .enable("false")) multiplexer_3 (
    .in0(RS2), .in1({32{1'b0}}), .out(multiplexer_3_out), .sel(\气泡 ));
  Multiplexer #(.width(32), .enable("false")) multiplexer_4 (
    .in0(Imm32), .in1({32{1'b0}}), .out(multiplexer_4_out), .sel(\气泡 ));
  Multiplexer #(.width(32), .enable("false")) multiplexer_5 (
    .in0(IR), .in1({32{1'b0}}), .out(multiplexer_5_out), .sel(\气泡 ));
  Multiplexer #(.width(32), .enable("false")) multiplexer_6 (
    .in0(Reserved1), .in1({32{1'b0}}), .out(multiplexer_6_out), .sel(\气泡 ));
  Multiplexer #(.width(32), .enable("false")) multiplexer_7 (
    .in0(Reserved2), .in1({32{1'b0}}), .out(multiplexer_7_out), .sel(\气泡 ));
  Multiplexer #(.width(16), .enable("false")) multiplexer_8 (
    .in0({ControlBusIn, PredictJump, rs1Fwd, rs2Fwd, ALuSrc, MemWrite, MemToReg, RegWrite}),
    .in1({16{1'b0}}), .out(multiplexer_8_out), .sel(\气泡 ));
  Multiplexer #(.width(5), .enable("false")) multiplexer_9 (
    .in0(WriteReg_num), .in1({5{1'b0}}), .out(multiplexer_9_out), .sel(\气泡 ));
  Multiplexer #(.width(4), .enable("false")) multiplexer_10 (
    .in0(ALUOP), .in1(4'b0000), .out(multiplexer_10_out), .sel(\气泡 ));
  Multiplexer #(.width(10), .enable("false")) multiplexer_11 (
    .in0(\指令译码信号 ), .in1({10{1'b0}}), .out(multiplexer_11_out), .sel(\气泡 ));
  not not_1 (not_1_out, \EN_低电平有效 );
  Pull_Resistor pull_resistor_4 (.node(\EN_低电平有效 ));
  Register #(.width(32)) u_PC (.D(multiplexer_1_out), .en(not_1_out), .Q(PC_2), .clk(CLK));  // open: clr
  Register #(.width(32)) register_1 (.D(multiplexer_2_out), .en(not_1_out), .Q(RS1_2), .clk(CLK));  // open: clr
  Register #(.width(32)) register_2 (.D(multiplexer_3_out), .en(not_1_out), .Q(RS2_2), .clk(CLK));  // open: clr
  Register #(.width(32)) register_3 (.D(multiplexer_4_out), .en(not_1_out), .Q(Imm32_2), .clk(CLK));  // open: clr
  Register #(.width(32)) register_4 (.D(multiplexer_5_out), .en(not_1_out), .Q(IR_2), .clk(CLK));  // open: clr
  Register #(.width(32)) register_5 (.D(multiplexer_6_out), .en(not_1_out), .Q(Reserved1_2), .clk(CLK));  // open: clr
  Register #(.width(32)) register_6 (.D(multiplexer_7_out), .en(not_1_out), .Q(Reserved2_2), .clk(CLK));  // open: clr
  Register #(.width(16)) register_7 (
    .D(multiplexer_8_out), .en(not_1_out),
    .Q({ControlBusOut, PredictJump_2, rs1Fwd_2, rs2Fwd_2, ALuSrc_2, MemWrite_2, MemToReg_2, RegWrite_2}),
    .clk(CLK));  // open: clr
  Register #(.width(5)) register_8 (.D(multiplexer_9_out), .en(not_1_out), .Q(WriteReg_num_2), .clk(CLK));  // open: clr
  Register #(.width(4)) register_9 (.D(multiplexer_10_out), .en(not_1_out), .Q(ALUOP_2), .clk(CLK));  // open: clr
  Register #(.width(10)) register_10 (.D(multiplexer_11_out), .en(not_1_out), .Q(\指令译码信号_2 ), .clk(CLK));  // open: clr

  // Other names for the same wires on the sheet: ControlBusIn[8:0] = {PredictJump, rs1Fwd, rs2Fwd, ALuSrc, MemWrite, MemToReg, RegWrite};
  //   ControlBusOut[8:0] = {PredictJump_2, rs1Fwd_2, rs2Fwd_2, ALuSrc_2, MemWrite_2, MemToReg_2, RegWrite_2}

  // Notes on the sheet:
  //   EN_低电平有效: pull=down
  //   保留引脚，自己决定是否使用
  //   PC、IR都应该一致传送，方便调试保留引脚，自己决定是否使用
  //   指令译码信号汇总在一起传输（bne，beq，jal，jalr，ecall，uret等）
  //   分线器已经设置好了，需要用的复制即可
  //   请将控制器输出的所有指令译码信号通过分线器汇总在一起后进行传输，后段需要使用的时候直接用分线器从多位宽线缆引出即可
  //   控制信号汇总在一起，预留了位宽，需要增加引脚可以利用剩余的线缆进行连接
endmodule

// EX/MEM
module EX_MEM (
  input  [31:0] PC,
  input  [31:0] AluResult,
  input  RegWrite,
  input  MemToReg,
  input  MemWrite,
  input  [31:0] WriteData,
  input  [31:0] IR,
  input  [31:0] Reserved1,
  input  [31:0] Reserved2,
  input  [4:0] WriteReg_num,
  input  [9:0] \指令译码信号 ,
  input  \气泡 ,
  input  \EN_低电平有效 ,
  input  CLK,
  output [31:0] PC_2,
  output [31:0] AluResult_2,
  output [31:0] WriteData_2,
  output [31:0] IR_2,
  output RegWrite_2,
  output MemToReg_2,
  output MemWrite_2,
  output [31:0] Reserved1_2,
  output [31:0] Reserved2_2,
  output [4:0] WriteReg_num_2,
  output [9:0] \指令译码信号_2 
);

  wire not_1_out;
  wire [4:0] multiplexer_8_out;
  wire [9:0] multiplexer_9_out;
  wire [15:0] multiplexer_7_out;
  wire [15:3] ControlBusIn, ControlBusOut;
  wire [31:0] multiplexer_1_out, multiplexer_2_out, multiplexer_3_out, multiplexer_4_out, multiplexer_5_out,
       multiplexer_6_out;

  Pull_Resistor pull_resistor_1 (.node({ControlBusIn, MemWrite, MemToReg, RegWrite}));
  Pull_Resistor pull_resistor_2 (.node(\指令译码信号 ));
  Pull_Resistor pull_resistor_3 (.node(\气泡 ));
  Multiplexer #(.width(32), .enable("false")) multiplexer_1 (
    .in0(PC), .in1({32{1'b0}}), .out(multiplexer_1_out), .sel(\气泡 ));
  Multiplexer #(.width(32), .enable("false")) multiplexer_2 (
    .in0(AluResult), .in1({32{1'b0}}), .out(multiplexer_2_out), .sel(\气泡 ));
  Multiplexer #(.width(32), .enable("false")) multiplexer_3 (
    .in0(WriteData), .in1({32{1'b0}}), .out(multiplexer_3_out), .sel(\气泡 ));
  Multiplexer #(.width(32), .enable("false")) multiplexer_4 (
    .in0(IR), .in1({32{1'b0}}), .out(multiplexer_4_out), .sel(\气泡 ));
  Multiplexer #(.width(32), .enable("false")) multiplexer_5 (
    .in0(Reserved1), .in1({32{1'b0}}), .out(multiplexer_5_out), .sel(\气泡 ));
  Multiplexer #(.width(32), .enable("false")) multiplexer_6 (
    .in0(Reserved2), .in1({32{1'b0}}), .out(multiplexer_6_out), .sel(\气泡 ));
  Multiplexer #(.width(16), .enable("false")) multiplexer_7 (
    .in0({ControlBusIn, MemWrite, MemToReg, RegWrite}), .in1({16{1'b0}}), .out(multiplexer_7_out), .sel(\气泡 ));
  Multiplexer #(.width(5), .enable("false")) multiplexer_8 (
    .in0(WriteReg_num), .in1({5{1'b0}}), .out(multiplexer_8_out), .sel(\气泡 ));
  Multiplexer #(.width(10), .enable("false")) multiplexer_9 (
    .in0(\指令译码信号 ), .in1({10{1'b0}}), .out(multiplexer_9_out), .sel(\气泡 ));
  not not_1 (not_1_out, \EN_低电平有效 );
  Pull_Resistor pull_resistor_4 (.node(\EN_低电平有效 ));
  Register #(.width(32)) u_PC (.D(multiplexer_1_out), .en(not_1_out), .Q(PC_2), .clk(CLK));  // open: clr
  Register #(.width(32)) register_1 (.D(multiplexer_2_out), .en(not_1_out), .Q(AluResult_2), .clk(CLK));  // open: clr
  Register #(.width(32)) register_2 (.D(multiplexer_3_out), .en(not_1_out), .Q(WriteData_2), .clk(CLK));  // open: clr
  Register #(.width(32)) register_3 (.D(multiplexer_4_out), .en(not_1_out), .Q(IR_2), .clk(CLK));  // open: clr
  Register #(.width(32)) register_4 (.D(multiplexer_5_out), .en(not_1_out), .Q(Reserved1_2), .clk(CLK));  // open: clr
  Register #(.width(32)) register_5 (.D(multiplexer_6_out), .en(not_1_out), .Q(Reserved2_2), .clk(CLK));  // open: clr
  Register #(.width(16)) register_6 (
    .D(multiplexer_7_out), .en(not_1_out), .Q({ControlBusOut, MemWrite_2, MemToReg_2, RegWrite_2}), .clk(CLK));  // open: clr
  Register #(.width(5)) register_7 (.D(multiplexer_8_out), .en(not_1_out), .Q(WriteReg_num_2), .clk(CLK));  // open: clr
  Register #(.width(10)) register_8 (.D(multiplexer_9_out), .en(not_1_out), .Q(\指令译码信号_2 ), .clk(CLK));  // open: clr

  // Other names for the same wires on the sheet: ControlBusIn[2:0] = {MemWrite, MemToReg, RegWrite};
  //   ControlBusOut[2:0] = {MemWrite_2, MemToReg_2, RegWrite_2}

  // Notes on the sheet:
  //   EN_低电平有效: pull=down
  //   保留引脚，自己决定是否使用
  //   PC、IR都应该一致传送，方便调试保留引脚，自己决定是否使用
  //   指令译码信号汇总在一起传输（bne，beq，jal，jalr，ecall，uret等）
  //   分线器已经设置好了，需要用的复制即可
  //   请将控制器输出的所有指令译码信号通过分线器汇总在一起后进行传输，后段需要使用的时候直接用分线器从多位宽线缆引出即可
endmodule

// MEM/WB
module MEM_WB (
  input  [31:0] PC,
  input  [31:0] AluResult,
  input  RegWrite,
  input  MemToReg,
  input  [31:0] MemData,
  input  [31:0] IR,
  input  [31:0] Reserved1,
  input  [31:0] Reserved2,
  input  [4:0] WriteReg_num,
  input  [9:0] \指令译码信号 ,
  input  \气泡 ,
  input  \EN_低电平有效 ,
  input  CLK,
  output [31:0] PC_2,
  output [31:0] AluResult_2,
  output [31:0] MemData_2,
  output [31:0] IR_2,
  output RegWrite_2,
  output MemToReg_2,
  output [31:0] Reserved1_2,
  output [31:0] Reserved2_2,
  output [4:0] WriteReg_num_2,
  output [9:0] \指令译码信号_2 
);

  wire not_1_out;
  wire [4:0] multiplexer_8_out;
  wire [9:0] multiplexer_9_out;
  wire [15:0] multiplexer_7_out;
  wire [15:2] ControlBusIn, ControlBusOut;
  wire [31:0] multiplexer_1_out, multiplexer_2_out, multiplexer_3_out, multiplexer_4_out, multiplexer_5_out,
       multiplexer_6_out;

  Pull_Resistor pull_resistor_1 (.node({ControlBusIn, MemToReg, RegWrite}));
  Pull_Resistor pull_resistor_2 (.node(\指令译码信号 ));
  Pull_Resistor pull_resistor_3 (.node(\气泡 ));
  Multiplexer #(.width(32), .enable("false")) multiplexer_1 (
    .in0(PC), .in1({32{1'b0}}), .out(multiplexer_1_out), .sel(\气泡 ));
  Multiplexer #(.width(32), .enable("false")) multiplexer_2 (
    .in0(AluResult), .in1({32{1'b0}}), .out(multiplexer_2_out), .sel(\气泡 ));
  Multiplexer #(.width(32), .enable("false")) multiplexer_3 (
    .in0(MemData), .in1({32{1'b0}}), .out(multiplexer_3_out), .sel(\气泡 ));
  Multiplexer #(.width(32), .enable("false")) multiplexer_4 (
    .in0(IR), .in1({32{1'b0}}), .out(multiplexer_4_out), .sel(\气泡 ));
  Multiplexer #(.width(32), .enable("false")) multiplexer_5 (
    .in0(Reserved1), .in1({32{1'b0}}), .out(multiplexer_5_out), .sel(\气泡 ));
  Multiplexer #(.width(32), .enable("false")) multiplexer_6 (
    .in0(Reserved2), .in1({32{1'b0}}), .out(multiplexer_6_out), .sel(\气泡 ));
  Multiplexer #(.width(16), .enable("false")) multiplexer_7 (
    .in0({ControlBusIn, MemToReg, RegWrite}), .in1({16{1'b0}}), .out(multiplexer_7_out), .sel(\气泡 ));
  Multiplexer #(.width(5), .enable("false")) multiplexer_8 (
    .in0(WriteReg_num), .in1({5{1'b0}}), .out(multiplexer_8_out), .sel(\气泡 ));
  Multiplexer #(.width(10), .enable("false")) multiplexer_9 (
    .in0(\指令译码信号 ), .in1({10{1'b0}}), .out(multiplexer_9_out), .sel(\气泡 ));
  not not_1 (not_1_out, \EN_低电平有效 );
  Pull_Resistor pull_resistor_4 (.node(\EN_低电平有效 ));
  Register #(.width(32)) u_PC (.D(multiplexer_1_out), .en(not_1_out), .Q(PC_2), .clk(CLK));  // open: clr
  Register #(.width(32)) register_1 (.D(multiplexer_2_out), .en(not_1_out), .Q(AluResult_2), .clk(CLK));  // open: clr
  Register #(.width(32)) register_2 (.D(multiplexer_3_out), .en(not_1_out), .Q(MemData_2), .clk(CLK));  // open: clr
  Register #(.width(32)) register_3 (.D(multiplexer_4_out), .en(not_1_out), .Q(IR_2), .clk(CLK));  // open: clr
  Register #(.width(32)) register_4 (.D(multiplexer_5_out), .en(not_1_out), .Q(Reserved1_2), .clk(CLK));  // open: clr
  Register #(.width(32)) register_5 (.D(multiplexer_6_out), .en(not_1_out), .Q(Reserved2_2), .clk(CLK));  // open: clr
  Register #(.width(16)) register_6 (
    .D(multiplexer_7_out), .en(not_1_out), .Q({ControlBusOut, MemToReg_2, RegWrite_2}), .clk(CLK));  // open: clr
  Register #(.width(5)) register_7 (.D(multiplexer_8_out), .en(not_1_out), .Q(WriteReg_num_2), .clk(CLK));  // open: clr
  Register #(.width(10)) register_8 (.D(multiplexer_9_out), .en(not_1_out), .Q(\指令译码信号_2 ), .clk(CLK));  // open: clr

  // Other names for the same wires on the sheet: ControlBusIn[1:0] = {MemToReg, RegWrite};
  //   ControlBusOut[1:0] = {MemToReg_2, RegWrite_2}

  // Notes on the sheet:
  //   EN_低电平有效: pull=down
  //   保留引脚，自己决定是否使用
  //   PC、IR都应该一致传送，方便调试保留引脚，自己决定是否使用
  //   指令译码信号汇总在一起传输（bne，beq，jal，jalr，ecall，uret等）
  //   分线器已经设置好了，需要用的复制即可
  //   请将控制器输出的所有指令译码信号通过分线器汇总在一起后进行传输，后段需要使用的时候直接用分线器从多位宽线缆引出即可
endmodule
