// Logisim project ping-pong.circ as structural Verilog: 5 circuits, main circuit main
module main (
);

  wire CLEAR, CLK, EXEC, FAULT, HALTED, KEY_ACK, KEY_CLEAR, KEY_DOWN, KEY_VALID, PCLK, PRESENT, RD, RESET,
       WR, WRITE;
  wire [2:0] KEY;
  wire [4:0] X, Y;
  wire [7:0] COLOR, KEY_HELD;
  wire [15:0] ADDR, DEBUG, PC, RDATA, WDATA;
  wire [31:0] INST;

  Clock #(.highDuration(1), .lowDuration(1)) CPU_clock (.out(CLK));
  Button u_RESET (.out(RESET));
  G16_CPU G16_CPU (
    .CLK(CLK), .RESET(RESET), .INST(INST), .RDATA(RDATA), .PC(PC), .ADDR(ADDR), .WDATA(WDATA), .RD(RD),
    .WR(WR), .HALTED(HALTED), .FAULT(FAULT), .EXEC(EXEC));
  ROM #(.addrWidth(16), .dataWidth(32), .Select("high")) Program_ROM___import__hex (.addr(PC), .data(INST), .sel(1'b1));
  // keyboard keyboard_1: pin names not known; wires that end beside it: CLK, KEY_ACK, KEY_CLEAR, KEY_HELD, KEY, KEY_DOWN, KEY_VALID
  G16_memory_and_IO G16_memory_and_IO (
    .CLK(CLK), .RESET(RESET), .ADDR(ADDR), .WDATA(WDATA), .WR(WR), .KEY_HELD(KEY_HELD), .KEY(KEY),
    .KEY_DOWN(KEY_DOWN), .KEY_VALID(KEY_VALID), .RDATA(RDATA), .X(X), .Y(Y), .COLOR(COLOR), .DEBUG(DEBUG),
    .KEY_ACK(KEY_ACK), .KEY_CLEAR(KEY_CLEAR), .WRITE(WRITE), .CLEAR(CLEAR), .PRESENT(PRESENT));
  not not_1 (PCLK, CLK);
  // framebuffer16 framebuffer16_1: pin names not known; wires that end beside it: PCLK, X, Y, COLOR, WRITE, CLEAR, PRESENT
  LED #(.active("true")) u_HALTED (.in(HALTED));
  // Probe on PC
  // Probe on DEBUG
  LED #(.active("true")) u_FAULT (.in(FAULT));

  // Notes on the sheet:
  //   G16 programmable computer / software controls keyboard and pixels
  //   Software in Program ROM / import another .hex and Reset to change programs
  //   4096 Hz Auto ticks. Poke keyboard; Space starts/pauses, Enter restarts games. Esc releases focus.
  //   Snake: arrows. Ping Pong: Up/Down left, Z/X right. Rules and controls are defined in .asm.
  //   contents of Program_ROM___import__hex (hex, n*v repeats v):
  //   8800000a 8800ff03 88000006 88000007 8800000b 8800000c 9000006 89000000 89000001 9000001 89000008
  //   89000004 89000005 9000008 89000002 89000003 9000001 8900000a a0000087 8100ff01 90200027 8800ff02
  //   6a200008 90400027 69200007 6220fffb 90400000 6220fffc 98400027 81000008 a000002 52280000 90400027
  //   79200001 89000008 8100ff20 89000009 af0000d6 a0000013 81000008 98200013 8100ff20 82000009 19280000
  //   a0000a0 51280000 98200013 81000000 8200ff00 af0000bc 89000000 81000001 8200ff00 b000006 424c0000
  //   af0000bc 89000001 8100000c 79200001 8900000c 98200087 81000002 82000003 83000004 84000005 12500000
  //   d000002 55540000 98a00048 d000010 55540000 98a0004c 1c100000 8c000005 82000003 12500000 112c0000
  //   90200051 6520fff1 90a0005b a000006b 85000000 56540000 98c00078 1e540000 d000004 55d40000 90a00078
  //   b000001 9000001 a0000064 85000001 56540000 98c0006e 1e540000 d000004 55d40000 90a0006e b00ffff
  //   900000e 8b000004 c000001 d000002 55d40000 90a0006a c00ffff 8c000005 89000002 8a000003 a0000087
  //   81000006 61200001 89000006 b000001 8b000004 6220fff9 98400081 9000002 89000008 a0000081 81000007
  //   61200001 89000007 b00ffff 8b000004 6220fff9 98400081 9000003 89000008 9000008 89000002 89000003
  //   9000001 89000005 8800000c 8800ff12 e000002 8e00ff13 e000001 8800ff10 a00001c 8a00ff12 81000000
  //   a000004 af0000c9 900000f 8900ff10 a000003 8a00ff12 81000001 a000004 af0000c9 81000002 8900ff10
  //   81000003 8900ff11 90000ff 82000008 6340fffe 986000a1 900001c 6340fffd 986000a4 9000003 8900ff12
  //   8e00ff13 8800ff11 a00001c 8a00ff12 9000000 82000006 b000001 af0000cf a000003 8a00ff12 900000f
  //   82000007 b00ffff af0000cf 9000004 8900ff13 8100000b 61200001 8900000b 8100ff20 89000009 af0000d6
  //   a0000013 6a400003 6340ffff 906000c5 6340fffe 986000c8 6320fff4 906000c8 61200001 b0e00000 6320fffe
  //   906000c8 6120ffff b0e00000 8900ff11 8e00ff13 61200001 6240ffff 984000c9 b0e00000 904000d5 8900ff10
  //   8e00ff13 112c0000 6240ffff a00000cf b0e00000 81000008 a00000c 39280000 82000006 b000008 3a4c0000
  //   29280000 82000007 29280000 8900ff30 b0e00000
endmodule

module G16_registers (
  input  CLK,
  input  RESET,
  input  WE,
  input  [2:0] DEST,
  input  [2:0] RA,
  input  [2:0] RB,
  input  [15:0] WDATA,
  output [15:0] A,
  output [15:0] B
);

  wire n1, n2, n6, n7, n9, n10, n12, n13, n15, n16, n18, n19, n21, n22;
  wire [15:0] n27, n28, n29, n30, n31, n32, n37, n38, n39, n40, n41, n42, r1, r2, r3, r4, r5, r6, r7;

  Register #(.width(16), .trigger("rising"), .Select("high")) u_r1 (
    .D(WDATA), .en(n2), .Q(r1), .clk(CLK), .clr(RESET), .cs(1'b1), .preset(1'b0));
  Register #(.width(16), .trigger("rising"), .Select("high")) u_r4 (
    .D(WDATA), .en(n13), .Q(r4), .clk(CLK), .clr(RESET), .cs(1'b1), .preset(1'b0));
  Comparator #(.width(3), .mode("unsigned")) comparator_1 (.a(DEST), .b(3'b111), .eq(n21));  // open: gt, lt
  and u_n22 (n22, WE, n21);
  Multiplexer #(.width(16), .select(1), .enable("false")) multiplexer_1 (
    .in0({16{1'b0}}), .in1(r1), .out(n37), .sel(RB[0]));
  Comparator #(.width(3), .mode("unsigned")) comparator_2 (.a(DEST), .b(3'b001), .eq(n1));  // open: gt, lt
  Comparator #(.width(3), .mode("unsigned")) comparator_3 (.a(DEST), .b(3'b100), .eq(n12));  // open: gt, lt
  Multiplexer #(.width(16), .select(1), .enable("false")) multiplexer_2 (.in0(r2), .in1(r3), .out(n38), .sel(RB[0]));
  and u_n2 (n2, WE, n1);
  and u_n13 (n13, WE, n12);
  Multiplexer #(.width(16), .select(1), .enable("false")) multiplexer_3 (.in0(n37), .in1(n38), .out(n39), .sel(RB[1]));
  Register #(.width(16), .trigger("rising"), .Select("high")) u_r5 (
    .D(WDATA), .en(n16), .Q(r5), .clk(CLK), .clr(RESET), .cs(1'b1), .preset(1'b0));
  Multiplexer #(.width(16), .select(1), .enable("false")) multiplexer_4 (
    .in0({16{1'b0}}), .in1(r1), .out(n27), .sel(RA[0]));
  Multiplexer #(.width(16), .select(1), .enable("false")) multiplexer_5 (.in0(r4), .in1(r5), .out(n40), .sel(RB[0]));
  Multiplexer #(.width(16), .select(1), .enable("false")) multiplexer_6 (.in0(r2), .in1(r3), .out(n28), .sel(RA[0]));
  Multiplexer #(.width(16), .select(1), .enable("false")) multiplexer_7 (.in0(r6), .in1(r7), .out(n41), .sel(RB[0]));
  Register #(.width(16), .trigger("rising"), .Select("high")) u_r2 (
    .D(WDATA), .en(n7), .Q(r2), .clk(CLK), .clr(RESET), .cs(1'b1), .preset(1'b0));
  Comparator #(.width(3), .mode("unsigned")) comparator_4 (.a(DEST), .b(3'b101), .eq(n15));  // open: gt, lt
  Multiplexer #(.width(16), .select(1), .enable("false")) multiplexer_8 (.in0(n27), .in1(n28), .out(n29), .sel(RA[1]));
  Multiplexer #(.width(16), .select(1), .enable("false")) multiplexer_9 (.in0(n40), .in1(n41), .out(n42), .sel(RB[1]));
  and u_n16 (n16, WE, n15);
  Multiplexer #(.width(16), .select(1), .enable("false")) multiplexer_10 (.in0(r4), .in1(r5), .out(n30), .sel(RA[0]));
  Multiplexer #(.width(16), .select(1), .enable("false")) multiplexer_11 (.in0(n39), .in1(n42), .out(B), .sel(RB[2]));
  Comparator #(.width(3), .mode("unsigned")) comparator_5 (.a(DEST), .b(3'b010), .eq(n6));  // open: gt, lt
  Register #(.width(16), .trigger("rising"), .Select("high")) u_r6 (
    .D(WDATA), .en(n19), .Q(r6), .clk(CLK), .clr(RESET), .cs(1'b1), .preset(1'b0));
  Multiplexer #(.width(16), .select(1), .enable("false")) multiplexer_12 (.in0(r6), .in1(r7), .out(n31), .sel(RA[0]));
  and u_n7 (n7, WE, n6);
  Multiplexer #(.width(16), .select(1), .enable("false")) multiplexer_13 (.in0(n30), .in1(n31), .out(n32), .sel(RA[1]));
  Register #(.width(16), .trigger("rising"), .Select("high")) u_r3 (
    .D(WDATA), .en(n10), .Q(r3), .clk(CLK), .clr(RESET), .cs(1'b1), .preset(1'b0));
  Comparator #(.width(3), .mode("unsigned")) comparator_6 (.a(DEST), .b(3'b110), .eq(n18));  // open: gt, lt
  Multiplexer #(.width(16), .select(1), .enable("false")) multiplexer_14 (.in0(n29), .in1(n32), .out(A), .sel(RA[2]));
  and u_n19 (n19, WE, n18);
  Comparator #(.width(3), .mode("unsigned")) comparator_7 (.a(DEST), .b(3'b011), .eq(n9));  // open: gt, lt
  Register #(.width(16), .trigger("rising"), .Select("high")) u_r7 (
    .D(WDATA), .en(n22), .Q(r7), .clk(CLK), .clr(RESET), .cs(1'b1), .preset(1'b0));
  and u_n10 (n10, WE, n9);

  // Other names for the same wires on the sheet: n33[15:0] = A; n43[15:0] = B; n25 = RA[0]; n24 = RA[1]; n23 = RA[2];
  //   n36 = RB[0]; n35 = RB[1]; n34 = RB[2]

  // Notes on the sheet:
  //   G16 registers / r0 is zero / two read ports, one write port
  //   Writable registers / simultaneous old-value reads
  //   Balanced read selection
endmodule

module G16_ALU (
  input  [4:0] OP,
  input  [15:0] A,
  input  [15:0] B,
  input  [15:0] IMM,
  output [15:0] RESULT
);

  wire n1, n3, n5, n7, n9, n11, n13, n15, n17, n19, n21, n23, n25, n27, n29, n40, n44;
  wire [15:0] n31, n32, n33, n34, n35, n36, n38, n39, n43, n46, n48, n49, n50, n51, n52, n53, n54, n55, n56,
       n57, n58, n59, n60, n61, n62, n63;

  assign n56 = A | B;  // OR_Gate n56, 16 bits wide
  Comparator #(.width(5), .mode("unsigned")) comparator_1 (.a(OP), .b(5'b00001), .eq(n1));  // open: gt, lt
  Comparator #(.width(5), .mode("unsigned")) comparator_2 (.a(OP), .b(5'b01000), .eq(n15));  // open: gt, lt
  Comparator #(.width(5), .mode("unsigned")) comparator_3 (.a(OP), .b(5'b01111), .eq(n29));  // open: gt, lt
  Multiplexer #(.width(16), .select(1), .enable("false")) multiplexer_1 (
    .in0(n39), .in1({{15{1'b0}}, n40}), .out(n43), .sel(n21));
  Multiplexer #(.width(16), .select(1), .enable("false")) multiplexer_2 (.in0(n55), .in1(n56), .out(n57), .sel(n9));
  Comparator #(.width(16), .mode("unsigned")) comparator_4 (.a(A), .b(B), .lt(n44));  // open: gt, eq
  assign n58 = A & B;  // AND_Gate n58, 16 bits wide
  Comparator #(.width(5), .mode("unsigned")) comparator_5 (.a(OP), .b(5'b00010), .eq(n3));  // open: gt, lt
  Comparator #(.width(5), .mode("unsigned")) comparator_6 (.a(OP), .b(5'b01001), .eq(n17));  // open: gt, lt
  assign n31 = A ^ IMM;  // XOR_Gate n31, 16 bits wide
  Multiplexer #(.width(16), .select(1), .enable("false")) multiplexer_3 (.in0(n57), .in1(n58), .out(n59), .sel(n7));
  Multiplexer #(.width(16), .select(1), .enable("false")) multiplexer_4 (
    .in0({16{1'b0}}), .in1(n31), .out(n32), .sel(n29));
  Multiplexer #(.width(16), .select(1), .enable("false")) multiplexer_5 (
    .in0(n43), .in1({{15{1'b0}}, n44}), .out(n46), .sel(n19));
  Subtractor #(.width(16)) subtractor_1 (.a(A), .b(B), .out(n60), .bin(1'b0));  // open: bout
  Comparator #(.width(5), .mode("unsigned")) comparator_7 (.a(OP), .b(5'b00011), .eq(n5));  // open: gt, lt
  Comparator #(.width(5), .mode("unsigned")) comparator_8 (.a(OP), .b(5'b01010), .eq(n19));  // open: gt, lt
  assign n33 = A | IMM;  // OR_Gate n33, 16 bits wide
  Multiplexer #(.width(16), .select(1), .enable("false")) multiplexer_6 (.in0(n59), .in1(n60), .out(n61), .sel(n5));
  Multiplexer #(.width(16), .select(1), .enable("false")) multiplexer_7 (.in0(n32), .in1(n33), .out(n34), .sel(n27));
  Shifter #(.width(16), .shift("ar")) shifter_1 (.in(A), .\dist (B[3:0]), .out(n48));
  Adder #(.width(16)) adder_1 (.a(A), .b(B), .out(n62), .cin(1'b0));  // open: cout
  Comparator #(.width(5), .mode("unsigned")) comparator_9 (.a(OP), .b(5'b00100), .eq(n7));  // open: gt, lt
  Comparator #(.width(5), .mode("unsigned")) comparator_10 (.a(OP), .b(5'b01011), .eq(n21));  // open: gt, lt
  assign n35 = A & IMM;  // AND_Gate n35, 16 bits wide
  Multiplexer #(.width(16), .select(1), .enable("false")) multiplexer_8 (.in0(n46), .in1(n48), .out(n49), .sel(n17));
  Multiplexer #(.width(16), .select(1), .enable("false")) multiplexer_9 (.in0(n61), .in1(n62), .out(n63), .sel(n3));
  Multiplexer #(.width(16), .select(1), .enable("false")) multiplexer_10 (.in0(n34), .in1(n35), .out(n36), .sel(n25));
  Shifter #(.width(16), .shift("lr")) shifter_2 (.in(A), .\dist (B[3:0]), .out(n50));
  Multiplexer #(.width(16), .select(1), .enable("false")) multiplexer_11 (.in0(n63), .in1(IMM), .out(RESULT), .sel(n1));
  Comparator #(.width(5), .mode("unsigned")) comparator_11 (.a(OP), .b(5'b00101), .eq(n9));  // open: gt, lt
  Comparator #(.width(5), .mode("unsigned")) comparator_12 (.a(OP), .b(5'b01100), .eq(n23));  // open: gt, lt
  Multiplexer #(.width(16), .select(1), .enable("false")) multiplexer_12 (.in0(n49), .in1(n50), .out(n51), .sel(n15));
  Adder #(.width(16)) adder_2 (.a(A), .b(IMM), .out(n38), .cin(1'b0));  // open: cout
  Shifter #(.width(16)) shifter_3 (.in(A), .\dist (B[3:0]), .out(n52));
  Comparator #(.width(5), .mode("unsigned")) comparator_13 (.a(OP), .b(5'b00110), .eq(n11));  // open: gt, lt
  Comparator #(.width(5), .mode("unsigned")) comparator_14 (.a(OP), .b(5'b01101), .eq(n25));  // open: gt, lt
  Multiplexer #(.width(16), .select(1), .enable("false")) multiplexer_13 (.in0(n36), .in1(n38), .out(n39), .sel(n23));
  Multiplexer #(.width(16), .select(1), .enable("false")) multiplexer_14 (.in0(n51), .in1(n52), .out(n53), .sel(n13));
  Comparator #(.width(16)) comparator_15 (.a(A), .b(B), .lt(n40));  // open: gt, eq
  assign n54 = A ^ B;  // XOR_Gate n54, 16 bits wide
  Comparator #(.width(5), .mode("unsigned")) comparator_16 (.a(OP), .b(5'b00111), .eq(n13));  // open: gt, lt
  Comparator #(.width(5), .mode("unsigned")) comparator_17 (.a(OP), .b(5'b01110), .eq(n27));  // open: gt, lt
  Multiplexer #(.width(16), .select(1), .enable("false")) multiplexer_15 (.in0(n53), .in1(n54), .out(n55), .sel(n11));

  // Other names for the same wires on the sheet: n47[3:0] = B[3:0]; n42[0] = n40; n45[0] = n44; n64[15:0] = RESULT

  // Notes on the sheet:
  //   G16 ALU / wrapping arithmetic / shifts use B[3:0]
  //   Operations / result selection
endmodule

module G16_CPU (
  input  CLK,
  input  RESET,
  input  [31:0] INST,
  input  [15:0] RDATA,
  output [15:0] PC,
  output [15:0] ADDR,
  output [15:0] WDATA,
  output RD,
  output WR,
  output HALTED,
  output FAULT,
  output EXEC
);

  wire n0, n1, n2, n3, n4, n7, n11, n15, n16, n20, n21, n23, n24, n26, n27, n29, n30, n32, n33, n35, n36,
       n38, n39, n41, n42, n44, n45, n47, n48, n52, n53, n55, n56, n58, n59, n61, n62, n64, n65, n67, n68,
       n72, n73, n75, n76, n80, n81, n83, n84, n88, n89, n91, n92, n93, n96, n97, n98, n99, n101, n103, n104,
       n106, n107, n109, n110, n112, n113, n115, n116, n118, n119, n121, n122, n124, n125, n127, n128, n130,
       n131, n133, n134, n136, n137, n139, n140, n142, n143, n145, n146, n148, n149, n150, n154, n163, n165,
       n167, n168, n170, n171, n172, n173, n175, n176, n177, n180, n181;
  wire [2:0] n156;
  wire [15:0] A, n158, n159, n160, n178, n179, RESULT;
  wire [31:0] ir, n9, n13, n18, n50, n70, n78, n86;

  Register #(.width(32), .trigger("rising"), .Select("high")) u_ir (
    .D(INST), .en(n4), .Q(ir), .clk(CLK), .clr(RESET), .cs(1'b1), .preset(1'b0));
  Comparator #(.width(32), .mode("unsigned")) comparator_1 (.a(n9), .b({32{1'b0}}), .eq(n11));  // open: gt, lt
  or u_n39 (n39, n36, n38);
  or u_n53 (n53, n48, n52);
  Comparator #(.width(32), .mode("unsigned")) comparator_2 (.a(n50), .b(32'h88000000), .eq(n67));  // open: gt, lt
  or u_n81 (n81, n76, n80);
  G16_registers G16_registers (
    .CLK(CLK), .RESET(RESET), .WE(n150), .DEST(ir[26:24]), .RA(ir[23:21]), .RB(n156), .WDATA(n160), .A(A),
    .B(WDATA));
  or u_n128 (n128, n125, n127);
  Comparator #(.width(5), .mode("unsigned")) comparator_3 (.a(ir[31:27]), .b(5'b01111), .eq(n142));  // open: gt, lt
  Multiplexer #(.width(3), .select(1), .enable("false")) multiplexer_1 (
    .in0(ir[20:18]), .in1(ir[26:24]), .out(n156), .sel(n154));
  G16_ALU G16_ALU (.OP(ir[31:27]), .A(A), .B(WDATA), .IMM(ir[15:0]), .RESULT(RESULT));
  Register #(.width(16), .trigger("rising"), .Select("high")) u_pc (
    .D(n179), .en(n181), .Q(PC), .clk(CLK), .clr(RESET), .cs(1'b1), .preset(1'b0));
  Comparator #(.width(5), .mode("unsigned")) comparator_4 (.a(ir[31:27]), .b(5'b10100), .eq(n175));  // open: gt, lt
  or u_n0 (n0, HALTED, FAULT);
  Comparator #(.width(32), .mode("unsigned")) comparator_5 (.a(n18), .b(32'h20000000), .eq(n26));  // open: gt, lt
  or u_n68 (n68, n65, n67);
  Comparator #(.width(5), .mode("unsigned")) comparator_6 (.a(ir[31:27]), .b({5{1'b1}}), .eq(n96));  // open: gt, lt
  Comparator #(.width(5), .mode("unsigned")) comparator_7 (.a(ir[31:27]), .b(5'b00001), .eq(n101));  // open: gt, lt
  Comparator #(.width(5), .mode("unsigned")) comparator_8 (.a(ir[31:27]), .b(5'b00110), .eq(n115));  // open: gt, lt
  or u_n143 (n143, n140, n142);
  or u_n176 (n176, n173, n175);
  or u_n1 (n1, n0, RESET);
  assign n13 = ir & 32'hf8ff0000;  // AND_Gate n13, 32 bits wide
  or u_n27 (n27, n24, n26);
  Comparator #(.width(32), .mode("unsigned")) comparator_9 (.a(n18), .b(32'h48000000), .eq(n41));  // open: gt, lt
  Comparator #(.width(32), .mode("unsigned")) comparator_10 (.a(n50), .b(32'h68000000), .eq(n55));  // open: gt, lt
  Comparator #(.width(32), .mode("unsigned")) comparator_11 (.a(n13), .b(32'ha8000000), .eq(n83));  // open: gt, lt
  and u_n97 (n97, n93, n96);
  or u_n116 (n116, n113, n115);
  Comparator #(.width(5), .mode("unsigned")) comparator_12 (.a(ir[31:27]), .b(5'b01011), .eq(n130));  // open: gt, lt
  Adder #(.width(16)) adder_1 (.a(PC), .b(16'h1), .out(n158), .cin(1'b0));  // open: cout
  Comparator #(.width(5), .mode("unsigned")) comparator_13 (.a(ir[31:27]), .b(5'b10110), .eq(n163));  // open: gt, lt
  or u_n177 (n177, n176, n148);
  not u_n2 (n2, n1);
  or u_n42 (n42, n39, n41);
  or u_n56 (n56, n53, n55);
  assign n70 = ir & 32'hff1f0000;  // AND_Gate n70, 32 bits wide
  or u_n84 (n84, n81, n83);
  Register #(.width(1), .trigger("rising"), .Select("high")) u_fault (
    .D(1'b1), .en(n99), .Q(FAULT), .clk(CLK), .clr(RESET), .cs(1'b1), .preset(1'b0));
  Comparator #(.width(5), .mode("unsigned")) comparator_14 (.a(ir[31:27]), .b(5'b00010), .eq(n103));  // open: gt, lt
  or u_n131 (n131, n128, n130);
  Comparator #(.width(5), .mode("unsigned")) comparator_15 (.a(ir[31:27]), .b(5'b10000), .eq(n145));  // open: gt, lt
  Multiplexer #(.width(16), .select(1), .enable("false")) multiplexer_2 (
    .in0(RESULT), .in1(n158), .out(n159), .sel(n148));
  Multiplexer #(.width(16), .select(1), .enable("false")) multiplexer_3 (
    .in0(n158), .in1(ir[15:0]), .out(n178), .sel(n177));
  not u_n3 (n3, EXEC);
  Comparator #(.width(32), .mode("unsigned")) comparator_16 (.a(n13), .b(32'h8000000), .eq(n15));  // open: gt, lt
  Comparator #(.width(32), .mode("unsigned")) comparator_17 (.a(n18), .b(32'h28000000), .eq(n29));  // open: gt, lt
  not u_n98 (n98, n92);
  or u_n104 (n104, n101, n103);
  Comparator #(.width(5), .mode("unsigned")) comparator_18 (.a(ir[31:27]), .b(5'b00111), .eq(n118));  // open: gt, lt
  or u_n146 (n146, n143, n145);
  Multiplexer #(.width(16), .select(1), .enable("false")) multiplexer_4 (
    .in0(n159), .in1(RDATA), .out(n160), .sel(n145));
  Comparator #(.width(5), .mode("unsigned")) comparator_19 (.a(ir[31:27]), .b(5'b10010), .eq(n165));  // open: gt, lt
  Multiplexer #(.width(16), .select(1), .enable("false")) multiplexer_5 (.in0(n178), .in1(A), .out(n179), .sel(n163));
  and u_n4 (n4, n2, n3);
  or u_n16 (n16, n11, n15);
  or u_n30 (n30, n27, n29);
  Comparator #(.width(32), .mode("unsigned")) comparator_20 (.a(n18), .b(32'h50000000), .eq(n44));  // open: gt, lt
  Comparator #(.width(32), .mode("unsigned")) comparator_21 (.a(n50), .b(32'h70000000), .eq(n58));  // open: gt, lt
  Comparator #(.width(32), .mode("unsigned")) comparator_22 (.a(n70), .b(32'h90000000), .eq(n72));  // open: gt, lt
  assign n86 = ir & 32'hff1fffff;  // AND_Gate n86, 32 bits wide
  and u_n99 (n99, n7, n98);
  or u_n119 (n119, n116, n118);
  Comparator #(.width(5), .mode("unsigned")) comparator_23 (.a(ir[31:27]), .b(5'b01100), .eq(n133));  // open: gt, lt
  not u_n180 (n180, n96);
  or u_n45 (n45, n42, n44);
  or u_n59 (n59, n56, n58);
  or u_n73 (n73, n68, n72);
  Comparator #(.width(5), .mode("unsigned")) comparator_24 (.a(ir[31:27]), .b(5'b00011), .eq(n106));  // open: gt, lt
  or u_n134 (n134, n131, n133);
  Comparator #(.width(5), .mode("unsigned")) comparator_25 (.a(ir[31:27]), .b(5'b10101), .eq(n148));  // open: gt, lt
  Comparator #(.width(16), .mode("unsigned")) comparator_26 (.a(A), .b({16{1'b0}}), .eq(n167));  // open: gt, lt
  and u_n181 (n181, n93, n180);
  assign n18 = ir & 32'hf803ffff;  // AND_Gate n18, 32 bits wide
  Comparator #(.width(32), .mode("unsigned")) comparator_27 (.a(n18), .b(32'h30000000), .eq(n32));  // open: gt, lt
  Comparator #(.width(32), .mode("unsigned")) comparator_28 (.a(n86), .b(32'hb0000000), .eq(n88));  // open: gt, lt
  or u_n107 (n107, n104, n106);
  Comparator #(.width(5), .mode("unsigned")) comparator_29 (.a(ir[31:27]), .b(5'b01000), .eq(n121));  // open: gt, lt
  or u_n149 (n149, n146, n148);
  and u_n168 (n168, n165, n167);
  Register #(.width(1), .trigger("rising"), .Select("high")) phase (
    .D(n3), .en(n2), .Q(EXEC), .clk(CLK), .clr(RESET), .cs(1'b1), .preset(1'b0));
  or u_n33 (n33, n30, n32);
  Comparator #(.width(32), .mode("unsigned")) comparator_30 (.a(n18), .b(32'h58000000), .eq(n47));  // open: gt, lt
  Comparator #(.width(32), .mode("unsigned")) comparator_31 (.a(n50), .b(32'h78000000), .eq(n61));  // open: gt, lt
  Comparator #(.width(32), .mode("unsigned")) comparator_32 (.a(n70), .b(32'h98000000), .eq(n75));  // open: gt, lt
  or u_n89 (n89, n84, n88);
  or u_n122 (n122, n119, n121);
  Comparator #(.width(5), .mode("unsigned")) comparator_33 (.a(ir[31:27]), .b(5'b01101), .eq(n136));  // open: gt, lt
  and u_n150 (n150, n93, n149);
  Adder #(.width(16)) adder_2 (.a(A), .b(ir[15:0]), .out(ADDR), .cin(1'b0));  // open: cout
  Register #(.width(1), .trigger("rising"), .Select("high")) u_halted (
    .D(1'b1), .en(n97), .Q(HALTED), .clk(CLK), .clr(RESET), .cs(1'b1), .preset(1'b0));
  Comparator #(.width(32), .mode("unsigned")) comparator_34 (.a(n18), .b(32'h10000000), .eq(n20));  // open: gt, lt
  or u_n48 (n48, n45, n47);
  or u_n62 (n62, n59, n61);
  or u_n76 (n76, n73, n75);
  Comparator #(.width(5), .mode("unsigned")) comparator_35 (.a(ir[31:27]), .b(5'b00100), .eq(n109));  // open: gt, lt
  or u_n137 (n137, n134, n136);
  Comparator #(.width(5), .mode("unsigned")) comparator_36 (.a(ir[31:27]), .b(5'b10011), .eq(n170));  // open: gt, lt
  and u_n7 (n7, n2, EXEC);
  or u_n21 (n21, n16, n20);
  Comparator #(.width(32), .mode("unsigned")) comparator_37 (.a(n18), .b(32'h38000000), .eq(n35));  // open: gt, lt
  Comparator #(.width(32), .mode("unsigned")) comparator_38 (.a(n9), .b(32'hf8000000), .eq(n91));  // open: gt, lt
  or u_n110 (n110, n107, n109);
  Comparator #(.width(5), .mode("unsigned")) comparator_39 (.a(ir[31:27]), .b(5'b01001), .eq(n124));  // open: gt, lt
  not u_n171 (n171, n167);
  or u_n36 (n36, n33, n35);
  assign n50 = ir & 32'hf81f0000;  // AND_Gate n50, 32 bits wide
  Comparator #(.width(32), .mode("unsigned")) comparator_40 (.a(n50), .b(32'h80000000), .eq(n64));  // open: gt, lt
  assign n78 = ir & 32'hffff0000;  // AND_Gate n78, 32 bits wide
  or u_n92 (n92, n89, n91);
  or u_n125 (n125, n122, n124);
  Comparator #(.width(5), .mode("unsigned")) comparator_41 (.a(ir[31:27]), .b(5'b01110), .eq(n139));  // open: gt, lt
  and u_n172 (n172, n170, n171);
  and n183 (RD, n93, n145);
  assign n9 = ir & {32{1'b1}};  // AND_Gate n9, 32 bits wide
  Comparator #(.width(32), .mode("unsigned")) comparator_42 (.a(n18), .b(32'h18000000), .eq(n23));  // open: gt, lt
  or u_n65 (n65, n62, n64);
  and u_n93 (n93, n7, n92);
  Comparator #(.width(5), .mode("unsigned")) comparator_43 (.a(ir[31:27]), .b(5'b00101), .eq(n112));  // open: gt, lt
  or u_n140 (n140, n137, n139);
  Comparator #(.width(5), .mode("unsigned")) comparator_44 (.a(ir[31:27]), .b(5'b10001), .eq(n154));  // open: gt, lt
  or u_n173 (n173, n168, n172);
  or u_n24 (n24, n21, n23);
  Comparator #(.width(32), .mode("unsigned")) comparator_45 (.a(n18), .b(32'h40000000), .eq(n38));  // open: gt, lt
  Comparator #(.width(32), .mode("unsigned")) comparator_46 (.a(n50), .b(32'h60000000), .eq(n52));  // open: gt, lt
  Comparator #(.width(32), .mode("unsigned")) comparator_47 (.a(n78), .b(32'ha0000000), .eq(n80));  // open: gt, lt
  or u_n113 (n113, n110, n112);
  Comparator #(.width(5), .mode("unsigned")) comparator_48 (.a(ir[31:27]), .b(5'b01010), .eq(n127));  // open: gt, lt
  and n184 (WR, n93, n154);

  // Other names for the same wires on the sheet: B[15:0] = WDATA; n161[15:0] = ir[15:0]; n155[2:0] = ir[20:18];
  //   n152[2:0] = ir[23:21]; n151[2:0] = ir[26:24]; n94[4:0] = ir[31:27]; n182[15:0] = ADDR; n183 = RD; n184 = WR;
  //   phase = EXEC

  // Notes on the sheet:
  //   G16 v1 / fetch and execute / 16-bit data, 32-bit instructions
  //   1. Instruction register / phase / checked decoding
  //   2. Register file and combinational ALU
  //   3. ALU / address generation
  //   4. Program counter / branches / external bus
endmodule

module G16_memory_and_IO (
  input  CLK,
  input  RESET,
  input  [15:0] ADDR,
  input  [15:0] WDATA,
  input  WR,
  input  [7:0] KEY_HELD,
  input  [2:0] KEY,
  input  KEY_DOWN,
  input  KEY_VALID,
  output [15:0] RDATA,
  output [4:0] X,
  output [4:0] Y,
  output [7:0] COLOR,
  output [15:0] DEBUG,
  output KEY_ACK,
  output KEY_CLEAR,
  output WRITE,
  output CLEAR,
  output PRESENT
);

  wire key_clear_t, n2, n3, n6, n7, n10, n11, n14, n15, n18, n19, n22, n23, n25, n26, n31, n32, n34, n35,
       n39, n41, n43, n45;
  wire [2:0] n29;
  wire [2:1] command;
  wire [15:0] n37, n47, n48, n49, n52, n55, n57, n61, n63, RAM, random, timer;

  RAM #(.addrWidth(12), .dataWidth(16), .Select("high"), .simpleMode("false"), .bus("separate")) u_RAM (
    .addr(ADDR[11:0]), .din(WDATA), .data(RAM), .str(n7), .sel(1'b1), .clk(CLK), .clr(RESET));  // open: ld
  Register #(.width(5), .trigger("rising"), .Select("high")) u_x (
    .D(WDATA[4:0]), .en(n11), .Q(X), .clk(CLK), .clr(RESET), .cs(1'b1), .preset(1'b0));
  and u_n19 (n19, n3, n18);
  Register #(.width(16), .trigger("rising"), .Select("high")) u_timer (
    .D(n37), .en(1'b1), .Q(timer), .clk(CLK), .clr(RESET), .cs(1'b1), .preset(1'b0));
  Multiplexer #(.width(16), .select(1), .enable("false")) multiplexer_1 (
    .in0(n49), .in1({{8{1'b0}}, COLOR}), .out(n52), .sel(n18));
  Register #(.width(16), .trigger("rising"), .Select("high")) u_debug (
    .D(WDATA), .en(n23), .Q(DEBUG), .clk(CLK), .clr(RESET), .cs(1'b1), .preset(1'b0));
  Comparator #(.width(16), .mode("unsigned")) comparator_1 (.a(ADDR), .b(16'hff02), .eq(n31));  // open: gt, lt
  Comparator #(.width(16), .mode("unsigned")) comparator_2 (.a(ADDR), .b(16'hff00), .eq(n39));  // open: gt, lt
  and u_n32 (n32, n3, n31);
  Adder #(.width(16)) adder_1 (.a(timer), .b(16'h1), .out(n37), .cin(1'b0));  // open: cout
  not u_n2 (n2, RESET);
  Comparator #(.width(16), .mode("unsigned")) comparator_3 (.a(ADDR), .b(16'hff10), .eq(n10));  // open: gt, lt
  Register #(.width(1), .trigger("rising"), .Select("high")) u_key_clear (
    .D(n35), .en(1'b1), .Q(key_clear_t), .clk(CLK), .clr(RESET), .cs(1'b1), .preset(1'b0));
  Random #(.width(16), .trigger("rising"), .seed(12345)) u_random (.clk(CLK), .next(1'b1), .out(random), .clr(RESET));
  Comparator #(.width(16), .mode("unsigned")) comparator_4 (.a(ADDR), .b(16'hff01), .eq(n41));  // open: gt, lt
  Multiplexer #(.width(16), .select(1), .enable("false")) multiplexer_2 (
    .in0(n52), .in1({{11{1'b0}}, Y}), .out(n55), .sel(n14));
  and u_n3 (n3, WR, n2);
  and u_n11 (n11, n3, n10);
  Comparator #(.width(16), .mode("unsigned")) comparator_5 (.a(ADDR), .b(16'hff30), .eq(n22));  // open: gt, lt
  and u_n23 (n23, n3, n22);
  Comparator #(.width(16), .mode("unsigned")) comparator_6 (.a(ADDR), .b(16'hff03), .eq(n34));  // open: gt, lt
  Comparator #(.width(16), .mode("unsigned")) comparator_7 (.a(ADDR), .b(16'hff20), .eq(n43));  // open: gt, lt
  Multiplexer #(.width(16), .select(1), .enable("false")) multiplexer_3 (
    .in0(n55), .in1({{11{1'b0}}, X}), .out(n57), .sel(n10));
  or n65 (KEY_CLEAR, key_clear_t, RESET);
  Register #(.width(5), .trigger("rising"), .Select("high")) u_y (
    .D(WDATA[4:0]), .en(n15), .Q(Y), .clk(CLK), .clr(RESET), .cs(1'b1), .preset(1'b0));
  Register #(.width(3), .trigger("rising"), .Select("high")) u_command (
    .D(n29), .en(1'b1), .Q({command, WRITE}), .clk(CLK), .clr(RESET), .cs(1'b1), .preset(1'b0));
  and u_n35 (n35, n3, n34);
  Comparator #(.width(4), .mode("unsigned")) comparator_8 (.a(ADDR[15:12]), .b(4'b0000), .eq(n6));  // open: gt, lt
  Comparator #(.width(16), .mode("unsigned")) comparator_9 (.a(ADDR), .b(16'hff21), .eq(n45));  // open: gt, lt
  and u_n7 (n7, n3, n6);
  Comparator #(.width(16), .mode("unsigned")) comparator_10 (.a(ADDR), .b(16'hff11), .eq(n14));  // open: gt, lt
  Comparator #(.width(16), .mode("unsigned")) comparator_11 (.a(ADDR), .b(16'hff13), .eq(n25));  // open: gt, lt
  and u_n15 (n15, n3, n14);
  and u_n26 (n26, n3, n25);
  Multiplexer #(.width(16), .select(1), .enable("false")) multiplexer_4 (
    .in0({16{1'b0}}), .in1(DEBUG), .out(n47), .sel(n22));
  Multiplexer #(.width(16), .select(1), .enable("false")) multiplexer_5 (
    .in0(n57), .in1({KEY_VALID, {11{1'b0}}, KEY_DOWN, KEY}), .out(n61), .sel(n41));
  Register #(.width(8), .trigger("rising"), .Select("high")) u_color (
    .D(WDATA[7:0]), .en(n19), .Q(COLOR), .clk(CLK), .clr(RESET), .cs(1'b1), .preset(1'b0));
  Multiplexer #(.width(16), .select(1), .enable("false")) multiplexer_6 (.in0(n47), .in1(random), .out(n48), .sel(n45));
  or n68 (CLEAR, command[1], RESET);
  Multiplexer #(.width(16), .select(1), .enable("false")) multiplexer_7 (.in0(n48), .in1(timer), .out(n49), .sel(n43));
  Multiplexer #(.width(16), .select(1), .enable("false")) multiplexer_8 (
    .in0(n61), .in1({{8{1'b0}}, KEY_HELD}), .out(n63), .sel(n39));
  Multiplexer #(.width(3), .select(1), .enable("false")) multiplexer_9 (
    .in0(3'b000), .in1(WDATA[2:0]), .out(n29), .sel(n26));
  Multiplexer #(.width(16), .select(1), .enable("false")) multiplexer_10 (.in0(n63), .in1(RAM), .out(RDATA), .sel(n6));
  Comparator #(.width(16), .mode("unsigned")) comparator_12 (.a(ADDR), .b(16'hff12), .eq(n18));  // open: gt, lt
  Register #(.width(1), .trigger("rising"), .Select("high")) u_key_ack (
    .D(n32), .en(1'b1), .Q(KEY_ACK), .clk(CLK), .clr(RESET), .cs(1'b1), .preset(1'b0));
  or n70 (PRESENT, command[2], RESET);

  // Other names for the same wires on the sheet: n0[11:0] = ADDR[11:0]; n4[3:0] = ADDR[15:12]; command[0] = WRITE;
  //   n66 = WRITE; n67 = command[1]; n69 = command[2]; n51[7:0] = COLOR; n54[4:0] = Y; n56[4:0] = X;
  //   n58[3:0] = {KEY_DOWN, KEY}; n59[3:0] = {KEY_DOWN, KEY}; n60 (some bits) = {KEY_VALID, KEY_DOWN, KEY};
  //   n62[7:0] = KEY_HELD; n64[15:0] = RDATA; n65 = KEY_CLEAR; n68 = CLEAR; n70 = PRESENT; n8[4:0] = WDATA[4:0];
  //   n16[7:0] = WDATA[7:0]; n20[15:0] = WDATA; n28[2:0] = WDATA[2:0]

  // Notes on the sheet:
  //   G16 bus / RAM 0000-0fff / IO ff00-ff30 / unmapped reads zero
  //   1. Data RAM / 4096 x 16 / reset clears contents
  //   2. Peripheral registers / command strobes held for one cycle
  //   3. Cycle counter and random source
  //   4. Read bus / display and keyboard interface
endmodule
