// Logisim project snake.circ as structural Verilog: 2 circuits, main circuit main
module main (
);

  wire CLEAR, CLK, DEAD, DOWN, PAUSED, PRESENT, READ, RESET, VALID, WON, WRITE;
  wire [2:0] KEY;
  wire [4:0] X, Y;
  wire [7:0] COLOR, SCORE;

  // keyboard keyboard_1: pin names not known; wires that end beside it: CLK, READ, RESET, KEY, DOWN, VALID
  Clock #(.highDuration(1), .lowDuration(1)) System_clock (.out(CLK));
  // framebuffer16 framebuffer16_1: pin names not known; wires that end beside it: CLK, X, Y, COLOR, WRITE, CLEAR, PRESENT
  LED #(.active("true")) u_PAUSED (.in(PAUSED));
  // Probe on SCORE
  LED #(.active("true")) u_DEAD (.in(DEAD));
  LED #(.active("true")) u_WON (.in(WON));
  Snake_engine snake_engine_1 (
    .CLK(CLK), .KEY(KEY), .DOWN(DOWN), .VALID(VALID), .READ(READ), .RESET(RESET), .X(X), .Y(Y),
    .COLOR(COLOR), .WRITE(WRITE), .CLEAR(CLEAR), .PRESENT(PRESENT), .PAUSED(PAUSED), .DEAD(DEAD), .WON(WON),
    .SCORE(SCORE));

  // Notes on the sheet:
  //   SNAKE / keyboard + pixel display plugins
  //   Poke the keyboard · Arrows: turn · Space: pause · Enter: restart
  //   Enable Auto ticks at 1024 Hz (about 7 moves/s). Escape releases keyboard focus.
  //   Green: snake · Red: food · Walls and body collisions end the game
  //   Snake memory is runtime-only. Reset or Enter starts a fresh game.
  //   Open Snake engine in circuit tree
endmodule

module Snake_engine (
  input  CLK,
  input  [2:0] KEY,
  input  DOWN,
  input  VALID,
  output READ,
  output RESET,
  output [4:0] X,
  output [4:0] Y,
  output [7:0] COLOR,
  output WRITE,
  output CLEAR,
  output PRESENT,
  output PAUSED,
  output DEAD,
  output WON,
  output [7:0] SCORE
);

  wire ate, n1, n4, n7, n8, n9, n10, n11, n13, n14, n15, n17, n19, n21, n29, n30, n32, n33, n34, n35, n36,
       n37, n43, n45, n46, n48, n49, n50, n51, n52, n53, n54, n55, n57, n58, n59, n61, n62, n63, n64, n69,
       n70, n71, n72, n79, n80, n88, n90, n91, n93, n94, n95, n96, n97, n98, n99, n100, n101, n102, n103,
       n104, n105, n106, n107, n108, n109, n110, n113, n114, n119, n120, n125, n126, n131, n133, n135, n140,
       n141, n142, n144, n147, n148, n150, n151, n152, n154, n155, n157, n159, n160, n161, n162, n163, n165,
       n167, n169, n182, n196, n201, n202, n205, occupied, turn_lock;
  wire [1:0] dir, n24, n26, n28, n31, n47;
  wire [3:0] n75, n76, n77, n78, n82, n83, n84, n85;
  wire [4:0] n170, n171, n172, n173, n174, n175, n176, n177, n178, n179, n180, n183, n184, n185, n186, n187,
       n188, n189, phase;
  wire [7:0] body, candidate, food, head, init_idx, initial_cell, n67, n68, n111, n121, n123, n124, n127,
       n128, n129, n130, n136, n137, n138, n139, n145, n146, n149, n190, n198, next_head, old_tail, random,
       tail_ptr, timer, tries, write_ptr;
  wire [8:0] length, n116, n118, n206;

  Register #(.width(1), .trigger("rising"), .Select("high")) ack (
    .D(n37), .en(1'b1), .Q(READ), .clk(CLK), .clr(CLEAR), .cs(1'b1), .preset(1'b0));
  not u_n13 (n13, KEY[2]);
  Comparator #(.width(5), .mode("unsigned")) comparator_1 (.a(phase), .b({5{1'b0}}), .eq(CLEAR));  // open: gt, lt
  and u_n52 (n52, n51, n9);
  or u_n64 (n64, n62, n54);
  Register #(.width(8), .trigger("rising"), .Select("high")) u_next_head (
    .D({n85, n78}), .en(n110), .Q(next_head), .clk(CLK), .clr(CLEAR), .cs(1'b1), .preset(1'b0));
  Adder #(.width(4)) adder_1 (.a(head[7:4]), .b(4'b0001), .out(n84), .cin(1'b0));  // open: cout
  or u_n98 (n98, n95, n97);
  Register #(.width(1), .trigger("rising"), .Select("high")) u_ate (
    .D(n103), .en(n110), .Q(ate), .clk(CLK), .clr(CLEAR), .cs(1'b1), .preset(1'b0));
  Adder #(.width(8)) adder_2 (.a(write_ptr), .b(8'h1), .out(n121), .cin(1'b0));  // open: cout
  ROM #(.addrWidth(8), .dataWidth(8), .Select("high")) Initial_path__tail_to_head (
    .addr(init_idx), .data(initial_cell), .sel(1'b1));
  Multiplexer #(.width(8), .select(1), .enable("false")) multiplexer_1 (
    .in0(n136), .in1({n85, n78}), .out(n137), .sel(n88));
  Random #(.width(8), .trigger("rising"), .seed(12345)) u_random (.clk(CLK), .next(1'b1), .out(random), .clr(CLEAR));
  Register #(.width(5), .trigger("rising"), .Select("high")) u_phase (
    .D(n189), .en(1'b1), .Q(phase), .clk(CLK), .clr(1'b0), .cs(1'b1), .preset(1'b0));
  Multiplexer #(.width(5), .select(1), .enable("false")) multiplexer_2 (
    .in0(n179), .in1(5'b00111), .out(n180), .sel(n157));
  and u_n14 (n14, n11, n13);
  Multiplexer #(.width(2), .select(1), .enable("false")) multiplexer_3 (.in0(n26), .in1(2'b11), .out(n28), .sel(n17));
  not u_n53 (n53, turn_lock);
  Register #(.width(8), .trigger("rising"), .Select("high")) u_timer (
    .D(n68), .en(n70), .Q(timer), .clk(CLK), .clr(CLEAR), .cs(1'b1), .preset(1'b0));
  Comparator #(.width(2), .mode("unsigned")) comparator_2 (.a(dir), .b(2'b00), .eq(n71));  // open: gt, lt
  Multiplexer #(.width(4), .select(1), .enable("false")) multiplexer_4 (.in0(n83), .in1(n84), .out(n85), .sel(n79));
  Comparator #(.width(4), .mode("unsigned")) comparator_3 (.a(head[7:4]), .b(4'b0000), .eq(n99));  // open: gt, lt
  Register #(.width(8), .trigger("rising"), .Select("high")) u_head (
    .D(n111), .en(n114), .Q(head), .clk(CLK), .clr(CLEAR), .cs(1'b1), .preset(1'b0));
  Register #(.width(8), .trigger("rising"), .Select("high")) u_init_idx (
    .D(n127), .en(n43), .Q(init_idx), .clk(CLK), .clr(CLEAR), .cs(1'b1), .preset(1'b0));
  Multiplexer #(.width(8), .select(1), .enable("false")) multiplexer_5 (
    .in0(n137), .in1(candidate), .out(n138), .sel(n133));
  Register #(.width(8), .trigger("rising"), .Select("high")) u_candidate (
    .D(n146), .en(n148), .Q(candidate), .clk(CLK), .clr(CLEAR), .cs(1'b1), .preset(1'b0));
  Comparator #(.width(5), .mode("unsigned")) comparator_4 (.a(phase), .b(5'b01100), .eq(n167));  // open: gt, lt
  or n204 (PRESENT, n61, n165);
  Comparator #(.width(5), .mode("unsigned")) comparator_5 (.a(phase), .b(5'b01000), .eq(n1));  // open: gt, lt
  and u_n15 (n15, n14, DOWN);
  Comparator #(.width(2), .mode("unsigned")) comparator_6 (.a(n28), .b(dir), .eq(n29));  // open: gt, lt
  and u_n54 (n54, n52, n53);
  Comparator #(.width(2), .mode("unsigned")) comparator_7 (.a(dir), .b(2'b10), .eq(n72));  // open: gt, lt
  and u_n100 (n100, n80, n99);
  Multiplexer #(.width(8), .select(1), .enable("false")) multiplexer_6 (
    .in0(next_head), .in1(initial_cell), .out(n111), .sel(n46));
  Multiplexer #(.width(8), .select(1), .enable("false")) multiplexer_7 (.in0(n121), .in1(8'h3), .out(n123), .sel(n46));
  Adder #(.width(8)) adder_3 (.a(init_idx), .b(8'h1), .out(n127), .cin(1'b0));  // open: cout
  Multiplexer #(.width(8), .select(1), .enable("false")) multiplexer_8 (
    .in0(n138), .in1(initial_cell), .out(n139), .sel(n43));
  Comparator #(.width(3), .mode("unsigned")) comparator_8 (.a(KEY), .b(3'b101), .eq(n154));  // open: gt, lt
  Comparator #(.width(8), .mode("unsigned")) comparator_9 (.a(tries), .b({8{1'b1}}), .eq(n182));  // open: gt, lt
  not u_n30 (n30, n29);
  Register #(.width(2), .trigger("rising"), .Select("high")) u_dir (
    .D(n47), .en(n55), .Q(dir), .clk(CLK), .clr(CLEAR), .cs(1'b1), .preset(1'b0));
  or u_n55 (n55, n46, n54);
  or u_n101 (n101, n98, n100);
  Register #(.width(8), .trigger("rising"), .Select("high")) u_tail_ptr (
    .D(n124), .en(n126), .Q(tail_ptr), .clk(CLK), .clr(CLEAR), .cs(1'b1), .preset(1'b0));
  RAM #(.addrWidth(8), .dataWidth(8), .Select("high"), .simpleMode("false"), .bus("separate")) u_body (
    .addr(n129), .din(n130), .data(body), .str(n131), .sel(1'b1), .clk(CLK), .clr(CLEAR));  // open: ld
  Multiplexer #(.width(1), .select(1), .enable("false")) multiplexer_9 (.in0(1'b1), .in1(1'b0), .out(n140), .sel(n135));
  Comparator #(.width(5), .mode("unsigned")) comparator_10 (.a(phase), .b(5'b00100), .eq(n144));  // open: gt, lt
  and u_n155 (n155, n48, n154);
  Comparator #(.width(9), .mode("unsigned")) comparator_11 (.a(length), .b(9'h100), .eq(n169));  // open: gt, lt
  Multiplexer #(.width(5), .select(1), .enable("false")) multiplexer_10 (
    .in0(5'b00101), .in1(5'b01101), .out(n183), .sel(n182));
  Comparator #(.width(5), .mode("unsigned")) comparator_12 (.a(phase), .b(5'b10000), .eq(DEAD));  // open: gt, lt
  Comparator #(.width(3), .mode("unsigned")) comparator_13 (.a(KEY), .b(3'b000), .eq(n17));  // open: gt, lt
  assign n31 = dir ^ 2'b10;  // XOR_Gate n31, 2 bits wide
  Register #(.width(1), .trigger("rising"), .Select("high")) u_paused (
    .D(n9), .en(n59), .Q(PAUSED), .clk(CLK), .clr(CLEAR), .cs(1'b1), .preset(1'b0));
  Adder #(.width(8)) adder_4 (.a(timer), .b(8'h1), .out(n67), .cin(1'b0));  // open: cout
  Comparator #(.width(5), .mode("unsigned")) comparator_14 (.a(phase), .b(5'b01001), .eq(n88));  // open: gt, lt
  Comparator #(.width(8), .mode("unsigned")) comparator_15 (.a({n85, n78}), .b(body), .eq(n102));  // open: gt, lt
  Comparator #(.width(5), .mode("unsigned")) comparator_16 (.a(phase), .b(5'b01011), .eq(n113));  // open: gt, lt
  Adder #(.width(8)) adder_5 (.a(tail_ptr), .b(8'h1), .out(n124), .cin(1'b0));  // open: cout
  Multiplexer #(.width(8), .select(1), .enable("false")) multiplexer_11 (
    .in0(tail_ptr), .in1(write_ptr), .out(n128), .sel(n113));
  and u_n141 (n141, n135, n125);
  Adder #(.width(8)) adder_6 (.a(candidate), .b(8'h1), .out(n145), .cin(1'b0));  // open: cout
  Multiplexer #(.width(5), .select(1), .enable("false")) multiplexer_12 (
    .in0(5'b00100), .in1(5'b01101), .out(n170), .sel(n169));
  Multiplexer #(.width(5), .select(1), .enable("false")) multiplexer_13 (
    .in0(5'b00110), .in1(n183), .out(n184), .sel(occupied));
  or u_n196 (n196, CLEAR, n135);
  or u_n4 (n4, n1, DEAD);
  Comparator #(.width(2), .mode("unsigned")) comparator_17 (.a(n28), .b(n31), .eq(n32));  // open: gt, lt
  Comparator #(.width(5), .mode("unsigned")) comparator_18 (.a(phase), .b(5'b00001), .eq(n43));  // open: gt, lt
  Multiplexer #(.width(8), .select(1), .enable("false")) multiplexer_14 (
    .in0({8{1'b0}}), .in1(n67), .out(n68), .sel(n1));
  Subtractor #(.width(4)) subtractor_1 (.a(head[3:0]), .b(4'b0001), .out(n75), .bin(1'b0));  // open: bout
  Comparator #(.width(8), .mode("unsigned")) comparator_19 (.a({n85, n78}), .b(food), .eq(n103));  // open: gt, lt
  or u_n114 (n114, n46, n113);
  not u_n125 (n125, ate);
  Multiplexer #(.width(8), .select(1), .enable("false")) multiplexer_15 (
    .in0(n128), .in1(init_idx), .out(n129), .sel(n43));
  or u_n142 (n142, n131, n141);
  Multiplexer #(.width(8), .select(1), .enable("false")) multiplexer_16 (
    .in0(n145), .in1(random), .out(n146), .sel(n144));
  Comparator #(.width(5), .mode("unsigned")) comparator_20 (.a(phase), .b(5'b00110), .eq(n157));  // open: gt, lt
  Multiplexer #(.width(5), .select(1), .enable("false")) multiplexer_17 (
    .in0(5'b00111), .in1(n170), .out(n171), .sel(ate));
  Multiplexer #(.width(5), .select(1), .enable("false")) multiplexer_18 (
    .in0(n180), .in1(n184), .out(n185), .sel(n133));
  Comparator #(.width(3), .mode("unsigned")) comparator_21 (.a(KEY), .b(3'b001), .eq(n19));  // open: gt, lt
  not u_n33 (n33, n32);
  Comparator #(.width(3), .mode("unsigned")) comparator_22 (.a(KEY), .b(3'b100), .eq(n57));  // open: gt, lt
  not u_n69 (n69, n1);
  Multiplexer #(.width(4), .select(1), .enable("false")) multiplexer_19 (
    .in0(head[3:0]), .in1(n75), .out(n76), .sel(n72));
  Comparator #(.width(4), .mode("unsigned")) comparator_23 (.a(head[3:0]), .b(4'b1111), .eq(n90));  // open: gt, lt
  not u_n104 (n104, n103);
  Register #(.width(9), .trigger("rising"), .Select("high")) u_length (
    .D(n118), .en(n120), .Q(length), .clk(CLK), .clr(CLEAR), .cs(1'b1), .preset(1'b0));
  and u_n126 (n126, n113, n125);
  Multiplexer #(.width(8), .select(1), .enable("false")) multiplexer_20 (
    .in0(next_head), .in1(initial_cell), .out(n130), .sel(n43));
  and u_n147 (n147, n133, occupied);
  Multiplexer #(.width(5), .select(1), .enable("false")) multiplexer_21 (
    .in0(phase), .in1(n171), .out(n172), .sel(n167));
  Multiplexer #(.width(5), .select(1), .enable("false")) multiplexer_22 (
    .in0(n185), .in1(5'b00101), .out(n186), .sel(n144));
  Multiplexer #(.width(8), .select(1), .enable("false")) multiplexer_23 (
    .in0(8'h1c), .in1({8{1'b0}}), .out(n198), .sel(n196));
  or u_n205 (n205, CLEAR, n43);
  Comparator #(.width(5), .mode("unsigned")) comparator_24 (.a(phase), .b(5'b01111), .eq(WON));  // open: gt, lt
  and u_n34 (n34, n30, n33);
  Comparator #(.width(8), .mode("unsigned")) comparator_25 (.a(init_idx), .b(8'h2), .eq(n45));  // open: gt, lt
  and u_n58 (n58, n48, n57);
  or u_n70 (n70, n9, n69);
  Adder #(.width(4)) adder_7 (.a(head[3:0]), .b(4'b0001), .out(n77), .cin(1'b0));  // open: cout
  and u_n91 (n91, n71, n90);
  and u_n105 (n105, n102, n104);
  or u_n131 (n131, n43, n113);
  or u_n148 (n148, n144, n147);
  Comparator #(.width(8), .mode("unsigned")) comparator_26 (.a(timer), .b(8'h3f), .eq(n159));  // open: gt, lt
  Multiplexer #(.width(5), .select(1), .enable("false")) multiplexer_24 (
    .in0(n172), .in1(5'b01100), .out(n173), .sel(n113));
  Multiplexer #(.width(5), .select(1), .enable("false")) multiplexer_25 (
    .in0(n186), .in1(5'b00100), .out(n187), .sel(n46));
  Subtractor #(.width(9)) subtractor_2 (.a(length), .b(9'h3), .out(n206), .bin(1'b0));  // open: bout
  or u_n7 (n7, n4, WON);
  Comparator #(.width(3), .mode("unsigned")) comparator_27 (.a(KEY), .b(3'b010), .eq(n21));  // open: gt, lt
  and u_n35 (n35, n15, n34);
  and u_n46 (n46, n43, n45);
  and u_n59 (n59, n58, n1);
  Multiplexer #(.width(4), .select(1), .enable("false")) multiplexer_26 (.in0(n76), .in1(n77), .out(n78), .sel(n71));
  not u_n106 (n106, n105);
  Adder #(.width(9)) adder_8 (.a(length), .b(9'h1), .out(n116), .cin(1'b0));  // open: cout
  RAM #(.addrWidth(8), .dataWidth(1), .Select("high"), .simpleMode("false"), .bus("separate")) u_occupied (
    .addr(n139), .din(n140), .data(occupied), .str(n142), .sel(1'b1), .clk(CLK), .clr(CLEAR));  // open: ld
  Register #(.width(8), .trigger("rising"), .Select("high")) u_tries (
    .D(n149), .en(n147), .Q(tries), .clk(CLK), .clr(n150), .cs(1'b1), .preset(1'b0));
  and u_n160 (n160, n1, n159);
  Multiplexer #(.width(5), .select(1), .enable("false")) multiplexer_27 (
    .in0(n173), .in1(5'b01111), .out(n174), .sel(n165));
  Multiplexer #(.width(5), .select(1), .enable("false")) multiplexer_28 (
    .in0(n187), .in1(5'b00001), .out(n188), .sel(CLEAR));
  Multiplexer #(.width(8), .select(1), .enable("false")) multiplexer_29 (
    .in0(n198), .in1(8'he0), .out(COLOR), .sel(n157));
  and u_n8 (n8, n7, VALID);
  not u_n36 (n36, n35);
  Multiplexer #(.width(2), .select(1), .enable("false")) multiplexer_30 (.in0(n28), .in1(2'b00), .out(n47), .sel(n46));
  Register #(.width(1), .trigger("rising"), .Select("high")) u_turn_lock (
    .D(n63), .en(n64), .Q(turn_lock), .clk(CLK), .clr(CLEAR), .cs(1'b1), .preset(1'b0));
  Comparator #(.width(2), .mode("unsigned")) comparator_28 (.a(dir), .b(2'b01), .eq(n79));  // open: gt, lt
  Comparator #(.width(4), .mode("unsigned")) comparator_29 (.a(head[3:0]), .b(4'b0000), .eq(n93));  // open: gt, lt
  and u_n107 (n107, occupied, n106);
  Adder #(.width(8)) adder_9 (.a(tries), .b(8'h1), .out(n149), .cin(1'b0));  // open: cout
  and u_n161 (n161, n160, n9);
  Multiplexer #(.width(5), .select(1), .enable("false")) multiplexer_31 (
    .in0(n174), .in1(5'b01011), .out(n175), .sel(n135));
  Multiplexer #(.width(5), .select(1), .enable("false")) multiplexer_32 (
    .in0(n188), .in1({5{1'b0}}), .out(n189), .sel(n155));
  Multiplexer #(.width(8), .select(1), .enable("false")) multiplexer_33 (
    .in0(n206[7:0]), .in1({8{1'b0}}), .out(SCORE), .sel(n205));
  not u_n9 (n9, PAUSED);
  and u_n37 (n37, n8, n36);
  and u_n48 (n48, n37, DOWN);
  Comparator #(.width(2), .mode("unsigned")) comparator_30 (.a(dir), .b(2'b11), .eq(n80));  // open: gt, lt
  and u_n94 (n94, n72, n93);
  or u_n108 (n108, n101, n107);
  Multiplexer #(.width(9), .select(1), .enable("false")) multiplexer_34 (.in0(n116), .in1(9'h3), .out(n118), .sel(n46));
  Comparator #(.width(5), .mode("unsigned")) comparator_31 (.a(phase), .b(5'b00101), .eq(n133));  // open: gt, lt
  or u_n150 (n150, CLEAR, n144);
  not u_n162 (n162, n59);
  Multiplexer #(.width(5), .select(1), .enable("false")) multiplexer_35 (
    .in0(5'b01010), .in1(5'b10000), .out(n176), .sel(n108));
  Multiplexer #(.width(8), .select(1), .enable("false")) multiplexer_36 (
    .in0(n136), .in1(food), .out(n190), .sel(n157));
  or u_n201 (n201, n43, n157);
  and u_n10 (n10, n1, n9);
  Multiplexer #(.width(2), .select(1), .enable("false")) multiplexer_37 (
    .in0(2'b00), .in1(2'b10), .out(n24), .sel(n21));
  and u_n49 (n49, n48, n13);
  Comparator #(.width(5), .mode("unsigned")) comparator_32 (.a(phase), .b(5'b00111), .eq(n61));  // open: gt, lt
  or u_n95 (n95, n91, n94);
  not u_n109 (n109, n108);
  and u_n119 (n119, n113, ate);
  Register #(.width(8), .trigger("rising"), .Select("high")) u_food (
    .D(candidate), .en(n152), .Q(food), .clk(CLK), .clr(CLEAR), .cs(1'b1), .preset(1'b0));
  and u_n163 (n163, n161, n162);
  Multiplexer #(.width(5), .select(1), .enable("false")) multiplexer_38 (.in0(n175), .in1(n176), .out(n177), .sel(n88));
  Multiplexer #(.width(8), .select(1), .enable("false")) multiplexer_39 (
    .in0(n190), .in1(initial_cell), .out({Y[3:0], X[3:0]}), .sel(n43));
  or u_n202 (n202, n201, n141);
  and u_n11 (n11, n10, turn_lock);
  and u_n50 (n50, n49, n34);
  or u_n62 (n62, n61, n59);
  Subtractor #(.width(4)) subtractor_3 (.a(head[7:4]), .b(4'b0001), .out(n82), .bin(1'b0));  // open: bout
  Comparator #(.width(4), .mode("unsigned")) comparator_33 (.a(head[7:4]), .b(4'b1111), .eq(n96));  // open: gt, lt
  and u_n110 (n110, n88, n109);
  or u_n120 (n120, n46, n119);
  Comparator #(.width(5), .mode("unsigned")) comparator_34 (.a(phase), .b(5'b01010), .eq(n135));  // open: gt, lt
  not u_n151 (n151, occupied);
  Multiplexer #(.width(5), .select(1), .enable("false")) multiplexer_40 (
    .in0(n177), .in1(5'b01001), .out(n178), .sel(n163));
  or n203 (WRITE, n202, n113);
  Multiplexer #(.width(2), .select(1), .enable("false")) multiplexer_41 (.in0(n24), .in1(2'b01), .out(n26), .sel(n19));
  and u_n51 (n51, n50, n1);
  Multiplexer #(.width(1), .select(1), .enable("false")) multiplexer_42 (.in0(1'b1), .in1(1'b0), .out(n63), .sel(n62));
  Multiplexer #(.width(4), .select(1), .enable("false")) multiplexer_43 (
    .in0(head[7:4]), .in1(n82), .out(n83), .sel(n80));
  and u_n97 (n97, n79, n96);
  Register #(.width(8), .trigger("rising"), .Select("high")) u_old_tail (
    .D(body), .en(n110), .Q(old_tail), .clk(CLK), .clr(CLEAR), .cs(1'b1), .preset(1'b0));
  Register #(.width(8), .trigger("rising"), .Select("high")) u_write_ptr (
    .D(n123), .en(n114), .Q(write_ptr), .clk(CLK), .clr(CLEAR), .cs(1'b1), .preset(1'b0));
  Multiplexer #(.width(8), .select(1), .enable("false")) multiplexer_44 (
    .in0(next_head), .in1(old_tail), .out(n136), .sel(n135));
  and u_n152 (n152, n133, n151);
  Comparator #(.width(5), .mode("unsigned")) comparator_35 (.a(phase), .b(5'b01101), .eq(n165));  // open: gt, lt
  Multiplexer #(.width(5), .select(1), .enable("false")) multiplexer_45 (
    .in0(n178), .in1(5'b01000), .out(n179), .sel(n61));

  assign RESET = CLEAR;
  assign X[4] = 1'b0;
  assign Y[4] = 1'b0;

  // Other names for the same wires on the sheet: ack = READ; n73[3:0] = head[3:0]; n81[3:0] = head[7:4]; n12 = KEY[2];
  //   n3 = DEAD; n6 = WON; n41 = CLEAR; n86[7:0] = {n85, n78}; n191[7:0] = {Y[3:0], X[3:0]}; n192[3:0] = X[3:0];
  //   n193[3:0] = X[3:0]; n194[3:0] = Y[3:0]; n195[3:0] = Y[3:0]; n200[7:0] = COLOR; n203 = WRITE; n204 = PRESENT;
  //   n207[7:0] = n206[7:0]; n208[7:0] = SCORE

  // Notes on the sheet:
  //   Snake engine / editable state machine and memories
  //   1. Input handshake / one turn per move
  //   2. Coordinates / boundary and tail-aware collision
  //   3. Initial path ROM / body ring RAM / occupancy RAM
  //   4. Random candidate / bounded free-cell scan
  //   5. State machine / explicit frame presentation
  //   contents of Initial_path__tail_to_head (hex, n*v repeats v):
  //   85 86 87
endmodule
